// Logisim project cpu.circ as structural Verilog
module half_adder (
  input  A,
  input  B,
  output SUM___A_xor_B,
  output CARRY___A_and_B
);

  xor xor_1 (SUM___A_xor_B, B, A);
  and and_1 (CARRY___A_and_B, A, B);

  // Notes on the sheet:
  //   CARRY___A_and_B: pull=down
  //   B: pull=down
  //   A: pull=down
  //   SUM___A_xor_B: pull=down
endmodule

module full_adder (
  input  in_1,
  input  in_2,
  input  in_3,
  output sum,
  output carry_out
);

  wire A_xor_B, and_1_out, and_2_out;

  xor xor_1 (A_xor_B, in_1, in_2);
  and and_1 (and_1_out, in_3, A_xor_B);
  and and_2 (and_2_out, in_1, in_2);
  xor xor_2 (sum, A_xor_B, in_3);
  or or_1 (carry_out, and_1_out, and_2_out);

  // Other names for the same wires on the sheet: A = in_1; B = in_2; carry_in = in_3

  // Notes on the sheet:
  //   sum: pull=down
  //   carry_out: pull=down
endmodule

module _8_bit_full_adder (
  input  [7:0] A,
  input  [7:0] B,
  input  in_3,
  output [7:0] sum,
  output carry_out
);

  wire full_adder_1_carry_out, full_adder_2_carry_out, full_adder_3_carry_out, full_adder_4_carry_out,
       full_adder_5_carry_out, full_adder_6_carry_out, full_adder_7_carry_out;

  full_adder full_adder_1 (.in_1(A[0]), .in_2(B[0]), .in_3(in_3), .sum(sum[0]), .carry_out(full_adder_1_carry_out));
  full_adder full_adder_2 (
    .in_1(A[1]), .in_2(B[1]), .in_3(full_adder_1_carry_out), .sum(sum[1]), .carry_out(full_adder_2_carry_out));
  full_adder full_adder_3 (
    .in_1(A[2]), .in_2(B[2]), .in_3(full_adder_2_carry_out), .sum(sum[2]), .carry_out(full_adder_3_carry_out));
  full_adder full_adder_4 (
    .in_1(A[3]), .in_2(B[3]), .in_3(full_adder_3_carry_out), .sum(sum[3]), .carry_out(full_adder_4_carry_out));
  full_adder full_adder_5 (
    .in_1(A[4]), .in_2(B[4]), .in_3(full_adder_4_carry_out), .sum(sum[4]), .carry_out(full_adder_5_carry_out));
  full_adder full_adder_6 (
    .in_1(A[5]), .in_2(B[5]), .in_3(full_adder_5_carry_out), .sum(sum[5]), .carry_out(full_adder_6_carry_out));
  full_adder full_adder_7 (
    .in_1(A[6]), .in_2(B[6]), .in_3(full_adder_6_carry_out), .sum(sum[6]), .carry_out(full_adder_7_carry_out));
  full_adder full_adder_8 (
    .in_1(A[7]), .in_2(B[7]), .in_3(full_adder_7_carry_out), .sum(sum[7]), .carry_out(carry_out));

  // Other names for the same wires on the sheet: carry_in = in_3

  // Notes on the sheet:
  //   sum: pull=down
  //   carry_out: pull=down
endmodule

module _16_bit_full_adder (
  input  [15:0] A,
  input  [15:0] B,
  input  in_3,
  output [15:0] \output ,
  output carry_out
);

  wire full_adder_1_carry_out, full_adder_2_carry_out, full_adder_3_carry_out, full_adder_4_carry_out,
       full_adder_5_carry_out, full_adder_6_carry_out, full_adder_7_carry_out, full_adder_8_carry_out,
       full_adder_9_carry_out, full_adder_10_carry_out, full_adder_11_carry_out, full_adder_12_carry_out,
       full_adder_13_carry_out, full_adder_14_carry_out, full_adder_15_carry_out;

  full_adder full_adder_1 (
    .in_1(A[0]), .in_2(B[0]), .in_3(in_3), .sum(\output [0]), .carry_out(full_adder_1_carry_out));
  full_adder full_adder_2 (
    .in_1(A[1]), .in_2(B[1]), .in_3(full_adder_1_carry_out), .sum(\output [1]),
    .carry_out(full_adder_2_carry_out));
  full_adder full_adder_3 (
    .in_1(A[2]), .in_2(B[2]), .in_3(full_adder_2_carry_out), .sum(\output [2]),
    .carry_out(full_adder_3_carry_out));
  full_adder full_adder_4 (
    .in_1(A[3]), .in_2(B[3]), .in_3(full_adder_3_carry_out), .sum(\output [3]),
    .carry_out(full_adder_4_carry_out));
  full_adder full_adder_5 (
    .in_1(A[4]), .in_2(B[4]), .in_3(full_adder_4_carry_out), .sum(\output [4]),
    .carry_out(full_adder_5_carry_out));
  full_adder full_adder_6 (
    .in_1(A[5]), .in_2(B[5]), .in_3(full_adder_5_carry_out), .sum(\output [5]),
    .carry_out(full_adder_6_carry_out));
  full_adder full_adder_7 (
    .in_1(A[6]), .in_2(B[6]), .in_3(full_adder_6_carry_out), .sum(\output [6]),
    .carry_out(full_adder_7_carry_out));
  full_adder full_adder_8 (
    .in_1(A[7]), .in_2(B[7]), .in_3(full_adder_7_carry_out), .sum(\output [7]),
    .carry_out(full_adder_8_carry_out));
  full_adder full_adder_9 (
    .in_1(A[8]), .in_2(B[8]), .in_3(full_adder_8_carry_out), .sum(\output [8]),
    .carry_out(full_adder_9_carry_out));
  full_adder full_adder_10 (
    .in_1(A[9]), .in_2(B[9]), .in_3(full_adder_9_carry_out), .sum(\output [9]),
    .carry_out(full_adder_10_carry_out));
  full_adder full_adder_11 (
    .in_1(A[10]), .in_2(B[10]), .in_3(full_adder_10_carry_out), .sum(\output [10]),
    .carry_out(full_adder_11_carry_out));
  full_adder full_adder_12 (
    .in_1(A[11]), .in_2(B[11]), .in_3(full_adder_11_carry_out), .sum(\output [11]),
    .carry_out(full_adder_12_carry_out));
  full_adder full_adder_13 (
    .in_1(A[12]), .in_2(B[12]), .in_3(full_adder_12_carry_out), .sum(\output [12]),
    .carry_out(full_adder_13_carry_out));
  full_adder full_adder_14 (
    .in_1(A[13]), .in_2(B[13]), .in_3(full_adder_13_carry_out), .sum(\output [13]),
    .carry_out(full_adder_14_carry_out));
  full_adder full_adder_15 (
    .in_1(A[14]), .in_2(B[14]), .in_3(full_adder_14_carry_out), .sum(\output [14]),
    .carry_out(full_adder_15_carry_out));
  full_adder full_adder_16 (
    .in_1(A[15]), .in_2(B[15]), .in_3(full_adder_15_carry_out), .sum(\output [15]), .carry_out(carry_out));

  // Other names for the same wires on the sheet: carry_in = in_3

  // Notes on the sheet:
  //   carry_out: pull=down
  //   A: pull=down
  //   output: pull=down
  //   B: pull=down
endmodule

module _16_bit_full_subtractor (
  input  [15:0] in_1,
  input  [15:0] in_2,
  input  in_3,
  output [15:0] \output ,
  output carry_out
);

  wire [15:0] B_s_complement, n16_bit_full_adder_1_output;

  _16_bit_full_adder u_16_bit_full_adder_1 (
    .A({{15{1'b0}}, in_3}), .B(in_2), .in_3(1'b0), .\output (n16_bit_full_adder_1_output));  // open: carry_out
  _16_bit_2_s_complement u_16_bit_2_s_complement_1 (
    .\input (n16_bit_full_adder_1_output), .in_2(1'b1), .out_3(B_s_complement));
  _16_bit_full_adder u_16_bit_full_adder_2 (
    .A(in_1), .B(B_s_complement), .in_3(1'b0), .\output (\output ), .carry_out(carry_out));

  // Other names for the same wires on the sheet: carry_in = in_3; A[15:0] = in_1; B[15:0] = in_2

  // Notes on the sheet:
  //   output: pull=down
  //   carry_out: pull=down
  //   in_2: pull=down
  //   in_1: pull=down
endmodule

module _16_bit_2_s_complement (
  input  [15:0] \input ,
  input  in_2,
  output [15:0] out_3
);

  wire and_1_out, and_2_out, and_3_out, and_4_out, and_5_out, and_6_out, and_7_out, and_8_out, and_9_out,
       and_10_out, and_11_out, and_12_out, and_13_out, and_14_out, and_15_out, and_16_out, and_17_out,
       and_18_out, and_19_out, and_20_out, and_21_out, and_22_out, and_23_out, and_24_out, and_25_out,
       and_26_out, and_27_out, and_28_out, and_29_out, and_30_out, and_31_out, and_32_out, carry0, carry1,
       carry2, carry3, carry4, carry5, carry6, carry7, carry8, carry9, carry10, carry11, carry12, carry13,
       carry14, carry15, not_1_out, not_2_out, not_3_out, not_4_out, not_5_out, not_6_out, not_7_out,
       not_8_out, not_9_out, not_10_out, not_11_out, not_12_out, not_13_out, not_14_out, not_15_out,
       not_16_out, not_17_out, out0, out1, out2, out3, out4, out5, out6, out7, out8, out9, out10, out11,
       out12, out13, out14, out15, xor_1_out, xor_2_out, xor_3_out, xor_4_out, xor_5_out, xor_6_out,
       xor_7_out, xor_8_out, xor_9_out, xor_28_out, xor_29_out, xor_30_out, xor_31_out, xor_40_out,
       xor_41_out, xor_42_out;

  not not_1 (not_1_out, \input [0]);
  not not_2 (not_2_out, \input [1]);
  not not_3 (not_3_out, \input [2]);
  not not_4 (not_4_out, \input [3]);
  not not_5 (not_5_out, \input [4]);
  not not_6 (not_6_out, \input [5]);
  not not_7 (not_7_out, \input [6]);
  not not_8 (not_8_out, \input [7]);
  not not_9 (not_9_out, \input [8]);
  xor xor_1 (xor_1_out, not_1_out, 1'b1);
  and and_1 (and_1_out, not_1_out, 1'b1);
  xor xor_2 (xor_2_out, not_2_out, 1'b0);
  and and_2 (and_2_out, not_2_out, 1'b0);
  xor xor_3 (xor_3_out, not_3_out, 1'b0);
  and and_3 (and_3_out, not_3_out, 1'b0);
  xor xor_4 (xor_4_out, not_4_out, 1'b0);
  and and_4 (and_4_out, not_4_out, 1'b0);
  xor xor_5 (xor_5_out, not_5_out, 1'b0);
  and and_5 (and_5_out, not_5_out, 1'b0);
  xor xor_6 (xor_6_out, not_6_out, 1'b0);
  and and_6 (and_6_out, not_6_out, 1'b0);
  xor xor_7 (xor_7_out, not_7_out, 1'b0);
  and and_7 (and_7_out, not_7_out, 1'b0);
  xor xor_8 (xor_8_out, not_8_out, 1'b0);
  and and_8 (and_8_out, not_8_out, 1'b0);
  xor xor_9 (xor_9_out, not_9_out, 1'b0);
  and and_9 (and_9_out, not_9_out, 1'b0);
  xor xor_10 (out0, 1'b0, xor_1_out);
  and and_10 (and_10_out, xor_1_out, 1'b0);
  xor xor_11 (out1, carry0, xor_2_out);
  and and_11 (and_11_out, xor_2_out, carry0);
  xor xor_12 (out2, carry1, xor_3_out);
  and and_12 (and_12_out, xor_3_out, carry1);
  xor xor_13 (out3, carry2, xor_4_out);
  and and_13 (and_13_out, xor_4_out, carry2);
  xor xor_14 (out4, carry3, xor_5_out);
  and and_14 (and_14_out, xor_5_out, carry3);
  xor xor_15 (out5, carry4, xor_6_out);
  and and_15 (and_15_out, xor_6_out, carry4);
  xor xor_16 (out6, carry5, xor_7_out);
  and and_16 (and_16_out, xor_7_out, carry5);
  xor xor_17 (out7, carry6, xor_8_out);
  and and_17 (and_17_out, xor_8_out, carry6);
  xor xor_18 (out8, carry7, xor_9_out);
  and and_18 (and_18_out, xor_9_out, carry7);
  xor xor_19 (carry0, and_10_out, and_1_out);
  xor xor_20 (carry1, and_11_out, and_2_out);
  xor xor_21 (carry2, and_12_out, and_3_out);
  xor xor_22 (carry3, and_13_out, and_4_out);
  xor xor_23 (carry4, and_14_out, and_5_out);
  xor xor_24 (carry5, and_15_out, and_6_out);
  xor xor_25 (carry6, and_16_out, and_7_out);
  xor xor_26 (carry7, and_17_out, and_8_out);
  xor xor_27 (carry8, and_18_out, and_9_out);
  not not_10 (not_10_out, \input [9]);
  not not_11 (not_11_out, \input [10]);
  not not_12 (not_12_out, \input [11]);
  not not_13 (not_13_out, \input [12]);
  xor xor_28 (xor_28_out, not_10_out, 1'b0);
  and and_19 (and_19_out, not_10_out, 1'b0);
  xor xor_29 (xor_29_out, not_11_out, 1'b0);
  and and_20 (and_20_out, not_11_out, 1'b0);
  xor xor_30 (xor_30_out, not_12_out, 1'b0);
  and and_21 (and_21_out, not_12_out, 1'b0);
  xor xor_31 (xor_31_out, not_13_out, 1'b0);
  and and_22 (and_22_out, not_13_out, 1'b0);
  assign out_3[0] = not_14_out ? \input [0] : 1'bz;  // Controlled_Buffer controlled_buffer_1
  assign out_3[1] = not_14_out ? \input [1] : 1'bz;  // Controlled_Buffer controlled_buffer_2
  assign out_3[2] = not_14_out ? \input [2] : 1'bz;  // Controlled_Buffer controlled_buffer_3
  assign out_3[3] = not_14_out ? \input [3] : 1'bz;  // Controlled_Buffer controlled_buffer_4
  assign out_3[4] = not_14_out ? \input [4] : 1'bz;  // Controlled_Buffer controlled_buffer_5
  assign out_3[5] = not_14_out ? \input [5] : 1'bz;  // Controlled_Buffer controlled_buffer_6
  assign out_3[6] = not_14_out ? \input [6] : 1'bz;  // Controlled_Buffer controlled_buffer_7
  assign out_3[7] = not_14_out ? \input [7] : 1'bz;  // Controlled_Buffer controlled_buffer_8
  assign out_3[8] = not_14_out ? \input [8] : 1'bz;  // Controlled_Buffer controlled_buffer_9
  assign out_3[9] = not_14_out ? \input [9] : 1'bz;  // Controlled_Buffer controlled_buffer_10
  assign out_3[10] = not_14_out ? \input [10] : 1'bz;  // Controlled_Buffer controlled_buffer_11
  assign out_3[11] = not_14_out ? \input [11] : 1'bz;  // Controlled_Buffer controlled_buffer_12
  assign out_3[12] = not_14_out ? \input [12] : 1'bz;  // Controlled_Buffer controlled_buffer_13
  assign out_3[13] = not_14_out ? \input [13] : 1'bz;  // Controlled_Buffer controlled_buffer_14
  assign out_3[14] = not_14_out ? \input [14] : 1'bz;  // Controlled_Buffer controlled_buffer_15
  assign out_3[15] = not_14_out ? \input [15] : 1'bz;  // Controlled_Buffer controlled_buffer_16
  xor xor_32 (out9, carry8, xor_28_out);
  and and_23 (and_23_out, xor_28_out, carry8);
  xor xor_33 (out10, carry9, xor_29_out);
  and and_24 (and_24_out, xor_29_out, carry9);
  xor xor_34 (out11, carry10, xor_30_out);
  and and_25 (and_25_out, xor_30_out, carry10);
  xor xor_35 (out12, carry11, xor_31_out);
  and and_26 (and_26_out, xor_31_out, carry11);
  assign out_3[0] = in_2 ? out0 : 1'bz;  // Controlled_Buffer controlled_buffer_17
  assign out_3[1] = in_2 ? out1 : 1'bz;  // Controlled_Buffer controlled_buffer_18
  assign out_3[2] = in_2 ? out2 : 1'bz;  // Controlled_Buffer controlled_buffer_19
  assign out_3[3] = in_2 ? out3 : 1'bz;  // Controlled_Buffer controlled_buffer_20
  assign out_3[4] = in_2 ? out4 : 1'bz;  // Controlled_Buffer controlled_buffer_21
  assign out_3[5] = in_2 ? out5 : 1'bz;  // Controlled_Buffer controlled_buffer_22
  assign out_3[6] = in_2 ? out6 : 1'bz;  // Controlled_Buffer controlled_buffer_23
  assign out_3[7] = in_2 ? out7 : 1'bz;  // Controlled_Buffer controlled_buffer_24
  assign out_3[8] = in_2 ? out8 : 1'bz;  // Controlled_Buffer controlled_buffer_25
  assign out_3[9] = in_2 ? out9 : 1'bz;  // Controlled_Buffer controlled_buffer_26
  assign out_3[10] = in_2 ? out10 : 1'bz;  // Controlled_Buffer controlled_buffer_27
  assign out_3[11] = in_2 ? out11 : 1'bz;  // Controlled_Buffer controlled_buffer_28
  assign out_3[12] = in_2 ? out12 : 1'bz;  // Controlled_Buffer controlled_buffer_29
  assign out_3[13] = in_2 ? out13 : 1'bz;  // Controlled_Buffer controlled_buffer_30
  assign out_3[14] = in_2 ? out14 : 1'bz;  // Controlled_Buffer controlled_buffer_31
  assign out_3[15] = in_2 ? out15 : 1'bz;  // Controlled_Buffer controlled_buffer_32
  xor xor_36 (carry9, and_23_out, and_19_out);
  xor xor_37 (carry10, and_24_out, and_20_out);
  xor xor_38 (carry11, and_25_out, and_21_out);
  xor xor_39 (carry12, and_26_out, and_22_out);
  not not_14 (not_14_out, in_2);
  not not_15 (not_15_out, \input [13]);
  not not_16 (not_16_out, \input [14]);
  not not_17 (not_17_out, \input [15]);
  xor xor_40 (xor_40_out, not_15_out, 1'b0);
  and and_27 (and_27_out, not_15_out, 1'b0);
  xor xor_41 (xor_41_out, not_16_out, 1'b0);
  and and_28 (and_28_out, not_16_out, 1'b0);
  xor xor_42 (xor_42_out, not_17_out, 1'b0);
  and and_29 (and_29_out, not_17_out, 1'b0);
  xor xor_43 (out13, carry12, xor_40_out);
  and and_30 (and_30_out, xor_40_out, carry12);
  xor xor_44 (out14, carry13, xor_41_out);
  and and_31 (and_31_out, xor_41_out, carry13);
  xor xor_45 (out15, carry14, xor_42_out);
  and and_32 (and_32_out, xor_42_out, carry14);
  xor xor_46 (carry13, and_30_out, and_27_out);
  xor xor_47 (carry14, and_31_out, and_28_out);
  xor xor_48 (carry15, and_32_out, and_29_out);

  // Other names for the same wires on the sheet: enable = in_2; i0 = \input [0]; i1 = \input [1]; i2 = \input [2];
  //   i3 = \input [3]; i4 = \input [4]; i5 = \input [5]; i6 = \input [6]; i7 = \input [7]; i8 = \input [8];
  //   i9 = \input [9]; i10 = \input [10]; i11 = \input [11]; i12 = \input [12]; i13 = \input [13]; i14 = \input [14];
  //   i15 = \input [15]

  // Notes on the sheet:
  //   out_3: pull=down
  //   input: pull=down
  //   in_2: pull=down
endmodule

module active_low_SR_latch (
  input  in_1,
  input  in_2,
  output Q,
  output Q_prime
);

  nand nand_1 (Q, in_1, Q_prime);
  nand nand_2 (Q_prime, Q, in_2);

  // Other names for the same wires on the sheet: R = in_2; S = in_1

  // Notes on the sheet:
  //   Q_prime: pull=down
  //   Q: pull=up
endmodule

module active_high_SR_latch (
  input  in_1,
  input  in_2,
  output Q,
  output Q_prime
);

  nor nor_1 (Q, in_2, Q_prime);
  nor nor_2 (Q_prime, Q, in_1);

  // Other names for the same wires on the sheet: R = in_2; S = in_1

  // Notes on the sheet:
  //   Q: pull=down
  //   Q_prime: pull=down
endmodule

module _1_bit_memory_cell (
  input  in_1,
  input  in_2,
  output \output 
);

  Register #(.width(1), .trigger("high")) register_1 (.D(in_1), .en(in_2), .Q(\output ), .clk(1'b1), .clr(1'b0));

  // Other names for the same wires on the sheet: data = in_1; set = in_2

  // Notes on the sheet:
  //   output: pull=down
endmodule

module _1_byte_memory_cell (
  input  [7:0] \input ,
  input  in_2,
  output [7:0] \output 
);

  _1_bit_memory_cell u_1_bit_memory_cell_1 (.in_1(\input [0]), .in_2(in_2), .\output (\output [0]));
  _1_bit_memory_cell u_1_bit_memory_cell_2 (.in_1(\input [1]), .in_2(in_2), .\output (\output [1]));
  _1_bit_memory_cell u_1_bit_memory_cell_3 (.in_1(\input [2]), .in_2(in_2), .\output (\output [2]));
  _1_bit_memory_cell u_1_bit_memory_cell_4 (.in_1(\input [3]), .in_2(in_2), .\output (\output [3]));
  _1_bit_memory_cell u_1_bit_memory_cell_5 (.in_1(\input [4]), .in_2(in_2), .\output (\output [4]));
  _1_bit_memory_cell u_1_bit_memory_cell_6 (.in_1(\input [5]), .in_2(in_2), .\output (\output [5]));
  _1_bit_memory_cell u_1_bit_memory_cell_7 (.in_1(\input [6]), .in_2(in_2), .\output (\output [6]));
  _1_bit_memory_cell u_1_bit_memory_cell_8 (.in_1(\input [7]), .in_2(in_2), .\output (\output [7]));

  // Other names for the same wires on the sheet: enable = in_2

  // Notes on the sheet:
  //   output: pull=down
endmodule

module _2_bytes_memory_cell (
  input  [15:0] \input ,
  input  in_2,
  output [15:0] \output 
);

  _1_bit_memory_cell u_1_bit_memory_cell_1 (.in_1(\input [0]), .in_2(in_2), .\output (\output [0]));
  _1_bit_memory_cell u_1_bit_memory_cell_2 (.in_1(\input [1]), .in_2(in_2), .\output (\output [1]));
  _1_bit_memory_cell u_1_bit_memory_cell_3 (.in_1(\input [2]), .in_2(in_2), .\output (\output [2]));
  _1_bit_memory_cell u_1_bit_memory_cell_4 (.in_1(\input [3]), .in_2(in_2), .\output (\output [3]));
  _1_bit_memory_cell u_1_bit_memory_cell_5 (.in_1(\input [4]), .in_2(in_2), .\output (\output [4]));
  _1_bit_memory_cell u_1_bit_memory_cell_6 (.in_1(\input [5]), .in_2(in_2), .\output (\output [5]));
  _1_bit_memory_cell u_1_bit_memory_cell_7 (.in_1(\input [6]), .in_2(in_2), .\output (\output [6]));
  _1_bit_memory_cell u_1_bit_memory_cell_8 (.in_1(\input [7]), .in_2(in_2), .\output (\output [7]));
  _1_bit_memory_cell u_1_bit_memory_cell_9 (.in_1(\input [8]), .in_2(in_2), .\output (\output [8]));
  _1_bit_memory_cell u_1_bit_memory_cell_10 (.in_1(\input [9]), .in_2(in_2), .\output (\output [9]));
  _1_bit_memory_cell u_1_bit_memory_cell_11 (.in_1(\input [10]), .in_2(in_2), .\output (\output [10]));
  _1_bit_memory_cell u_1_bit_memory_cell_12 (.in_1(\input [11]), .in_2(in_2), .\output (\output [11]));
  _1_bit_memory_cell u_1_bit_memory_cell_13 (.in_1(\input [12]), .in_2(in_2), .\output (\output [12]));
  _1_bit_memory_cell u_1_bit_memory_cell_14 (.in_1(\input [13]), .in_2(in_2), .\output (\output [13]));
  _1_bit_memory_cell u_1_bit_memory_cell_15 (.in_1(\input [14]), .in_2(in_2), .\output (\output [14]));
  _1_bit_memory_cell u_1_bit_memory_cell_16 (.in_1(\input [15]), .in_2(in_2), .\output (\output [15]));

  // Other names for the same wires on the sheet: enable = in_2

  // Notes on the sheet:
  //   input: pull=down
  //   output: pull=down
endmodule

module _3_bytes_memory_cell (
  input  [23:0] \input ,
  input  in_2,
  output [23:0] \output 
);

  _1_bit_memory_cell u_1_bit_memory_cell_1 (.in_1(\input [0]), .in_2(in_2), .\output (\output [0]));
  _1_bit_memory_cell u_1_bit_memory_cell_2 (.in_1(\input [1]), .in_2(in_2), .\output (\output [1]));
  _1_bit_memory_cell u_1_bit_memory_cell_3 (.in_1(\input [2]), .in_2(in_2), .\output (\output [2]));
  _1_bit_memory_cell u_1_bit_memory_cell_4 (.in_1(\input [3]), .in_2(in_2), .\output (\output [3]));
  _1_bit_memory_cell u_1_bit_memory_cell_5 (.in_1(\input [4]), .in_2(in_2), .\output (\output [4]));
  _1_bit_memory_cell u_1_bit_memory_cell_6 (.in_1(\input [5]), .in_2(in_2), .\output (\output [5]));
  _1_bit_memory_cell u_1_bit_memory_cell_7 (.in_1(\input [6]), .in_2(in_2), .\output (\output [6]));
  _1_bit_memory_cell u_1_bit_memory_cell_8 (.in_1(\input [7]), .in_2(in_2), .\output (\output [7]));
  _1_bit_memory_cell u_1_bit_memory_cell_9 (.in_1(\input [8]), .in_2(in_2), .\output (\output [8]));
  _1_bit_memory_cell u_1_bit_memory_cell_10 (.in_1(\input [9]), .in_2(in_2), .\output (\output [9]));
  _1_bit_memory_cell u_1_bit_memory_cell_11 (.in_1(\input [10]), .in_2(in_2), .\output (\output [10]));
  _1_bit_memory_cell u_1_bit_memory_cell_12 (.in_1(\input [11]), .in_2(in_2), .\output (\output [11]));
  _1_bit_memory_cell u_1_bit_memory_cell_13 (.in_1(\input [12]), .in_2(in_2), .\output (\output [12]));
  _1_bit_memory_cell u_1_bit_memory_cell_14 (.in_1(\input [13]), .in_2(in_2), .\output (\output [13]));
  _1_bit_memory_cell u_1_bit_memory_cell_15 (.in_1(\input [14]), .in_2(in_2), .\output (\output [14]));
  _1_bit_memory_cell u_1_bit_memory_cell_16 (.in_1(\input [15]), .in_2(in_2), .\output (\output [15]));
  _1_bit_memory_cell u_1_bit_memory_cell_17 (.in_1(\input [16]), .in_2(in_2), .\output (\output [16]));
  _1_bit_memory_cell u_1_bit_memory_cell_18 (.in_1(\input [17]), .in_2(in_2), .\output (\output [17]));
  _1_bit_memory_cell u_1_bit_memory_cell_19 (.in_1(\input [18]), .in_2(in_2), .\output (\output [18]));
  _1_bit_memory_cell u_1_bit_memory_cell_20 (.in_1(\input [19]), .in_2(in_2), .\output (\output [19]));
  _1_bit_memory_cell u_1_bit_memory_cell_21 (.in_1(\input [20]), .in_2(in_2), .\output (\output [20]));
  _1_bit_memory_cell u_1_bit_memory_cell_22 (.in_1(\input [21]), .in_2(in_2), .\output (\output [21]));
  _1_bit_memory_cell u_1_bit_memory_cell_23 (.in_1(\input [22]), .in_2(in_2), .\output (\output [22]));
  _1_bit_memory_cell u_1_bit_memory_cell_24 (.in_1(\input [23]), .in_2(in_2), .\output (\output [23]));

  // Other names for the same wires on the sheet: enable = in_2

  // Notes on the sheet:
  //   output: pull=down
  //   input: pull=down
endmodule

module _8_bit_enable_cell (
  input  [7:0] in_1,
  input  in_2,
  output [7:0] out_3
);

  wire and_1_out, and_2_out, and_3_out, and_4_out, and_5_out, and_6_out, and_7_out, and_8_out;

  and and_1 (and_1_out, in_1[0], in_2);
  and and_2 (and_2_out, in_1[1], in_2);
  and and_3 (and_3_out, in_1[2], in_2);
  and and_4 (and_4_out, in_1[3], in_2);
  and and_5 (and_5_out, in_1[4], in_2);
  and and_6 (and_6_out, in_1[5], in_2);
  and and_7 (and_7_out, in_1[6], in_2);
  and and_8 (and_8_out, in_1[7], in_2);
  assign out_3[0] = in_2 ? and_1_out : 1'bz;  // Controlled_Buffer controlled_buffer_1
  assign out_3[1] = in_2 ? and_2_out : 1'bz;  // Controlled_Buffer controlled_buffer_2
  assign out_3[2] = in_2 ? and_3_out : 1'bz;  // Controlled_Buffer controlled_buffer_3
  assign out_3[3] = in_2 ? and_4_out : 1'bz;  // Controlled_Buffer controlled_buffer_4
  assign out_3[4] = in_2 ? and_5_out : 1'bz;  // Controlled_Buffer controlled_buffer_5
  assign out_3[5] = in_2 ? and_6_out : 1'bz;  // Controlled_Buffer controlled_buffer_6
  assign out_3[6] = in_2 ? and_7_out : 1'bz;  // Controlled_Buffer controlled_buffer_7
  assign out_3[7] = in_2 ? and_8_out : 1'bz;  // Controlled_Buffer controlled_buffer_8

  // Other names for the same wires on the sheet: enable = in_2

  // Notes on the sheet:
  //   out_3: pull=down
endmodule

module _16_bit_enable_cell (
  input  [15:0] \input ,
  input  in_2,
  output [15:0] \output 
);

  wire and_1_out, and_2_out, and_3_out, and_4_out, and_5_out, and_6_out, and_7_out, and_8_out, and_9_out,
       and_10_out, and_11_out, and_12_out, and_13_out, and_14_out, and_15_out, and_16_out;

  and and_1 (and_1_out, \input [0], in_2);
  and and_2 (and_2_out, \input [1], in_2);
  and and_3 (and_3_out, \input [2], in_2);
  and and_4 (and_4_out, \input [3], in_2);
  and and_5 (and_5_out, \input [4], in_2);
  and and_6 (and_6_out, \input [5], in_2);
  and and_7 (and_7_out, \input [6], in_2);
  and and_8 (and_8_out, \input [7], in_2);
  and and_9 (and_9_out, \input [8], in_2);
  and and_10 (and_10_out, \input [9], in_2);
  and and_11 (and_11_out, \input [10], in_2);
  and and_12 (and_12_out, \input [11], in_2);
  and and_13 (and_13_out, \input [12], in_2);
  and and_14 (and_14_out, \input [13], in_2);
  and and_15 (and_15_out, \input [14], in_2);
  and and_16 (and_16_out, \input [15], in_2);
  assign \output [0] = in_2 ? and_1_out : 1'bz;  // Controlled_Buffer controlled_buffer_1
  assign \output [1] = in_2 ? and_2_out : 1'bz;  // Controlled_Buffer controlled_buffer_2
  assign \output [2] = in_2 ? and_3_out : 1'bz;  // Controlled_Buffer controlled_buffer_3
  assign \output [3] = in_2 ? and_4_out : 1'bz;  // Controlled_Buffer controlled_buffer_4
  assign \output [4] = in_2 ? and_5_out : 1'bz;  // Controlled_Buffer controlled_buffer_5
  assign \output [5] = in_2 ? and_6_out : 1'bz;  // Controlled_Buffer controlled_buffer_6
  assign \output [6] = in_2 ? and_7_out : 1'bz;  // Controlled_Buffer controlled_buffer_7
  assign \output [7] = in_2 ? and_8_out : 1'bz;  // Controlled_Buffer controlled_buffer_8
  assign \output [8] = in_2 ? and_9_out : 1'bz;  // Controlled_Buffer controlled_buffer_9
  assign \output [9] = in_2 ? and_10_out : 1'bz;  // Controlled_Buffer controlled_buffer_10
  assign \output [10] = in_2 ? and_11_out : 1'bz;  // Controlled_Buffer controlled_buffer_11
  assign \output [11] = in_2 ? and_12_out : 1'bz;  // Controlled_Buffer controlled_buffer_12
  assign \output [12] = in_2 ? and_13_out : 1'bz;  // Controlled_Buffer controlled_buffer_13
  assign \output [13] = in_2 ? and_14_out : 1'bz;  // Controlled_Buffer controlled_buffer_14
  assign \output [14] = in_2 ? and_15_out : 1'bz;  // Controlled_Buffer controlled_buffer_15
  assign \output [15] = in_2 ? and_16_out : 1'bz;  // Controlled_Buffer controlled_buffer_16

  // Other names for the same wires on the sheet: enable = in_2

  // Notes on the sheet:
  //   output: pull=down
  //   input: pull=down
endmodule

module _8_bit_register (
  input  [7:0] in_1,
  input  in_2,
  input  in_3,
  output [7:0] out_4,
  output [7:0] out_5
);

  wire [7:0] n8_bit_enable_cell_1_out_3;

  _1_byte_memory_cell u_1_byte_memory_cell_1 (.\input (in_1), .in_2(in_2), .\output (out_5));
  _8_bit_enable_cell u_8_bit_enable_cell_1 (.in_1(out_5), .in_2(in_3), .out_3(n8_bit_enable_cell_1_out_3));
  assign out_4 = in_3 ? n8_bit_enable_cell_1_out_3 : 8'bz;  // Controlled_Buffer controlled_buffer_1

  // Other names for the same wires on the sheet: enable = in_3; input[7:0] = in_1; output[7:0] = out_4; set = in_2;
  //   storage[7:0] = out_5

  // Notes on the sheet:
  //   in_2: pull=down
  //   out_4: pull=down
  //   out_5: pull=down
  //   in_3: pull=down
  //   in_1: pull=down
endmodule

module _16_bit_register (
  input  [15:0] in_1,
  input  in_2,
  input  in_3,
  output [15:0] out_4,
  output [15:0] out_5
);

  wire [15:0] n16_bit_enable_cell_1_output;

  _2_bytes_memory_cell u_2_bytes_memory_cell_1 (.\input (in_1), .in_2(in_2), .\output (out_5));
  _16_bit_enable_cell u_16_bit_enable_cell_1 (.\input (out_5), .in_2(in_3), .\output (n16_bit_enable_cell_1_output));
  assign out_4 = in_3 ? n16_bit_enable_cell_1_output : 16'bz;  // Controlled_Buffer controlled_buffer_1

  // Other names for the same wires on the sheet: enable = in_3; input[15:0] = in_1; output[15:0] = out_4; set = in_2;
  //   storage[15:0] = out_5

  // Notes on the sheet:
  //   out_5: pull=down
  //   in_2: pull=down
  //   in_1: pull=down
  //   in_3: pull=down
  //   out_4: pull=down
endmodule

module _24_bit_register (
  input  [23:0] in_1,
  input  in_2,
  input  in_3,
  output [23:0] out_4,
  output [23:0] out_5
);

  wire [23:0] n3_bytes_memory_cell_2_output;

  _3_bytes_memory_cell u_3_bytes_memory_cell_1 (.\input (in_1), .in_2(in_2), .\output (out_5));
  _3_bytes_memory_cell u_3_bytes_memory_cell_2 (.\input (out_5), .in_2(in_3), .\output (n3_bytes_memory_cell_2_output));
  assign out_4 = in_3 ? n3_bytes_memory_cell_2_output : 24'bz;  // Controlled_Buffer controlled_buffer_1

  // Other names for the same wires on the sheet: enable = in_3; input[23:0] = in_1; output[23:0] = out_4; set = in_2;
  //   storage[23:0] = out_5

  // Notes on the sheet:
  //   out_4: pull=down
  //   in_3: pull=down
  //   in_1: pull=down
  //   in_2: pull=down
  //   out_5: pull=down
endmodule

module _2x4_decoder (
  input  in_1,
  input  in_2,
  output _00,
  output _01,
  output _10,
  output _11
);

  wire nA, nB;

  not not_1 (nA, in_1);
  not not_2 (nB, in_2);
  and and_1 (_00, nA, nB);
  and and_2 (_01, nA, in_2);
  and and_3 (_10, in_1, nB);
  and and_4 (_11, in_2, in_1);

  // Other names for the same wires on the sheet: A = in_1; A_prime_B = _01; A_prime_B_prime = _00; AB = _11;
  //   AB_prime = _10; B = in_2

  // Notes on the sheet:
  //   _01: pull=down
  //   _10: pull=down
  //   in_2: pull=down
  //   _00: pull=down
  //   in_1: pull=down
  //   _11: pull=down
endmodule

module _3x8_decoder (
  input  in_1,
  input  in_2,
  input  in_3,
  output _000,
  output _001,
  output _010,
  output _011,
  output _100,
  output _101,
  output _110,
  output _111
);

  wire nA, nB, nC;

  not not_1 (nA, in_1);
  not not_2 (nB, in_2);
  not not_3 (nC, in_3);
  and and_1 (_000, nA, nB, nC);
  and and_2 (_001, nA, nB, in_3);
  and and_3 (_010, nA, in_2, nC);
  and and_4 (_011, nA, in_2, in_3);
  and and_5 (_100, in_1, nB, nC);
  and and_6 (_101, in_1, nB, in_3);
  and and_7 (_110, in_1, in_2, nC);
  and and_8 (_111, in_1, in_2, in_3);

  // Other names for the same wires on the sheet: A = in_1; A_prime_B_prime_C = _001; A_prime_B_prime_C_prime = _000;
  //   A_prime_BC = _011; A_prime_BC_prime = _010; AB_prime_C = _101; AB_prime_C_prime = _100; ABC = _111;
  //   ABC_prime = _110; B = in_2; C = in_3

  // Notes on the sheet:
  //   _011: pull=down
  //   in_1: pull=down
  //   _100: pull=down
  //   _010: pull=down
  //   _111: pull=down
  //   _110: pull=down
  //   _001: pull=down
  //   _000: pull=down
  //   _101: pull=down
  //   in_3: pull=down
  //   in_2: pull=down
endmodule

module _4x16_decoder (
  input  in_1,
  input  in_2,
  input  in_3,
  input  in_4,
  output _0000,
  output _0001,
  output _0010,
  output _0011,
  output _0100,
  output _0101,
  output _0110,
  output _0111,
  output _1000,
  output _1001,
  output _1010,
  output _1011,
  output _1100,
  output _1101,
  output _1110,
  output _1111
);

  wire nA, nB, nC, nD;

  not not_1 (nA, in_1);
  not not_2 (nB, in_2);
  not not_3 (nC, in_3);
  not not_4 (nD, in_4);
  and and_1 (_0000, nA, nB, nC, nD);
  and and_2 (_0001, nA, nB, nC, in_4);
  and and_3 (_0010, nA, nB, in_3, nD);
  and and_4 (_0011, nA, nB, in_3, in_4);
  and and_5 (_0100, nA, in_2, nC, nD);
  and and_6 (_0101, nA, in_2, nC, in_4);
  and and_7 (_0110, nA, in_2, in_3, nD);
  and and_8 (_0111, nA, in_2, in_3, in_4);
  and and_9 (_1000, in_1, nB, nC, nD);
  and and_10 (_1001, in_1, nB, nC, in_4);
  and and_11 (_1010, in_1, nB, in_3, nD);
  and and_12 (_1011, in_1, nB, in_3, in_4);
  and and_13 (_1100, in_1, in_2, nC, nD);
  and and_14 (_1101, in_1, in_2, nC, in_4);
  and and_15 (_1110, in_1, in_2, in_3, nD);
  and and_16 (_1111, in_1, in_2, in_3, in_4);

  // Other names for the same wires on the sheet: A = in_1; A_prime_B_prime_C_prime_D = _0001;
  //   A_prime_B_prime_C_prime_D_prime = _0000; A_prime_B_prime_CD = _0011; A_prime_B_prime_CD_prime = _0010;
  //   A_prime_BC_prime_D = _0101; A_prime_BC_prime_D_prime = _0100; A_prime_BCD = _0111; A_prime_BCD_prime = _0110;
  //   AB_prime_C_prime_D = _1001; AB_prime_C_prime_D_prime = _1000; AB_prime_CD = _1011; AB_prime_CD_prime = _1010;
  //   ABC_prime_D = _1101; ABC_prime_D_prime = _1100; ABCD = _1111; ABCD_prime = _1110; B = in_2; C = in_3; D = in_4

  // Notes on the sheet:
  //   _0000: pull=down
  //   _1011: pull=down
  //   _0001: pull=down
  //   _0110: pull=down
  //   _1010: pull=down
  //   _1001: pull=down
  //   _1000: pull=down
  //   _1101: pull=down
  //   _1100: pull=down
  //   _1111: pull=down
  //   _0100: pull=down
  //   _1110: pull=down
  //   _0010: pull=down
  //   _0011: pull=down
  //   in_4: pull=down
  //   in_3: pull=down
  //   in_1: pull=down
  //   in_2: pull=down
  //   _0111: pull=down
  //   _0101: pull=down
endmodule

module _8_bit_reverter (
  input  [7:0] in_1,
  output [7:0] out_2
);

  not not_1 (out_2[0], in_1[0]);
  not not_2 (out_2[1], in_1[1]);
  not not_3 (out_2[2], in_1[2]);
  not not_4 (out_2[3], in_1[3]);
  not not_5 (out_2[4], in_1[4]);
  not not_6 (out_2[5], in_1[5]);
  not not_7 (out_2[6], in_1[6]);
  not not_8 (out_2[7], in_1[7]);

  // Notes on the sheet:
  //   out_2: pull=down
endmodule

module _16_bit_reverter (
  input  [15:0] in_1,
  output [15:0] out_2
);

  not not_1 (out_2[0], in_1[0]);
  not not_2 (out_2[1], in_1[1]);
  not not_3 (out_2[2], in_1[2]);
  not not_4 (out_2[3], in_1[3]);
  not not_5 (out_2[4], in_1[4]);
  not not_6 (out_2[5], in_1[5]);
  not not_7 (out_2[6], in_1[6]);
  not not_8 (out_2[7], in_1[7]);
  not not_9 (out_2[8], in_1[8]);
  not not_10 (out_2[9], in_1[9]);
  not not_11 (out_2[10], in_1[10]);
  not not_12 (out_2[11], in_1[11]);
  not not_13 (out_2[12], in_1[12]);
  not not_14 (out_2[13], in_1[13]);
  not not_15 (out_2[14], in_1[14]);
  not not_16 (out_2[15], in_1[15]);

  // Notes on the sheet:
  //   out_2: pull=down
endmodule

module _8_bit_negator (
  input  [7:0] in_1,
  output [7:0] out_2
);

  not not_1 (out_2[7], in_1[7]);

  assign out_2[6:0] = in_1[6:0];

  // Notes on the sheet:
  //   out_2: pull=down
endmodule

module _16_bit_negator (
  input  [15:0] in_1,
  output [15:0] out_2
);

  not not_1 (out_2[15], in_1[15]);

  assign out_2[14:0] = in_1[14:0];

  // Notes on the sheet:
  //   out_2: pull=down
endmodule

module _8_bit_right_shifter (
  input  [7:0] in_1,
  input  in_2,
  output [7:0] out_3,
  output out_4
);

  wire [7:1] n8_bit_register_1_out_4;

  _8_bit_register u_8_bit_register_1 (
    .in_1(in_1), .in_2(1'b1), .in_3(1'b1), .out_4({n8_bit_register_1_out_4, out_4}));  // open: out_5
  _8_bit_register u_8_bit_register_2 (
    .in_1({in_2, n8_bit_register_1_out_4}), .in_2(1'b1), .in_3(1'b1), .out_4(out_3));  // open: out_5

  // Other names for the same wires on the sheet: shift_out = out_4; shift_in = in_2; input[7:0] = in_1;
  //   output[7:0] = out_3

  // Notes on the sheet:
  //   in_1: pull=down
  //   out_3: pull=down
  //   out_4: pull=down
  //   in_2: pull=down
endmodule

module _16_bit_right_shifter (
  input  [15:0] in_1,
  input  in_2,
  output [15:0] out_3,
  output out_4
);

  wire [15:1] n16_bit_register_1_out_4;

  _16_bit_register u_16_bit_register_1 (
    .in_1(in_1), .in_2(1'b1), .in_3(1'b1), .out_4({n16_bit_register_1_out_4, out_4}));  // open: out_5
  _16_bit_register u_16_bit_register_2 (
    .in_1({in_2, n16_bit_register_1_out_4}), .in_2(1'b1), .in_3(1'b1), .out_4(out_3));  // open: out_5

  // Other names for the same wires on the sheet: shift_out = out_4; shift_in = in_2; input[15:0] = in_1;
  //   output[15:0] = out_3

  // Notes on the sheet:
  //   out_3: pull=down
  //   in_1: pull=down
  //   in_2: pull=down
  //   out_4: pull=down
endmodule

module _8_bit_left_shifter (
  input  [7:0] in_1,
  input  in_2,
  output [7:0] out_3,
  output out_4
);

  wire [6:0] n8_bit_register_1_out_4;

  _8_bit_register u_8_bit_register_1 (
    .in_1(in_1), .in_2(1'b1), .in_3(1'b1), .out_4({out_4, n8_bit_register_1_out_4}));  // open: out_5
  _8_bit_register u_8_bit_register_2 (
    .in_1({n8_bit_register_1_out_4, in_2}), .in_2(1'b1), .in_3(1'b1), .out_4(out_3));  // open: out_5

  // Other names for the same wires on the sheet: shift_out = out_4; shift_in = in_2; input[7:0] = in_1;
  //   output[7:0] = out_3

  // Notes on the sheet:
  //   in_1: pull=down
  //   in_2: pull=down
  //   out_4: pull=down
  //   out_3: pull=down
endmodule

module _16_bit_left_shifter (
  input  [15:0] in_1,
  input  in_2,
  output [15:0] out_3,
  output out_4
);

  wire [14:0] n16_bit_register_1_out_4;

  _16_bit_register u_16_bit_register_1 (
    .in_1(in_1), .in_2(1'b1), .in_3(1'b1), .out_4({out_4, n16_bit_register_1_out_4}));  // open: out_5
  _16_bit_register u_16_bit_register_2 (
    .in_1({n16_bit_register_1_out_4, in_2}), .in_2(1'b1), .in_3(1'b1), .out_4(out_3));  // open: out_5

  // Other names for the same wires on the sheet: shift_out = out_4; shift_in = in_2; input[15:0] = in_1;
  //   output[15:0] = out_3

  // Notes on the sheet:
  //   out_3: pull=down
  //   in_1: pull=down
  //   out_4: pull=down
  //   in_2: pull=down
endmodule

module _1_bit_comparator (
  input  in_1,
  input  in_2,
  input  in_3,
  input  in_4,
  input  in_5,
  output out_6,
  output out_7,
  output out_8
);

  wire and_2_out, and_3_out, and_4_out, and_5_out, local_A____B, local_A___B, prev_A____B;

  or or_1 (prev_A____B, in_4, in_5);
  xor xor_1 (local_A____B, in_1, in_2);
  and and_1 (out_6, in_3, local_A___B);
  and and_2 (and_2_out, in_1, local_A____B);
  and and_3 (and_3_out, in_4, local_A___B);
  and and_4 (and_4_out, in_2, local_A____B);
  and and_5 (and_5_out, in_5, local_A___B);
  not not_1 (local_A___B, local_A____B);
  or or_2 (out_7, and_2_out, and_3_out);
  or or_3 (out_8, and_4_out, and_5_out);

  // Other names for the same wires on the sheet: A = in_1; A___B = out_8; A___B_t = out_6; A___B_t_t = out_7;
  //   B = in_2; prev_A___B = in_5; prev_A___B_t = in_3; prev_A___B_t_t = in_4

  // Notes on the sheet:
  //   in_3: pull=down
  //   out_6: pull=down
  //   in_2: pull=down
  //   in_1: pull=down
  //   out_8: pull=down
  //   out_7: pull=down
  //   in_5: pull=down
  //   in_4: pull=down
endmodule

module _8_bit_comparator (
  input  [7:0] in_1,
  input  [7:0] in_2,
  output out_3,
  output out_4,
  output out_5
);

  wire n1_bit_comparator_1_out_6, n1_bit_comparator_1_out_7, n1_bit_comparator_1_out_8,
       n1_bit_comparator_2_out_6, n1_bit_comparator_2_out_7, n1_bit_comparator_2_out_8,
       n1_bit_comparator_3_out_6, n1_bit_comparator_3_out_7, n1_bit_comparator_3_out_8,
       n1_bit_comparator_4_out_6, n1_bit_comparator_4_out_7, n1_bit_comparator_4_out_8,
       n1_bit_comparator_5_out_6, n1_bit_comparator_5_out_7, n1_bit_comparator_5_out_8,
       n1_bit_comparator_6_out_6, n1_bit_comparator_6_out_7, n1_bit_comparator_6_out_8,
       n1_bit_comparator_7_out_6, n1_bit_comparator_7_out_7, n1_bit_comparator_7_out_8;

  _1_bit_comparator u_1_bit_comparator_1 (
    .in_1(in_1[0]), .in_2(in_2[0]), .in_3(1'b1), .in_4(1'b0), .in_5(1'b0), .out_6(n1_bit_comparator_1_out_6),
    .out_7(n1_bit_comparator_1_out_7), .out_8(n1_bit_comparator_1_out_8));
  _1_bit_comparator u_1_bit_comparator_2 (
    .in_1(in_1[1]), .in_2(in_2[1]), .in_3(n1_bit_comparator_1_out_6), .in_4(n1_bit_comparator_1_out_7),
    .in_5(n1_bit_comparator_1_out_8), .out_6(n1_bit_comparator_2_out_6), .out_7(n1_bit_comparator_2_out_7),
    .out_8(n1_bit_comparator_2_out_8));
  _1_bit_comparator u_1_bit_comparator_3 (
    .in_1(in_1[2]), .in_2(in_2[2]), .in_3(n1_bit_comparator_2_out_6), .in_4(n1_bit_comparator_2_out_7),
    .in_5(n1_bit_comparator_2_out_8), .out_6(n1_bit_comparator_3_out_6), .out_7(n1_bit_comparator_3_out_7),
    .out_8(n1_bit_comparator_3_out_8));
  _1_bit_comparator u_1_bit_comparator_4 (
    .in_1(in_1[3]), .in_2(in_2[3]), .in_3(n1_bit_comparator_3_out_6), .in_4(n1_bit_comparator_3_out_7),
    .in_5(n1_bit_comparator_3_out_8), .out_6(n1_bit_comparator_4_out_6), .out_7(n1_bit_comparator_4_out_7),
    .out_8(n1_bit_comparator_4_out_8));
  _1_bit_comparator u_1_bit_comparator_5 (
    .in_1(in_1[4]), .in_2(in_2[4]), .in_3(n1_bit_comparator_4_out_6), .in_4(n1_bit_comparator_4_out_7),
    .in_5(n1_bit_comparator_4_out_8), .out_6(n1_bit_comparator_5_out_6), .out_7(n1_bit_comparator_5_out_7),
    .out_8(n1_bit_comparator_5_out_8));
  _1_bit_comparator u_1_bit_comparator_6 (
    .in_1(in_1[5]), .in_2(in_2[5]), .in_3(n1_bit_comparator_5_out_6), .in_4(n1_bit_comparator_5_out_7),
    .in_5(n1_bit_comparator_5_out_8), .out_6(n1_bit_comparator_6_out_6), .out_7(n1_bit_comparator_6_out_7),
    .out_8(n1_bit_comparator_6_out_8));
  _1_bit_comparator u_1_bit_comparator_7 (
    .in_1(in_1[6]), .in_2(in_2[6]), .in_3(n1_bit_comparator_6_out_6), .in_4(n1_bit_comparator_6_out_7),
    .in_5(n1_bit_comparator_6_out_8), .out_6(n1_bit_comparator_7_out_6), .out_7(n1_bit_comparator_7_out_7),
    .out_8(n1_bit_comparator_7_out_8));
  _1_bit_comparator u_1_bit_comparator_8 (
    .in_1(in_1[7]), .in_2(in_2[7]), .in_3(n1_bit_comparator_7_out_6), .in_4(n1_bit_comparator_7_out_7),
    .in_5(n1_bit_comparator_7_out_8), .out_6(out_3), .out_7(out_4), .out_8(out_5));

  // Other names for the same wires on the sheet: A[7:0] = in_1; A0 = in_1[0]; A1 = in_1[1]; A2 = in_1[2];
  //   A3 = in_1[3]; A4 = in_1[4]; A5 = in_1[5]; A6 = in_1[6]; A7 = in_1[7]; A___B = out_5; A___B_t = out_3;
  //   A___B_t_t = out_4; B[7:0] = in_2; B0 = in_2[0]; B1 = in_2[1]; B2 = in_2[2]; B3 = in_2[3]; B4 = in_2[4];
  //   B5 = in_2[5]; B6 = in_2[6]; B7 = in_2[7]

  // Notes on the sheet:
  //   in_1: pull=down
  //   out_4: pull=down
  //   out_5: pull=down
  //   in_2: pull=down
  //   out_3: pull=down
endmodule

module _16_bit_comparator (
  input  [15:0] in_1,
  input  [15:0] in_2,
  output out_3,
  output out_4,
  output out_5
);

  wire n1_bit_comparator_1_out_6, n1_bit_comparator_1_out_7, n1_bit_comparator_1_out_8,
       n1_bit_comparator_2_out_6, n1_bit_comparator_2_out_7, n1_bit_comparator_2_out_8,
       n1_bit_comparator_3_out_6, n1_bit_comparator_3_out_7, n1_bit_comparator_3_out_8,
       n1_bit_comparator_4_out_6, n1_bit_comparator_4_out_7, n1_bit_comparator_4_out_8,
       n1_bit_comparator_5_out_6, n1_bit_comparator_5_out_7, n1_bit_comparator_5_out_8,
       n1_bit_comparator_6_out_6, n1_bit_comparator_6_out_7, n1_bit_comparator_6_out_8,
       n1_bit_comparator_7_out_6, n1_bit_comparator_7_out_7, n1_bit_comparator_7_out_8,
       n1_bit_comparator_8_out_6, n1_bit_comparator_8_out_7, n1_bit_comparator_8_out_8,
       n1_bit_comparator_9_out_6, n1_bit_comparator_9_out_7, n1_bit_comparator_9_out_8,
       n1_bit_comparator_10_out_6, n1_bit_comparator_10_out_7, n1_bit_comparator_10_out_8,
       n1_bit_comparator_11_out_6, n1_bit_comparator_11_out_7, n1_bit_comparator_11_out_8,
       n1_bit_comparator_12_out_6, n1_bit_comparator_12_out_7, n1_bit_comparator_12_out_8,
       n1_bit_comparator_13_out_6, n1_bit_comparator_13_out_7, n1_bit_comparator_13_out_8,
       n1_bit_comparator_14_out_6, n1_bit_comparator_14_out_7, n1_bit_comparator_14_out_8,
       n1_bit_comparator_15_out_6, n1_bit_comparator_15_out_7, n1_bit_comparator_15_out_8;

  _1_bit_comparator u_1_bit_comparator_1 (
    .in_1(in_1[0]), .in_2(in_2[0]), .in_3(1'b1), .in_4(1'b0), .in_5(1'b0), .out_6(n1_bit_comparator_1_out_6),
    .out_7(n1_bit_comparator_1_out_7), .out_8(n1_bit_comparator_1_out_8));
  _1_bit_comparator u_1_bit_comparator_2 (
    .in_1(in_1[1]), .in_2(in_2[1]), .in_3(n1_bit_comparator_1_out_6), .in_4(n1_bit_comparator_1_out_7),
    .in_5(n1_bit_comparator_1_out_8), .out_6(n1_bit_comparator_2_out_6), .out_7(n1_bit_comparator_2_out_7),
    .out_8(n1_bit_comparator_2_out_8));
  _1_bit_comparator u_1_bit_comparator_3 (
    .in_1(in_1[2]), .in_2(in_2[2]), .in_3(n1_bit_comparator_2_out_6), .in_4(n1_bit_comparator_2_out_7),
    .in_5(n1_bit_comparator_2_out_8), .out_6(n1_bit_comparator_3_out_6), .out_7(n1_bit_comparator_3_out_7),
    .out_8(n1_bit_comparator_3_out_8));
  _1_bit_comparator u_1_bit_comparator_4 (
    .in_1(in_1[3]), .in_2(in_2[3]), .in_3(n1_bit_comparator_3_out_6), .in_4(n1_bit_comparator_3_out_7),
    .in_5(n1_bit_comparator_3_out_8), .out_6(n1_bit_comparator_4_out_6), .out_7(n1_bit_comparator_4_out_7),
    .out_8(n1_bit_comparator_4_out_8));
  _1_bit_comparator u_1_bit_comparator_5 (
    .in_1(in_1[4]), .in_2(in_2[4]), .in_3(n1_bit_comparator_4_out_6), .in_4(n1_bit_comparator_4_out_7),
    .in_5(n1_bit_comparator_4_out_8), .out_6(n1_bit_comparator_5_out_6), .out_7(n1_bit_comparator_5_out_7),
    .out_8(n1_bit_comparator_5_out_8));
  _1_bit_comparator u_1_bit_comparator_6 (
    .in_1(in_1[5]), .in_2(in_2[5]), .in_3(n1_bit_comparator_5_out_6), .in_4(n1_bit_comparator_5_out_7),
    .in_5(n1_bit_comparator_5_out_8), .out_6(n1_bit_comparator_6_out_6), .out_7(n1_bit_comparator_6_out_7),
    .out_8(n1_bit_comparator_6_out_8));
  _1_bit_comparator u_1_bit_comparator_7 (
    .in_1(in_1[6]), .in_2(in_2[6]), .in_3(n1_bit_comparator_6_out_6), .in_4(n1_bit_comparator_6_out_7),
    .in_5(n1_bit_comparator_6_out_8), .out_6(n1_bit_comparator_7_out_6), .out_7(n1_bit_comparator_7_out_7),
    .out_8(n1_bit_comparator_7_out_8));
  _1_bit_comparator u_1_bit_comparator_8 (
    .in_1(in_1[7]), .in_2(in_2[7]), .in_3(n1_bit_comparator_7_out_6), .in_4(n1_bit_comparator_7_out_7),
    .in_5(n1_bit_comparator_7_out_8), .out_6(n1_bit_comparator_8_out_6), .out_7(n1_bit_comparator_8_out_7),
    .out_8(n1_bit_comparator_8_out_8));
  _1_bit_comparator u_1_bit_comparator_9 (
    .in_1(in_1[8]), .in_2(in_2[8]), .in_3(n1_bit_comparator_8_out_6), .in_4(n1_bit_comparator_8_out_7),
    .in_5(n1_bit_comparator_8_out_8), .out_6(n1_bit_comparator_9_out_6), .out_7(n1_bit_comparator_9_out_7),
    .out_8(n1_bit_comparator_9_out_8));
  _1_bit_comparator u_1_bit_comparator_10 (
    .in_1(in_1[9]), .in_2(in_2[9]), .in_3(n1_bit_comparator_9_out_6), .in_4(n1_bit_comparator_9_out_7),
    .in_5(n1_bit_comparator_9_out_8), .out_6(n1_bit_comparator_10_out_6), .out_7(n1_bit_comparator_10_out_7),
    .out_8(n1_bit_comparator_10_out_8));
  _1_bit_comparator u_1_bit_comparator_11 (
    .in_1(in_1[10]), .in_2(in_2[10]), .in_3(n1_bit_comparator_10_out_6), .in_4(n1_bit_comparator_10_out_7),
    .in_5(n1_bit_comparator_10_out_8), .out_6(n1_bit_comparator_11_out_6),
    .out_7(n1_bit_comparator_11_out_7), .out_8(n1_bit_comparator_11_out_8));
  _1_bit_comparator u_1_bit_comparator_12 (
    .in_1(in_1[11]), .in_2(in_2[11]), .in_3(n1_bit_comparator_11_out_6), .in_4(n1_bit_comparator_11_out_7),
    .in_5(n1_bit_comparator_11_out_8), .out_6(n1_bit_comparator_12_out_6),
    .out_7(n1_bit_comparator_12_out_7), .out_8(n1_bit_comparator_12_out_8));
  _1_bit_comparator u_1_bit_comparator_13 (
    .in_1(in_1[12]), .in_2(in_2[12]), .in_3(n1_bit_comparator_12_out_6), .in_4(n1_bit_comparator_12_out_7),
    .in_5(n1_bit_comparator_12_out_8), .out_6(n1_bit_comparator_13_out_6),
    .out_7(n1_bit_comparator_13_out_7), .out_8(n1_bit_comparator_13_out_8));
  _1_bit_comparator u_1_bit_comparator_14 (
    .in_1(in_1[13]), .in_2(in_2[13]), .in_3(n1_bit_comparator_13_out_6), .in_4(n1_bit_comparator_13_out_7),
    .in_5(n1_bit_comparator_13_out_8), .out_6(n1_bit_comparator_14_out_6),
    .out_7(n1_bit_comparator_14_out_7), .out_8(n1_bit_comparator_14_out_8));
  _1_bit_comparator u_1_bit_comparator_15 (
    .in_1(in_1[14]), .in_2(in_2[14]), .in_3(n1_bit_comparator_14_out_6), .in_4(n1_bit_comparator_14_out_7),
    .in_5(n1_bit_comparator_14_out_8), .out_6(n1_bit_comparator_15_out_6),
    .out_7(n1_bit_comparator_15_out_7), .out_8(n1_bit_comparator_15_out_8));
  _1_bit_comparator u_1_bit_comparator_16 (
    .in_1(in_1[15]), .in_2(in_2[15]), .in_3(n1_bit_comparator_15_out_6), .in_4(n1_bit_comparator_15_out_7),
    .in_5(n1_bit_comparator_15_out_8), .out_6(out_3), .out_7(out_4), .out_8(out_5));

  // Other names for the same wires on the sheet: A[15:0] = in_1; A0 = in_1[0]; A1 = in_1[1]; A2 = in_1[2];
  //   A3 = in_1[3]; A4 = in_1[4]; A5 = in_1[5]; A6 = in_1[6]; A7 = in_1[7]; A8 = in_1[8]; A9 = in_1[9];
  //   A10 = in_1[10]; A11 = in_1[11]; A12 = in_1[12]; A13 = in_1[13]; A14 = in_1[14]; A15 = in_1[15]; A___B = out_5;
  //   A___B_t = out_3; A___B_t_t = out_4; B[15:0] = in_2; B0 = in_2[0]; B1 = in_2[1]; B2 = in_2[2]; B3 = in_2[3];
  //   B4 = in_2[4]; B5 = in_2[5]; B6 = in_2[6]; B7 = in_2[7]; B8 = in_2[8]; B9 = in_2[9]; B10 = in_2[10];
  //   B11 = in_2[11]; B12 = in_2[12]; B13 = in_2[13]; B14 = in_2[14]; B15 = in_2[15]

  // Notes on the sheet:
  //   out_3: pull=down
  //   in_1: pull=down
  //   in_2: pull=down
  //   out_5: pull=down
  //   out_4: pull=down
endmodule

module _8_bit_bus1 (
  input  [7:0] \input ,
  input  in_2,
  output [7:0] out_3
);

  wire not_1_out;

  not not_1 (not_1_out, in_2);
  or or_1 (out_3[0], \input [0], in_2);
  and and_1 (out_3[1], \input [1], not_1_out);
  and and_2 (out_3[2], \input [2], not_1_out);
  and and_3 (out_3[3], \input [3], not_1_out);
  and and_4 (out_3[4], \input [4], not_1_out);
  and and_5 (out_3[5], \input [5], not_1_out);
  and and_6 (out_3[6], \input [6], not_1_out);
  and and_7 (out_3[7], \input [7], not_1_out);

  // Other names for the same wires on the sheet: BUS = in_2

  // Notes on the sheet:
  //   input: pull=down
  //   in_2: pull=down
  //   out_3: pull=down
endmodule

module _16_bit_bus1 (
  input  [15:0] \input ,
  input  in_2,
  output [15:0] out_3
);

  wire not_1_out;

  not not_1 (not_1_out, in_2);
  or or_1 (out_3[0], \input [0], in_2);
  and and_1 (out_3[1], \input [1], not_1_out);
  and and_2 (out_3[2], \input [2], not_1_out);
  and and_3 (out_3[3], \input [3], not_1_out);
  and and_4 (out_3[4], \input [4], not_1_out);
  and and_5 (out_3[5], \input [5], not_1_out);
  and and_6 (out_3[6], \input [6], not_1_out);
  and and_7 (out_3[7], \input [7], not_1_out);
  and and_8 (out_3[8], \input [8], not_1_out);
  and and_9 (out_3[9], \input [9], not_1_out);
  and and_10 (out_3[10], \input [10], not_1_out);
  and and_11 (out_3[11], \input [11], not_1_out);
  and and_12 (out_3[12], \input [12], not_1_out);
  and and_13 (out_3[13], \input [13], not_1_out);
  and and_14 (out_3[14], \input [14], not_1_out);
  and and_15 (out_3[15], \input [15], not_1_out);

  // Other names for the same wires on the sheet: BUS = in_2

  // Notes on the sheet:
  //   out_3: pull=down
  //   input: pull=down
  //   in_2: pull=down
endmodule

module _16_bit_clear (
  input  [15:0] \input ,
  input  in_2,
  output [15:0] out_3
);

  wire not_1_out;

  not not_1 (not_1_out, in_2);
  and and_1 (out_3[0], \input [0], not_1_out);
  and and_2 (out_3[1], \input [1], not_1_out);
  and and_3 (out_3[2], \input [2], not_1_out);
  and and_4 (out_3[3], \input [3], not_1_out);
  and and_5 (out_3[4], \input [4], not_1_out);
  and and_6 (out_3[5], \input [5], not_1_out);
  and and_7 (out_3[6], \input [6], not_1_out);
  and and_8 (out_3[7], \input [7], not_1_out);
  and and_9 (out_3[8], \input [8], not_1_out);
  and and_10 (out_3[9], \input [9], not_1_out);
  and and_11 (out_3[10], \input [10], not_1_out);
  and and_12 (out_3[11], \input [11], not_1_out);
  and and_13 (out_3[12], \input [12], not_1_out);
  and and_14 (out_3[13], \input [13], not_1_out);
  and and_15 (out_3[14], \input [14], not_1_out);
  and and_16 (out_3[15], \input [15], not_1_out);

  // Other names for the same wires on the sheet: BUS = in_2

  // Notes on the sheet:
  //   in_2: pull=down
  //   out_3: pull=down
  //   input: pull=down
endmodule

module _1_bit_temp (
  input  in_1,
  input  in_2,
  output out_3
);

  wire controlled_buffer_1_out;

  assign controlled_buffer_1_out = in_2 ? in_1 : 1'bz;  // Controlled_Buffer controlled_buffer_1
  _1_bit_memory_cell u_1_bit_memory_cell_1 (.in_1(controlled_buffer_1_out), .in_2(in_2), .\output (out_3));

  // Other names for the same wires on the sheet: input = in_1; output = out_3; set = in_2

  // Notes on the sheet:
  //   in_2: pull=down
  //   in_1: pull=down
  //   out_3: pull=down
endmodule

module _8_bit_temp (
  input  [7:0] in_1,
  input  in_2,
  output [7:0] out_3
);

  wire [7:0] controlled_buffer_1_out;

  assign controlled_buffer_1_out = in_2 ? in_1 : 8'bz;  // Controlled_Buffer controlled_buffer_1
  _1_byte_memory_cell u_1_byte_memory_cell_1 (.\input (controlled_buffer_1_out), .in_2(in_2), .\output (out_3));

  // Other names for the same wires on the sheet: input[7:0] = in_1; output[7:0] = out_3; set = in_2

  // Notes on the sheet:
  //   in_2: pull=down
  //   out_3: pull=down
  //   in_1: pull=down
endmodule

module _16_bit_temp (
  input  [15:0] in_1,
  input  in_2,
  output [15:0] out_3
);

  wire [15:0] controlled_buffer_1_out;

  assign controlled_buffer_1_out = in_2 ? in_1 : 16'bz;  // Controlled_Buffer controlled_buffer_1
  _2_bytes_memory_cell u_2_bytes_memory_cell_1 (.\input (controlled_buffer_1_out), .in_2(in_2), .\output (out_3));

  // Other names for the same wires on the sheet: input[15:0] = in_1; output[15:0] = out_3; set = in_2

  // Notes on the sheet:
  //   in_2: pull=down
  //   out_3: pull=down
  //   in_1: pull=down
endmodule

module _16_bit_lower_mask (
  input  [15:0] \input ,
  input  in_2,
  output [15:0] out_3
);

  wire not_1_out;

  not not_1 (not_1_out, in_2);
  and and_1 (out_3[8], \input [8], not_1_out);
  and and_2 (out_3[9], \input [9], not_1_out);
  and and_3 (out_3[10], \input [10], not_1_out);
  and and_4 (out_3[11], \input [11], not_1_out);
  and and_5 (out_3[12], \input [12], not_1_out);
  and and_6 (out_3[13], \input [13], not_1_out);
  and and_7 (out_3[14], \input [14], not_1_out);
  and and_8 (out_3[15], \input [15], not_1_out);

  assign out_3[7:0] = \input [7:0];

  // Other names for the same wires on the sheet: BUS = in_2

  // Notes on the sheet:
  //   in_2: pull=down
  //   input: pull=down
  //   out_3: pull=down
endmodule

module _8_bit_accumulator (
  input  [7:0] in_1,
  input  in_2,
  input  in_3,
  output [7:0] out_4
);

  _8_bit_register u_8_bit_register_1 (.in_1(in_1), .in_2(in_2), .in_3(in_3), .out_4(out_4));  // open: out_5

  // Other names for the same wires on the sheet: enable = in_3; input[7:0] = in_1; output[7:0] = out_4; set = in_2

  // Notes on the sheet:
  //   in_2: pull=down
  //   in_1: pull=down
  //   out_4: pull=down
  //   in_3: pull=down
endmodule

module _16_bit_accumulator (
  input  [15:0] in_1,
  input  in_2,
  input  in_3,
  output [15:0] out_4,
  output [15:0] out_5
);

  _16_bit_register u_16_bit_register_1 (.in_1(in_1), .in_2(in_2), .in_3(in_3), .out_4(out_4), .out_5(out_5));

  // Other names for the same wires on the sheet: enable = in_3; input[15:0] = in_1; output[15:0] = out_4; set = in_2;
  //   storage[15:0] = out_5

  // Notes on the sheet:
  //   in_1: pull=down
  //   in_3: pull=down
  //   out_5: pull=down
  //   out_4: pull=down
  //   in_2: pull=down
endmodule

module _8_bit_and (
  input  [7:0] in_1,
  input  [7:0] in_2,
  output [7:0] out_3
);

  and and_1 (out_3[0], in_1[3], in_2[0]);
  and and_2 (out_3[1], in_1[3], in_2[1]);
  and and_3 (out_3[2], in_1[3], in_2[2]);
  and and_4 (out_3[3], in_1[3], in_2[3]);
  and and_5 (out_3[4], in_1[7], in_2[4]);
  and and_6 (out_3[5], in_1[7], in_2[5]);
  and and_7 (out_3[6], in_1[7], in_2[6]);
  and and_8 (out_3[7], in_1[7], in_2[7]);

  assign {in_1[6:4], in_1[2:0]} = {{3{in_1[7]}}, {3{in_1[3]}}};

  // Other names for the same wires on the sheet: A[7:0] = {{4{in_1[7]}}, {4{in_1[3]}}}; A0 = in_1[3]; A1 = in_1[3];
  //   A2 = in_1[3]; A3 = in_1[3]; A4 = in_1[7]; A5 = in_1[7]; A6 = in_1[7]; A7 = in_1[7]; B[7:0] = in_2; B0 = in_2[0];
  //   B1 = in_2[1]; B2 = in_2[2]; B3 = in_2[3]; B4 = in_2[4]; B5 = in_2[5]; B6 = in_2[6]; B7 = in_2[7];
  //   output[7:0] = out_3

  // Notes on the sheet:
  //   out_3: pull=down
  //   in_1: pull=down
  //   in_2: pull=down
endmodule

module _16_bit_and (
  input  [15:0] in_1,
  input  [15:0] in_2,
  output [15:0] out_3
);

  and and_1 (out_3[0], in_1[0], in_2[0]);
  and and_2 (out_3[1], in_1[1], in_2[1]);
  and and_3 (out_3[2], in_1[2], in_2[2]);
  and and_4 (out_3[3], in_1[3], in_2[3]);
  and and_5 (out_3[4], in_1[4], in_2[4]);
  and and_6 (out_3[5], in_1[5], in_2[5]);
  and and_7 (out_3[6], in_1[6], in_2[6]);
  and and_8 (out_3[7], in_1[7], in_2[7]);
  and and_9 (out_3[8], in_1[8], in_2[8]);
  and and_10 (out_3[9], in_1[9], in_2[9]);
  and and_11 (out_3[10], in_1[10], in_2[10]);
  and and_12 (out_3[11], in_1[11], in_2[11]);
  and and_13 (out_3[12], in_1[12], in_2[12]);
  and and_14 (out_3[13], in_1[13], in_2[13]);
  and and_15 (out_3[14], in_1[14], in_2[14]);
  and and_16 (out_3[15], in_1[15], in_2[15]);

  // Other names for the same wires on the sheet: A[15:0] = in_1; A0 = in_1[0]; A1 = in_1[1]; A2 = in_1[2];
  //   A3 = in_1[3]; A4 = in_1[4]; A5 = in_1[5]; A6 = in_1[6]; A7 = in_1[7]; A8 = in_1[8]; A9 = in_1[9];
  //   A10 = in_1[10]; A11 = in_1[11]; A12 = in_1[12]; A13 = in_1[13]; A14 = in_1[14]; A15 = in_1[15]; B[15:0] = in_2;
  //   B0 = in_2[0]; B1 = in_2[1]; B2 = in_2[2]; B3 = in_2[3]; B4 = in_2[4]; B5 = in_2[5]; B6 = in_2[6]; B7 = in_2[7];
  //   B8 = in_2[8]; B9 = in_2[9]; B10 = in_2[10]; B11 = in_2[11]; B12 = in_2[12]; B13 = in_2[13]; B14 = in_2[14];
  //   B15 = in_2[15]; output[15:0] = out_3

  // Notes on the sheet:
  //   in_2: pull=down
  //   in_1: pull=down
  //   out_3: pull=down
endmodule

module _8_bit_or (
  input  [7:0] in_1,
  input  [7:0] in_2,
  output [7:0] out_3
);

  or or_1 (out_3[0], in_1[3], in_2[0]);
  or or_2 (out_3[1], in_1[3], in_2[1]);
  or or_3 (out_3[2], in_1[3], in_2[2]);
  or or_4 (out_3[3], in_1[3], in_2[3]);
  or or_5 (out_3[4], in_1[7], in_2[4]);
  or or_6 (out_3[5], in_1[7], in_2[5]);
  or or_7 (out_3[6], in_1[7], in_2[6]);
  or or_8 (out_3[7], in_1[7], in_2[7]);

  assign {in_1[6:4], in_1[2:0]} = {{3{in_1[7]}}, {3{in_1[3]}}};

  // Other names for the same wires on the sheet: A[7:0] = {{4{in_1[7]}}, {4{in_1[3]}}}; A0 = in_1[3]; A1 = in_1[3];
  //   A2 = in_1[3]; A3 = in_1[3]; A4 = in_1[7]; A5 = in_1[7]; A6 = in_1[7]; A7 = in_1[7]; B[7:0] = in_2; B0 = in_2[0];
  //   B1 = in_2[1]; B2 = in_2[2]; B3 = in_2[3]; B4 = in_2[4]; B5 = in_2[5]; B6 = in_2[6]; B7 = in_2[7];
  //   output[7:0] = out_3

  // Notes on the sheet:
  //   in_1: pull=down
  //   out_3: pull=down
  //   in_2: pull=down
endmodule

module _16_bit_or (
  input  [15:0] in_1,
  input  [15:0] in_2,
  output [15:0] out_3
);

  or or_1 (out_3[0], in_1[0], in_2[0]);
  or or_2 (out_3[1], in_1[1], in_2[1]);
  or or_3 (out_3[2], in_1[2], in_2[2]);
  or or_4 (out_3[3], in_1[3], in_2[3]);
  or or_5 (out_3[4], in_1[4], in_2[4]);
  or or_6 (out_3[5], in_1[5], in_2[5]);
  or or_7 (out_3[6], in_1[6], in_2[6]);
  or or_8 (out_3[7], in_1[7], in_2[7]);
  or or_9 (out_3[8], in_1[8], in_2[8]);
  or or_10 (out_3[9], in_1[9], in_2[9]);
  or or_11 (out_3[10], in_1[10], in_2[10]);
  or or_12 (out_3[11], in_1[11], in_2[11]);
  or or_13 (out_3[12], in_1[12], in_2[12]);
  or or_14 (out_3[13], in_1[13], in_2[13]);
  or or_15 (out_3[14], in_1[14], in_2[14]);
  or or_16 (out_3[15], in_1[15], in_2[15]);

  // Other names for the same wires on the sheet: A[15:0] = in_1; A0 = in_1[0]; A1 = in_1[1]; A2 = in_1[2];
  //   A3 = in_1[3]; A4 = in_1[4]; A5 = in_1[5]; A6 = in_1[6]; A7 = in_1[7]; A8 = in_1[8]; A9 = in_1[9];
  //   A10 = in_1[10]; A11 = in_1[11]; A12 = in_1[12]; A13 = in_1[13]; A14 = in_1[14]; A15 = in_1[15]; B[15:0] = in_2;
  //   B0 = in_2[0]; B1 = in_2[1]; B2 = in_2[2]; B3 = in_2[3]; B4 = in_2[4]; B5 = in_2[5]; B6 = in_2[6]; B7 = in_2[7];
  //   B8 = in_2[8]; B9 = in_2[9]; B10 = in_2[10]; B11 = in_2[11]; B12 = in_2[12]; B13 = in_2[13]; B14 = in_2[14];
  //   B15 = in_2[15]; output[15:0] = out_3

  // Notes on the sheet:
  //   in_1: pull=down
  //   in_2: pull=down
  //   out_3: pull=down
endmodule

module _8_bit_xor (
  input  [7:0] in_1,
  input  [7:0] in_2,
  output [7:0] out_3
);

  xor xor_1 (out_3[0], in_1[3], in_2[0]);
  xor xor_2 (out_3[1], in_1[3], in_2[1]);
  xor xor_3 (out_3[2], in_1[3], in_2[2]);
  xor xor_4 (out_3[3], in_1[3], in_2[3]);
  xor xor_5 (out_3[4], in_1[7], in_2[4]);
  xor xor_6 (out_3[5], in_1[7], in_2[5]);
  xor xor_7 (out_3[6], in_1[7], in_2[6]);
  xor xor_8 (out_3[7], in_1[7], in_2[7]);

  assign {in_1[6:4], in_1[2:0]} = {{3{in_1[7]}}, {3{in_1[3]}}};

  // Other names for the same wires on the sheet: A[7:0] = {{4{in_1[7]}}, {4{in_1[3]}}}; A0 = in_1[3]; A1 = in_1[3];
  //   A2 = in_1[3]; A3 = in_1[3]; A4 = in_1[7]; A5 = in_1[7]; A6 = in_1[7]; A7 = in_1[7]; B[7:0] = in_2; B0 = in_2[0];
  //   B1 = in_2[1]; B2 = in_2[2]; B3 = in_2[3]; B4 = in_2[4]; B5 = in_2[5]; B6 = in_2[6]; B7 = in_2[7];
  //   output[7:0] = out_3

  // Notes on the sheet:
  //   in_2: pull=down
  //   in_1: pull=down
  //   out_3: pull=down
endmodule

module _16_bit_xor (
  input  [15:0] in_1,
  input  [15:0] in_2,
  output [15:0] out_3
);

  xor xor_1 (out_3[0], in_1[0], in_2[0]);
  xor xor_2 (out_3[1], in_1[1], in_2[1]);
  xor xor_3 (out_3[2], in_1[2], in_2[2]);
  xor xor_4 (out_3[3], in_1[3], in_2[3]);
  xor xor_5 (out_3[4], in_1[4], in_2[4]);
  xor xor_6 (out_3[5], in_1[5], in_2[5]);
  xor xor_7 (out_3[6], in_1[6], in_2[6]);
  xor xor_8 (out_3[7], in_1[7], in_2[7]);
  xor xor_9 (out_3[8], in_1[8], in_2[8]);
  xor xor_10 (out_3[9], in_1[9], in_2[9]);
  xor xor_11 (out_3[10], in_1[10], in_2[10]);
  xor xor_12 (out_3[11], in_1[11], in_2[11]);
  xor xor_13 (out_3[12], in_1[12], in_2[12]);
  xor xor_14 (out_3[13], in_1[13], in_2[13]);
  xor xor_15 (out_3[14], in_1[14], in_2[14]);
  xor xor_16 (out_3[15], in_1[15], in_2[15]);

  // Other names for the same wires on the sheet: A[15:0] = in_1; A0 = in_1[0]; A1 = in_1[1]; A2 = in_1[2];
  //   A3 = in_1[3]; A4 = in_1[4]; A5 = in_1[5]; A6 = in_1[6]; A7 = in_1[7]; A8 = in_1[8]; A9 = in_1[9];
  //   A10 = in_1[10]; A11 = in_1[11]; A12 = in_1[12]; A13 = in_1[13]; A14 = in_1[14]; A15 = in_1[15]; B[15:0] = in_2;
  //   B0 = in_2[0]; B1 = in_2[1]; B2 = in_2[2]; B3 = in_2[3]; B4 = in_2[4]; B5 = in_2[5]; B6 = in_2[6]; B7 = in_2[7];
  //   B8 = in_2[8]; B9 = in_2[9]; B10 = in_2[10]; B11 = in_2[11]; B12 = in_2[12]; B13 = in_2[13]; B14 = in_2[14];
  //   B15 = in_2[15]; output[15:0] = out_3

  // Notes on the sheet:
  //   in_2: pull=down
  //   out_3: pull=down
  //   in_1: pull=down
endmodule

module _8_bit_zero_checker (
  input  [7:0] in_1,
  output out_2
);

  wire or_1_out;

  or or_1 (or_1_out, in_1[0], in_1[1], in_1[2], in_1[3], in_1[4], in_1[5], in_1[6], in_1[7]);
  not not_1 (out_2, or_1_out);

  // Notes on the sheet:
  //   out_2: pull=down
  //   in_1: pull=down
  //   if input = 0000 0000 then output := 1 else output := 0
endmodule

module _16_bit_zero_checker (
  input  [15:0] in_1,
  output out_2
);

  and and_1 (out_2, in_1[0], in_1[1], in_1[2], in_1[3], in_1[4], in_1[5], in_1[6], in_1[7], in_1[8], in_1[9], in_1[10], in_1[11], in_1[12], in_1[13], in_1[14], in_1[15]);

  // Notes on the sheet:
  //   in_1: pull=down
  //   out_2: pull=down
endmodule

module _16_bit_parity_check (
  input  [15:0] in_1,
  output out_2
);

  NotExactlyOne xnor_1 (
    .out(out_2), .in0(in_1[0]), .in1(in_1[1]), .in2(in_1[2]), .in3(in_1[3]), .in4(in_1[4]), .in5(in_1[5]),
    .in6(in_1[6]), .in7(in_1[7]), .in8(in_1[8]), .in9(in_1[9]), .in10(in_1[10]), .in11(in_1[11]),
    .in12(in_1[12]), .in13(in_1[13]), .in14(in_1[14]), .in15(in_1[15]));

  // Other names for the same wires on the sheet: input[15:0] = in_1

  // Notes on the sheet:
  //   out_2: pull=down
  //   in_1: pull=down
  //   1 for even 0s or 1s / 0 for odd 0s or 1s
endmodule

module _16_bit_negativity_check (
  input  [15:0] in_1,
  output \output 
);


  assign \output  = in_1[15];

  // Other names for the same wires on the sheet: input[15:0] = in_1

  // Notes on the sheet:
  //   output: pull=down
  //   in_1: pull=down
endmodule

module _16_bit_positivity_check (
  input  [15:0] in_1,
  output \output 
);

  not not_1 (\output , in_1[15]);

  // Other names for the same wires on the sheet: input[15:0] = in_1

  // Notes on the sheet:
  //   in_1: pull=down
  //   output: pull=down
endmodule

module _8_bit_ALU (
  input  [7:0] in_1,
  input  [7:0] in_2,
  input  in_3,
  input  in_4,
  input  in_5,
  input  in_6,
  output [7:0] out_7,
  output out_8,
  output out_9,
  output out_10,
  output out_11,
  output out_12
);

  wire _000, _001, _010, _011, _100, _101, _110, _111, and_1_out, and_2_out, and_3_out,
       n8_bit_comparator_1_out_3, n8_bit_comparator_1_out_4, n8_bit_comparator_1_out_5,
       n8_bit_full_adder_1_carry_out, n8_bit_left_shifter_1_out_4, n8_bit_right_shifter_1_out_4;
  wire [7:0] n8_bit_and_1_out_3, n8_bit_full_adder_1_sum, n8_bit_left_shifter_1_out_3, n8_bit_or_1_out_3,
       n8_bit_reverter_1_out_2, n8_bit_right_shifter_1_out_3, n8_bit_xor_1_out_3;

  _3x8_decoder u_3x8_decoder_1 (
    .in_1(in_6), .in_2(in_5), .in_3(in_4), ._000(_000), ._001(_001), ._010(_010), ._011(_011), ._100(_100),
    ._101(_101), ._110(_110), ._111(_111));
  _8_bit_full_adder u_8_bit_full_adder_1 (
    .A(in_1), .B(in_2), .in_3(in_3), .sum(n8_bit_full_adder_1_sum), .carry_out(n8_bit_full_adder_1_carry_out));
  _8_bit_right_shifter u_8_bit_right_shifter_1 (
    .in_1(in_1), .in_2(in_3), .out_3(n8_bit_right_shifter_1_out_3), .out_4(n8_bit_right_shifter_1_out_4));
  _8_bit_left_shifter u_8_bit_left_shifter_1 (
    .in_1(in_1), .in_2(in_3), .out_3(n8_bit_left_shifter_1_out_3), .out_4(n8_bit_left_shifter_1_out_4));
  and and_1 (and_1_out, n8_bit_full_adder_1_carry_out, _000);
  assign out_8 = _000 ? and_1_out : 1'bz;  // Controlled_Buffer controlled_buffer_1
  and and_2 (and_2_out, n8_bit_right_shifter_1_out_4, _001);
  and and_3 (and_3_out, n8_bit_left_shifter_1_out_4, _010);
  _8_bit_enable_cell u_8_bit_enable_cell_1 (.in_1(n8_bit_full_adder_1_sum), .in_2(_000), .out_3(out_7));
  _8_bit_enable_cell u_8_bit_enable_cell_2 (.in_1(n8_bit_right_shifter_1_out_3), .in_2(_001), .out_3(out_7));
  assign out_8 = _001 ? and_2_out : 1'bz;  // Controlled_Buffer controlled_buffer_2
  _8_bit_enable_cell u_8_bit_enable_cell_3 (.in_1(n8_bit_left_shifter_1_out_3), .in_2(_010), .out_3(out_7));
  assign out_8 = _010 ? and_3_out : 1'bz;  // Controlled_Buffer controlled_buffer_3
  _8_bit_zero_checker u_8_bit_zero_checker_1 (.in_1(out_7), .out_2(out_12));
  _8_bit_and u_8_bit_and_1 (.in_1(in_1), .in_2(in_2), .out_3(n8_bit_and_1_out_3));
  _8_bit_or u_8_bit_or_1 (.in_1(in_1), .in_2(in_2), .out_3(n8_bit_or_1_out_3));
  _8_bit_xor u_8_bit_xor_1 (.in_1(in_1), .in_2(in_2), .out_3(n8_bit_xor_1_out_3));
  _8_bit_comparator u_8_bit_comparator_1 (
    .in_1(in_1), .in_2(in_2), .out_3(n8_bit_comparator_1_out_3), .out_4(n8_bit_comparator_1_out_4),
    .out_5(n8_bit_comparator_1_out_5));
  _8_bit_reverter u_8_bit_reverter_1 (.in_1(in_1), .out_2(n8_bit_reverter_1_out_2));
  _8_bit_enable_cell u_8_bit_enable_cell_4 (.in_1(n8_bit_reverter_1_out_2), .in_2(_011), .out_3(out_7));
  _8_bit_enable_cell u_8_bit_enable_cell_5 (.in_1(n8_bit_and_1_out_3), .in_2(_100), .out_3(out_7));
  _8_bit_enable_cell u_8_bit_enable_cell_6 (.in_1(n8_bit_or_1_out_3), .in_2(_101), .out_3(out_7));
  _8_bit_enable_cell u_8_bit_enable_cell_7 (.in_1(n8_bit_xor_1_out_3), .in_2(_110), .out_3(out_7));
  assign out_11 = _111 ? n8_bit_comparator_1_out_5 : 1'bz;  // Controlled_Buffer controlled_buffer_4
  assign out_9 = _111 ? n8_bit_comparator_1_out_3 : 1'bz;  // Controlled_Buffer controlled_buffer_5
  assign out_10 = _111 ? n8_bit_comparator_1_out_4 : 1'bz;  // Controlled_Buffer controlled_buffer_6

  // Other names for the same wires on the sheet: A[7:0] = in_1; A___B = out_11; A___B_t = out_9; A___B_t_t = out_10;
  //   B[7:0] = in_2; carry_in = in_3; carry_out = out_8; output[7:0] = out_7; sel0 = in_4; sel1 = in_5; sel2 = in_6;
  //   zero = out_12

  // Notes on the sheet:
  //   in_6: pull=down
  //   out_8: pull=down
  //   out_12: pull=down
  //   in_1: pull=down
  //   in_4: pull=down
  //   in_5: pull=down
  //   out_7: pull=down
  //   in_3: pull=down
  //   out_9: pull=down
  //   out_11: pull=down
  //   out_10: pull=down
  //   in_2: pull=down
endmodule

module _16_bit_ALU (
  input  [15:0] in_1,
  input  [15:0] in_2,
  input  in_3,
  input  in_4,
  input  in_5,
  input  in_6,
  input  in_7,
  output [15:0] out_8,
  output out_9,
  output out_10,
  output out_11,
  output out_12,
  output out_13,
  output out_14,
  output out_15,
  output out_16
);

  wire _0000, _0001, _0010, _0011, _0100, _0101, _0110, _0111, _1000, _1001, _1010, _1011, _1100, _1101,
       _1110, _1111, and_1_out, and_2_out, and_3_out, and_4_out, and_5_out, and_6_out, and_7_out, and_8_out,
       and_9_out, and_10_out, n16_bit_comparator_1_out_3, n16_bit_comparator_1_out_4,
       n16_bit_comparator_1_out_5, n16_bit_full_adder_1_carry_out, n16_bit_full_adder_2_carry_out,
       n16_bit_full_subtractor_1_carry_out, n16_bit_full_subtractor_2_carry_out, not_1_out, or_1_out,
       or_2_out, or_3_out;
  wire [15:0] divider_1_rem, divider_2_out, divider_2_rem, multiplier_1_cout, multiplier_1_out,
       n16_bit_and_1_out_3, n16_bit_full_adder_1_output, n16_bit_full_adder_2_output,
       n16_bit_full_subtractor_1_output, n16_bit_full_subtractor_2_output, n16_bit_negator_1_out_2,
       n16_bit_or_1_out_3, n16_bit_reverter_1_out_2, n16_bit_xor_1_out_3, shifter_1_out, shifter_2_out,
       shifter_3_out;

  _4x16_decoder u_4x16_decoder_1 (
    .in_1(in_7), .in_2(in_6), .in_3(in_5), .in_4(in_4), ._0000(_0000), ._0001(_0001), ._0010(_0010),
    ._0011(_0011), ._0100(_0100), ._0101(_0101), ._0110(_0110), ._0111(_0111), ._1000(_1000), ._1001(_1001),
    ._1010(_1010), ._1011(_1011), ._1100(_1100), ._1101(_1101), ._1110(_1110), ._1111(_1111));
  _16_bit_full_adder u_16_bit_full_adder_1 (
    .A(in_1), .B(in_2), .in_3(1'b0), .\output (n16_bit_full_adder_1_output),
    .carry_out(n16_bit_full_adder_1_carry_out));
  Shifter #(.width(16), .shift("lr")) shifter_1 (.in(in_1), .\dist (in_2[3:0]), .out(shifter_1_out));
  Shifter #(.width(16)) shifter_2 (.in(in_1), .\dist (in_2[3:0]), .out(shifter_2_out));
  _16_bit_full_adder u_16_bit_full_adder_2 (
    .A(in_1), .B(in_2), .in_3(in_3), .\output (n16_bit_full_adder_2_output),
    .carry_out(n16_bit_full_adder_2_carry_out));
  Shifter #(.width(16), .shift("ar")) shifter_3 (.in(in_1), .\dist (in_2[3:0]), .out(shifter_3_out));
  _16_bit_full_subtractor u_16_bit_full_subtractor_1 (
    .in_1(in_1), .in_2(in_2), .in_3(in_3), .\output (n16_bit_full_subtractor_1_output),
    .carry_out(n16_bit_full_subtractor_1_carry_out));
  _16_bit_full_subtractor u_16_bit_full_subtractor_2 (
    .in_1(in_1), .in_2(in_2), .in_3(1'b0), .\output (n16_bit_full_subtractor_2_output),
    .carry_out(n16_bit_full_subtractor_2_carry_out));
  Multiplier #(.width(16)) multiplier_1 (
    .a(in_1), .b(in_2), .out(multiplier_1_out), .cin({16{1'b0}}), .cout(multiplier_1_cout));
  or or_1 (or_1_out, multiplier_1_cout[0], multiplier_1_cout[1], multiplier_1_cout[2], multiplier_1_cout[3], multiplier_1_cout[4], multiplier_1_cout[5], multiplier_1_cout[6], multiplier_1_cout[7], multiplier_1_cout[8], multiplier_1_cout[9], multiplier_1_cout[10], multiplier_1_cout[11], multiplier_1_cout[12], multiplier_1_cout[13], multiplier_1_cout[14], multiplier_1_cout[15]);
  and and_1 (and_1_out, n16_bit_full_adder_1_carry_out, _0000);
  and and_2 (and_2_out, n16_bit_full_adder_2_carry_out, _1000);
  assign out_9 = _0000 ? and_1_out : 1'bz;  // Controlled_Buffer controlled_buffer_1
  and and_3 (and_3_out, in_1[0], _0001);
  and and_4 (and_4_out, in_1[15], _0010);
  assign out_9 = _1000 ? and_2_out : 1'bz;  // Controlled_Buffer controlled_buffer_2
  and and_5 (and_5_out, in_1[0], _1001);
  and and_6 (and_6_out, n16_bit_full_subtractor_1_carry_out, _1010);
  and and_7 (and_7_out, n16_bit_full_subtractor_2_carry_out, _1100);
  not not_1 (not_1_out, and_7_out);
  and and_8 (and_8_out, or_1_out, _1101);
  _16_bit_enable_cell u_16_bit_enable_cell_1 (.\input (n16_bit_full_adder_1_output), .in_2(_0000), .\output (out_8));
  _16_bit_enable_cell u_16_bit_enable_cell_2 (.\input (shifter_1_out), .in_2(_0001), .\output (out_8));
  assign out_9 = _0001 ? and_3_out : 1'bz;  // Controlled_Buffer controlled_buffer_3
  _16_bit_enable_cell u_16_bit_enable_cell_3 (.\input (shifter_2_out), .in_2(_0010), .\output (out_8));
  assign out_9 = _0010 ? and_4_out : 1'bz;  // Controlled_Buffer controlled_buffer_4
  _16_bit_enable_cell u_16_bit_enable_cell_4 (.\input (n16_bit_full_adder_2_output), .in_2(_1000), .\output (out_8));
  _16_bit_enable_cell u_16_bit_enable_cell_5 (.\input (shifter_3_out), .in_2(_1001), .\output (out_8));
  assign out_9 = _1001 ? and_5_out : 1'bz;  // Controlled_Buffer controlled_buffer_5
  _16_bit_enable_cell u_16_bit_enable_cell_6 (
    .\input (n16_bit_full_subtractor_1_output), .in_2(_1010), .\output (out_8));
  assign out_9 = _1010 ? and_6_out : 1'bz;  // Controlled_Buffer controlled_buffer_6
  _16_bit_enable_cell u_16_bit_enable_cell_7 (
    .\input (n16_bit_full_subtractor_2_output), .in_2(_1100), .\output (out_8));
  assign out_9 = _1100 ? not_1_out : 1'bz;  // Controlled_Buffer controlled_buffer_7
  _16_bit_enable_cell u_16_bit_enable_cell_8 (.\input (multiplier_1_out), .in_2(_1101), .\output (out_8));
  assign out_9 = _1101 ? and_8_out : 1'bz;  // Controlled_Buffer controlled_buffer_8
  Divider #(.width(16)) divider_1 (.a(in_1), .b(in_2), .upper({16{1'b0}}), .rem(divider_1_rem));  // open: out
  _16_bit_negativity_check u_16_bit_negativity_check_1 (.in_1(out_8), .\output (out_16));
  _16_bit_positivity_check u_16_bit_positivity_check_1 (.in_1(out_8), .\output (out_15));
  _16_bit_parity_check u_16_bit_parity_check_1 (.in_1(out_8), .out_2(out_14));
  _16_bit_zero_checker u_16_bit_zero_checker_1 (.in_1(out_8), .out_2(out_13));
  _16_bit_and u_16_bit_and_1 (.in_1(in_1), .in_2(in_2), .out_3(n16_bit_and_1_out_3));
  _16_bit_or u_16_bit_or_1 (.in_1(in_1), .in_2(in_2), .out_3(n16_bit_or_1_out_3));
  _16_bit_xor u_16_bit_xor_1 (.in_1(in_1), .in_2(in_2), .out_3(n16_bit_xor_1_out_3));
  _16_bit_comparator u_16_bit_comparator_1 (
    .in_1(in_1), .in_2(in_2), .out_3(n16_bit_comparator_1_out_3), .out_4(n16_bit_comparator_1_out_4),
    .out_5(n16_bit_comparator_1_out_5));
  Divider #(.width(16)) divider_2 (.a(in_1), .b(in_2), .out(divider_2_out), .upper({16{1'b0}}), .rem(divider_2_rem));
  or or_2 (or_2_out, divider_2_rem[0], divider_2_rem[1], divider_2_rem[2], divider_2_rem[3], divider_2_rem[4], divider_2_rem[5], divider_2_rem[6], divider_2_rem[7], divider_2_rem[8], divider_2_rem[9], divider_2_rem[10], divider_2_rem[11], divider_2_rem[12], divider_2_rem[13], divider_2_rem[14], divider_2_rem[15]);
  or or_3 (or_3_out, divider_1_rem[0], divider_1_rem[1], divider_1_rem[2], divider_1_rem[3], divider_1_rem[4], divider_1_rem[5], divider_1_rem[6], divider_1_rem[7], divider_1_rem[8], divider_1_rem[9], divider_1_rem[10], divider_1_rem[11], divider_1_rem[12], divider_1_rem[13], divider_1_rem[14], divider_1_rem[15]);
  _16_bit_reverter u_16_bit_reverter_1 (.in_1(in_1), .out_2(n16_bit_reverter_1_out_2));
  _16_bit_negator u_16_bit_negator_1 (.in_1(in_1), .out_2(n16_bit_negator_1_out_2));
  and and_9 (and_9_out, or_2_out, _1110);
  and and_10 (and_10_out, or_3_out, _1111);
  _16_bit_enable_cell u_16_bit_enable_cell_9 (.\input (n16_bit_reverter_1_out_2), .in_2(_0011), .\output (out_8));
  _16_bit_enable_cell u_16_bit_enable_cell_10 (.\input (n16_bit_and_1_out_3), .in_2(_0100), .\output (out_8));
  _16_bit_enable_cell u_16_bit_enable_cell_11 (.\input (n16_bit_or_1_out_3), .in_2(_0101), .\output (out_8));
  _16_bit_enable_cell u_16_bit_enable_cell_12 (.\input (n16_bit_xor_1_out_3), .in_2(_0110), .\output (out_8));
  and and_11 (out_12, n16_bit_comparator_1_out_5, _0111);
  and and_12 (out_10, n16_bit_comparator_1_out_3, _0111);
  and and_13 (out_11, n16_bit_comparator_1_out_4, _0111);
  _16_bit_enable_cell u_16_bit_enable_cell_13 (.\input (n16_bit_negator_1_out_2), .in_2(_1011), .\output (out_8));
  assign out_9 = _1110 ? and_9_out : 1'bz;  // Controlled_Buffer controlled_buffer_9
  assign out_9 = _1111 ? and_10_out : 1'bz;  // Controlled_Buffer controlled_buffer_10
  _16_bit_enable_cell u_16_bit_enable_cell_14 (.\input (divider_2_out), .in_2(_1110), .\output (out_8));
  _16_bit_enable_cell u_16_bit_enable_cell_15 (.\input (divider_1_rem), .in_2(_1111), .\output (out_8));

  // Other names for the same wires on the sheet: A[15:0] = in_1; A0 = in_1[0]; A15 = in_1[15]; A___B = out_12;
  //   A___B_t = out_10; A___B_t_t = out_11; B[15:0] = in_2; carry_in = in_3; carry_out = out_9; even = out_14;
  //   lower_4_bits_of_B[3:0] = in_2[3:0]; minus_1 = out_16; output[15:0] = out_8; positive = out_15; sel0 = in_4;
  //   sel1 = in_5; sel2 = in_6; sel3 = in_7; zero = out_13

  // Notes on the sheet:
  //   in_5: pull=down
  //   in_2: pull=down
  //   out_16: pull=down
  //   in_1: pull=down
  //   out_10: pull=down
  //   out_9: pull=down
  //   out_14: pull=down
  //   in_7: pull=down
  //   out_12: pull=down
  //   out_8: pull=down
  //   in_4: pull=down
  //   out_11: pull=down
  //   out_13: pull=down
  //   in_3: pull=down
  //   out_15: pull=down
  //   in_6: pull=down
endmodule

module cpu_clock (
  input  in_1,
  output out_2,
  output out_3,
  output out_4
);

  wire Q_prime;

  and and_1 (out_4, in_1, out_2);
  nand nand_1 (out_3, in_1, Q_prime);
  J_K_Flip_Flop j_k_ff_1 (.J(1'b1), .clk(in_1), .K(1'b1), .Q(out_2), .Qn(Q_prime));  // open: preset, en, reset

  // Other names for the same wires on the sheet: clk = out_2; Q = out_2; clk_en = out_3; CLK_IN = in_1;
  //   clk_set = out_4

  // Notes on the sheet:
  //   out_2: pull=down
  //   out_4: pull=down
  //   in_1: pull=down
  //   out_3: pull=down
endmodule

module _8_step_stepper (
  input  in_1,
  input  in_2,
  output out_3,
  output out_4,
  output out_5,
  output out_6,
  output out_7,
  output out_8,
  output out_9,
  output out_10
);

  wire n1_bit_memory_cell_1_output, n1_bit_memory_cell_2_output, n1_bit_memory_cell_3_output,
       n1_bit_memory_cell_4_output, n1_bit_memory_cell_5_output, n1_bit_memory_cell_6_output,
       n1_bit_memory_cell_7_output, n1_bit_memory_cell_8_output, n1_bit_memory_cell_9_output,
       n1_bit_memory_cell_10_output, n1_bit_memory_cell_11_output, n1_bit_memory_cell_12_output,
       n1_bit_memory_cell_13_output, not_1_out, not_2_out, not_3_out, not_4_out, not_5_out, not_6_out,
       not_7_out, not_8_out, not_9_out, or_1_out, or_2_out;

  not not_1 (not_1_out, in_2);
  not not_2 (not_2_out, in_1);
  or or_1 (or_1_out, in_1, in_2);
  or or_2 (or_2_out, in_1, not_1_out);
  or or_3 (out_3, in_1, not_3_out);
  _1_bit_memory_cell u_1_bit_memory_cell_1 (.in_1(not_2_out), .in_2(or_1_out), .\output (n1_bit_memory_cell_1_output));
  not not_3 (not_3_out, n1_bit_memory_cell_2_output);
  _1_bit_memory_cell u_1_bit_memory_cell_2 (
    .in_1(n1_bit_memory_cell_1_output), .in_2(or_2_out), .\output (n1_bit_memory_cell_2_output));
  and and_1 (out_4, n1_bit_memory_cell_2_output, not_4_out);
  _1_bit_memory_cell u_1_bit_memory_cell_3 (
    .in_1(n1_bit_memory_cell_2_output), .in_2(or_1_out), .\output (n1_bit_memory_cell_3_output));
  not not_4 (not_4_out, n1_bit_memory_cell_4_output);
  _1_bit_memory_cell u_1_bit_memory_cell_4 (
    .in_1(n1_bit_memory_cell_3_output), .in_2(or_2_out), .\output (n1_bit_memory_cell_4_output));
  and and_2 (out_5, n1_bit_memory_cell_4_output, not_5_out);
  _1_bit_memory_cell u_1_bit_memory_cell_5 (
    .in_1(n1_bit_memory_cell_4_output), .in_2(or_1_out), .\output (n1_bit_memory_cell_5_output));
  not not_5 (not_5_out, n1_bit_memory_cell_6_output);
  _1_bit_memory_cell u_1_bit_memory_cell_6 (
    .in_1(n1_bit_memory_cell_5_output), .in_2(or_2_out), .\output (n1_bit_memory_cell_6_output));
  and and_3 (out_6, n1_bit_memory_cell_6_output, not_6_out);
  _1_bit_memory_cell u_1_bit_memory_cell_7 (
    .in_1(n1_bit_memory_cell_6_output), .in_2(or_1_out), .\output (n1_bit_memory_cell_7_output));
  not not_6 (not_6_out, n1_bit_memory_cell_8_output);
  _1_bit_memory_cell u_1_bit_memory_cell_8 (
    .in_1(n1_bit_memory_cell_7_output), .in_2(or_2_out), .\output (n1_bit_memory_cell_8_output));
  and and_4 (out_7, n1_bit_memory_cell_8_output, not_7_out);
  _1_bit_memory_cell u_1_bit_memory_cell_9 (
    .in_1(n1_bit_memory_cell_8_output), .in_2(or_1_out), .\output (n1_bit_memory_cell_9_output));
  not not_7 (not_7_out, n1_bit_memory_cell_10_output);
  _1_bit_memory_cell u_1_bit_memory_cell_10 (
    .in_1(n1_bit_memory_cell_9_output), .in_2(or_2_out), .\output (n1_bit_memory_cell_10_output));
  and and_5 (out_8, n1_bit_memory_cell_10_output, not_8_out);
  _1_bit_memory_cell u_1_bit_memory_cell_11 (
    .in_1(n1_bit_memory_cell_10_output), .in_2(or_1_out), .\output (n1_bit_memory_cell_11_output));
  not not_8 (not_8_out, n1_bit_memory_cell_12_output);
  _1_bit_memory_cell u_1_bit_memory_cell_12 (
    .in_1(n1_bit_memory_cell_11_output), .in_2(or_2_out), .\output (n1_bit_memory_cell_12_output));
  and and_6 (out_9, n1_bit_memory_cell_12_output, not_9_out);
  _1_bit_memory_cell u_1_bit_memory_cell_13 (
    .in_1(n1_bit_memory_cell_12_output), .in_2(or_1_out), .\output (n1_bit_memory_cell_13_output));
  not not_9 (not_9_out, out_10);
  _1_bit_memory_cell u_1_bit_memory_cell_14 (.in_1(n1_bit_memory_cell_13_output), .in_2(or_2_out), .\output (out_10));

  // Other names for the same wires on the sheet: clk = in_2; reset = in_1; step_0 = out_3; step_1 = out_4;
  //   step_2 = out_5; step_3 = out_6; step_4 = out_7; step_5 = out_8; step_6 = out_9; step_7 = out_10

  // Notes on the sheet:
  //   out_3: pull=down
  //   out_8: pull=down
  //   out_5: pull=down
  //   out_4: pull=down
  //   out_10: pull=down
  //   out_6: pull=down
  //   out_9: pull=down
  //   in_2: pull=down
  //   in_1: pull=down
  //   out_7: pull=down
endmodule

module _16_step_stepper (
  input  in_1,
  input  in_2,
  output out_3,
  output out_4,
  output out_5,
  output out_6,
  output out_7,
  output out_8,
  output out_9,
  output out_10,
  output out_11,
  output out_12,
  output out_13,
  output out_14,
  output out_15,
  output out_16,
  output out_17,
  output out_18,
  output out_19
);

  wire n1_bit_memory_cell_1_output, n1_bit_memory_cell_2_output, n1_bit_memory_cell_3_output,
       n1_bit_memory_cell_4_output, n1_bit_memory_cell_5_output, n1_bit_memory_cell_6_output,
       n1_bit_memory_cell_7_output, n1_bit_memory_cell_8_output, n1_bit_memory_cell_9_output,
       n1_bit_memory_cell_10_output, n1_bit_memory_cell_11_output, n1_bit_memory_cell_12_output,
       n1_bit_memory_cell_13_output, n1_bit_memory_cell_14_output, n1_bit_memory_cell_15_output,
       n1_bit_memory_cell_16_output, n1_bit_memory_cell_17_output, n1_bit_memory_cell_18_output,
       n1_bit_memory_cell_19_output, n1_bit_memory_cell_20_output, n1_bit_memory_cell_21_output,
       n1_bit_memory_cell_22_output, n1_bit_memory_cell_23_output, n1_bit_memory_cell_24_output,
       n1_bit_memory_cell_25_output, n1_bit_memory_cell_26_output, n1_bit_memory_cell_27_output,
       n1_bit_memory_cell_28_output, n1_bit_memory_cell_29_output, n1_bit_memory_cell_30_output,
       n1_bit_memory_cell_31_output, not_1_out, not_2_out, not_3_out, not_4_out, not_5_out, not_6_out,
       not_7_out, not_8_out, not_9_out, not_10_out, not_11_out, not_12_out, not_13_out, not_14_out,
       not_15_out, not_16_out, not_17_out, not_18_out, or_1_out, or_2_out;

  not not_1 (not_1_out, in_2);
  not not_2 (not_2_out, in_1);
  or or_1 (or_1_out, in_1, in_2);
  or or_2 (or_2_out, in_1, not_1_out);
  or or_3 (out_3, in_1, not_3_out);
  _1_bit_memory_cell u_1_bit_memory_cell_1 (.in_1(not_2_out), .in_2(or_1_out), .\output (n1_bit_memory_cell_1_output));
  not not_3 (not_3_out, n1_bit_memory_cell_2_output);
  _1_bit_memory_cell u_1_bit_memory_cell_2 (
    .in_1(n1_bit_memory_cell_1_output), .in_2(or_2_out), .\output (n1_bit_memory_cell_2_output));
  and and_1 (out_4, n1_bit_memory_cell_2_output, not_4_out);
  _1_bit_memory_cell u_1_bit_memory_cell_3 (
    .in_1(n1_bit_memory_cell_2_output), .in_2(or_1_out), .\output (n1_bit_memory_cell_3_output));
  not not_4 (not_4_out, n1_bit_memory_cell_4_output);
  _1_bit_memory_cell u_1_bit_memory_cell_4 (
    .in_1(n1_bit_memory_cell_3_output), .in_2(or_2_out), .\output (n1_bit_memory_cell_4_output));
  and and_2 (out_5, n1_bit_memory_cell_4_output, not_5_out);
  _1_bit_memory_cell u_1_bit_memory_cell_5 (
    .in_1(n1_bit_memory_cell_4_output), .in_2(or_1_out), .\output (n1_bit_memory_cell_5_output));
  not not_5 (not_5_out, n1_bit_memory_cell_6_output);
  _1_bit_memory_cell u_1_bit_memory_cell_6 (
    .in_1(n1_bit_memory_cell_5_output), .in_2(or_2_out), .\output (n1_bit_memory_cell_6_output));
  and and_3 (out_6, n1_bit_memory_cell_6_output, not_6_out);
  _1_bit_memory_cell u_1_bit_memory_cell_7 (
    .in_1(n1_bit_memory_cell_6_output), .in_2(or_1_out), .\output (n1_bit_memory_cell_7_output));
  not not_6 (not_6_out, n1_bit_memory_cell_8_output);
  _1_bit_memory_cell u_1_bit_memory_cell_8 (
    .in_1(n1_bit_memory_cell_7_output), .in_2(or_2_out), .\output (n1_bit_memory_cell_8_output));
  and and_4 (out_7, n1_bit_memory_cell_8_output, not_7_out);
  _1_bit_memory_cell u_1_bit_memory_cell_9 (
    .in_1(n1_bit_memory_cell_8_output), .in_2(or_1_out), .\output (n1_bit_memory_cell_9_output));
  not not_7 (not_7_out, n1_bit_memory_cell_10_output);
  _1_bit_memory_cell u_1_bit_memory_cell_10 (
    .in_1(n1_bit_memory_cell_9_output), .in_2(or_2_out), .\output (n1_bit_memory_cell_10_output));
  and and_5 (out_8, n1_bit_memory_cell_10_output, not_8_out);
  _1_bit_memory_cell u_1_bit_memory_cell_11 (
    .in_1(n1_bit_memory_cell_10_output), .in_2(or_1_out), .\output (n1_bit_memory_cell_11_output));
  not not_8 (not_8_out, n1_bit_memory_cell_12_output);
  _1_bit_memory_cell u_1_bit_memory_cell_12 (
    .in_1(n1_bit_memory_cell_11_output), .in_2(or_2_out), .\output (n1_bit_memory_cell_12_output));
  and and_6 (out_9, n1_bit_memory_cell_12_output, not_9_out);
  _1_bit_memory_cell u_1_bit_memory_cell_13 (
    .in_1(n1_bit_memory_cell_12_output), .in_2(or_1_out), .\output (n1_bit_memory_cell_13_output));
  not not_9 (not_9_out, n1_bit_memory_cell_14_output);
  _1_bit_memory_cell u_1_bit_memory_cell_14 (
    .in_1(n1_bit_memory_cell_13_output), .in_2(or_2_out), .\output (n1_bit_memory_cell_14_output));
  and and_7 (out_10, n1_bit_memory_cell_14_output, not_10_out);
  _1_bit_memory_cell u_1_bit_memory_cell_15 (
    .in_1(n1_bit_memory_cell_14_output), .in_2(or_1_out), .\output (n1_bit_memory_cell_15_output));
  not not_10 (not_10_out, n1_bit_memory_cell_16_output);
  _1_bit_memory_cell u_1_bit_memory_cell_16 (
    .in_1(n1_bit_memory_cell_15_output), .in_2(or_2_out), .\output (n1_bit_memory_cell_16_output));
  and and_8 (out_11, n1_bit_memory_cell_16_output, not_11_out);
  _1_bit_memory_cell u_1_bit_memory_cell_17 (
    .in_1(n1_bit_memory_cell_16_output), .in_2(or_1_out), .\output (n1_bit_memory_cell_17_output));
  not not_11 (not_11_out, n1_bit_memory_cell_18_output);
  _1_bit_memory_cell u_1_bit_memory_cell_18 (
    .in_1(n1_bit_memory_cell_17_output), .in_2(or_2_out), .\output (n1_bit_memory_cell_18_output));
  and and_9 (out_12, n1_bit_memory_cell_18_output, not_12_out);
  _1_bit_memory_cell u_1_bit_memory_cell_19 (
    .in_1(n1_bit_memory_cell_18_output), .in_2(or_1_out), .\output (n1_bit_memory_cell_19_output));
  not not_12 (not_12_out, n1_bit_memory_cell_20_output);
  _1_bit_memory_cell u_1_bit_memory_cell_20 (
    .in_1(n1_bit_memory_cell_19_output), .in_2(or_2_out), .\output (n1_bit_memory_cell_20_output));
  and and_10 (out_13, n1_bit_memory_cell_20_output, not_13_out);
  _1_bit_memory_cell u_1_bit_memory_cell_21 (
    .in_1(n1_bit_memory_cell_20_output), .in_2(or_1_out), .\output (n1_bit_memory_cell_21_output));
  not not_13 (not_13_out, n1_bit_memory_cell_22_output);
  _1_bit_memory_cell u_1_bit_memory_cell_22 (
    .in_1(n1_bit_memory_cell_21_output), .in_2(or_2_out), .\output (n1_bit_memory_cell_22_output));
  and and_11 (out_14, n1_bit_memory_cell_22_output, not_14_out);
  _1_bit_memory_cell u_1_bit_memory_cell_23 (
    .in_1(n1_bit_memory_cell_22_output), .in_2(or_1_out), .\output (n1_bit_memory_cell_23_output));
  not not_14 (not_14_out, n1_bit_memory_cell_24_output);
  _1_bit_memory_cell u_1_bit_memory_cell_24 (
    .in_1(n1_bit_memory_cell_23_output), .in_2(or_2_out), .\output (n1_bit_memory_cell_24_output));
  and and_12 (out_15, n1_bit_memory_cell_24_output, not_15_out);
  _1_bit_memory_cell u_1_bit_memory_cell_25 (
    .in_1(n1_bit_memory_cell_24_output), .in_2(or_1_out), .\output (n1_bit_memory_cell_25_output));
  not not_15 (not_15_out, n1_bit_memory_cell_26_output);
  _1_bit_memory_cell u_1_bit_memory_cell_26 (
    .in_1(n1_bit_memory_cell_25_output), .in_2(or_2_out), .\output (n1_bit_memory_cell_26_output));
  and and_13 (out_16, n1_bit_memory_cell_26_output, not_16_out);
  _1_bit_memory_cell u_1_bit_memory_cell_27 (
    .in_1(n1_bit_memory_cell_26_output), .in_2(or_1_out), .\output (n1_bit_memory_cell_27_output));
  not not_16 (not_16_out, n1_bit_memory_cell_28_output);
  _1_bit_memory_cell u_1_bit_memory_cell_28 (
    .in_1(n1_bit_memory_cell_27_output), .in_2(or_2_out), .\output (n1_bit_memory_cell_28_output));
  and and_14 (out_17, n1_bit_memory_cell_28_output, not_17_out);
  _1_bit_memory_cell u_1_bit_memory_cell_29 (
    .in_1(n1_bit_memory_cell_28_output), .in_2(or_1_out), .\output (n1_bit_memory_cell_29_output));
  not not_17 (not_17_out, n1_bit_memory_cell_30_output);
  _1_bit_memory_cell u_1_bit_memory_cell_30 (
    .in_1(n1_bit_memory_cell_29_output), .in_2(or_2_out), .\output (n1_bit_memory_cell_30_output));
  and and_15 (out_18, n1_bit_memory_cell_30_output, not_18_out);
  _1_bit_memory_cell u_1_bit_memory_cell_31 (
    .in_1(n1_bit_memory_cell_30_output), .in_2(or_1_out), .\output (n1_bit_memory_cell_31_output));
  not not_18 (not_18_out, out_19);
  _1_bit_memory_cell u_1_bit_memory_cell_32 (.in_1(n1_bit_memory_cell_31_output), .in_2(or_2_out), .\output (out_19));

  // Other names for the same wires on the sheet: clk = in_2; reset = in_1; step_0 = out_3; step_1 = out_4;
  //   step_2 = out_5; step_3 = out_6; step_4 = out_7; step_5 = out_8; step_6 = out_9; step_7 = out_10;
  //   step_8 = out_11; step_9 = out_12; step_10 = out_13; step_11 = out_14; step_12 = out_15; step_13 = out_16;
  //   step_14 = out_17; step_15 = out_18; step_16 = out_19

  // Notes on the sheet:
  //   out_14: pull=down
  //   out_5: pull=down
  //   out_11: pull=down
  //   out_13: pull=down
  //   out_10: pull=down
  //   out_8: pull=down
  //   in_2: pull=down
  //   out_16: pull=down
  //   out_4: pull=down
  //   out_9: pull=down
  //   out_18: pull=down
  //   out_7: pull=down
  //   in_1: pull=down
  //   out_3: pull=down
  //   out_19: pull=down
  //   out_12: pull=down
  //   out_6: pull=down
  //   out_15: pull=down
  //   out_17: pull=down
endmodule

module _16_bit_FLAGS (
  input  in_1,
  input  in_2,
  input  in_3,
  input  in_4,
  input  in_5,
  input  in_6,
  input  in_7,
  input  in_8,
  input  in_9,
  input  in_10,
  input  in_11,
  input  in_12,
  input  in_13,
  input  in_14,
  input  in_15,
  input  in_16,
  input  in_17,
  output out_18,
  output out_19,
  output out_20,
  output out_21,
  output out_22,
  output out_23,
  output out_24,
  output out_25,
  output out_26,
  output out_27,
  output out_28,
  output out_29,
  output out_30,
  output out_31,
  output out_32,
  output out_33
);

  _1_bit_memory_cell u_1_bit_memory_cell_1 (.in_1(in_1), .in_2(in_17), .\output (out_18));
  _1_bit_memory_cell u_1_bit_memory_cell_2 (.in_1(in_2), .in_2(in_17), .\output (out_19));
  _1_bit_memory_cell u_1_bit_memory_cell_3 (.in_1(in_3), .in_2(in_17), .\output (out_20));
  _1_bit_memory_cell u_1_bit_memory_cell_4 (.in_1(in_4), .in_2(in_17), .\output (out_21));
  _1_bit_memory_cell u_1_bit_memory_cell_5 (.in_1(in_5), .in_2(in_17), .\output (out_22));
  _1_bit_memory_cell u_1_bit_memory_cell_6 (.in_1(in_6), .in_2(in_17), .\output (out_23));
  _1_bit_memory_cell u_1_bit_memory_cell_7 (.in_1(in_7), .in_2(in_17), .\output (out_24));
  _1_bit_memory_cell u_1_bit_memory_cell_8 (.in_1(in_8), .in_2(in_17), .\output (out_25));
  _1_bit_memory_cell u_1_bit_memory_cell_9 (.in_1(in_9), .in_2(in_17), .\output (out_26));
  _1_bit_memory_cell u_1_bit_memory_cell_10 (.in_1(in_10), .in_2(in_17), .\output (out_27));
  _1_bit_memory_cell u_1_bit_memory_cell_11 (.in_1(in_11), .in_2(in_17), .\output (out_28));
  _1_bit_memory_cell u_1_bit_memory_cell_12 (.in_1(in_12), .in_2(in_17), .\output (out_29));
  _1_bit_memory_cell u_1_bit_memory_cell_13 (.in_1(in_13), .in_2(in_17), .\output (out_30));
  _1_bit_memory_cell u_1_bit_memory_cell_14 (.in_1(in_14), .in_2(in_17), .\output (out_31));
  _1_bit_memory_cell u_1_bit_memory_cell_15 (.in_1(in_15), .in_2(in_17), .\output (out_32));
  _1_bit_memory_cell u_1_bit_memory_cell_16 (.in_1(in_16), .in_2(in_17), .\output (out_33));

  // Other names for the same wires on the sheet: A___B = in_4; A___B_t = in_2; A___B_t_t = in_3; carry = in_1;
  //   even = in_6; minus_1 = in_8; positive = in_7; reserved = in_16; reserved3 = in_9; reserved4 = in_10;
  //   reserved5 = in_11; reserved6 = in_12; reserved7 = in_13; reserved8 = in_14; reserved9 = in_15; set = in_17;
  //   zero = in_5

  // Notes on the sheet:
  //   out_25: pull=down
  //   out_30: pull=down
  //   in_1: pull=down
  //   out_22: pull=down
  //   in_14: pull=down
  //   in_6: pull=down
  //   out_23: pull=down
  //   out_27: pull=down
  //   out_24: pull=down
  //   out_19: pull=down
  //   out_21: pull=down
  //   in_15: pull=down
  //   in_8: pull=down
  //   in_4: pull=down
  //   out_28: pull=down
  //   in_17: pull=down
  //   in_3: pull=down
  //   out_20: pull=down
  //   in_10: pull=down
  //   out_29: pull=down
  //   in_13: pull=down
  //   in_9: pull=down
  //   in_16: pull=down
  //   out_33: pull=down
  //   in_11: pull=down
  //   out_26: pull=down
  //   in_7: pull=down
  //   in_12: pull=down
  //   out_31: pull=down
  //   out_18: pull=down
  //   in_2: pull=down
  //   out_32: pull=down
  //   in_5: pull=down
endmodule

module _16_bit_IR (
  input  [15:0] in_1,
  input  in_2,
  output [15:0] out_3
);

  _2_bytes_memory_cell u_2_bytes_memory_cell_1 (.\input (in_1), .in_2(in_2), .\output (out_3));

  // Other names for the same wires on the sheet: enable = in_2; input[15:0] = in_1; output[15:0] = out_3

  // Notes on the sheet:
  //   in_2: pull=down
  //   in_1: pull=down
  //   out_3: pull=down
endmodule

module _7_segment_display_demo (
);

  wire _1_out, _2_out, _3_out, _4_out, _5_out, _6_out, _7_out, dot_out;

  Button _2 (.out(_2_out));
  Button _4 (.out(_4_out));
  Button _5 (.out(_5_out));
  Button _7 (.out(_7_out));
  _7_Segment_Display u_7_segment_display_1 (
    .g(_4_out), .f(_2_out), .a(_1_out), .b(_3_out), .e(_5_out), .d(_7_out), .c(_6_out), .dp(dot_out));
  Button _1 (.out(_1_out));
  Button _3 (.out(_3_out));
  Button dot (.out(dot_out));
  Button _6 (.out(_6_out));

  // Notes on the sheet:
  //   2
  //   5
  //   1
  //   -
  //   3
  //   |
  //   |
  //   4
  //   -
  //   6
  //   |
  //   |
  //   -
  //   7
endmodule
module cpu_control_section (
  input  [15:0] in_1,
  input  in_2,
  input  in_3,
  input  in_4,
  input  in_5,
  input  in_6,
  input  in_7,
  input  in_8,
  input  in_9,
  input  in_10,
  input  in_11,
  input  in_12,
  input  in_13,
  output out_14,
  output out_15,
  output out_16,
  output out_17,
  output out_18,
  output out_19,
  output out_20,
  output out_21,
  output out_22,
  output out_23,
  output out_24,
  output out_25,
  output out_26,
  output out_27,
  output out_28,
  output out_29,
  output [15:0] load_register,
  output [15:0] store_register,
  output [15:0] select_register,
  output out_33,
  output out_34,
  output out_35,
  output out_36
);

  wire adc_ra__imm16, adc_ra__rb, adc_ra__word__rb, add_ra__byte__rb, add_ra__imm16, add_ra__rb,
       add_ra__word__rb, add_word__ra___rb, add_word__ra_rb___imm16, ALU_0000, ALU_0001, ALU_0010, ALU_0011,
       ALU_0100, ALU_0101, ALU_0110, ALU_0111, ALU_1000, ALU_1001, ALU_1010, ALU_1011, ALU_1100, ALU_1101,
       ALU_1110, ALU_1111, and_100_out, and_101_out, and_102_out, and_103_out, and_104_out, and_105_out,
       and_106_out, and_107_out, and_108_out, and_109_out, and_110_out, and_111_out, and_112_out,
       and_113_out, and_114_out, and_115_out, and_116_out, and_117_out, and_118_out, and_119_out,
       and_120_out, and_121_out, and_122_out, and_123_out, and_124_out, and_125_out, and_126_out,
       and_128_out, and_129_out, and_130_out, and_131_out, and_132_out, and_133_out, and_134_out,
       and_135_out, and_136_out, and_137_out, and_138_out, and_139_out, and_140_out, and_141_out,
       and_142_out, and_143_out, and_144_out, and_145_out, and_146_out, and_147_out, and_148_out,
       and_149_out, and_150_out, and_151_out, and_152_out, and_153_out, and_154_out, and_155_out,
       and_157_out, and_163_out, and_164_out, and_168_out, and_177_out, and_178_out, and_179_out,
       and_180_out, and_181_out, and_182_out, and_183_out, and_184_out, and_185_out, and_186_out,
       and_187_out, and_188_out, and_189_out, and_190_out, and_191_out, and_192_out, and_193_out,
       and_194_out, and_195_out, and_196_out, and_198_out, and_199_out, and_200_out, and_202_out,
       and_203_out, and_204_out, and_205_out, and_206_out, and_207_out, and_208_out, and_209_out,
       and_210_out, and_211_out, and_212_out, and_213_out, and_215_out, and_216_out, and_218_out,
       and_220_out, and_222_out, and_223_out, and_224_out, and_225_out, and_226_out, and_227_out,
       and_229_out, and_231_out, and_232_out, and_233_out, and_234_out, and_235_out, and_236_out,
       and_237_out, and_238_out, and_239_out, and_240_out, and_241_out, and_242_out, and_244_out,
       and_245_out, and_246_out, and_248_out, and_249_out, and_250_out, and_251_out, and_252_out,
       and_253_out, and_254_out, and_257_out, and_258_out, and_259_out, and_260_out, and_261_out,
       and_262_out, and_264_out, and_265_out, and_266_out, and_267_out, and_268_out, and_270_out,
       and_271_out, and_272_out, and_273_out, and_274_out, and_275_out, and_276_out, and_278_out,
       and_279_out, and_280_out, and_282_out, and_283_out, and_284_out, and_285_out, and_288_out,
       and_290_out, and_291_out, and_292_out, and_293_out, and_295_out, and_296_out, and_304_out,
       and_305_out, and_306_out, and_307_out, and_308_out, and_309_out, and_310_out, and_311_out,
       and_312_out, and_313_out, and_314_out, and_315_out, and_316_out, and_317_out, and_318_out,
       and_319_out, and_320_out, and_321_out, and_322_out, and_323_out, and_324_out, and_325_out,
       and_326_out, and_327_out, and_328_out, and_329_out, and_330_out, and_331_out, and_332_out,
       and_333_out, and_334_out, and_335_out, and_ra__imm16, and_ra__rb, and_ra__word__rb,
       and_word__ra_rb___imm16, arith_ra, arith_ra__imm16, arith_ra__rb, arith_ra__word__rb,
       arith_word__ra_rb, arith_word__ra_rb___imm16, clock0, clock1, clock2, clock3, clock4, clock5, clock6,
       clock7, clock8, clock9, clock10, clock11, clock12, clock13, clock14, clock15, cmp_ra__imm16,
       cmp_ra__rb, cmp_ra__word__rb, cmp_word__ra_rb___imm16, div_ra__imm16, div_ra__rb, div_ra__word__rb,
       flip_ra, flip_word__ra_rb, ja_ra_imm16, ja_ra_rb, jb_ra_imm16, jb_ra_rb, jc_ra_imm16, jc_ra_rb,
       jeq_ra_imm16, jeq_ra_rb, jev_ra_imm16, jev_ra_rb, jmp_ra_imm16, jmp_ra_rb, jna_ra_imm16, jna_ra_rb,
       jnb_ra_imm16, jnb_ra_rb, jnc_ra_imm16, jnc_ra_rb, jneq_ra_imm16, jneq_ra_rb, jnev_ra_imm16,
       jnev_ra_rb, jnp_ra_imm16, jnp_ra_rb, jnr_ra_imm16, jnr_ra_rb, jnz_ra_imm16, jnz_ra_rb, jp_ra_imm16,
       jp_ra_rb, jr_ra_imm16, jr_ra_rb, jump, jump_ra_imm16, jump_ra_rb, jz_ra_imm16, jz_ra_rb, load_cs,
       load_IAR, load_ra, load_rb, load_sp, load_ss, mod_ra__imm16, mod_ra__rb, mod_ra__word__rb,
       mov_ra__byte__rb, mov_ra__byte__rb_imm16, mov_ra__imm16, mov_ra__rb, mov_ra__word__rb,
       mov_ra__word__rb_imm16, mov_word__ra___rb, mov_word__ra_rb___imm16, mul_ra__imm16, mul_ra__rb,
       mul_ra__word__rb, n4x16_decoder_1__0000, n4x16_decoder_1__0001, n4x16_decoder_1__0010,
       n4x16_decoder_1__0011, n4x16_decoder_1__0100, n4x16_decoder_1__0101, n4x16_decoder_1__0110,
       n4x16_decoder_1__0111, n4x16_decoder_1__1000, n4x16_decoder_1__1001, n4x16_decoder_1__1010,
       n4x16_decoder_1__1011, n4x16_decoder_1__1100, n4x16_decoder_1__1101, n4x16_decoder_1__1110,
       n4x16_decoder_1__1111, n4x16_decoder_2__0000, n4x16_decoder_2__0001, n4x16_decoder_2__0010,
       n4x16_decoder_2__0011, n4x16_decoder_2__0100, n4x16_decoder_2__0101, n4x16_decoder_2__0110,
       n4x16_decoder_2__0111, n4x16_decoder_2__1000, n4x16_decoder_2__1001, n4x16_decoder_2__1010,
       n4x16_decoder_2__1011, n4x16_decoder_2__1100, n4x16_decoder_2__1101, n4x16_decoder_2__1110,
       n4x16_decoder_2__1111, n4x16_decoder_3__0000, n4x16_decoder_3__0001, n4x16_decoder_3__0010,
       n4x16_decoder_3__0011, n4x16_decoder_3__0100, n4x16_decoder_3__0101, n4x16_decoder_3__0110,
       n4x16_decoder_3__0111, n4x16_decoder_3__1000, n4x16_decoder_3__1001, n4x16_decoder_3__1010,
       n4x16_decoder_3__1011, n4x16_decoder_3__1100, n4x16_decoder_3__1101, n4x16_decoder_3__1110,
       n4x16_decoder_3__1111, n4x16_decoder_4__0000, n4x16_decoder_4__0001, n4x16_decoder_4__0010,
       n4x16_decoder_4__0011, n4x16_decoder_4__0100, n4x16_decoder_4__0101, n4x16_decoder_4__0110,
       n4x16_decoder_4__0111, n4x16_decoder_4__1000, n4x16_decoder_4__1001, n4x16_decoder_4__1010,
       n4x16_decoder_4__1011, n4x16_decoder_4__1100, n4x16_decoder_4__1101, n4x16_decoder_4__1110,
       n4x16_decoder_4__1111, n4x16_decoder_5__0000, n4x16_decoder_5__0001, n4x16_decoder_5__0010,
       n4x16_decoder_5__0011, n4x16_decoder_5__0100, n4x16_decoder_5__0101, n4x16_decoder_5__0110,
       n4x16_decoder_5__0111, n4x16_decoder_5__1000, n4x16_decoder_5__1001, n4x16_decoder_5__1010,
       n4x16_decoder_5__1011, n4x16_decoder_5__1100, n4x16_decoder_5__1101, n4x16_decoder_5__1110,
       n4x16_decoder_5__1111, n4x16_decoder_6__0000, n4x16_decoder_6__0001, n4x16_decoder_6__0010,
       n4x16_decoder_6__0011, n4x16_decoder_6__0100, n4x16_decoder_6__0101, n4x16_decoder_6__0110,
       n4x16_decoder_6__0111, n4x16_decoder_6__1000, n4x16_decoder_6__1001, n4x16_decoder_6__1010,
       n4x16_decoder_6__1011, n4x16_decoder_6__1100, n4x16_decoder_6__1101, n4x16_decoder_6__1110,
       n4x16_decoder_6__1111, n16_step_stepper_1_out_19, neg_ra, neg_word__ra_rb, no_ALU, nop, not_1_out,
       not_2_out, not_3_out, not_4_out, not_5_out, not_6_out, not_7_out, not_8_out, not_9_out, not_10_out,
       not_11_out, not_12_out, not_13_out, not_14_out, not_15_out, not_16_out, not_17_out, not_18_out,
       not_19_out, not_20_out, not_21_out, not_22_out, not_23_out, not_24_out, not_25_out, not_26_out,
       not_27_out, not_28_out, not_29_out, not_30_out, not_31_out, not_32_out, not_33_out, not_34_out,
       not_35_out, not_36_out, not_37_out, not_38_out, not_39_out, not_40_out, not_41_out, not_42_out,
       not_43_out, not_44_out, not_45_out, not_46_out, not_47_out, not_48_out, not_49_out, not_50_out,
       not_51_out, not_52_out, not_53_out, not_54_out, not_55_out, not_56_out, not_57_out, not_58_out,
       not_59_out, not_60_out, not_61_out, not_62_out, not_63_out, not_64_out, not_65_out, not_66_out,
       not_67_out, not_68_out, not_69_out, not_70_out, not_71_out, not_72_out, not_73_out, not_74_out,
       not_75_out, not_76_out, not_77_out, not_78_out, not_79_out, not_80_out, not_81_out, not_82_out,
       not_83_out, not_84_out, not_85_out, not_86_out, not_87_out, not_88_out, not_89_out, not_90_out,
       not_91_out, not_92_out, not_93_out, not_94_out, not_95_out, not_96_out, not_97_out, not_98_out,
       not_99_out, not_100_out, not_101_out, not_102_out, not_103_out, not_104_out, not_105_out, not_106_out,
       not_107_out, not_108_out, not_109_out, not_110_out, not_111_out, not_112_out, not_113_out,
       not_114_out, not_115_out, not_116_out, not_117_out, not_118_out, not_119_out, not_120_out,
       not_121_out, not_122_out, not_123_out, not_124_out, not_125_out, not_126_out, not_127_out,
       not_128_out, not_129_out, not_130_out, not_131_out, not_132_out, not_133_out, not_134_out,
       not_135_out, not_136_out, not_137_out, not_138_out, not_139_out, not_140_out, not_141_out,
       not_142_out, not_143_out, not_144_out, not_145_out, not_146_out, not_147_out, not_148_out,
       not_149_out, not_150_out, not_151_out, not_152_out, not_153_out, not_154_out, not_155_out,
       not_156_out, not_157_out, not_158_out, not_159_out, not_160_out, not_161_out, not_162_out,
       not_163_out, not_164_out, not_165_out, not_166_out, not_167_out, not_168_out, not_169_out,
       not_170_out, not_171_out, not_172_out, not_173_out, not_174_out, not_175_out, not_176_out,
       not_177_out, not_178_out, not_179_out, not_180_out, not_181_out, not_182_out, not_183_out,
       not_184_out, not_185_out, not_186_out, not_187_out, not_188_out, not_189_out, not_190_out,
       not_191_out, not_192_out, not_193_out, not_194_out, not_195_out, not_196_out, not_197_out,
       not_198_out, not_199_out, not_200_out, not_201_out, not_202_out, not_203_out, not_204_out,
       not_205_out, not_206_out, not_207_out, not_208_out, not_209_out, not_210_out, not_211_out,
       not_212_out, not_213_out, not_214_out, not_215_out, not_216_out, not_217_out, not_218_out,
       not_219_out, not_220_out, not_221_out, not_222_out, not_223_out, not_224_out, not_225_out,
       not_226_out, not_227_out, not_228_out, not_229_out, not_230_out, not_231_out, not_232_out,
       not_233_out, not_234_out, not_235_out, not_236_out, not_237_out, not_238_out, not_239_out,
       not_240_out, not_241_out, not_242_out, not_243_out, not_244_out, not_245_out, not_246_out,
       not_247_out, not_248_out, not_249_out, not_250_out, not_251_out, not_252_out, not_253_out,
       not_254_out, not_255_out, not_256_out, not_257_out, not_258_out, not_259_out, not_260_out,
       not_261_out, not_262_out, not_263_out, not_264_out, not_265_out, not_266_out, not_267_out,
       not_268_out, not_269_out, not_270_out, not_271_out, not_272_out, not_273_out, not_274_out,
       not_275_out, not_276_out, not_277_out, not_278_out, not_279_out, not_280_out, not_281_out,
       not_282_out, not_283_out, not_284_out, not_285_out, not_286_out, not_287_out, not_288_out,
       not_289_out, not_290_out, not_291_out, not_292_out, not_293_out, not_294_out, not_295_out,
       not_296_out, not_297_out, not_298_out, not_299_out, not_300_out, not_301_out, not_302_out,
       not_303_out, not_304_out, not_305_out, not_306_out, not_307_out, not_308_out, not_309_out,
       not_310_out, not_311_out, not_312_out, not_313_out, not_314_out, not_315_out, not_316_out,
       not_317_out, not_318_out, not_319_out, not_320_out, not_321_out, not_322_out, not_323_out,
       not_324_out, not_325_out, not_326_out, not_327_out, not_328_out, not_329_out, not_330_out,
       not_331_out, not_332_out, not_333_out, not_334_out, not_335_out, not_336_out, not_337_out,
       not_338_out, not_339_out, not_340_out, not_341_out, not_342_out, not_343_out, not_344_out,
       not_345_out, not_346_out, not_347_out, not_348_out, not_349_out, not_350_out, not_351_out,
       not_352_out, not_353_out, not_354_out, not_355_out, not_356_out, not_357_out, not_358_out,
       not_359_out, not_360_out, not_361_out, not_362_out, not_363_out, not_364_out, not_365_out,
       not_366_out, not_367_out, not_368_out, not_369_out, not_370_out, not_371_out, not_372_out,
       not_373_out, not_374_out, not_375_out, not_376_out, not_377_out, not_378_out, not_379_out,
       not_380_out, not_381_out, not_382_out, not_383_out, not_384_out, not_385_out, not_386_out,
       not_387_out, not_388_out, not_389_out, not_390_out, not_391_out, not_392_out, not_393_out,
       not_394_out, not_395_out, not_396_out, not_397_out, not_398_out, not_399_out, not_400_out,
       not_401_out, not_402_out, not_403_out, not_404_out, not_405_out, not_406_out, not_407_out,
       not_408_out, not_409_out, not_410_out, not_411_out, not_412_out, not_413_out, not_414_out,
       not_415_out, not_416_out, not_417_out, not_418_out, not_419_out, not_420_out, not_421_out,
       not_422_out, not_423_out, not_424_out, not_425_out, not_426_out, not_427_out, not_428_out,
       not_429_out, not_430_out, not_431_out, not_432_out, not_433_out, not_434_out, not_435_out,
       not_436_out, not_437_out, not_438_out, not_439_out, not_440_out, not_441_out, not_442_out,
       not_443_out, not_444_out, not_445_out, not_446_out, not_447_out, not_448_out, not_449_out,
       not_450_out, not_451_out, not_452_out, not_453_out, not_454_out, not_455_out, not_456_out,
       not_457_out, not_458_out, not_459_out, not_above, not_below, not_carry, not_equal, not_even,
       not_positive, not_reserved, not_zero, or_1_out, or_2_out, or_3_out, or_4_out, or_5_out, or_6_out,
       or_7_out, or_8_out, or_9_out, or_10_out, or_11_out, or_12_out, or_13_out, or_14_out, or_15_out,
       or_16_out, or_17_out, or_18_out, or_19_out, or_20_out, or_21_out, or_22_out, or_23_out, or_24_out,
       or_25_out, or_26_out, or_27_out, or_28_out, or_29_out, or_30_out, or_31_out, or_32_out, or_33_out,
       or_34_out, or_35_out, or_36_out, or_37_out, or_38_out, or_39_out, or_40_out, or_41_out, or_42_out,
       or_43_out, or_44_out, or_45_out, or_46_out, or_47_out, or_48_out, or_49_out, or_50_out, or_51_out,
       or_52_out, or_53_out, or_54_out, or_55_out, or_56_out, or_57_out, or_58_out, or_59_out, or_60_out,
       or_61_out, or_62_out, or_63_out, or_64_out, or_65_out, or_66_out, or_67_out, or_68_out, or_69_out,
       or_70_out, or_72_out, or_73_out, or_74_out, or_75_out, or_76_out, or_77_out, or_78_out, or_79_out,
       or_80_out, or_81_out, or_82_out, or_83_out, or_84_out, or_85_out, or_86_out, or_87_out, or_88_out,
       or_89_out, or_90_out, or_91_out, or_92_out, or_93_out, or_94_out, or_95_out, or_96_out, or_97_out,
       or_98_out, or_99_out, or_100_out, or_101_out, or_102_out, or_103_out, or_104_out, or_105_out,
       or_106_out, or_107_out, or_108_out, or_109_out, or_110_out, or_111_out, or_112_out, or_113_out,
       or_114_out, or_115_out, or_116_out, or_117_out, or_118_out, or_119_out, or_120_out, or_121_out,
       or_122_out, or_123_out, or_124_out, or_125_out, or_126_out, or_127_out, or_128_out, or_129_out,
       or_130_out, or_131_out, or_132_out, or_133_out, or_134_out, or_135_out, or_136_out, or_137_out,
       or_138_out, or_139_out, or_141_out, or_142_out, or_143_out, or_144_out, or_145_out, or_146_out,
       or_147_out, or_148_out, or_149_out, or_150_out, or_151_out, or_152_out, or_153_out, or_154_out,
       or_155_out, or_156_out, or_157_out, or_158_out, or_159_out, or_160_out, or_161_out, or_162_out,
       or_163_out, or_164_out, or_165_out, or_166_out, or_167_out, or_168_out, or_169_out, or_170_out,
       or_171_out, or_172_out, or_173_out, or_174_out, or_175_out, or_179_out, or_180_out, or_181_out,
       or_182_out, or_183_out, or_184_out, or_185_out, or_186_out, or_187_out, or_188_out, or_189_out,
       or_190_out, or_191_out, or_192_out, or_193_out, or_194_out, or_195_out, or_196_out, or_197_out,
       or_198_out, or_199_out, or_200_out, or_201_out, or_202_out, or_203_out, or_204_out, or_205_out,
       or_206_out, or_207_out, or_208_out, or_209_out, or_210_out, or_211_out, or_212_out, or_213_out,
       or_214_out, or_215_out, or_216_out, or_217_out, or_218_out, or_219_out, or_220_out, or_221_out,
       or_222_out, or_223_out, or_224_out, or_225_out, or_226_out, or_227_out, or_228_out, or_229_out,
       or_230_out, or_231_out, or_232_out, or_233_out, or_234_out, or_235_out, or_236_out, or_237_out,
       or_238_out, or_239_out, or_240_out, or_241_out, or_242_out, or_243_out, or_244_out, or_293_out,
       or_294_out, or_295_out, or_296_out, or_297_out, or_298_out, or_299_out, or_300_out, or_ra__imm16,
       or_ra__rb, or_ra__word__rb, or_word__ra_rb___imm16, pop, pop0, pop_byte__ra_rb, pop_ra,
       pop_word__ra_rb, push, push_byte__ra_rb, push_imm16, push_ra, push_word__ra_rb, ra_load_r0,
       ra_load_r1, ra_load_r2, ra_load_r3, ra_load_r4, ra_load_r5, ra_load_r6, ra_load_r7, ra_load_r8,
       ra_load_r9, ra_load_r10, ra_load_r11, ra_load_r12, ra_load_r13, ra_load_r14, ra_load_r15, ra_sel_r0,
       ra_sel_r1, ra_sel_r2, ra_sel_r3, ra_sel_r4, ra_sel_r5, ra_sel_r6, ra_sel_r7, ra_sel_r8, ra_sel_r9,
       ra_sel_r10, ra_sel_r11, ra_sel_r12, ra_sel_r13, ra_sel_r14, ra_sel_r15, ra_store_r0, ra_store_r1,
       ra_store_r2, ra_store_r3, ra_store_r4, ra_store_r5, ra_store_r6, ra_store_r7, ra_store_r8,
       ra_store_r9, ra_store_r10, ra_store_r11, ra_store_r12, ra_store_r13, ra_store_r14, ra_store_r15,
       rb_load_r0, rb_load_r1, rb_load_r2, rb_load_r3, rb_load_r4, rb_load_r5, rb_load_r6, rb_load_r7,
       rb_load_r8, rb_load_r9, rb_load_r10, rb_load_r11, rb_load_r12, rb_load_r13, rb_load_r14, rb_load_r15,
       rb_sel_r0, rb_sel_r1, rb_sel_r2, rb_sel_r3, rb_sel_r4, rb_sel_r5, rb_sel_r6, rb_sel_r7, rb_sel_r8,
       rb_sel_r9, rb_sel_r10, rb_sel_r11, rb_sel_r12, rb_sel_r13, rb_sel_r14, rb_sel_r15, rb_store_r0,
       rb_store_r1, rb_store_r2, rb_store_r3, rb_store_r4, rb_store_r5, rb_store_r6, rb_store_r7,
       rb_store_r8, rb_store_r9, rb_store_r10, rb_store_r11, rb_store_r12, rb_store_r13, rb_store_r14,
       rb_store_r15, sar_ra__imm4, sar_word__ra_rb___imm4, sel_cs, sel_ds, sel_ra, sel_rb, sel_ss, set_IAR,
       shift_ra__imm4, shift_word__ra_rb___imm4, shl_ra__imm4, shl_word__ra_rb___imm4, shr_ra__imm4,
       shr_word__ra_rb___imm4, store_cs, store_ra, store_rb, store_sp, store_ss, sub_ra__imm16, sub_ra__rb,
       subc_ra__rb, xchg_ra__rb, xor_ra__imm16, xor_ra__rb, xor_ra__word__rb, xor_word__ra_rb___imm16;

  not not_1 (not_1_out, in_1[8]);
  not not_2 (not_2_out, in_1[9]);
  not not_3 (not_3_out, in_1[10]);
  not not_4 (not_4_out, in_1[11]);
  not not_5 (not_5_out, in_1[12]);
  not not_6 (not_6_out, in_1[13]);
  not not_7 (not_7_out, in_1[14]);
  not not_8 (not_8_out, in_1[15]);
  not not_9 (not_9_out, in_1[9]);
  not not_10 (not_10_out, in_1[10]);
  not not_11 (not_11_out, in_1[11]);
  not not_12 (not_12_out, in_1[12]);
  not not_13 (not_13_out, in_1[13]);
  not not_14 (not_14_out, in_1[14]);
  not not_15 (not_15_out, in_1[15]);
  not not_16 (not_16_out, in_1[8]);
  not not_17 (not_17_out, in_1[10]);
  not not_18 (not_18_out, in_1[11]);
  not not_19 (not_19_out, in_1[12]);
  not not_20 (not_20_out, in_1[13]);
  not not_21 (not_21_out, in_1[14]);
  not not_22 (not_22_out, in_1[15]);
  not not_23 (not_23_out, in_1[10]);
  not not_24 (not_24_out, in_1[11]);
  not not_25 (not_25_out, in_1[12]);
  not not_26 (not_26_out, in_1[13]);
  not not_27 (not_27_out, in_1[14]);
  not not_28 (not_28_out, in_1[15]);
  not not_29 (not_29_out, in_1[8]);
  not not_30 (not_30_out, in_1[9]);
  not not_31 (not_31_out, in_1[11]);
  not not_32 (not_32_out, in_1[12]);
  not not_33 (not_33_out, in_1[13]);
  not not_34 (not_34_out, in_1[14]);
  not not_35 (not_35_out, in_1[15]);
  not not_36 (not_36_out, in_1[9]);
  not not_37 (not_37_out, in_1[11]);
  not not_38 (not_38_out, in_1[12]);
  not not_39 (not_39_out, in_1[13]);
  not not_40 (not_40_out, in_1[14]);
  not not_41 (not_41_out, in_1[15]);
  not not_42 (not_42_out, in_1[8]);
  not not_43 (not_43_out, in_1[11]);
  not not_44 (not_44_out, in_1[12]);
  not not_45 (not_45_out, in_1[13]);
  not not_46 (not_46_out, in_1[14]);
  not not_47 (not_47_out, in_1[15]);
  not not_48 (not_48_out, in_1[11]);
  not not_49 (not_49_out, in_1[12]);
  not not_50 (not_50_out, in_1[13]);
  not not_51 (not_51_out, in_1[14]);
  not not_52 (not_52_out, in_1[15]);
  not not_53 (not_53_out, in_1[8]);
  not not_54 (not_54_out, in_1[9]);
  not not_55 (not_55_out, in_1[10]);
  not not_56 (not_56_out, in_1[12]);
  not not_57 (not_57_out, in_1[13]);
  not not_58 (not_58_out, in_1[14]);
  not not_59 (not_59_out, in_1[15]);
  not not_60 (not_60_out, in_1[9]);
  not not_61 (not_61_out, in_1[10]);
  not not_62 (not_62_out, in_1[12]);
  not not_63 (not_63_out, in_1[13]);
  not not_64 (not_64_out, in_1[14]);
  not not_65 (not_65_out, in_1[15]);
  not not_66 (not_66_out, in_1[8]);
  not not_67 (not_67_out, in_1[10]);
  not not_68 (not_68_out, in_1[12]);
  not not_69 (not_69_out, in_1[13]);
  not not_70 (not_70_out, in_1[14]);
  not not_71 (not_71_out, in_1[15]);
  not not_72 (not_72_out, in_1[10]);
  not not_73 (not_73_out, in_1[12]);
  not not_74 (not_74_out, in_1[13]);
  not not_75 (not_75_out, in_1[14]);
  not not_76 (not_76_out, in_1[15]);
  not not_77 (not_77_out, in_1[8]);
  not not_78 (not_78_out, in_1[9]);
  not not_79 (not_79_out, in_1[12]);
  not not_80 (not_80_out, in_1[13]);
  not not_81 (not_81_out, in_1[14]);
  not not_82 (not_82_out, in_1[15]);
  not not_83 (not_83_out, in_1[9]);
  not not_84 (not_84_out, in_1[12]);
  not not_85 (not_85_out, in_1[13]);
  not not_86 (not_86_out, in_1[14]);
  not not_87 (not_87_out, in_1[15]);
  not not_88 (not_88_out, in_1[8]);
  not not_89 (not_89_out, in_1[12]);
  not not_90 (not_90_out, in_1[13]);
  not not_91 (not_91_out, in_1[14]);
  not not_92 (not_92_out, in_1[15]);
  not not_93 (not_93_out, in_1[12]);
  not not_94 (not_94_out, in_1[13]);
  not not_95 (not_95_out, in_1[14]);
  not not_96 (not_96_out, in_1[15]);
  not not_97 (not_97_out, in_1[8]);
  not not_98 (not_98_out, in_1[9]);
  not not_99 (not_99_out, in_1[10]);
  not not_100 (not_100_out, in_1[11]);
  not not_101 (not_101_out, in_1[13]);
  not not_102 (not_102_out, in_1[14]);
  not not_103 (not_103_out, in_1[15]);
  not not_104 (not_104_out, in_1[9]);
  not not_105 (not_105_out, in_1[10]);
  not not_106 (not_106_out, in_1[11]);
  not not_107 (not_107_out, in_1[13]);
  not not_108 (not_108_out, in_1[14]);
  not not_109 (not_109_out, in_1[15]);
  not not_110 (not_110_out, in_1[8]);
  not not_111 (not_111_out, in_1[10]);
  not not_112 (not_112_out, in_1[11]);
  not not_113 (not_113_out, in_1[13]);
  not not_114 (not_114_out, in_1[14]);
  not not_115 (not_115_out, in_1[15]);
  not not_116 (not_116_out, in_1[10]);
  not not_117 (not_117_out, in_1[11]);
  not not_118 (not_118_out, in_1[13]);
  not not_119 (not_119_out, in_1[14]);
  not not_120 (not_120_out, in_1[15]);
  not not_121 (not_121_out, in_1[8]);
  not not_122 (not_122_out, in_1[9]);
  not not_123 (not_123_out, in_1[11]);
  not not_124 (not_124_out, in_1[13]);
  not not_125 (not_125_out, in_1[14]);
  not not_126 (not_126_out, in_1[15]);
  not not_127 (not_127_out, in_1[9]);
  not not_128 (not_128_out, in_1[11]);
  not not_129 (not_129_out, in_1[13]);
  not not_130 (not_130_out, in_1[14]);
  not not_131 (not_131_out, in_1[15]);
  not not_132 (not_132_out, in_1[8]);
  not not_133 (not_133_out, in_1[11]);
  not not_134 (not_134_out, in_1[13]);
  not not_135 (not_135_out, in_1[14]);
  not not_136 (not_136_out, in_1[15]);
  not not_137 (not_137_out, in_1[11]);
  not not_138 (not_138_out, in_1[13]);
  not not_139 (not_139_out, in_1[14]);
  not not_140 (not_140_out, in_1[15]);
  not not_141 (not_141_out, in_1[8]);
  not not_142 (not_142_out, in_1[9]);
  not not_143 (not_143_out, in_1[10]);
  not not_144 (not_144_out, in_1[13]);
  not not_145 (not_145_out, in_1[14]);
  not not_146 (not_146_out, in_1[15]);
  not not_147 (not_147_out, in_1[9]);
  not not_148 (not_148_out, in_1[10]);
  not not_149 (not_149_out, in_1[11]);
  not not_150 (not_150_out, in_1[12]);
  not not_151 (not_151_out, in_1[14]);
  not not_152 (not_152_out, in_1[15]);
  not not_153 (not_153_out, in_1[8]);
  not not_154 (not_154_out, in_1[10]);
  not not_155 (not_155_out, in_1[11]);
  not not_156 (not_156_out, in_1[12]);
  not not_157 (not_157_out, in_1[14]);
  not not_158 (not_158_out, in_1[15]);
  not not_159 (not_159_out, in_1[8]);
  not not_160 (not_160_out, in_1[9]);
  not not_161 (not_161_out, in_1[11]);
  not not_162 (not_162_out, in_1[12]);
  not not_163 (not_163_out, in_1[14]);
  not not_164 (not_164_out, in_1[15]);
  not not_165 (not_165_out, in_1[9]);
  not not_166 (not_166_out, in_1[11]);
  not not_167 (not_167_out, in_1[12]);
  not not_168 (not_168_out, in_1[14]);
  not not_169 (not_169_out, in_1[15]);
  not not_170 (not_170_out, in_1[11]);
  not not_171 (not_171_out, in_1[12]);
  not not_172 (not_172_out, in_1[14]);
  not not_173 (not_173_out, in_1[15]);
  not not_174 (not_174_out, in_1[8]);
  not not_175 (not_175_out, in_1[9]);
  not not_176 (not_176_out, in_1[10]);
  not not_177 (not_177_out, in_1[12]);
  not not_178 (not_178_out, in_1[14]);
  not not_179 (not_179_out, in_1[15]);
  not not_180 (not_180_out, in_1[8]);
  not not_181 (not_181_out, in_1[10]);
  not not_182 (not_182_out, in_1[12]);
  not not_183 (not_183_out, in_1[14]);
  not not_184 (not_184_out, in_1[15]);
  not not_185 (not_185_out, in_1[10]);
  not not_186 (not_186_out, in_1[12]);
  not not_187 (not_187_out, in_1[14]);
  not not_188 (not_188_out, in_1[15]);
  not not_189 (not_189_out, in_1[9]);
  not not_190 (not_190_out, in_1[12]);
  not not_191 (not_191_out, in_1[14]);
  not not_192 (not_192_out, in_1[15]);
  not not_193 (not_193_out, in_1[8]);
  not not_194 (not_194_out, in_1[12]);
  not not_195 (not_195_out, in_1[14]);
  not not_196 (not_196_out, in_1[15]);
  not not_197 (not_197_out, in_1[8]);
  not not_198 (not_198_out, in_1[9]);
  not not_199 (not_199_out, in_1[10]);
  not not_200 (not_200_out, in_1[11]);
  not not_201 (not_201_out, in_1[14]);
  not not_202 (not_202_out, in_1[15]);
  not not_203 (not_203_out, in_1[9]);
  not not_204 (not_204_out, in_1[10]);
  not not_205 (not_205_out, in_1[11]);
  not not_206 (not_206_out, in_1[14]);
  not not_207 (not_207_out, in_1[15]);
  not not_208 (not_208_out, in_1[10]);
  not not_209 (not_209_out, in_1[11]);
  not not_210 (not_210_out, in_1[14]);
  not not_211 (not_211_out, in_1[15]);
  not not_212 (not_212_out, in_1[8]);
  not not_213 (not_213_out, in_1[9]);
  not not_214 (not_214_out, in_1[11]);
  not not_215 (not_215_out, in_1[14]);
  not not_216 (not_216_out, in_1[15]);
  not not_217 (not_217_out, in_1[8]);
  not not_218 (not_218_out, in_1[11]);
  not not_219 (not_219_out, in_1[14]);
  not not_220 (not_220_out, in_1[15]);
  not not_221 (not_221_out, in_1[11]);
  not not_222 (not_222_out, in_1[14]);
  not not_223 (not_223_out, in_1[15]);
  not not_224 (not_224_out, in_1[9]);
  not not_225 (not_225_out, in_1[10]);
  not not_226 (not_226_out, in_1[14]);
  not not_227 (not_227_out, in_1[15]);
  not not_228 (not_228_out, in_1[8]);
  not not_229 (not_229_out, in_1[10]);
  not not_230 (not_230_out, in_1[14]);
  not not_231 (not_231_out, in_1[15]);
  not not_232 (not_232_out, in_1[8]);
  not not_233 (not_233_out, in_1[9]);
  not not_234 (not_234_out, in_1[14]);
  not not_235 (not_235_out, in_1[15]);
  not not_236 (not_236_out, in_1[9]);
  not not_237 (not_237_out, in_1[14]);
  not not_238 (not_238_out, in_1[15]);
  not not_239 (not_239_out, in_1[14]);
  not not_240 (not_240_out, in_1[15]);
  not not_241 (not_241_out, in_1[8]);
  not not_242 (not_242_out, in_1[9]);
  not not_243 (not_243_out, in_1[10]);
  not not_244 (not_244_out, in_1[11]);
  not not_245 (not_245_out, in_1[12]);
  not not_246 (not_246_out, in_1[13]);
  not not_247 (not_247_out, in_1[15]);
  not not_248 (not_248_out, in_1[8]);
  not not_249 (not_249_out, in_1[10]);
  not not_250 (not_250_out, in_1[11]);
  not not_251 (not_251_out, in_1[12]);
  not not_252 (not_252_out, in_1[13]);
  not not_253 (not_253_out, in_1[15]);
  not not_254 (not_254_out, in_1[10]);
  not not_255 (not_255_out, in_1[11]);
  not not_256 (not_256_out, in_1[12]);
  not not_257 (not_257_out, in_1[13]);
  not not_258 (not_258_out, in_1[15]);
  not not_259 (not_259_out, in_1[9]);
  not not_260 (not_260_out, in_1[11]);
  not not_261 (not_261_out, in_1[12]);
  not not_262 (not_262_out, in_1[13]);
  not not_263 (not_263_out, in_1[15]);
  not not_264 (not_264_out, in_1[8]);
  not not_265 (not_265_out, in_1[11]);
  not not_266 (not_266_out, in_1[12]);
  not not_267 (not_267_out, in_1[13]);
  not not_268 (not_268_out, in_1[15]);
  not not_269 (not_269_out, in_1[8]);
  not not_270 (not_270_out, in_1[9]);
  not not_271 (not_271_out, in_1[10]);
  not not_272 (not_272_out, in_1[12]);
  not not_273 (not_273_out, in_1[13]);
  not not_274 (not_274_out, in_1[15]);
  not not_275 (not_275_out, in_1[9]);
  not not_276 (not_276_out, in_1[10]);
  not not_277 (not_277_out, in_1[12]);
  not not_278 (not_278_out, in_1[13]);
  not not_279 (not_279_out, in_1[15]);
  not not_280 (not_280_out, in_1[10]);
  not not_281 (not_281_out, in_1[12]);
  not not_282 (not_282_out, in_1[13]);
  not not_283 (not_283_out, in_1[15]);
  not not_284 (not_284_out, in_1[8]);
  not not_285 (not_285_out, in_1[9]);
  not not_286 (not_286_out, in_1[12]);
  not not_287 (not_287_out, in_1[13]);
  not not_288 (not_288_out, in_1[15]);
  not not_289 (not_289_out, in_1[8]);
  not not_290 (not_290_out, in_1[12]);
  not not_291 (not_291_out, in_1[13]);
  not not_292 (not_292_out, in_1[15]);
  not not_293 (not_293_out, in_1[12]);
  not not_294 (not_294_out, in_1[13]);
  not not_295 (not_295_out, in_1[15]);
  not not_296 (not_296_out, in_1[9]);
  not not_297 (not_297_out, in_1[10]);
  not not_298 (not_298_out, in_1[11]);
  not not_299 (not_299_out, in_1[13]);
  not not_300 (not_300_out, in_1[15]);
  not not_301 (not_301_out, in_1[8]);
  not not_302 (not_302_out, in_1[10]);
  not not_303 (not_303_out, in_1[11]);
  not not_304 (not_304_out, in_1[13]);
  not not_305 (not_305_out, in_1[15]);
  not not_306 (not_306_out, in_1[8]);
  not not_307 (not_307_out, in_1[9]);
  not not_308 (not_308_out, in_1[10]);
  not not_309 (not_309_out, in_1[11]);
  not not_310 (not_310_out, in_1[12]);
  not not_311 (not_311_out, in_1[13]);
  not not_312 (not_312_out, in_1[14]);
  not not_313 (not_313_out, in_1[9]);
  not not_314 (not_314_out, in_1[10]);
  not not_315 (not_315_out, in_1[11]);
  not not_316 (not_316_out, in_1[12]);
  not not_317 (not_317_out, in_1[13]);
  not not_318 (not_318_out, in_1[14]);
  not not_319 (not_319_out, in_1[8]);
  not not_320 (not_320_out, in_1[10]);
  not not_321 (not_321_out, in_1[11]);
  not not_322 (not_322_out, in_1[12]);
  not not_323 (not_323_out, in_1[13]);
  not not_324 (not_324_out, in_1[14]);
  not not_325 (not_325_out, in_1[10]);
  not not_326 (not_326_out, in_1[11]);
  not not_327 (not_327_out, in_1[12]);
  not not_328 (not_328_out, in_1[13]);
  not not_329 (not_329_out, in_1[14]);
  not not_330 (not_330_out, in_1[8]);
  not not_331 (not_331_out, in_1[9]);
  not not_332 (not_332_out, in_1[11]);
  not not_333 (not_333_out, in_1[12]);
  not not_334 (not_334_out, in_1[13]);
  not not_335 (not_335_out, in_1[14]);
  not not_336 (not_336_out, in_1[9]);
  not not_337 (not_337_out, in_1[10]);
  not not_338 (not_338_out, in_1[12]);
  not not_339 (not_339_out, in_1[13]);
  not not_340 (not_340_out, in_1[14]);
  not not_341 (not_341_out, in_1[8]);
  not not_342 (not_342_out, in_1[10]);
  not not_343 (not_343_out, in_1[12]);
  not not_344 (not_344_out, in_1[13]);
  not not_345 (not_345_out, in_1[14]);
  not not_346 (not_346_out, in_1[10]);
  not not_347 (not_347_out, in_1[12]);
  not not_348 (not_348_out, in_1[13]);
  not not_349 (not_349_out, in_1[14]);
  not not_350 (not_350_out, in_1[8]);
  not not_351 (not_351_out, in_1[9]);
  not not_352 (not_352_out, in_1[10]);
  not not_353 (not_353_out, in_1[11]);
  not not_354 (not_354_out, in_1[12]);
  not not_355 (not_355_out, in_1[14]);
  not not_356 (not_356_out, in_1[8]);
  not not_357 (not_357_out, in_1[9]);
  not not_358 (not_358_out, in_1[10]);
  not not_359 (not_359_out, in_1[11]);
  not not_360 (not_360_out, in_1[14]);
  not not_361 (not_361_out, in_1[9]);
  not not_362 (not_362_out, in_1[10]);
  not not_363 (not_363_out, in_1[11]);
  not not_364 (not_364_out, in_1[14]);
  not not_365 (not_365_out, in_1[8]);
  not not_366 (not_366_out, in_1[10]);
  not not_367 (not_367_out, in_1[11]);
  not not_368 (not_368_out, in_1[14]);
  not not_369 (not_369_out, in_1[9]);
  not not_370 (not_370_out, in_1[10]);
  not not_371 (not_371_out, in_1[14]);
  not not_372 (not_372_out, in_1[10]);
  not not_373 (not_373_out, in_1[11]);
  not not_374 (not_374_out, in_1[14]);
  not not_375 (not_375_out, in_1[8]);
  not not_376 (not_376_out, in_1[9]);
  not not_377 (not_377_out, in_1[11]);
  not not_378 (not_378_out, in_1[14]);
  not not_379 (not_379_out, in_1[9]);
  not not_380 (not_380_out, in_1[11]);
  not not_381 (not_381_out, in_1[14]);
  not not_382 (not_382_out, in_1[8]);
  not not_383 (not_383_out, in_1[11]);
  not not_384 (not_384_out, in_1[14]);
  not not_385 (not_385_out, in_1[11]);
  not not_386 (not_386_out, in_1[14]);
  not not_387 (not_387_out, in_1[8]);
  not not_388 (not_388_out, in_1[9]);
  not not_389 (not_389_out, in_1[10]);
  not not_390 (not_390_out, in_1[14]);
  not not_391 (not_391_out, in_1[10]);
  not not_392 (not_392_out, in_1[14]);
  not not_393 (not_393_out, in_1[9]);
  not not_394 (not_394_out, in_1[14]);
  not not_395 (not_395_out, in_1[8]);
  not not_396 (not_396_out, in_1[14]);
  not not_397 (not_397_out, in_1[14]);
  not not_398 (not_398_out, in_1[8]);
  not not_399 (not_399_out, in_1[9]);
  not not_400 (not_400_out, in_1[10]);
  not not_401 (not_401_out, in_1[11]);
  not not_402 (not_402_out, in_1[12]);
  not not_403 (not_403_out, in_1[13]);
  not not_404 (not_404_out, in_1[8]);
  not not_405 (not_405_out, in_1[9]);
  not not_406 (not_406_out, in_1[11]);
  not not_407 (not_407_out, in_1[12]);
  not not_408 (not_408_out, in_1[13]);
  not not_409 (not_409_out, in_1[9]);
  not not_410 (not_410_out, in_1[11]);
  not not_411 (not_411_out, in_1[12]);
  not not_412 (not_412_out, in_1[13]);
  not not_413 (not_413_out, in_1[8]);
  not not_414 (not_414_out, in_1[11]);
  not not_415 (not_415_out, in_1[12]);
  not not_416 (not_416_out, in_1[13]);
  not not_417 (not_417_out, in_1[11]);
  not not_418 (not_418_out, in_1[12]);
  not not_419 (not_419_out, in_1[13]);
  not not_420 (not_420_out, in_1[8]);
  not not_421 (not_421_out, in_1[9]);
  not not_422 (not_422_out, in_1[10]);
  not not_423 (not_423_out, in_1[12]);
  not not_424 (not_424_out, in_1[13]);
  not not_425 (not_425_out, in_1[8]);
  not not_426 (not_426_out, in_1[9]);
  not not_427 (not_427_out, in_1[12]);
  not not_428 (not_428_out, in_1[13]);
  not not_429 (not_429_out, in_1[9]);
  not not_430 (not_430_out, in_1[12]);
  not not_431 (not_431_out, in_1[13]);
  not not_432 (not_432_out, in_1[8]);
  not not_433 (not_433_out, in_1[12]);
  not not_434 (not_434_out, in_1[13]);
  not not_435 (not_435_out, in_1[12]);
  not not_436 (not_436_out, in_1[13]);
  not not_437 (not_437_out, in_1[8]);
  not not_438 (not_438_out, in_1[9]);
  not not_439 (not_439_out, in_1[10]);
  not not_440 (not_440_out, in_1[11]);
  not not_441 (not_441_out, in_1[13]);
  not not_442 (not_442_out, in_1[8]);
  not not_443 (not_443_out, in_1[9]);
  not not_444 (not_444_out, in_1[10]);
  not not_445 (not_445_out, in_1[11]);
  not not_446 (not_446_out, in_1[12]);
  not not_447 (not_447_out, in_1[8]);
  not not_448 (not_448_out, in_1[9]);
  not not_449 (not_449_out, in_1[11]);
  not not_450 (not_450_out, in_1[12]);
  not not_451 (not_451_out, in_1[9]);
  not not_452 (not_452_out, in_1[11]);
  not not_453 (not_453_out, in_1[12]);
  not not_454 (not_454_out, in_1[8]);
  not not_455 (not_455_out, in_1[11]);
  not not_456 (not_456_out, in_1[12]);
  not not_457 (not_457_out, in_1[11]);
  not not_458 (not_458_out, in_1[12]);
  not not_459 (not_459_out, in_1[8]);
  and and_1 (add_ra__rb, not_1_out, not_2_out, not_3_out, not_4_out, not_5_out, not_6_out, not_7_out, not_8_out);
  and and_2 (shr_ra__imm4, in_1[8], not_9_out, not_10_out, not_11_out, not_12_out, not_13_out, not_14_out, not_15_out);
  and and_3 (shl_ra__imm4, not_16_out, in_1[9], not_17_out, not_18_out, not_19_out, not_20_out, not_21_out, not_22_out);
  and and_4 (flip_ra, in_1[8], in_1[9], not_23_out, not_24_out, not_25_out, not_26_out, not_27_out, not_28_out);
  and and_5 (and_ra__rb, not_29_out, not_30_out, in_1[10], not_31_out, not_32_out, not_33_out, not_34_out, not_35_out);
  and and_6 (or_ra__rb, in_1[8], not_36_out, in_1[10], not_37_out, not_38_out, not_39_out, not_40_out, not_41_out);
  and and_7 (xor_ra__rb, not_42_out, in_1[9], in_1[10], not_43_out, not_44_out, not_45_out, not_46_out, not_47_out);
  and and_8 (cmp_ra__rb, in_1[8], in_1[9], in_1[10], not_48_out, not_49_out, not_50_out, not_51_out, not_52_out);
  and and_9 (adc_ra__rb, not_53_out, not_54_out, not_55_out, in_1[11], not_56_out, not_57_out, not_58_out, not_59_out);
  and and_10 (sar_ra__imm4, in_1[8], not_60_out, not_61_out, in_1[11], not_62_out, not_63_out, not_64_out, not_65_out);
  and and_11 (subc_ra__rb, not_66_out, in_1[9], not_67_out, in_1[11], not_68_out, not_69_out, not_70_out, not_71_out);
  and and_12 (neg_ra, in_1[8], in_1[9], not_72_out, in_1[11], not_73_out, not_74_out, not_75_out, not_76_out);
  and and_13 (sub_ra__rb, not_77_out, not_78_out, in_1[10], in_1[11], not_79_out, not_80_out, not_81_out, not_82_out);
  and and_14 (mul_ra__rb, in_1[8], not_83_out, in_1[10], in_1[11], not_84_out, not_85_out, not_86_out, not_87_out);
  and and_15 (div_ra__rb, not_88_out, in_1[9], in_1[10], in_1[11], not_89_out, not_90_out, not_91_out, not_92_out);
  and and_16 (mod_ra__rb, in_1[8], in_1[9], in_1[10], in_1[11], not_93_out, not_94_out, not_95_out, not_96_out);
  and and_17 (mov_ra__imm16, not_97_out, not_98_out, not_99_out, not_100_out, in_1[12], not_101_out, not_102_out, not_103_out);
  and and_18 (mov_ra__byte__rb_imm16, in_1[8], not_104_out, not_105_out, not_106_out, in_1[12], not_107_out, not_108_out, not_109_out);
  and and_19 (mov_ra__word__rb_imm16, not_110_out, in_1[9], not_111_out, not_112_out, in_1[12], not_113_out, not_114_out, not_115_out);
  and and_20 (mov_ra__byte__rb, in_1[8], in_1[9], not_116_out, not_117_out, in_1[12], not_118_out, not_119_out, not_120_out);
  and and_21 (mov_ra__word__rb, not_121_out, not_122_out, in_1[10], not_123_out, in_1[12], not_124_out, not_125_out, not_126_out);
  and and_22 (xchg_ra__rb, in_1[8], not_127_out, in_1[10], not_128_out, in_1[12], not_129_out, not_130_out, not_131_out);
  and and_23 (mov_ra__rb, not_132_out, in_1[9], in_1[10], not_133_out, in_1[12], not_134_out, not_135_out, not_136_out);
  and and_24 (mov_word__ra_rb___imm16, in_1[8], in_1[9], in_1[10], not_137_out, in_1[12], not_138_out, not_139_out, not_140_out);
  and and_25 (mov_word__ra___rb, not_141_out, not_142_out, not_143_out, in_1[11], in_1[12], not_144_out, not_145_out, not_146_out);
  and and_26 (jmp_ra_imm16, in_1[8], not_147_out, not_148_out, not_149_out, not_150_out, in_1[13], not_151_out, not_152_out);
  and and_27 (jmp_ra_rb, not_153_out, in_1[9], not_154_out, not_155_out, not_156_out, in_1[13], not_157_out, not_158_out);
  and and_28 (ja_ra_imm16, not_159_out, not_160_out, in_1[10], not_161_out, not_162_out, in_1[13], not_163_out, not_164_out);
  and and_29 (ja_ra_rb, in_1[8], not_165_out, in_1[10], not_166_out, not_167_out, in_1[13], not_168_out, not_169_out);
  and and_30 (jna_ra_imm16, in_1[8], in_1[9], in_1[10], not_170_out, not_171_out, in_1[13], not_172_out, not_173_out);
  and and_31 (jna_ra_rb, not_174_out, not_175_out, not_176_out, in_1[11], not_177_out, in_1[13], not_178_out, not_179_out);
  and and_32 (jb_ra_imm16, not_180_out, in_1[9], not_181_out, in_1[11], not_182_out, in_1[13], not_183_out, not_184_out);
  and and_33 (jb_ra_rb, in_1[8], in_1[9], not_185_out, in_1[11], not_186_out, in_1[13], not_187_out, not_188_out);
  and and_34 (jnb_ra_imm16, in_1[8], not_189_out, in_1[10], in_1[11], not_190_out, in_1[13], not_191_out, not_192_out);
  and and_35 (jnb_ra_rb, not_193_out, in_1[9], in_1[10], in_1[11], not_194_out, in_1[13], not_195_out, not_196_out);
  and and_36 (jeq_ra_imm16, not_197_out, not_198_out, not_199_out, not_200_out, in_1[12], in_1[13], not_201_out, not_202_out);
  and and_37 (jeq_ra_rb, in_1[8], not_203_out, not_204_out, not_205_out, in_1[12], in_1[13], not_206_out, not_207_out);
  and and_38 (jneq_ra_imm16, in_1[8], in_1[9], not_208_out, not_209_out, in_1[12], in_1[13], not_210_out, not_211_out);
  and and_39 (jneq_ra_rb, not_212_out, not_213_out, in_1[10], not_214_out, in_1[12], in_1[13], not_215_out, not_216_out);
  and and_40 (jc_ra_imm16, not_217_out, in_1[9], in_1[10], not_218_out, in_1[12], in_1[13], not_219_out, not_220_out);
  and and_41 (jc_ra_rb, in_1[8], in_1[9], in_1[10], not_221_out, in_1[12], in_1[13], not_222_out, not_223_out);
  and and_42 (jnc_ra_imm16, in_1[8], not_224_out, not_225_out, in_1[11], in_1[12], in_1[13], not_226_out, not_227_out);
  and and_43 (jnc_ra_rb, not_228_out, in_1[9], not_229_out, in_1[11], in_1[12], in_1[13], not_230_out, not_231_out);
  and and_44 (jev_ra_imm16, not_232_out, not_233_out, in_1[10], in_1[11], in_1[12], in_1[13], not_234_out, not_235_out);
  and and_45 (jev_ra_rb, in_1[8], not_236_out, in_1[10], in_1[11], in_1[12], in_1[13], not_237_out, not_238_out);
  and and_46 (jnev_ra_imm16, in_1[8], in_1[9], in_1[10], in_1[11], in_1[12], in_1[13], not_239_out, not_240_out);
  and and_47 (jnev_ra_rb, not_241_out, not_242_out, not_243_out, not_244_out, not_245_out, not_246_out, in_1[14], not_247_out);
  and and_48 (jp_ra_imm16, not_248_out, in_1[9], not_249_out, not_250_out, not_251_out, not_252_out, in_1[14], not_253_out);
  and and_49 (jp_ra_rb, in_1[8], in_1[9], not_254_out, not_255_out, not_256_out, not_257_out, in_1[14], not_258_out);
  and and_50 (jnp_ra_imm16, in_1[8], not_259_out, in_1[10], not_260_out, not_261_out, not_262_out, in_1[14], not_263_out);
  and and_51 (jnp_ra_rb, not_264_out, in_1[9], in_1[10], not_265_out, not_266_out, not_267_out, in_1[14], not_268_out);
  and and_52 (jz_ra_imm16, not_269_out, not_270_out, not_271_out, in_1[11], not_272_out, not_273_out, in_1[14], not_274_out);
  and and_53 (jz_ra_rb, in_1[8], not_275_out, not_276_out, in_1[11], not_277_out, not_278_out, in_1[14], not_279_out);
  and and_54 (jnz_ra_imm16, in_1[8], in_1[9], not_280_out, in_1[11], not_281_out, not_282_out, in_1[14], not_283_out);
  and and_55 (jnz_ra_rb, not_284_out, not_285_out, in_1[10], in_1[11], not_286_out, not_287_out, in_1[14], not_288_out);
  and and_56 (jr_ra_imm16, not_289_out, in_1[9], in_1[10], in_1[11], not_290_out, not_291_out, in_1[14], not_292_out);
  and and_57 (jr_ra_rb, in_1[8], in_1[9], in_1[10], in_1[11], not_293_out, not_294_out, in_1[14], not_295_out);
  and and_58 (jnr_ra_imm16, in_1[8], not_296_out, not_297_out, not_298_out, in_1[12], not_299_out, in_1[14], not_300_out);
  and and_59 (jnr_ra_rb, not_301_out, in_1[9], not_302_out, not_303_out, in_1[12], not_304_out, in_1[14], not_305_out);
  and and_60 (push_ra, not_306_out, not_307_out, not_308_out, not_309_out, not_310_out, not_311_out, not_312_out, in_1[15]);
  and and_61 (pop_ra, in_1[8], not_313_out, not_314_out, not_315_out, not_316_out, not_317_out, not_318_out, in_1[15]);
  and and_62 (push_imm16, not_319_out, in_1[9], not_320_out, not_321_out, not_322_out, not_323_out, not_324_out, in_1[15]);
  and and_63 (push_byte__ra_rb, in_1[8], in_1[9], not_325_out, not_326_out, not_327_out, not_328_out, not_329_out, in_1[15]);
  and and_64 (push_word__ra_rb, not_330_out, not_331_out, in_1[10], not_332_out, not_333_out, not_334_out, not_335_out, in_1[15]);
  and and_65 (pop_byte__ra_rb, in_1[8], not_336_out, not_337_out, in_1[11], not_338_out, not_339_out, not_340_out, in_1[15]);
  and and_66 (pop_word__ra_rb, not_341_out, in_1[9], not_342_out, in_1[11], not_343_out, not_344_out, not_345_out, in_1[15]);
  and and_67 (pop0, in_1[8], in_1[9], not_346_out, in_1[11], not_347_out, not_348_out, not_349_out, in_1[15]);
  and and_68 (add_ra__byte__rb, not_350_out, not_351_out, not_352_out, not_353_out, not_354_out, in_1[13], not_355_out, in_1[15]);
  and and_69 (add_ra__word__rb, not_356_out, not_357_out, not_358_out, not_359_out, in_1[12], in_1[13], not_360_out, in_1[15]);
  and and_70 (shr_word__ra_rb___imm4, in_1[8], not_361_out, not_362_out, not_363_out, in_1[12], in_1[13], not_364_out, in_1[15]);
  and and_71 (shl_word__ra_rb___imm4, not_365_out, in_1[9], not_366_out, not_367_out, in_1[12], in_1[13], not_368_out, in_1[15]);
  and and_72 (sar_word__ra_rb___imm4, in_1[8], not_369_out, not_370_out, in_1[11], in_1[12], in_1[13], not_371_out, in_1[15]);
  and and_73 (flip_word__ra_rb, in_1[8], in_1[9], not_372_out, not_373_out, in_1[12], in_1[13], not_374_out, in_1[15]);
  and and_74 (and_ra__word__rb, not_375_out, not_376_out, in_1[10], not_377_out, in_1[12], in_1[13], not_378_out, in_1[15]);
  and and_75 (or_ra__word__rb, in_1[8], not_379_out, in_1[10], not_380_out, in_1[12], in_1[13], not_381_out, in_1[15]);
  and and_76 (xor_ra__word__rb, not_382_out, in_1[9], in_1[10], not_383_out, in_1[12], in_1[13], not_384_out, in_1[15]);
  and and_77 (cmp_ra__word__rb, in_1[8], in_1[9], in_1[10], not_385_out, in_1[12], in_1[13], not_386_out, in_1[15]);
  and and_78 (adc_ra__word__rb, not_387_out, not_388_out, not_389_out, in_1[11], in_1[12], in_1[13], not_390_out, in_1[15]);
  and and_79 (neg_word__ra_rb, in_1[8], in_1[9], not_391_out, in_1[11], in_1[12], in_1[13], not_392_out, in_1[15]);
  and and_80 (mul_ra__word__rb, in_1[8], not_393_out, in_1[10], in_1[11], in_1[12], in_1[13], not_394_out, in_1[15]);
  and and_81 (div_ra__word__rb, not_395_out, in_1[9], in_1[10], in_1[11], in_1[12], in_1[13], not_396_out, in_1[15]);
  and and_82 (mod_ra__word__rb, in_1[8], in_1[9], in_1[10], in_1[11], in_1[12], in_1[13], not_397_out, in_1[15]);
  and and_83 (add_ra__imm16, not_398_out, not_399_out, not_400_out, not_401_out, not_402_out, not_403_out, in_1[14], in_1[15]);
  and and_84 (and_ra__imm16, not_404_out, not_405_out, in_1[10], not_406_out, not_407_out, not_408_out, in_1[14], in_1[15]);
  and and_85 (or_ra__imm16, in_1[8], not_409_out, in_1[10], not_410_out, not_411_out, not_412_out, in_1[14], in_1[15]);
  and and_86 (xor_ra__imm16, not_413_out, in_1[9], in_1[10], not_414_out, not_415_out, not_416_out, in_1[14], in_1[15]);
  and and_87 (cmp_ra__imm16, in_1[8], in_1[9], in_1[10], not_417_out, not_418_out, not_419_out, in_1[14], in_1[15]);
  and and_88 (adc_ra__imm16, not_420_out, not_421_out, not_422_out, in_1[11], not_423_out, not_424_out, in_1[14], in_1[15]);
  and and_89 (sub_ra__imm16, not_425_out, not_426_out, in_1[10], in_1[11], not_427_out, not_428_out, in_1[14], in_1[15]);
  and and_90 (mul_ra__imm16, in_1[8], not_429_out, in_1[10], in_1[11], not_430_out, not_431_out, in_1[14], in_1[15]);
  and and_91 (div_ra__imm16, not_432_out, in_1[9], in_1[10], in_1[11], not_433_out, not_434_out, in_1[14], in_1[15]);
  and and_92 (mod_ra__imm16, in_1[8], in_1[9], in_1[10], in_1[11], not_435_out, not_436_out, in_1[14], in_1[15]);
  and and_93 (add_word__ra___rb, not_437_out, not_438_out, not_439_out, not_440_out, in_1[12], not_441_out, in_1[14], in_1[15]);
  and and_94 (add_word__ra_rb___imm16, not_442_out, not_443_out, not_444_out, not_445_out, not_446_out, in_1[13], in_1[14], in_1[15]);
  and and_95 (and_word__ra_rb___imm16, not_447_out, not_448_out, in_1[10], not_449_out, not_450_out, in_1[13], in_1[14], in_1[15]);
  and and_96 (or_word__ra_rb___imm16, in_1[8], not_451_out, in_1[10], not_452_out, not_453_out, in_1[13], in_1[14], in_1[15]);
  and and_97 (xor_word__ra_rb___imm16, not_454_out, in_1[9], in_1[10], not_455_out, not_456_out, in_1[13], in_1[14], in_1[15]);
  and and_98 (cmp_word__ra_rb___imm16, in_1[8], in_1[9], in_1[10], not_457_out, not_458_out, in_1[13], in_1[14], in_1[15]);
  and and_99 (nop, not_459_out, in_1[9], in_1[10], in_1[11], in_1[12], in_1[13], in_1[14], in_1[15]);
  not not_460 (not_above, in_7);
  not not_461 (not_below, in_8);
  not not_462 (not_equal, in_6);
  not not_463 (not_carry, in_5);
  not not_464 (not_even, in_10);
  not not_465 (not_positive, in_11);
  not not_466 (not_zero, in_9);
  not not_467 (not_reserved, in_13);
  _16_step_stepper u_16_step_stepper_1 (
    .in_1(n16_step_stepper_1_out_19), .in_2(in_2), .out_3(clock0), .out_4(clock1), .out_5(clock2),
    .out_6(clock3), .out_7(clock4), .out_8(clock5), .out_9(clock6), .out_10(clock7), .out_11(clock8),
    .out_12(clock9), .out_13(clock10), .out_14(clock11), .out_15(clock12), .out_16(clock13),
    .out_17(clock14), .out_18(clock15), .out_19(n16_step_stepper_1_out_19));
  and and_100 (and_100_out, clock9, push_imm16);
  or or_1 (or_1_out, shift_ra__imm4, shift_word__ra_rb___imm4);
  or or_2 (or_2_out, arith_ra__imm16, cmp_ra__imm16);
  or or_3 (or_3_out, arith_word__ra_rb___imm16, cmp_word__ra_rb___imm16);
  or or_4 (or_4_out, mov_ra__imm16, mov_word__ra_rb___imm16);
  or or_5 (or_5_out, mov_ra__byte__rb_imm16, mov_ra__word__rb_imm16);
  or or_6 (or_6_out, jump_ra_rb, jump_ra_imm16);
  or or_7 (or_7_out, shift_ra__imm4, shift_word__ra_rb___imm4);
  or or_8 (or_8_out, arith_ra__imm16, cmp_ra__imm16);
  or or_9 (or_9_out, arith_word__ra_rb___imm16, cmp_word__ra_rb___imm16);
  or or_10 (or_10_out, mov_ra__byte__rb_imm16, mov_ra__word__rb_imm16, mov_word__ra_rb___imm16);
  and and_101 (and_101_out, clock10, push_imm16);
  or or_11 (or_11_out, mov_ra__byte__rb, mov_ra__word__rb);
  or or_12 (or_12_out, add_ra__byte__rb, arith_word__ra_rb, arith_ra__word__rb, cmp_ra__word__rb);
  and and_102 (and_102_out, clock7, add_word__ra___rb);
  or or_13 (or_13_out, shift_ra__imm4, shift_word__ra_rb___imm4);
  or or_14 (or_14_out, mov_ra__imm16, mov_word__ra_rb___imm16);
  or or_15 (or_15_out, mov_ra__byte__rb_imm16, mov_ra__word__rb_imm16);
  or or_16 (or_16_out, arith_word__ra_rb___imm16, cmp_word__ra_rb___imm16);
  or or_17 (or_17_out, arith_ra__imm16, cmp_ra__imm16);
  or or_18 (or_18_out, pop_ra, pop_byte__ra_rb, pop_word__ra_rb);
  or or_19 (or_19_out, push_byte__ra_rb, push_word__ra_rb);
  or or_20 (or_20_out, or_19_out, or_21_out);
  or or_21 (or_21_out, mov_ra__byte__rb_imm16, mov_ra__word__rb_imm16);
  and and_103 (and_103_out, clock11, or_22_out);
  or or_22 (or_22_out, arith_word__ra_rb___imm16, cmp_word__ra_rb___imm16);
  and and_104 (and_104_out, clock13, push_imm16);
  and and_105 (and_105_out, clock6, mov_word__ra___rb);
  and and_106 (and_106_out, clock7, arith_word__ra_rb);
  and and_107 (and_107_out, clock8, add_word__ra___rb);
  and and_108 (and_108_out, clock11, or_23_out);
  or or_23 (or_23_out, pop_byte__ra_rb, pop_word__ra_rb, mov_word__ra_rb___imm16);
  and and_109 (and_109_out, clock12, or_24_out);
  or or_24 (or_24_out, push_byte__ra_rb, push_word__ra_rb, shift_word__ra_rb___imm4, arith_word__ra_rb___imm16);
  and and_110 (and_110_out, clock15, push_imm16);
  or or_25 (or_25_out, shift_ra__imm4, shift_word__ra_rb___imm4);
  or or_26 (or_26_out, arith_word__ra_rb___imm16, cmp_word__ra_rb___imm16);
  or or_27 (or_27_out, mov_ra__imm16, arith_ra__imm16, cmp_ra__imm16);
  or or_28 (or_28_out, mov_word__ra_rb___imm16, mov_ra__byte__rb_imm16, mov_ra__word__rb_imm16);
  and and_111 (and_111_out, clock6, add_ra__rb);
  and and_112 (and_112_out, clock7, or_29_out);
  or or_29 (or_29_out, add_word__ra___rb, add_ra__word__rb);
  and and_113 (and_113_out, clock8, add_ra__byte__rb);
  or or_30 (or_30_out, push_imm16, pop_word__ra_rb, mov_word__ra_rb___imm16);
  and and_114 (and_114_out, clock10, or_31_out);
  or or_31 (or_31_out, add_ra__imm16, push_word__ra_rb);
  and and_115 (and_115_out, clock11, add_word__ra_rb___imm16);
  and and_116 (and_116_out, clock13, push_imm16);
  or or_32 (or_32_out, pop, pop0);
  or or_33 (or_33_out, pop, pop0);
  and and_117 (and_117_out, clock6, sub_ra__rb);
  and and_118 (and_118_out, clock10, sub_ra__imm16);
  and and_119 (and_119_out, clock5, mov_ra__rb);
  and and_120 (and_120_out, clock6, or_34_out);
  or or_34 (or_34_out, mov_ra__byte__rb, mov_ra__word__rb);
  and and_121 (and_121_out, clock7, or_35_out);
  or or_35 (or_35_out, arith_ra, arith_ra__rb, xchg_ra__rb);
  and and_122 (and_122_out, clock8, or_36_out);
  or or_36 (or_36_out, mov_ra__byte__rb, arith_ra__word__rb);
  and and_123 (and_123_out, clock9, or_37_out);
  or or_37 (or_37_out, pop_ra, mov_ra__imm16, add_ra__byte__rb);
  and and_124 (and_124_out, clock10, or_38_out);
  or or_38 (or_38_out, mov_ra__byte__rb_imm16, mov_ra__word__rb_imm16);
  and and_125 (and_125_out, clock11, or_39_out);
  or or_39 (or_39_out, shift_ra__imm4, arith_ra__imm16);
  and and_126 (and_126_out, clock12, mov_ra__byte__rb_imm16);
  and and_127 (out_26, clock1, in_4);
  and and_128 (and_128_out, clock9, push_imm16);
  or or_40 (or_40_out, shift_ra__imm4, shift_word__ra_rb___imm4);
  or or_41 (or_41_out, arith_ra__imm16, cmp_ra__imm16);
  or or_42 (or_42_out, mov_ra__imm16, mov_word__ra_rb___imm16);
  or or_43 (or_43_out, mov_ra__byte__rb_imm16, mov_ra__word__rb_imm16);
  or or_44 (or_44_out, arith_word__ra_rb___imm16, cmp_word__ra_rb___imm16);
  or or_45 (or_45_out, pop0, pop);
  or or_46 (or_46_out, pop, pop0);
  or or_47 (or_47_out, arith_ra__imm16, cmp_ra__imm16);
  or or_48 (or_48_out, shift_ra__imm4, shift_word__ra_rb___imm4);
  and and_129 (and_129_out, clock6, or_49_out);
  or or_49 (or_49_out, arith_ra, arith_ra__rb, cmp_ra__rb, arith_word__ra_rb, adc_ra__word__rb);
  and and_130 (and_130_out, clock7, or_50_out);
  or or_50 (or_50_out, add_word__ra___rb, arith_ra__word__rb, cmp_ra__word__rb);
  and and_131 (and_131_out, clock8, add_ra__byte__rb);
  and and_132 (and_132_out, clock10, or_51_out);
  or or_51 (or_51_out, shift_ra__imm4, arith_ra__imm16, cmp_ra__imm16);
  and and_133 (and_133_out, clock11, or_52_out);
  or or_52 (or_52_out, shift_word__ra_rb___imm4, arith_word__ra_rb___imm16, cmp_word__ra_rb___imm16);
  and and_134 (and_134_out, clock6, or_53_out);
  or or_53 (or_53_out, or_11_out, or_12_out, jump_ra_imm16);
  and and_135 (and_135_out, clock9, or_54_out);
  or or_54 (or_54_out, or_13_out, or_14_out, or_15_out, or_16_out, or_17_out, or_18_out);
  and and_136 (and_136_out, clock10, or_20_out);
  and and_137 (and_137_out, clock10, push_ra);
  and and_138 (and_138_out, clock5, or_55_out);
  or or_55 (or_55_out, jump_ra_imm16, or_1_out, or_2_out, or_3_out, or_4_out, or_5_out);
  or or_56 (or_56_out, mov_ra__imm16, or_6_out, or_7_out, or_8_out, or_9_out, or_10_out);
  or or_57 (or_57_out, push, xchg_ra__rb, or_25_out, or_26_out, or_27_out, or_28_out);
  and and_139 (and_139_out, clock9, or_30_out);
  or or_58 (or_58_out, neg_ra, neg_word__ra_rb);
  and and_140 (and_140_out, clock5, or_33_out);
  or or_59 (or_59_out, and_140_out, and_117_out, and_118_out);
  and and_141 (and_141_out, clock6, mul_ra__rb);
  and and_142 (and_142_out, clock7, mul_ra__word__rb);
  and and_143 (and_143_out, clock10, mul_ra__imm16);
  and and_144 (and_144_out, clock6, div_ra__rb);
  and and_145 (and_145_out, clock7, div_ra__word__rb);
  or or_60 (or_60_out, and_144_out, and_145_out, and_146_out);
  and and_146 (and_146_out, clock10, div_ra__imm16);
  and and_147 (and_147_out, clock6, mod_ra__rb);
  or or_61 (or_61_out, and_147_out, and_148_out, and_149_out);
  and and_148 (and_148_out, clock7, mod_ra__word__rb);
  and and_149 (and_149_out, clock10, mod_ra__imm16);
  or or_62 (or_62_out, arith_word__ra_rb___imm16, cmp_word__ra_rb___imm16);
  or or_63 (or_63_out, mov_ra__imm16, mov_ra__byte__rb_imm16, mov_ra__word__rb_imm16, mov_word__ra_rb___imm16);
  or or_64 (or_64_out, clock0, and_100_out, and_138_out);
  or or_65 (or_65_out, clock2, and_150_out, and_101_out);
  and and_150 (and_150_out, clock6, or_56_out);
  and and_151 (and_151_out, clock5, or_57_out);
  and and_152 (and_152_out, clock6, in_3, cmp_ra__rb);
  and and_153 (and_153_out, clock7, in_3, cmp_ra__word__rb);
  and and_154 (and_154_out, clock10, in_3, cmp_ra__imm16);
  and and_155 (and_155_out, clock11, in_3, cmp_word__ra_rb___imm16);
  and and_156 (ALU_1010, clock7, in_3, or_32_out);
  and and_157 (and_157_out, clock6, or_58_out);
  and and_158 (ALU_1100, in_3, or_59_out);
  and and_159 (ALU_1101, in_3, or_66_out);
  or or_66 (or_66_out, and_141_out, and_142_out, and_143_out);
  and and_160 (ALU_1110, in_3, or_60_out);
  and and_161 (ALU_1111, in_3, or_61_out);
  or or_67 (or_67_out, or_40_out, or_41_out, or_42_out, or_43_out, or_44_out, or_45_out, push);
  or or_68 (or_68_out, push, or_46_out, or_47_out, or_48_out, or_62_out, or_63_out);
  or or_69 (or_69_out, and_129_out, and_130_out, and_131_out, and_132_out, and_133_out);
  or or_70 (or_70_out, and_105_out, and_106_out, and_107_out, and_137_out, and_108_out, and_109_out, and_110_out);
  or or_71 (ALU_0111, and_152_out, and_153_out, and_154_out, and_155_out);
  and and_162 (ALU_1011, in_3, and_157_out);
  or or_72 (or_72_out, and_119_out, and_120_out, and_121_out, and_122_out, and_123_out, and_124_out, and_125_out, and_126_out);
  and and_163 (and_163_out, clock9, push_imm16);
  and and_164 (and_164_out, clock5, or_68_out);
  and and_165 (out_25, in_4, or_70_out);
  and and_166 (load_IAR, in_3, or_64_out);
  and and_167 (set_IAR, in_4, or_65_out);
  or or_73 (or_73_out, clock0, and_151_out, and_111_out, and_112_out, and_113_out, and_139_out, and_114_out, and_115_out, and_116_out);
  and and_168 (and_168_out, clock5, or_67_out);
  and and_169 (out_22, in_4, or_69_out);
  or or_74 (or_74_out, clock1, and_134_out, and_102_out, and_135_out, and_136_out, and_103_out, and_104_out);
  and and_170 (store_ra, in_4, or_72_out);
  or or_75 (or_75_out, ALU_0000, no_ALU);
  assign {out_36, out_35, out_34, out_33} = or_75_out ? 4'b0000 : 4'bz;  // Controlled_Buffer controlled_buffer_1
  assign {out_36, out_35, out_34, out_33} = ALU_0001 ? 4'b0001 : 4'bz;  // Controlled_Buffer controlled_buffer_2
  assign {out_36, out_35, out_34, out_33} = ALU_0010 ? 4'b0010 : 4'bz;  // Controlled_Buffer controlled_buffer_3
  assign {out_36, out_35, out_34, out_33} = ALU_0011 ? 4'b0011 : 4'bz;  // Controlled_Buffer controlled_buffer_4
  assign {out_36, out_35, out_34, out_33} = ALU_0100 ? 4'b0100 : 4'bz;  // Controlled_Buffer controlled_buffer_5
  assign {out_36, out_35, out_34, out_33} = ALU_0101 ? 4'b0101 : 4'bz;  // Controlled_Buffer controlled_buffer_6
  assign {out_36, out_35, out_34, out_33} = ALU_0110 ? 4'b0110 : 4'bz;  // Controlled_Buffer controlled_buffer_7
  assign {out_36, out_35, out_34, out_33} = ALU_0111 ? 4'b0111 : 4'bz;  // Controlled_Buffer controlled_buffer_8
  assign {out_36, out_35, out_34, out_33} = ALU_1000 ? 4'b1000 : 4'bz;  // Controlled_Buffer controlled_buffer_9
  assign {out_36, out_35, out_34, out_33} = ALU_1001 ? 4'b1001 : 4'bz;  // Controlled_Buffer controlled_buffer_10
  assign {out_36, out_35, out_34, out_33} = ALU_1010 ? 4'b1010 : 4'bz;  // Controlled_Buffer controlled_buffer_11
  assign {out_36, out_35, out_34, out_33} = ALU_1011 ? 4'b1011 : 4'bz;  // Controlled_Buffer controlled_buffer_12
  assign {out_36, out_35, out_34, out_33} = ALU_1100 ? 4'b1100 : 4'bz;  // Controlled_Buffer controlled_buffer_13
  assign {out_36, out_35, out_34, out_33} = ALU_1101 ? 4'b1101 : 4'bz;  // Controlled_Buffer controlled_buffer_14
  assign {out_36, out_35, out_34, out_33} = ALU_1110 ? 4'b1110 : 4'bz;  // Controlled_Buffer controlled_buffer_15
  assign {out_36, out_35, out_34, out_33} = ALU_1111 ? 4'b1111 : 4'bz;  // Controlled_Buffer controlled_buffer_16
  or or_76 (or_76_out, clock0, and_128_out, and_168_out);
  or or_77 (or_77_out, clock0, and_163_out, and_164_out);
  and and_171 (out_24, in_3, or_74_out);
  and and_172 (ALU_0000, in_3, or_73_out);
  and and_173 (out_19, in_4, or_76_out);
  and and_174 (out_21, in_3, or_77_out);
  or or_78 (or_78_out, mov_ra__byte__rb_imm16, mov_ra__word__rb_imm16);
  or or_79 (or_79_out, flip_ra, flip_word__ra_rb);
  or or_80 (or_80_out, and_ra__rb, add_ra__byte__rb);
  or or_81 (or_81_out, mov_ra__byte__rb, and_ra__word__rb);
  or or_82 (or_82_out, and_ra__imm16, push_byte__ra_rb);
  or or_83 (or_83_out, mov_ra__byte__rb_imm16, and_word__ra_rb___imm16);
  and and_175 (sel_rb, clock9, in_3, or_78_out);
  and and_176 (store_rb, clock6, in_4, xchg_ra__rb);
  or or_84 (or_84_out, shift_ra__imm4, shift_word__ra_rb___imm4);
  or or_85 (or_85_out, arith_ra__imm16, cmp_ra__imm16);
  or or_86 (or_86_out, mov_ra__byte__rb_imm16, mov_ra__word__rb_imm16);
  or or_87 (or_87_out, arith_word__ra_rb___imm16, cmp_word__ra_rb___imm16);
  or or_88 (or_88_out, pop0, pop, push);
  or or_89 (or_89_out, xchg_ra__rb, mov_ra__imm16, mov_word__ra_rb___imm16);
  or or_90 (or_90_out, shift_ra__imm4, shift_word__ra_rb___imm4);
  or or_91 (or_91_out, arith_word__ra_rb___imm16, cmp_word__ra_rb___imm16);
  or or_92 (or_92_out, arith_ra__word__rb, cmp_ra__word__rb);
  or or_93 (or_93_out, arith_ra__imm16, cmp_ra__imm16);
  or or_94 (or_94_out, mov_ra__byte__rb, mov_ra__byte__rb_imm16, mov_ra__word__rb_imm16);
  or or_95 (or_95_out, add_word__ra___rb, mov_ra__imm16, mov_word__ra_rb___imm16);
  or or_96 (or_96_out, pop, pop0, push);
  or or_97 (or_97_out, push_imm16, pop_byte__ra_rb, pop_word__ra_rb);
  and and_177 (and_177_out, clock6, or_80_out);
  and and_178 (and_178_out, clock7, or_81_out);
  and and_179 (and_179_out, clock9, pop_byte__ra_rb);
  and and_180 (and_180_out, clock10, or_82_out);
  and and_181 (and_181_out, clock11, or_83_out);
  and and_182 (and_182_out, clock6, adc_ra__rb);
  or or_98 (or_98_out, arith_ra__imm16, cmp_ra__imm16);
  or or_99 (or_99_out, mov_ra__byte__rb_imm16, mov_ra__word__rb_imm16);
  or or_100 (or_100_out, shift_ra__imm4, shift_word__ra_rb___imm4);
  or or_101 (or_101_out, arith_word__ra_rb___imm16, cmp_word__ra_rb___imm16);
  or or_102 (or_102_out, mov_ra__imm16, mov_word__ra_rb___imm16, adc_ra__word__rb);
  and and_183 (and_183_out, clock10, adc_ra__imm16);
  and and_184 (and_184_out, clock11, push_imm16);
  and and_185 (and_185_out, clock5, jump_ra_rb);
  and and_186 (and_186_out, clock7, jump_ra_imm16);
  or or_103 (or_103_out, arith_ra__imm16, cmp_ra__imm16);
  or or_104 (or_104_out, arith_word__ra_rb___imm16, cmp_word__ra_rb___imm16);
  or or_105 (or_105_out, shift_ra__imm4, shift_word__ra_rb___imm4);
  and and_187 (and_187_out, clock12, push_imm16);
  and and_188 (and_188_out, clock6, or_106_out);
  or or_106 (or_106_out, arith_ra, arith_ra__rb, cmp_ra__rb, add_ra__byte__rb, arith_word__ra_rb);
  and and_189 (and_189_out, clock8, add_ra__byte__rb);
  and and_190 (and_190_out, clock10, or_107_out);
  or or_107 (or_107_out, shift_ra__imm4, arith_ra__imm16, cmp_ra__imm16, push_byte__ra_rb, push_word__ra_rb);
  and and_191 (and_191_out, clock11, or_108_out);
  or or_108 (or_108_out, push_imm16, shift_word__ra_rb___imm4, mov_ra__byte__rb_imm16, arith_word__ra_rb___imm16, cmp_word__ra_rb___imm16);
  and and_192 (and_192_out, clock13, push_imm16);
  and and_193 (and_193_out, clock6, or_79_out);
  or or_109 (or_109_out, and_177_out, and_178_out, and_179_out, and_180_out, and_181_out);
  and and_194 (and_194_out, clock9, push_imm16);
  or or_110 (or_110_out, shift_ra__imm4, shift_word__ra_rb___imm4);
  or or_111 (or_111_out, mov_ra__byte__rb_imm16, mov_ra__word__rb_imm16);
  or or_112 (or_112_out, arith_ra__imm16, cmp_ra__imm16, mov_ra__imm16);
  or or_113 (or_113_out, mov_word__ra_rb___imm16, cmp_word__ra_rb___imm16, arith_word__ra_rb___imm16);
  or or_114 (or_114_out, shift_ra__imm4, shift_word__ra_rb___imm4);
  or or_115 (or_115_out, arith_ra__imm16, cmp_ra__imm16);
  or or_116 (or_116_out, arith_word__ra_rb___imm16, cmp_word__ra_rb___imm16);
  or or_117 (or_117_out, mov_ra__byte__rb_imm16, mov_ra__word__rb_imm16);
  or or_118 (or_118_out, mov_ra__imm16, mov_word__ra_rb___imm16);
  and and_195 (and_195_out, clock11, push_imm16);
  or or_119 (or_119_out, mov_ra__imm16, mov_ra__byte__rb_imm16, mov_ra__word__rb_imm16, mov_word__ra_rb___imm16);
  and and_196 (and_196_out, clock9, or_120_out);
  or or_120 (or_120_out, mov_word__ra_rb___imm16, or_97_out);
  and and_197 (ALU_0011, in_3, and_193_out);
  or or_121 (or_121_out, or_114_out, or_115_out, or_116_out, or_117_out, or_118_out);
  and and_198 (and_198_out, clock8, or_122_out);
  or or_122 (or_122_out, or_103_out, or_104_out, or_105_out, or_119_out);
  nor nor_1 (no_ALU, ALU_0000, ALU_0001, ALU_0010, ALU_0011, ALU_0100, ALU_0101, ALU_0110, ALU_0111, ALU_1000, ALU_1001, ALU_1010, ALU_1011, ALU_1100, ALU_1101, ALU_1110, ALU_1111);
  or or_123 (or_123_out, or_84_out, or_85_out, or_86_out, or_87_out, or_88_out, or_89_out);
  or or_124 (or_124_out, or_90_out, or_91_out, or_92_out, or_93_out, or_94_out, or_95_out, or_96_out);
  and and_199 (and_199_out, clock10, in_3, shr_ra__imm4);
  and and_200 (and_200_out, clock11, in_3, shr_word__ra_rb___imm4);
  and and_201 (ALU_0100, in_3, or_109_out);
  and and_202 (and_202_out, clock7, or_125_out);
  or or_125 (or_125_out, push, or_98_out, or_99_out, or_100_out, or_101_out, or_102_out);
  and and_203 (and_203_out, clock5, or_126_out);
  or or_126 (or_126_out, or_110_out, or_111_out, or_112_out, or_113_out, jump_ra_imm16);
  and and_204 (and_204_out, clock7, or_121_out);
  or or_127 (or_127_out, mov_ra__imm16, mov_ra__word__rb);
  or or_128 (or_128_out, mov_word__ra___rb, mov_word__ra_rb___imm16);
  or or_129 (or_129_out, shift_ra__imm4, shift_word__ra_rb___imm4);
  or or_130 (or_130_out, arith_ra__imm16, cmp_ra__imm16);
  or or_131 (or_131_out, arith_ra__word__rb, cmp_ra__word__rb);
  or or_132 (or_132_out, arith_word__ra_rb, add_word__ra___rb);
  or or_133 (or_133_out, mov_ra__byte__rb_imm16, mov_ra__word__rb_imm16);
  or or_134 (or_134_out, push_ra, push_imm16);
  or or_135 (or_135_out, push_byte__ra_rb, push_word__ra_rb);
  or or_136 (or_136_out, pop_byte__ra_rb, pop_word__ra_rb);
  or or_137 (or_137_out, mov_word__ra_rb___imm16, shift_word__ra_rb___imm4);
  or or_138 (or_138_out, arith_word__ra_rb___imm16, cmp_word__ra_rb___imm16);
  and and_205 (and_205_out, clock11, or_139_out);
  or or_139 (or_139_out, push_byte__ra_rb, push_word__ra_rb);
  and and_206 (and_206_out, clock14, push_imm16);
  and and_207 (and_207_out, clock5, or_123_out);
  and and_208 (and_208_out, clock7, or_124_out);
  or or_140 (ALU_0001, and_199_out, and_200_out);
  or or_141 (or_141_out, clock0, and_194_out, and_203_out);
  or or_142 (or_142_out, clock3, and_204_out, and_195_out);
  and and_209 (and_209_out, sub_ra__rb, in_5);
  and and_210 (and_210_out, clock13, sub_ra__imm16, in_5);
  or or_143 (or_143_out, mov_ra__imm16, mov_ra__byte__rb_imm16, mov_ra__word__rb_imm16, mov_word__ra_rb___imm16);
  or or_144 (or_144_out, arith_word__ra_rb___imm16, cmp_word__ra_rb___imm16);
  or or_145 (or_145_out, shift_ra__imm4, shift_word__ra_rb___imm4);
  or or_146 (or_146_out, arith_ra__imm16, cmp_ra__imm16);
  or or_147 (or_147_out, pop, pop0);
  or or_148 (or_148_out, mov_ra__imm16, mov_ra__byte__rb_imm16, mov_ra__word__rb_imm16, mov_word__ra_rb___imm16);
  or or_149 (or_149_out, shift_ra__imm4, shift_word__ra_rb___imm4);
  or or_150 (or_150_out, arith_word__ra_rb___imm16, cmp_word__ra_rb___imm16);
  and and_211 (and_211_out, clock6, adc_ra__word__rb);
  and and_212 (and_212_out, clock9, or_151_out);
  or or_151 (or_151_out, push_imm16, adc_ra__imm16);
  or or_152 (or_152_out, mov_ra__imm16, arith_ra__imm16, arith_word__ra_rb___imm16, cmp_word__ra_rb___imm16);
  or or_153 (or_153_out, pop, pop0, push);
  or or_154 (or_154_out, arith_word__ra_rb___imm16, cmp_word__ra_rb___imm16);
  or or_155 (or_155_out, mov_ra__byte__rb_imm16, mov_ra__word__rb_imm16);
  or or_156 (or_156_out, mov_ra__byte__rb, add_ra__byte__rb);
  or or_157 (or_157_out, or_133_out, or_134_out, or_135_out);
  and and_213 (and_213_out, clock10, or_158_out);
  or or_158 (or_158_out, or_136_out, or_137_out, or_138_out);
  and and_214 (sel_cs, in_3, or_141_out);
  or or_159 (or_159_out, clock4, and_185_out, and_186_out, and_198_out, and_187_out);
  and and_215 (and_215_out, clock9, or_160_out);
  or or_160 (or_160_out, and_209_out, push_imm16);
  or or_161 (or_161_out, arith_ra__imm16, cmp_ra__imm16);
  or or_162 (or_162_out, pop, pop0);
  or or_163 (or_163_out, shift_ra__imm4, shift_word__ra_rb___imm4);
  or or_164 (or_164_out, adc_ra__rb, cmp_ra__imm16);
  or or_165 (or_165_out, mov_ra__byte__rb_imm16, mov_ra__word__rb_imm16, mov_word__ra_rb___imm16);
  and and_216 (and_216_out, clock9, or_157_out);
  and and_217 (load_cs, in_3, or_142_out);
  or or_166 (or_166_out, or_163_out, or_164_out, or_165_out, or_152_out, or_153_out);
  and and_218 (and_218_out, clock5, or_167_out);
  or or_167 (or_167_out, or_127_out, or_128_out, or_129_out, or_130_out, or_131_out, or_132_out, or_154_out, or_155_out, or_156_out, jump_ra_imm16, pop);
  or or_168 (or_168_out, clock3, and_182_out, and_202_out, and_183_out, and_184_out);
  and and_219 (store_cs, in_4, or_159_out);
  or or_169 (or_169_out, or_143_out, or_144_out, or_145_out, or_146_out, or_147_out, push);
  or or_170 (or_170_out, or_148_out, or_149_out, or_150_out, or_161_out, or_162_out, push);
  and and_220 (and_220_out, clock5, or_166_out);
  and and_221 (out_29, ~in_1[0], ~in_1[1], ~in_1[2], ~in_1[3], ~in_1[4], ~in_1[5], ~in_1[6], ~in_1[7], in_1[8], in_1[9], in_1[10], in_1[11], in_1[12], in_1[13], in_1[14], in_1[15]);  // AND_Gate
  and and_222 (and_222_out, clock5, xchg_ra__rb);
  and and_223 (and_223_out, clock9, or_171_out);
  or or_171 (or_171_out, pop_word__ra_rb, mov_word__ra_rb___imm16);
  and and_224 (and_224_out, clock10, push_word__ra_rb);
  and and_225 (and_225_out, clock11, push_imm16);
  and and_226 (and_226_out, clock13, push_imm16);
  and and_227 (and_227_out, clock7, or_170_out);
  or or_172 (or_172_out, clock0, clock3, and_207_out, and_188_out, and_208_out, and_189_out, and_196_out, and_190_out, and_191_out, and_192_out);
  and and_228 (ALU_1000, in_3, or_168_out);
  and and_229 (and_229_out, clock5, or_169_out);
  and and_230 (out_23, in_4, or_173_out);
  or or_173 (or_173_out, clock0, and_218_out, and_216_out, and_213_out, and_205_out, and_206_out);
  and and_231 (and_231_out, clock10, in_3, shl_ra__imm4);
  and and_232 (and_232_out, clock11, in_3, shl_word__ra_rb___imm4);
  and and_233 (and_233_out, clock6, in_3, or_ra__rb);
  and and_234 (and_234_out, clock7, in_3, or_ra__word__rb);
  and and_235 (and_235_out, clock10, in_3, or_ra__imm16);
  and and_236 (and_236_out, clock11, in_3, or_word__ra_rb___imm16);
  and and_237 (and_237_out, clock6, in_3, xor_ra__rb);
  and and_238 (and_238_out, clock7, in_3, xor_ra__word__rb);
  and and_239 (and_239_out, clock10, in_3, xor_ra__imm16);
  and and_240 (and_240_out, clock11, in_3, xor_word__ra_rb___imm16);
  and and_241 (and_241_out, clock10, sar_ra__imm4);
  and and_242 (and_242_out, clock11, sar_word__ra_rb___imm4);
  or or_174 (or_174_out, clock0, and_215_out, and_210_out, and_229_out);
  or or_175 (or_175_out, clock0, and_211_out, and_212_out, and_220_out);
  and and_243 (out_28, in_4, or_172_out);
  or or_176 (ALU_0010, and_231_out, and_232_out);
  or or_177 (ALU_0101, and_233_out, and_234_out, and_235_out, and_236_out);
  or or_178 (ALU_0110, and_237_out, and_238_out, and_239_out, and_240_out);
  or or_179 (or_179_out, and_241_out, and_242_out);
  and and_244 (and_244_out, clock5, arith_word__ra_rb);
  and and_245 (and_245_out, clock9, or_180_out);
  or or_180 (or_180_out, push_byte__ra_rb, push_word__ra_rb);
  or or_181 (or_181_out, mov_word__ra_rb___imm16, shift_word__ra_rb___imm4);
  or or_182 (or_182_out, arith_word__ra_rb___imm16, cmp_word__ra_rb___imm16);
  or or_183 (or_183_out, or_181_out, or_182_out, or_184_out);
  or or_184 (or_184_out, pop_byte__ra_rb, pop_word__ra_rb);
  or or_185 (or_185_out, add_word__ra___rb, mov_word__ra___rb, jump_ra_rb);
  or or_186 (or_186_out, arith_ra, arith_ra__rb, cmp_ra__rb, xchg_ra__rb);
  or or_187 (or_187_out, mov_ra__byte__rb, arith_ra__word__rb, cmp_ra__word__rb, jump_ra_imm16);
  or or_188 (or_188_out, shift_ra__imm4, arith_ra__imm16, cmp_ra__imm16, push_ra);
  or or_189 (or_189_out, shift_word__ra_rb___imm4, mov_ra__byte__rb_imm16);
  and and_246 (and_246_out, clock12, sub_ra__imm16, in_5);
  and and_247 (ALU_1001, in_3, or_179_out);
  or or_190 (or_190_out, and_244_out, and_245_out, and_248_out);
  and and_248 (and_248_out, clock10, or_183_out);
  and and_249 (and_249_out, clock5, or_185_out);
  and and_250 (and_250_out, clock6, or_186_out);
  and and_251 (and_251_out, clock7, or_187_out);
  and and_252 (and_252_out, clock8, add_ra__byte__rb);
  and and_253 (and_253_out, clock10, or_188_out);
  and and_254 (and_254_out, clock11, or_189_out);
  and and_255 (out_14, in_3, or_174_out);
  and and_256 (out_18, in_4, or_175_out);
  or or_191 (or_191_out, clock3, and_222_out, and_223_out, and_224_out, and_225_out, and_226_out, and_227_out);
  or or_192 (or_192_out, mov_ra__byte__rb, mov_ra__word__rb);
  or or_193 (or_193_out, arith_ra__rb, xchg_ra__rb, cmp_ra__rb, mov_ra__rb);
  or or_194 (or_194_out, add_ra__byte__rb, arith_word__ra_rb, arith_ra__word__rb, cmp_ra__word__rb);
  and and_257 (and_257_out, clock6, or_195_out);
  or or_195 (or_195_out, jump_ra_rb, mov_word__ra___rb, add_word__ra___rb);
  and and_258 (and_258_out, clock9, or_196_out);
  or or_196 (or_196_out, push_byte__ra_rb, push_word__ra_rb);
  or or_197 (or_197_out, pop_byte__ra_rb, pop_word__ra_rb);
  or or_198 (or_198_out, or_197_out, or_199_out);
  or or_199 (or_199_out, shift_word__ra_rb___imm4, mov_word__ra_rb___imm16, arith_word__ra_rb___imm16, cmp_word__ra_rb___imm16);
  and and_259 (and_259_out, clock5, pop);
  and and_260 (and_260_out, clock9, push_ra);
  and and_261 (and_261_out, clock11, or_200_out);
  or or_200 (or_200_out, push_byte__ra_rb, push_word__ra_rb);
  and and_262 (and_262_out, clock14, push_imm16);
  or or_201 (or_201_out, push, pop, pop0);
  or or_202 (or_202_out, push, pop, pop0);
  and and_263 (sel_ra, in_3, or_190_out);
  and and_264 (and_264_out, clock6, add_ra__byte__rb);
  and and_265 (and_265_out, clock7, mov_ra__byte__rb);
  and and_266 (and_266_out, clock9, pop_byte__ra_rb);
  and and_267 (and_267_out, clock10, push_byte__ra_rb);
  and and_268 (and_268_out, clock11, mov_ra__byte__rb_imm16);
  and and_269 (out_15, in_3, or_191_out);
  or or_203 (or_203_out, shift_ra__imm4, shift_word__ra_rb___imm4);
  or or_204 (or_204_out, arith_word__ra_rb___imm16, cmp_word__ra_rb___imm16);
  or or_205 (or_205_out, xchg_ra__rb, add_ra__byte__rb);
  or or_206 (or_206_out, mov_ra__imm16, mov_ra__byte__rb);
  or or_207 (or_207_out, mov_ra__byte__rb_imm16, mov_ra__word__rb_imm16);
  or or_208 (or_208_out, arith_ra__word__rb, add_word__ra___rb);
  or or_209 (or_209_out, arith_ra__imm16, cmp_ra__imm16);
  or or_210 (or_210_out, shift_ra__imm4, shift_word__ra_rb___imm4);
  and and_270 (and_270_out, clock10, push_imm16);
  and and_271 (and_271_out, clock5, or_211_out);
  or or_211 (or_211_out, or_192_out, or_193_out, or_194_out);
  and and_272 (and_272_out, clock10, or_198_out);
  or or_212 (or_212_out, mov_ra__byte__rb, mov_ra__word__rb, mov_word__ra___rb);
  or or_213 (or_213_out, or_212_out, or_214_out);
  or or_214 (or_214_out, arith_ra__word__rb, cmp_ra__word__rb, add_ra__byte__rb, add_word__ra___rb);
  or or_215 (or_215_out, and_249_out, and_250_out, and_251_out, and_252_out, and_253_out, and_254_out, and_246_out);
  or or_216 (or_216_out, and_264_out, and_265_out, and_266_out, and_267_out, and_268_out);
  or or_217 (or_217_out, arith_ra__imm16, cmp_ra__imm16);
  or or_218 (or_218_out, arith_word__ra_rb___imm16, cmp_word__ra_rb___imm16);
  or or_219 (or_219_out, shift_ra__imm4, shift_word__ra_rb___imm4);
  or or_220 (or_220_out, arith_ra__imm16, cmp_ra__imm16, mov_ra__imm16);
  or or_221 (or_221_out, mov_word__ra_rb___imm16, mov_ra__byte__rb_imm16, mov_ra__word__rb_imm16);
  or or_222 (or_222_out, pop, pop0, push);
  and and_273 (and_273_out, clock7, or_223_out);
  or or_223 (or_223_out, or_205_out, or_224_out);
  or or_224 (or_224_out, arith_ra, arith_ra__rb, arith_word__ra_rb);
  or or_225 (or_225_out, mov_word__ra_rb___imm16, arith_word__ra_rb___imm16, cmp_word__ra_rb___imm16);
  or or_226 (or_226_out, push, pop, pop0);
  and and_274 (and_274_out, clock11, or_227_out);
  or or_227 (or_227_out, shift_ra__imm4, pop_byte__ra_rb, pop_word__ra_rb, arith_ra__imm16, mov_word__ra_rb___imm16);
  or or_228 (or_228_out, push_imm16, push_byte__ra_rb, push_word__ra_rb);
  or or_229 (or_229_out, or_228_out, or_230_out);
  or or_230 (or_230_out, mov_ra__byte__rb_imm16, arith_word__ra_rb___imm16, shift_word__ra_rb___imm4);
  and and_275 (and_275_out, clock15, push_imm16);
  and and_276 (and_276_out, clock5, or_213_out);
  or or_231 (or_231_out, and_259_out, and_260_out, and_261_out, and_262_out);
  and and_277 (load_ss, clock7, in_3, or_201_out);
  or or_232 (or_232_out, pop, pop0, push);
  and and_278 (and_278_out, clock9, push_ra);
  and and_279 (and_279_out, clock11, or_233_out);
  or or_233 (or_233_out, push_byte__ra_rb, push_word__ra_rb);
  and and_280 (and_280_out, clock14, push_imm16);
  and and_281 (load_ra, in_3, or_215_out);
  or or_234 (or_234_out, add_word__ra___rb, arith_ra__word__rb, cmp_ra__word__rb);
  or or_235 (or_235_out, arith_ra__rb, cmp_ra__rb);
  or or_236 (or_236_out, or_217_out, or_218_out, or_219_out);
  and and_282 (and_282_out, clock5, adc_ra__rb);
  or or_237 (or_237_out, and_282_out, and_283_out);
  and and_283 (and_283_out, clock9, adc_ra__imm16);
  and and_284 (and_284_out, clock9, add_ra__byte__rb);
  and and_285 (and_285_out, clock12, or_229_out);
  or or_238 (or_238_out, and_271_out, and_257_out, and_258_out, and_272_out);
  and and_286 (sel_ss, in_3, or_231_out);
  and and_287 (store_ss, clock8, in_4, or_202_out);
  and and_288 (and_288_out, clock5, or_232_out);
  or or_239 (or_239_out, push, pop, pop0);
  and and_289 (out_16, in_3, or_216_out);
  and and_290 (and_290_out, clock6, or_234_out);
  and and_291 (and_291_out, clock5, or_235_out);
  and and_292 (and_292_out, clock7, add_ra__byte__rb);
  and and_293 (and_293_out, clock9, or_236_out);
  and and_294 (out_20, in_3, or_237_out);
  and and_295 (and_295_out, clock6, or_240_out);
  or or_240 (or_240_out, or_203_out, or_204_out, or_220_out, or_221_out, or_222_out);
  and and_296 (and_296_out, clock8, or_241_out);
  or or_241 (or_241_out, or_206_out, or_207_out, or_208_out, or_209_out, or_210_out, or_225_out, or_226_out);
  and and_297 (sel_ds, in_3, and_276_out);
  or or_242 (or_242_out, and_288_out, and_278_out, and_279_out, and_280_out);
  or or_243 (or_243_out, and_290_out, and_291_out, and_292_out, and_293_out);
  and and_298 (load_rb, in_3, or_238_out);
  and and_299 (store_rb, clock6, in_4, xchg_ra__rb);
  and and_300 (store_sp, clock6, in_4, or_239_out);
  and and_301 (load_sp, in_3, or_242_out);
  or or_244 (or_244_out, clock2, clock4, and_295_out, and_273_out, and_296_out, and_284_out, and_270_out, and_274_out, and_285_out, and_275_out);
  and and_302 (out_17, in_4, or_243_out);
  and and_303 (out_27, in_3, or_244_out);
  or or_245 (load_register[0], ra_load_r0, rb_load_r0);
  or or_246 (load_register[1], ra_load_r1, rb_load_r1);
  or or_247 (load_register[2], ra_load_r2, rb_load_r2);
  or or_248 (load_register[3], ra_load_r3, rb_load_r3);
  or or_249 (load_register[4], ra_load_r4, rb_load_r4);
  or or_250 (load_register[5], ra_load_r5, rb_load_r5);
  or or_251 (load_register[6], ra_load_r6, rb_load_r6);
  or or_252 (load_register[7], ra_load_r7, rb_load_r7);
  or or_253 (load_register[8], ra_load_r8, load_ss, rb_load_r8);
  or or_254 (load_register[9], ra_load_r9, load_cs, rb_load_r9);
  or or_255 (load_register[10], ra_load_r10, rb_load_r10);
  or or_256 (load_register[11], ra_load_r11, rb_load_r11);
  or or_257 (load_register[12], ra_load_r12, rb_load_r12);
  or or_258 (load_register[13], ra_load_r13, load_sp, rb_load_r13);
  or or_259 (load_register[14], ra_load_r14, rb_load_r14);
  or or_260 (load_register[15], ra_load_r15, load_IAR, rb_load_r15);
  or or_261 (store_register[0], ra_store_r0, rb_store_r0);
  or or_262 (store_register[1], ra_store_r1, rb_store_r1);
  or or_263 (store_register[2], ra_store_r2, rb_store_r2);
  or or_264 (store_register[3], ra_store_r3, rb_store_r3);
  or or_265 (store_register[4], ra_store_r4, rb_store_r4);
  or or_266 (store_register[5], ra_store_r5, rb_store_r5);
  or or_267 (store_register[6], ra_store_r6, rb_store_r6);
  or or_268 (store_register[7], ra_store_r7, rb_store_r7);
  or or_269 (store_register[8], ra_store_r8, store_ss, rb_store_r8);
  or or_270 (store_register[9], ra_store_r9, store_cs, rb_store_r9);
  or or_271 (store_register[10], ra_store_r10, rb_store_r10);
  or or_272 (store_register[11], ra_store_r11, rb_store_r11);
  or or_273 (store_register[12], ra_store_r12, rb_store_r12);
  or or_274 (store_register[13], ra_store_r13, store_sp, rb_store_r13);
  or or_275 (store_register[14], ra_store_r14, rb_store_r14);
  or or_276 (store_register[15], ra_store_r15, set_IAR, rb_store_r15);
  or or_277 (select_register[0], ra_sel_r0, rb_sel_r0);
  or or_278 (select_register[1], ra_sel_r1, rb_sel_r1);
  or or_279 (select_register[2], ra_sel_r2, rb_sel_r2);
  or or_280 (select_register[3], ra_sel_r3, rb_sel_r3);
  or or_281 (select_register[4], ra_sel_r4, rb_sel_r4);
  or or_282 (select_register[5], ra_sel_r5, rb_sel_r5);
  or or_283 (select_register[6], ra_sel_r6, rb_sel_r6);
  or or_284 (select_register[7], ra_sel_r7, rb_sel_r7);
  or or_285 (select_register[8], ra_sel_r8, sel_ss, rb_sel_r8);
  or or_286 (select_register[9], ra_sel_r9, sel_cs, rb_sel_r9);
  or or_287 (select_register[10], ra_sel_r10, sel_ds, rb_sel_r10);
  or or_288 (select_register[11], ra_sel_r11, rb_sel_r11);
  or or_289 (select_register[12], ra_sel_r12, rb_sel_r12);
  or or_290 (select_register[13], ra_sel_r13, rb_sel_r13);
  or or_291 (select_register[14], ra_sel_r14, rb_sel_r14);
  or or_292 (select_register[15], ra_sel_r15, rb_sel_r15);
  and and_304 (and_304_out, ja_ra_imm16, in_7);
  and and_305 (and_305_out, jna_ra_imm16, not_above);
  and and_306 (and_306_out, jb_ra_imm16, in_8);
  and and_307 (and_307_out, jnb_ra_imm16, not_below);
  and and_308 (and_308_out, jeq_ra_imm16, in_6);
  and and_309 (and_309_out, jneq_ra_imm16, not_equal);
  and and_310 (and_310_out, jc_ra_imm16, in_5);
  and and_311 (and_311_out, jnc_ra_imm16, not_carry);
  and and_312 (and_312_out, jev_ra_imm16, in_10);
  and and_313 (and_313_out, jnev_ra_imm16, not_even);
  and and_314 (and_314_out, jp_ra_imm16, in_11);
  and and_315 (and_315_out, jnp_ra_imm16, not_positive);
  and and_316 (and_316_out, jz_ra_imm16, in_9);
  and and_317 (and_317_out, jnz_ra_imm16, not_zero);
  and and_318 (and_318_out, jr_ra_imm16, in_13);
  and and_319 (and_319_out, jnr_ra_imm16, not_reserved);
  and and_320 (and_320_out, ja_ra_rb, in_7);
  and and_321 (and_321_out, jna_ra_rb, not_above);
  and and_322 (and_322_out, jb_ra_rb, in_8);
  and and_323 (and_323_out, jnb_ra_rb, not_below);
  and and_324 (and_324_out, jeq_ra_rb, in_6);
  and and_325 (and_325_out, jneq_ra_rb, not_equal);
  and and_326 (and_326_out, jc_ra_rb, in_5);
  and and_327 (and_327_out, jnc_ra_rb, not_carry);
  and and_328 (and_328_out, jev_ra_rb, in_10);
  and and_329 (and_329_out, jnev_ra_rb, not_even);
  and and_330 (and_330_out, jp_ra_rb, in_11);
  and and_331 (and_331_out, jnp_ra_rb, not_positive);
  and and_332 (and_332_out, jz_ra_rb, in_9);
  and and_333 (and_333_out, jnz_ra_rb, not_zero);
  and and_334 (and_334_out, jr_ra_rb, in_13);
  and and_335 (and_335_out, jnr_ra_rb, not_reserved);
  and and_336 (jump, jump_ra_rb, jump_ra_imm16);
  or or_293 (or_293_out, and_304_out, and_305_out, and_306_out, and_307_out);
  or or_294 (or_294_out, and_308_out, and_309_out, and_310_out, and_311_out);
  or or_295 (or_295_out, and_312_out, and_313_out, and_314_out, and_315_out);
  or or_296 (or_296_out, and_316_out, and_317_out, and_318_out, and_319_out);
  or or_297 (or_297_out, and_320_out, and_321_out, and_322_out, and_323_out);
  or or_298 (or_298_out, and_324_out, and_325_out, and_326_out, and_327_out);
  or or_299 (or_299_out, and_328_out, and_329_out, and_330_out, and_331_out);
  or or_300 (or_300_out, and_332_out, and_333_out, and_334_out, and_335_out);
  or or_301 (pop, pop_ra, pop_byte__ra_rb, pop_word__ra_rb);
  or or_302 (push, push_ra, push_imm16, push_byte__ra_rb, push_word__ra_rb);
  or or_303 (jump_ra_imm16, jmp_ra_imm16, or_293_out, or_294_out, or_295_out, or_296_out);
  or or_304 (jump_ra_rb, jmp_ra_rb, or_297_out, or_298_out, or_299_out, or_300_out);
  or or_305 (shift_word__ra_rb___imm4, shr_word__ra_rb___imm4, shl_word__ra_rb___imm4, sar_word__ra_rb___imm4);
  or or_306 (shift_ra__imm4, shr_ra__imm4, shl_ra__imm4, sar_ra__imm4);
  or or_307 (arith_word__ra_rb___imm16, add_word__ra_rb___imm16, and_word__ra_rb___imm16, or_word__ra_rb___imm16, xor_word__ra_rb___imm16);
  or or_308 (arith_ra__imm16, add_ra__imm16, and_ra__imm16, or_ra__imm16, xor_ra__imm16, mul_ra__imm16, div_ra__imm16, mod_ra__imm16, adc_ra__imm16, sub_ra__imm16);
  or or_309 (arith_ra__word__rb, add_ra__word__rb, and_ra__word__rb, or_ra__word__rb, xor_ra__word__rb, adc_ra__word__rb, mul_ra__word__rb, div_ra__word__rb, mod_ra__word__rb);
  or or_310 (arith_ra__rb, add_ra__rb, and_ra__rb, or_ra__rb, xor_ra__rb, mul_ra__rb, div_ra__rb, mod_ra__rb, adc_ra__rb, sub_ra__rb);
  _4x16_decoder u_4x16_decoder_1 (
    .in_1(in_1[3]), .in_2(in_1[2]), .in_3(in_1[1]), .in_4(in_1[0]), ._0000(n4x16_decoder_1__0000),
    ._0001(n4x16_decoder_1__0001), ._0010(n4x16_decoder_1__0010), ._0011(n4x16_decoder_1__0011),
    ._0100(n4x16_decoder_1__0100), ._0101(n4x16_decoder_1__0101), ._0110(n4x16_decoder_1__0110),
    ._0111(n4x16_decoder_1__0111), ._1000(n4x16_decoder_1__1000), ._1001(n4x16_decoder_1__1001),
    ._1010(n4x16_decoder_1__1010), ._1011(n4x16_decoder_1__1011), ._1100(n4x16_decoder_1__1100),
    ._1101(n4x16_decoder_1__1101), ._1110(n4x16_decoder_1__1110), ._1111(n4x16_decoder_1__1111));
  _4x16_decoder u_4x16_decoder_2 (
    .in_1(in_1[7]), .in_2(in_1[6]), .in_3(in_1[5]), .in_4(in_1[4]), ._0000(n4x16_decoder_2__0000),
    ._0001(n4x16_decoder_2__0001), ._0010(n4x16_decoder_2__0010), ._0011(n4x16_decoder_2__0011),
    ._0100(n4x16_decoder_2__0100), ._0101(n4x16_decoder_2__0101), ._0110(n4x16_decoder_2__0110),
    ._0111(n4x16_decoder_2__0111), ._1000(n4x16_decoder_2__1000), ._1001(n4x16_decoder_2__1001),
    ._1010(n4x16_decoder_2__1010), ._1011(n4x16_decoder_2__1011), ._1100(n4x16_decoder_2__1100),
    ._1101(n4x16_decoder_2__1101), ._1110(n4x16_decoder_2__1110), ._1111(n4x16_decoder_2__1111));
  and and_337 (rb_store_r0, n4x16_decoder_1__0000, store_rb);
  and and_338 (rb_store_r1, n4x16_decoder_1__0001, store_rb);
  and and_339 (rb_store_r2, n4x16_decoder_1__0010, store_rb);
  and and_340 (rb_store_r3, n4x16_decoder_1__0011, store_rb);
  and and_341 (rb_store_r4, n4x16_decoder_1__0100, store_rb);
  and and_342 (rb_store_r5, n4x16_decoder_1__0101, store_rb);
  and and_343 (rb_store_r6, n4x16_decoder_1__0110, store_rb);
  and and_344 (rb_store_r7, n4x16_decoder_1__0111, store_rb);
  and and_345 (rb_store_r8, n4x16_decoder_1__1000, store_rb);
  and and_346 (rb_store_r9, n4x16_decoder_1__1001, store_rb);
  and and_347 (rb_store_r10, n4x16_decoder_1__1010, store_rb);
  and and_348 (rb_store_r11, n4x16_decoder_1__1011, store_rb);
  and and_349 (rb_store_r12, n4x16_decoder_1__1100, store_rb);
  and and_350 (rb_store_r13, n4x16_decoder_1__1101, store_rb);
  and and_351 (rb_store_r14, n4x16_decoder_1__1110, store_rb);
  and and_352 (rb_store_r15, n4x16_decoder_1__1111, store_rb);
  and and_353 (ra_store_r0, n4x16_decoder_2__0000, store_ra);
  and and_354 (ra_store_r1, n4x16_decoder_2__0001, store_ra);
  and and_355 (ra_store_r2, n4x16_decoder_2__0010, store_ra);
  and and_356 (ra_store_r3, n4x16_decoder_2__0011, store_ra);
  and and_357 (ra_store_r4, n4x16_decoder_2__0100, store_ra);
  and and_358 (ra_store_r5, n4x16_decoder_2__0101, store_ra);
  and and_359 (ra_store_r6, n4x16_decoder_2__0110, store_ra);
  and and_360 (ra_store_r7, n4x16_decoder_2__0111, store_ra);
  and and_361 (ra_store_r8, n4x16_decoder_2__1000, store_ra);
  and and_362 (ra_store_r9, n4x16_decoder_2__1001, store_ra);
  and and_363 (ra_store_r10, n4x16_decoder_2__1010, store_ra);
  and and_364 (ra_store_r11, n4x16_decoder_2__1011, store_ra);
  and and_365 (ra_store_r12, n4x16_decoder_2__1100, store_ra);
  and and_366 (ra_store_r13, n4x16_decoder_2__1101, store_ra);
  and and_367 (ra_store_r14, n4x16_decoder_2__1110, store_ra);
  and and_368 (ra_store_r15, n4x16_decoder_2__1111, store_ra);
  or or_311 (arith_ra, flip_ra, neg_ra);
  or or_312 (arith_word__ra_rb, flip_word__ra_rb, neg_word__ra_rb);
  _4x16_decoder u_4x16_decoder_3 (
    .in_1(in_1[3]), .in_2(in_1[2]), .in_3(in_1[1]), .in_4(in_1[0]), ._0000(n4x16_decoder_3__0000),
    ._0001(n4x16_decoder_3__0001), ._0010(n4x16_decoder_3__0010), ._0011(n4x16_decoder_3__0011),
    ._0100(n4x16_decoder_3__0100), ._0101(n4x16_decoder_3__0101), ._0110(n4x16_decoder_3__0110),
    ._0111(n4x16_decoder_3__0111), ._1000(n4x16_decoder_3__1000), ._1001(n4x16_decoder_3__1001),
    ._1010(n4x16_decoder_3__1010), ._1011(n4x16_decoder_3__1011), ._1100(n4x16_decoder_3__1100),
    ._1101(n4x16_decoder_3__1101), ._1110(n4x16_decoder_3__1110), ._1111(n4x16_decoder_3__1111));
  _4x16_decoder u_4x16_decoder_4 (
    .in_1(in_1[7]), .in_2(in_1[6]), .in_3(in_1[5]), .in_4(in_1[4]), ._0000(n4x16_decoder_4__0000),
    ._0001(n4x16_decoder_4__0001), ._0010(n4x16_decoder_4__0010), ._0011(n4x16_decoder_4__0011),
    ._0100(n4x16_decoder_4__0100), ._0101(n4x16_decoder_4__0101), ._0110(n4x16_decoder_4__0110),
    ._0111(n4x16_decoder_4__0111), ._1000(n4x16_decoder_4__1000), ._1001(n4x16_decoder_4__1001),
    ._1010(n4x16_decoder_4__1010), ._1011(n4x16_decoder_4__1011), ._1100(n4x16_decoder_4__1100),
    ._1101(n4x16_decoder_4__1101), ._1110(n4x16_decoder_4__1110), ._1111(n4x16_decoder_4__1111));
  and and_369 (rb_load_r0, n4x16_decoder_3__0000, load_rb);
  and and_370 (rb_load_r1, n4x16_decoder_3__0001, load_rb);
  and and_371 (rb_load_r2, n4x16_decoder_3__0010, load_rb);
  and and_372 (rb_load_r3, n4x16_decoder_3__0011, load_rb);
  and and_373 (rb_load_r4, n4x16_decoder_3__0100, load_rb);
  and and_374 (rb_load_r5, n4x16_decoder_3__0101, load_rb);
  and and_375 (rb_load_r6, n4x16_decoder_3__0110, load_rb);
  and and_376 (rb_load_r7, n4x16_decoder_3__0111, load_rb);
  and and_377 (rb_load_r8, n4x16_decoder_3__1000, load_rb);
  and and_378 (rb_load_r9, n4x16_decoder_3__1001, load_rb);
  and and_379 (rb_load_r10, n4x16_decoder_3__1010, load_rb);
  and and_380 (rb_load_r11, n4x16_decoder_3__1011, load_rb);
  and and_381 (rb_load_r12, n4x16_decoder_3__1100, load_rb);
  and and_382 (rb_load_r13, n4x16_decoder_3__1101, load_rb);
  and and_383 (rb_load_r14, n4x16_decoder_3__1110, load_rb);
  and and_384 (rb_load_r15, n4x16_decoder_3__1111, load_rb);
  and and_385 (ra_load_r0, n4x16_decoder_4__0000, load_ra);
  and and_386 (ra_load_r1, n4x16_decoder_4__0001, load_ra);
  and and_387 (ra_load_r2, n4x16_decoder_4__0010, load_ra);
  and and_388 (ra_load_r3, n4x16_decoder_4__0011, load_ra);
  and and_389 (ra_load_r4, n4x16_decoder_4__0100, load_ra);
  and and_390 (ra_load_r5, n4x16_decoder_4__0101, load_ra);
  and and_391 (ra_load_r6, n4x16_decoder_4__0110, load_ra);
  and and_392 (ra_load_r7, n4x16_decoder_4__0111, load_ra);
  and and_393 (ra_load_r8, n4x16_decoder_4__1000, load_ra);
  and and_394 (ra_load_r9, n4x16_decoder_4__1001, load_ra);
  and and_395 (ra_load_r10, n4x16_decoder_4__1010, load_ra);
  and and_396 (ra_load_r11, n4x16_decoder_4__1011, load_ra);
  and and_397 (ra_load_r12, n4x16_decoder_4__1100, load_ra);
  and and_398 (ra_load_r13, n4x16_decoder_4__1101, load_ra);
  and and_399 (ra_load_r14, n4x16_decoder_4__1110, load_ra);
  and and_400 (ra_load_r15, n4x16_decoder_4__1111, load_ra);
  _4x16_decoder u_4x16_decoder_5 (
    .in_1(in_1[3]), .in_2(in_1[2]), .in_3(in_1[1]), .in_4(in_1[0]), ._0000(n4x16_decoder_5__0000),
    ._0001(n4x16_decoder_5__0001), ._0010(n4x16_decoder_5__0010), ._0011(n4x16_decoder_5__0011),
    ._0100(n4x16_decoder_5__0100), ._0101(n4x16_decoder_5__0101), ._0110(n4x16_decoder_5__0110),
    ._0111(n4x16_decoder_5__0111), ._1000(n4x16_decoder_5__1000), ._1001(n4x16_decoder_5__1001),
    ._1010(n4x16_decoder_5__1010), ._1011(n4x16_decoder_5__1011), ._1100(n4x16_decoder_5__1100),
    ._1101(n4x16_decoder_5__1101), ._1110(n4x16_decoder_5__1110), ._1111(n4x16_decoder_5__1111));
  _4x16_decoder u_4x16_decoder_6 (
    .in_1(in_1[7]), .in_2(in_1[6]), .in_3(in_1[5]), .in_4(in_1[4]), ._0000(n4x16_decoder_6__0000),
    ._0001(n4x16_decoder_6__0001), ._0010(n4x16_decoder_6__0010), ._0011(n4x16_decoder_6__0011),
    ._0100(n4x16_decoder_6__0100), ._0101(n4x16_decoder_6__0101), ._0110(n4x16_decoder_6__0110),
    ._0111(n4x16_decoder_6__0111), ._1000(n4x16_decoder_6__1000), ._1001(n4x16_decoder_6__1001),
    ._1010(n4x16_decoder_6__1010), ._1011(n4x16_decoder_6__1011), ._1100(n4x16_decoder_6__1100),
    ._1101(n4x16_decoder_6__1101), ._1110(n4x16_decoder_6__1110), ._1111(n4x16_decoder_6__1111));
  and and_401 (rb_sel_r0, n4x16_decoder_5__0000, sel_rb);
  and and_402 (rb_sel_r1, n4x16_decoder_5__0001, sel_rb);
  and and_403 (rb_sel_r2, n4x16_decoder_5__0010, sel_rb);
  and and_404 (rb_sel_r3, n4x16_decoder_5__0011, sel_rb);
  and and_405 (rb_sel_r4, n4x16_decoder_5__0100, sel_rb);
  and and_406 (rb_sel_r5, n4x16_decoder_5__0101, sel_rb);
  and and_407 (rb_sel_r6, n4x16_decoder_5__0110, sel_rb);
  and and_408 (rb_sel_r7, n4x16_decoder_5__0111, sel_rb);
  and and_409 (rb_sel_r8, n4x16_decoder_5__1000, sel_rb);
  and and_410 (rb_sel_r9, n4x16_decoder_5__1001, sel_rb);
  and and_411 (rb_sel_r10, n4x16_decoder_5__1010, sel_rb);
  and and_412 (rb_sel_r11, n4x16_decoder_5__1011, sel_rb);
  and and_413 (rb_sel_r12, n4x16_decoder_5__1100, sel_rb);
  and and_414 (rb_sel_r13, n4x16_decoder_5__1101, sel_rb);
  and and_415 (rb_sel_r14, n4x16_decoder_5__1110, sel_rb);
  and and_416 (rb_sel_r15, n4x16_decoder_5__1111, sel_rb);
  and and_417 (ra_sel_r0, n4x16_decoder_6__0000, sel_ra);
  and and_418 (ra_sel_r1, n4x16_decoder_6__0001, sel_ra);
  and and_419 (ra_sel_r2, n4x16_decoder_6__0010, sel_ra);
  and and_420 (ra_sel_r3, n4x16_decoder_6__0011, sel_ra);
  and and_421 (ra_sel_r4, n4x16_decoder_6__0100, sel_ra);
  and and_422 (ra_sel_r5, n4x16_decoder_6__0101, sel_ra);
  and and_423 (ra_sel_r6, n4x16_decoder_6__0110, sel_ra);
  and and_424 (ra_sel_r7, n4x16_decoder_6__0111, sel_ra);
  and and_425 (ra_sel_r8, n4x16_decoder_6__1000, sel_ra);
  and and_426 (ra_sel_r9, n4x16_decoder_6__1001, sel_ra);
  and and_427 (ra_sel_r10, n4x16_decoder_6__1010, sel_ra);
  and and_428 (ra_sel_r11, n4x16_decoder_6__1011, sel_ra);
  and and_429 (ra_sel_r12, n4x16_decoder_6__1100, sel_ra);
  and and_430 (ra_sel_r13, n4x16_decoder_6__1101, sel_ra);
  and and_431 (ra_sel_r14, n4x16_decoder_6__1110, sel_ra);
  and and_432 (ra_sel_r15, n4x16_decoder_6__1111, sel_ra);

  // Other names for the same wires on the sheet: ALU_sel0 = out_33; ALU_sel1 = out_34; ALU_sel2 = out_35;
  //   ALU_sel3 = out_36; c = in_5; clk = in_2; clk_en = in_3; clk_set = in_4; e = in_10; enable_arith_carry = out_20;
  //   enable_BUS1 = out_14; enable_carry = out_19; enable_CLR = out_15; enable_lowmask = out_16; enable_TMP = out_17;
  //   enable_TMP1 = out_18; END = out_29; IR[15:0] = in_1; IR0 = in_1[0]; IR1 = in_1[1]; IR2 = in_1[2]; IR3 = in_1[3];
  //   IR4 = in_1[4]; IR5 = in_1[5]; IR6 = in_1[6]; IR7 = in_1[7]; IR8 = in_1[8]; IR9 = in_1[9]; IR10 = in_1[10];
  //   IR11 = in_1[11]; IR12 = in_1[12]; IR13 = in_1[13]; IR14 = in_1[14]; IR15 = in_1[15]; load_ACC = out_27;
  //   load_RAM = out_24; minus_1 = in_12; p = in_11; r = in_13; sel_MAR = out_23; set_ACC = out_28;
  //   set_arith_flags = out_22; set_carry = out_21; store_IR = out_26; store_RAM = out_25; tunnel = in_8;
  //   tunnel_t = in_6; tunnel_t_t = in_7; z = in_9

  // Notes on the sheet:
  //   out_36: pull=down
  //   in_5: pull=down
  //   out_34: pull=down
  //   out_17: pull=down
  //   out_23: pull=down
  //   out_28: pull=down
  //   out_35: pull=down
  //   in_1: pull=down
  //   out_18: pull=down
  //   out_21: pull=down
  //   out_27: pull=down
  //   out_19: pull=down
  //   out_25: pull=down
  //   out_16: pull=down
  //   in_12: pull=down
  //   in_2: pull=down
  //   in_13: pull=down
  //   in_9: pull=down
  //   out_24: pull=down
  //   in_7: pull=down
  //   out_26: pull=down
  //   in_3: pull=down
  //   in_8: pull=down
  //   out_22: pull=down
  //   in_6: pull=down
  //   out_15: pull=down
  //   out_33: pull=down
  //   out_14: pull=down
  //   out_29: pull=down
  //   out_20: pull=down
  //   in_4: pull=down
  //   in_10: pull=down
  //   in_11: pull=down
endmodule
module cpu (
  input  in_1,
  output [15:0] out_2,
  output [15:0] out_3,
  output [15:0] out_4,
  output [15:0] out_5,
  output [15:0] out_6,
  output [15:0] out_7,
  output [15:0] out_8,
  output [15:0] out_9,
  output [15:0] out_10,
  output [15:0] out_11,
  output [15:0] out_12,
  output [15:0] out_13,
  output [15:0] out_14,
  output [15:0] out_15,
  output [15:0] out_16,
  output [15:0] out_17,
  output [15:0] out_18
);

  wire alu0, alu1, alu2, alu3, and_1_out, buffer_1_out, buffer_2_out, bus1, carry_in, carry_out, clk, clk_en,
       clk_in, clk_set, clr, controlled_buffer_35_out, en_arith_carry, en_carry, END, flag_carry_out,
       load_acc, load_r0, load_r1, load_r2, load_r3, load_r4, load_r5, load_r6, load_r7, load_r8, load_r9,
       load_r10, load_r11, load_r12, load_r13, load_r14, load_r15, load_ram, low_mask,
       n1_bit_memory_cell_1_output, n16_bit_alu_1_out_10, n16_bit_alu_1_out_11, n16_bit_alu_1_out_12,
       n16_bit_alu_1_out_13, n16_bit_alu_1_out_14, n16_bit_alu_1_out_15, n16_bit_alu_1_out_16,
       n16_bit_flags_1_out_19, n16_bit_flags_1_out_20, n16_bit_flags_1_out_21, n16_bit_flags_1_out_22,
       n16_bit_flags_1_out_23, n16_bit_flags_1_out_24, n16_bit_flags_1_out_25, n16_bit_flags_1_out_33,
       or_1_out, or_2_out, or_3_out, or_4_out, or_5_out, or_6_out, or_7_out, or_8_out, or_9_out, or_10_out,
       or_11_out, or_12_out, or_13_out, or_14_out, or_15_out, or_16_out, save_r0, save_r1, save_r2, save_r3,
       save_r4, save_r5, save_r6, save_r7, save_r8, save_r9, save_r10, save_r11, save_r12, save_r13,
       save_r14, save_r15, save_ram, sel_MAR, sel_r0, sel_r1, sel_r2, sel_r3, sel_r4, sel_r5, sel_r6, sel_r7,
       sel_r8, sel_r9, sel_r10, sel_r11, sel_r12, sel_r13, sel_r14, sel_r15, set_acc, set_carry, set_flags,
       set_IR, tmp1, tmp16;
  wire [15:0] bus, controlled_buffer_9_out, IR, n16_bit_alu_1_out_8, n16_bit_bus1_1_out_3,
       n16_bit_clear_1_out_3, n16_bit_lower_mask_1_out_3, n16_bit_temp_1_out_3, r0_out, r1_out, r2_out,
       r3_out, r4_out, r5_out, r6_out, r7_out, r8_out, r9_out, r10_out, r11_out, r12_out, r13_out, r14_out,
       r15_out, ram_1_data, segment;
  wire [23:0] n3_bytes_memory_cell_1_output;

  Clock clock_1 (.out(clk_in));
  and and_1 (and_1_out, ~END, clk_in);  // AND_Gate
  _16_bit_register u_16_bit_register_1 (.in_1(bus), .in_2(save_r0), .in_3(or_1_out), .out_4(r0_out), .out_5(out_3));
  or or_1 (or_1_out, load_r0, sel_r0);
  _16_bit_register u_16_bit_register_2 (.in_1(bus), .in_2(save_r4), .in_3(or_2_out), .out_4(r4_out), .out_5(out_7));
  or or_2 (or_2_out, load_r4, sel_r4);
  _16_bit_register u_16_bit_register_3 (.in_1(bus), .in_2(save_r8), .in_3(or_3_out), .out_4(r8_out), .out_5(out_11));
  or or_3 (or_3_out, load_r8, sel_r8);
  _16_bit_register u_16_bit_register_4 (.in_1(bus), .in_2(save_r12), .in_3(or_4_out), .out_4(r12_out), .out_5(out_15));
  or or_4 (or_4_out, load_r12, sel_r12);
  cpu_clock cpu_clock_1 (.in_1(and_1_out), .out_2(clk), .out_3(clk_en), .out_4(clk_set));
  assign bus = load_r0 ? r0_out : 16'bz;  // Controlled_Buffer controlled_buffer_1
  assign segment = sel_r0 ? r0_out : 16'bz;  // Controlled_Buffer controlled_buffer_2
  assign bus = load_r4 ? r4_out : 16'bz;  // Controlled_Buffer controlled_buffer_3
  assign segment = sel_r4 ? r4_out : 16'bz;  // Controlled_Buffer controlled_buffer_4
  assign bus = load_r8 ? r8_out : 16'bz;  // Controlled_Buffer controlled_buffer_5
  assign segment = sel_r8 ? r8_out : 16'bz;  // Controlled_Buffer controlled_buffer_6
  assign bus = load_r12 ? r12_out : 16'bz;  // Controlled_Buffer controlled_buffer_7
  assign segment = sel_r12 ? r12_out : 16'bz;  // Controlled_Buffer controlled_buffer_8
  _3_bytes_memory_cell u_3_bytes_memory_cell_1 (
    .\input ({segment[7:0], bus}), .in_2(sel_MAR), .\output (n3_bytes_memory_cell_1_output));
  assign controlled_buffer_9_out = save_ram ? bus : 16'bz;  // Controlled_Buffer controlled_buffer_9
  _16_bit_register u_16_bit_register_5 (.in_1(bus), .in_2(save_r1), .in_3(or_5_out), .out_4(r1_out), .out_5(out_4));
  or or_5 (or_5_out, load_r1, sel_r1);
  assign bus = load_r1 ? r1_out : 16'bz;  // Controlled_Buffer controlled_buffer_10
  assign segment = sel_r1 ? r1_out : 16'bz;  // Controlled_Buffer controlled_buffer_11
  _16_bit_register u_16_bit_register_6 (.in_1(bus), .in_2(save_r5), .in_3(or_6_out), .out_4(r5_out), .out_5(out_8));
  or or_6 (or_6_out, load_r5, sel_r5);
  assign bus = load_r5 ? r5_out : 16'bz;  // Controlled_Buffer controlled_buffer_12
  assign segment = sel_r5 ? r5_out : 16'bz;  // Controlled_Buffer controlled_buffer_13
  _16_bit_register u_16_bit_register_7 (.in_1(bus), .in_2(save_r9), .in_3(or_7_out), .out_4(r9_out), .out_5(out_12));
  or or_7 (or_7_out, load_r9, sel_r9);
  assign bus = load_r9 ? r9_out : 16'bz;  // Controlled_Buffer controlled_buffer_14
  assign segment = sel_r9 ? r9_out : 16'bz;  // Controlled_Buffer controlled_buffer_15
  _16_bit_register u_16_bit_register_8 (.in_1(bus), .in_2(save_r13), .in_3(or_8_out), .out_4(r13_out), .out_5(out_16));
  or or_8 (or_8_out, load_r13, sel_r13);
  assign bus = load_r13 ? r13_out : 16'bz;  // Controlled_Buffer controlled_buffer_16
  assign segment = sel_r13 ? r13_out : 16'bz;  // Controlled_Buffer controlled_buffer_17
  buf buffer_1 (buffer_1_out, save_ram);
  RAM #(.addrWidth(24), .dataWidth(16), .bus("separate")) ram_1 (
    .addr(n3_bytes_memory_cell_1_output), .din(controlled_buffer_9_out), .data(ram_1_data), .str(save_ram),
    .sel(1'b1), .clk(buffer_1_out), .ld(load_ram), .clr(1'b0));
  buf buffer_2 (buffer_2_out, load_ram);
  assign bus = buffer_2_out ? ram_1_data : 16'bz;  // Controlled_Buffer controlled_buffer_18
  _16_bit_register u_16_bit_register_9 (.in_1(bus), .in_2(save_r2), .in_3(or_9_out), .out_4(r2_out), .out_5(out_5));
  or or_9 (or_9_out, load_r2, sel_r2);
  assign bus = load_r2 ? r2_out : 16'bz;  // Controlled_Buffer controlled_buffer_19
  assign segment = sel_r2 ? r2_out : 16'bz;  // Controlled_Buffer controlled_buffer_20
  _16_bit_register u_16_bit_register_10 (.in_1(bus), .in_2(save_r6), .in_3(or_10_out), .out_4(r6_out), .out_5(out_9));
  or or_10 (or_10_out, load_r6, sel_r6);
  assign bus = load_r6 ? r6_out : 16'bz;  // Controlled_Buffer controlled_buffer_21
  assign segment = sel_r6 ? r6_out : 16'bz;  // Controlled_Buffer controlled_buffer_22
  _16_bit_register u_16_bit_register_11 (
    .in_1(bus), .in_2(save_r10), .in_3(or_11_out), .out_4(r10_out), .out_5(out_13));
  or or_11 (or_11_out, load_r10, sel_r10);
  assign bus = load_r10 ? r10_out : 16'bz;  // Controlled_Buffer controlled_buffer_23
  assign segment = sel_r10 ? r10_out : 16'bz;  // Controlled_Buffer controlled_buffer_24
  _16_bit_register u_16_bit_register_12 (
    .in_1(bus), .in_2(save_r14), .in_3(or_12_out), .out_4(r14_out), .out_5(out_17));
  or or_12 (or_12_out, load_r14, sel_r14);
  assign bus = load_r14 ? r14_out : 16'bz;  // Controlled_Buffer controlled_buffer_25
  assign segment = sel_r14 ? r14_out : 16'bz;  // Controlled_Buffer controlled_buffer_26
  _16_bit_temp u_16_bit_temp_1 (.in_1(bus), .in_2(tmp16), .out_3(n16_bit_temp_1_out_3));
  _16_bit_bus1 u_16_bit_bus1_1 (.\input (n16_bit_temp_1_out_3), .in_2(bus1), .out_3(n16_bit_bus1_1_out_3));
  _16_bit_clear u_16_bit_clear_1 (.\input (n16_bit_bus1_1_out_3), .in_2(clr), .out_3(n16_bit_clear_1_out_3));
  _16_bit_lower_mask u_16_bit_lower_mask_1 (
    .\input (n16_bit_clear_1_out_3), .in_2(low_mask), .out_3(n16_bit_lower_mask_1_out_3));
  _16_bit_ALU u_16_bit_alu_1 (
    .in_1(bus), .in_2(n16_bit_lower_mask_1_out_3), .in_3(carry_in), .in_4(alu0), .in_5(alu1), .in_6(alu2),
    .in_7(alu3), .out_8(n16_bit_alu_1_out_8), .out_9(carry_out), .out_10(n16_bit_alu_1_out_10),
    .out_11(n16_bit_alu_1_out_11), .out_12(n16_bit_alu_1_out_12), .out_13(n16_bit_alu_1_out_13),
    .out_14(n16_bit_alu_1_out_14), .out_15(n16_bit_alu_1_out_15), .out_16(n16_bit_alu_1_out_16));
  _16_bit_accumulator u_16_bit_accumulator_1 (
    .in_1(n16_bit_alu_1_out_8), .in_2(set_acc), .in_3(load_acc), .out_4(bus), .out_5(out_2));
  _16_bit_register u_16_bit_register_13 (.in_1(bus), .in_2(save_r3), .in_3(or_13_out), .out_4(r3_out), .out_5(out_6));
  or or_13 (or_13_out, load_r3, sel_r3);
  assign bus = load_r3 ? r3_out : 16'bz;  // Controlled_Buffer controlled_buffer_27
  assign segment = sel_r3 ? r3_out : 16'bz;  // Controlled_Buffer controlled_buffer_28
  _16_bit_register u_16_bit_register_14 (.in_1(bus), .in_2(save_r7), .in_3(or_14_out), .out_4(r7_out), .out_5(out_10));
  or or_14 (or_14_out, load_r7, sel_r7);
  assign bus = load_r7 ? r7_out : 16'bz;  // Controlled_Buffer controlled_buffer_29
  assign segment = sel_r7 ? r7_out : 16'bz;  // Controlled_Buffer controlled_buffer_30
  _16_bit_register u_16_bit_register_15 (
    .in_1(bus), .in_2(save_r11), .in_3(or_15_out), .out_4(r11_out), .out_5(out_14));
  or or_15 (or_15_out, load_r11, sel_r11);
  assign bus = load_r11 ? r11_out : 16'bz;  // Controlled_Buffer controlled_buffer_31
  assign segment = sel_r11 ? r11_out : 16'bz;  // Controlled_Buffer controlled_buffer_32
  _16_bit_register u_16_bit_register_16 (
    .in_1(bus), .in_2(save_r15), .in_3(or_16_out), .out_4(r15_out), .out_5(out_18));
  or or_16 (or_16_out, load_r15, sel_r15);
  assign bus = load_r15 ? r15_out : 16'bz;  // Controlled_Buffer controlled_buffer_33
  assign segment = sel_r15 ? r15_out : 16'bz;  // Controlled_Buffer controlled_buffer_34
  _16_bit_FLAGS u_16_bit_flags_1 (
    .in_1(carry_out), .in_2(n16_bit_alu_1_out_10), .in_3(n16_bit_alu_1_out_11), .in_4(n16_bit_alu_1_out_12),
    .in_5(n16_bit_alu_1_out_13), .in_6(n16_bit_alu_1_out_14), .in_7(n16_bit_alu_1_out_15),
    .in_8(n16_bit_alu_1_out_16), .in_16(1'b0), .in_17(set_flags), .out_18(flag_carry_out),
    .out_19(n16_bit_flags_1_out_19), .out_20(n16_bit_flags_1_out_20), .out_21(n16_bit_flags_1_out_21),
    .out_22(n16_bit_flags_1_out_22), .out_23(n16_bit_flags_1_out_23), .out_24(n16_bit_flags_1_out_24),
    .out_25(n16_bit_flags_1_out_25), .out_33(n16_bit_flags_1_out_33));  // open: in_9, in_10, in_11, in_12, in_13, in_14, in_15, out_26, out_27, out_28, out_29, out_30, out_31, out_32
  _16_bit_IR u_16_bit_ir_1 (.in_1(bus), .in_2(set_IR), .out_3(IR));
  _1_bit_memory_cell u_1_bit_memory_cell_1 (.in_1(carry_out), .in_2(set_carry), .\output (n1_bit_memory_cell_1_output));
  assign controlled_buffer_35_out = en_arith_carry ? flag_carry_out : 1'bz;  // Controlled_Buffer controlled_buffer_35
  assign controlled_buffer_35_out = en_carry ? n1_bit_memory_cell_1_output : 1'bz;  // Controlled_Buffer controlled_buffer_36
  _1_bit_temp u_1_bit_temp_1 (.in_1(controlled_buffer_35_out), .in_2(tmp1), .out_3(carry_in));
  cpu_control_section cpu_control_section_1 (
    .in_1(IR), .in_2(clk), .in_3(clk_en), .in_4(clk_set), .in_5(flag_carry_out),
    .in_6(n16_bit_flags_1_out_19), .in_7(n16_bit_flags_1_out_20), .in_8(n16_bit_flags_1_out_21),
    .in_9(n16_bit_flags_1_out_22), .in_10(n16_bit_flags_1_out_23), .in_11(n16_bit_flags_1_out_24),
    .in_12(n16_bit_flags_1_out_25), .in_13(n16_bit_flags_1_out_33), .out_14(bus1), .out_15(clr),
    .out_16(low_mask), .out_17(tmp16), .out_18(tmp1), .out_19(en_carry), .out_20(en_arith_carry),
    .out_21(set_carry), .out_22(set_flags), .out_23(sel_MAR), .out_24(load_ram), .out_25(save_ram),
    .out_26(set_IR), .out_27(load_acc), .out_28(set_acc), .out_29(END),
    .load_register({load_r15, load_r14, load_r13, load_r12, load_r11, load_r10, load_r9, load_r8, load_r7, load_r6, load_r5, load_r4, load_r3, load_r2, load_r1, load_r0}),
    .store_register({save_r15, save_r14, save_r13, save_r12, save_r11, save_r10, save_r9, save_r8, save_r7, save_r6, save_r5, save_r4, save_r3, save_r2, save_r1, save_r0}),
    .select_register({sel_r15, sel_r14, sel_r13, sel_r12, sel_r11, sel_r10, sel_r9, sel_r8, sel_r7, sel_r6, sel_r5, sel_r4, sel_r3, sel_r2, sel_r1, sel_r0}),
    .out_33(alu0), .out_34(alu1), .out_35(alu2), .out_36(alu3));

  // Other names for the same wires on the sheet: com0 = bus[0]; com1 = bus[1]; com2 = bus[2]; com3 = bus[3];
  //   com4 = bus[4]; com5 = bus[5]; com6 = bus[6]; com7 = bus[7]; com8 = bus[8]; com9 = bus[9]; com10 = bus[10];
  //   com11 = bus[11]; com12 = bus[12]; com13 = bus[13]; com14 = bus[14]; com15 = bus[15];
  //   load_reg[15:0] = {load_r15, load_r14, load_r13, load_r12, load_r11, load_r10, load_r9, load_r8, load_r7, load_r6, load_r5, load_r4, load_r3, load_r2, load_r1, load_r0};
  //   reset = in_1;
  //   save_reg[15:0] = {save_r15, save_r14, save_r13, save_r12, save_r11, save_r10, save_r9, save_r8, save_r7, save_r6, save_r5, save_r4, save_r3, save_r2, save_r1, save_r0};
  //   select_reg[15:0] = {sel_r15, sel_r14, sel_r13, sel_r12, sel_r11, sel_r10, sel_r9, sel_r8, sel_r7, sel_r6, sel_r5, sel_r4, sel_r3, sel_r2, sel_r1, sel_r0}

  // Notes on the sheet:
  //   in_1: pull=down
  //   SS
  //   FS
  //   CS
  //   SP
  //   BP
  //   DS
  //   ES
  //   IP
endmodule

module add_ra__rb (
);

  wire add_ra__rb, ALU_0000, clk_en, clk_set, clock5, clock6, clock7, enable_TMP, load_ACC, load_ra, load_rb,
       set_ACC, set_arith_FLAGS, store_ra;

  and and_1 (load_rb, clock5, clk_en, add_ra__rb);
  and and_2 (load_ra, clock6, clk_en, add_ra__rb);
  and and_3 (ALU_0000, clock6, clk_en, add_ra__rb);
  and and_4 (load_ACC, clock7, clk_en, add_ra__rb);
  and and_5 (enable_TMP, clock5, clk_set, add_ra__rb);
  and and_6 (set_ACC, clock6, clk_set, add_ra__rb);
  and and_7 (set_arith_FLAGS, clock6, clk_set, add_ra__rb);
  and and_8 (store_ra, clock7, clk_set, add_ra__rb);
endmodule

module shr_ra__imm4 (
);

  wire ALU_0000, ALU_0001, ALU_1000, clk_en, clk_set, clock5, clock6, clock7, clock8, clock9, clock10,
       clock11, enable_BUS1, enable_carry, enable_CLR, enable_TMP1, load_ACC, load_CS, load_IAR, load_ra,
       load_RAM, sel_CS, sel_MAR, set_ACC, set_arith_FLAGS, set_carry, shr_ra__imm4, store_CS, store_IAR,
       store_ra, store_TMP;

  and and_1 (sel_CS, clock5, clk_en, shr_ra__imm4);
  and and_2 (load_IAR, clock5, clk_en, shr_ra__imm4);
  and and_3 (enable_BUS1, clock5, clk_en, shr_ra__imm4);
  and and_4 (ALU_0000, clock5, clk_en, shr_ra__imm4);
  and and_5 (set_carry, clock5, clk_en, shr_ra__imm4);
  and and_6 (load_ACC, clock6, clk_en, shr_ra__imm4);
  and and_7 (enable_CLR, clock7, clk_en, shr_ra__imm4);
  and and_8 (load_CS, clock7, clk_en, shr_ra__imm4);
  and and_9 (ALU_1000, clock7, clk_en, shr_ra__imm4);
  and and_10 (load_ACC, clock8, clk_en, shr_ra__imm4);
  and and_11 (load_RAM, clock9, clk_en, shr_ra__imm4);
  and and_12 (load_ra, clock10, clk_en, shr_ra__imm4);
  and and_13 (ALU_0001, clock10, clk_en, shr_ra__imm4);
  and and_14 (load_ACC, clock11, clk_en, shr_ra__imm4);
  and and_15 (sel_MAR, clock5, clk_set, shr_ra__imm4);
  and and_16 (set_ACC, clock5, clk_set, shr_ra__imm4);
  and and_17 (enable_carry, clock5, clk_set, shr_ra__imm4);
  and and_18 (enable_TMP1, clock5, clk_set, shr_ra__imm4);
  and and_19 (store_IAR, clock6, clk_set, shr_ra__imm4);
  and and_20 (set_ACC, clock7, clk_set, shr_ra__imm4);
  and and_21 (store_CS, clock8, clk_set, shr_ra__imm4);
  and and_22 (store_TMP, clock9, clk_set, shr_ra__imm4);
  and and_23 (set_ACC, clock10, clk_set, shr_ra__imm4);
  and and_24 (set_arith_FLAGS, clock10, clk_set, shr_ra__imm4);
  and and_25 (store_ra, clock11, clk_set, shr_ra__imm4);
endmodule

module shl_ra__imm4 (
);

  wire ALU_0000, ALU_0010, ALU_1000, clk_en, clk_set, clock5, clock6, clock7, clock8, clock9, clock10,
       clock11, enable_BUS1, enable_carry, enable_CLR, enable_TMP1, load_ACC, load_CS, load_IAR, load_ra,
       load_RAM, sel_CS, sel_MAR, set_ACC, set_arith_FLAGS, set_carry, shl_ra__imm4, store_CS, store_IAR,
       store_ra, store_TMP;

  and and_1 (sel_CS, clock5, clk_en, shl_ra__imm4);
  and and_2 (load_IAR, clock5, clk_en, shl_ra__imm4);
  and and_3 (enable_BUS1, clock5, clk_en, shl_ra__imm4);
  and and_4 (ALU_0000, clock5, clk_en, shl_ra__imm4);
  and and_5 (set_carry, clock5, clk_en, shl_ra__imm4);
  and and_6 (load_ACC, clock6, clk_en, shl_ra__imm4);
  and and_7 (enable_CLR, clock7, clk_en, shl_ra__imm4);
  and and_8 (load_CS, clock7, clk_en, shl_ra__imm4);
  and and_9 (ALU_1000, clock7, clk_en, shl_ra__imm4);
  and and_10 (load_ACC, clock8, clk_en, shl_ra__imm4);
  and and_11 (load_RAM, clock9, clk_en, shl_ra__imm4);
  and and_12 (load_ra, clock10, clk_en, shl_ra__imm4);
  and and_13 (ALU_0010, clock10, clk_en, shl_ra__imm4);
  and and_14 (load_ACC, clock11, clk_en, shl_ra__imm4);
  and and_15 (sel_MAR, clock5, clk_set, shl_ra__imm4);
  and and_16 (set_ACC, clock5, clk_set, shl_ra__imm4);
  and and_17 (enable_carry, clock5, clk_set, shl_ra__imm4);
  and and_18 (enable_TMP1, clock5, clk_set, shl_ra__imm4);
  and and_19 (store_IAR, clock6, clk_set, shl_ra__imm4);
  and and_20 (set_ACC, clock7, clk_set, shl_ra__imm4);
  and and_21 (store_CS, clock8, clk_set, shl_ra__imm4);
  and and_22 (store_TMP, clock9, clk_set, shl_ra__imm4);
  and and_23 (set_ACC, clock10, clk_set, shl_ra__imm4);
  and and_24 (set_arith_FLAGS, clock10, clk_set, shl_ra__imm4);
  and and_25 (store_ra, clock11, clk_set, shl_ra__imm4);
endmodule

module sar_ra__imm4 (
);

  wire ALU_0000, ALU_1000, ALU_1001, clk_en, clk_set, clock5, clock6, clock7, clock8, clock9, clock10,
       clock11, enable_BUS1, enable_carry, enable_CLR, enable_TMP1, load_ACC, load_CS, load_IAR, load_ra,
       load_RAM, sar_ra__imm4, sel_CS, sel_MAR, set_ACC, set_arith_FLAGS, set_carry, store_CS, store_IAR,
       store_ra, store_TMP;

  and and_1 (sel_CS, clock5, clk_en, sar_ra__imm4);
  and and_2 (load_IAR, clock5, clk_en, sar_ra__imm4);
  and and_3 (enable_BUS1, clock5, clk_en, sar_ra__imm4);
  and and_4 (ALU_0000, clock5, clk_en, sar_ra__imm4);
  and and_5 (set_carry, clock5, clk_en, sar_ra__imm4);
  and and_6 (load_ACC, clock6, clk_en, sar_ra__imm4);
  and and_7 (enable_CLR, clock7, clk_en, sar_ra__imm4);
  and and_8 (load_CS, clock7, clk_en, sar_ra__imm4);
  and and_9 (ALU_1000, clock7, clk_en, sar_ra__imm4);
  and and_10 (load_ACC, clock8, clk_en, sar_ra__imm4);
  and and_11 (load_RAM, clock9, clk_en, sar_ra__imm4);
  and and_12 (load_ra, clock10, clk_en, sar_ra__imm4);
  and and_13 (ALU_1001, clock10, clk_en, sar_ra__imm4);
  and and_14 (load_ACC, clock11, clk_en, sar_ra__imm4);
  and and_15 (sel_MAR, clock5, clk_set, sar_ra__imm4);
  and and_16 (set_ACC, clock5, clk_set, sar_ra__imm4);
  and and_17 (enable_carry, clock5, clk_set, sar_ra__imm4);
  and and_18 (enable_TMP1, clock5, clk_set, sar_ra__imm4);
  and and_19 (store_IAR, clock6, clk_set, sar_ra__imm4);
  and and_20 (set_ACC, clock7, clk_set, sar_ra__imm4);
  and and_21 (store_CS, clock8, clk_set, sar_ra__imm4);
  and and_22 (store_TMP, clock9, clk_set, sar_ra__imm4);
  and and_23 (set_ACC, clock10, clk_set, sar_ra__imm4);
  and and_24 (set_arith_FLAGS, clock10, clk_set, sar_ra__imm4);
  and and_25 (store_ra, clock11, clk_set, sar_ra__imm4);
endmodule

module flip_ra (
);

  wire ALU_0011, clk_en, clk_set, clock6, clock7, flip_ra, lead_ra, load_ACC, set_ACC, set_arith_FLAGS,
       store_ra;

  and and_1 (lead_ra, clock6, clk_en, flip_ra);
  and and_2 (ALU_0011, clock6, clk_en, flip_ra);
  and and_3 (load_ACC, clock7, clk_en, flip_ra);
  and and_4 (set_ACC, clock6, clk_set, flip_ra);
  and and_5 (set_arith_FLAGS, clock6, clk_set, flip_ra);
  and and_6 (store_ra, clock7, clk_set, flip_ra);
endmodule

module and_ra__rb (
);

  wire ALU_0100, and_ra__rb, clk_en, clk_set, clock5, clock6, clock7, enable_TMP, load_ACC, load_ra, load_rb,
       set_ACC, set_arith_FLAGS, store_ra;

  and and_1 (load_rb, clock5, clk_en, and_ra__rb);
  and and_2 (load_ra, clock6, clk_en, and_ra__rb);
  and and_3 (ALU_0100, clock6, clk_en, and_ra__rb);
  and and_4 (load_ACC, clock7, clk_en, and_ra__rb);
  and and_5 (enable_TMP, clock5, clk_set, and_ra__rb);
  and and_6 (set_ACC, clock6, clk_set, and_ra__rb);
  and and_7 (set_arith_FLAGS, clock6, clk_set, and_ra__rb);
  and and_8 (store_ra, clock7, clk_set, and_ra__rb);
endmodule

module or_ra__rb (
);

  wire ALU_0101, clk_en, clk_set, clock5, clock6, clock7, enable_TMP, load_ACC, load_ra, load_rb, or_ra__rb,
       set_ACC, set_arith_FLAGS, store_ra;

  and and_1 (load_rb, clock5, clk_en, or_ra__rb);
  and and_2 (load_ra, clock6, clk_en, or_ra__rb);
  and and_3 (ALU_0101, clock6, clk_en, or_ra__rb);
  and and_4 (load_ACC, clock7, clk_en, or_ra__rb);
  and and_5 (enable_TMP, clock5, clk_set, or_ra__rb);
  and and_6 (set_ACC, clock6, clk_set, or_ra__rb);
  and and_7 (set_arith_FLAGS, clock6, clk_set, or_ra__rb);
  and and_8 (store_ra, clock7, clk_set, or_ra__rb);
endmodule

module xor_ra__rb (
);

  wire ALU_0110, clk_en, clk_set, clock5, clock6, clock7, enable_TMP, load_ACC, load_ra, load_rb, set_ACC,
       set_arith_FLAGS, store_ra, xor_ra__rb;

  and and_1 (load_rb, clock5, clk_en, xor_ra__rb);
  and and_2 (load_ra, clock6, clk_en, xor_ra__rb);
  and and_3 (ALU_0110, clock6, clk_en, xor_ra__rb);
  and and_4 (load_ACC, clock7, clk_en, xor_ra__rb);
  and and_5 (enable_TMP, clock5, clk_set, xor_ra__rb);
  and and_6 (set_ACC, clock6, clk_set, xor_ra__rb);
  and and_7 (set_arith_FLAGS, clock6, clk_set, xor_ra__rb);
  and and_8 (store_ra, clock7, clk_set, xor_ra__rb);
endmodule

module cmp_ra__rb (
);

  wire ALU_0111, clk_en, clk_set, clock5, clock6, cmp_ra__rb, enable_TMP, load_ra, load_rb, set_ACC,
       set_arith_FLAGS;

  and and_1 (load_rb, clock5, clk_en, cmp_ra__rb);
  and and_2 (load_ra, clock6, clk_en, cmp_ra__rb);
  and and_3 (ALU_0111, clock6, clk_en, cmp_ra__rb);
  and and_4 (enable_TMP, clock5, clk_set, cmp_ra__rb);
  and and_5 (set_ACC, clock6, clk_set, cmp_ra__rb);
  and and_6 (set_arith_FLAGS, clock6, clk_set, cmp_ra__rb);
endmodule

module adc_ra__rb (
);

  wire adc_ra__rb, ALU_1000, clk_en, clk_set, clock5, clock6, clock7, enable_arith_carry, enable_TMP,
       enable_TMP1, load_ACC, load_ra, load_rb, set_ACC, set_arith_FLAGS, store_ra;

  and and_1 (load_rb, clock5, clk_en, adc_ra__rb);
  and and_2 (enable_arith_carry, clock5, clk_en, adc_ra__rb);
  and and_3 (load_ra, clock6, clk_en, adc_ra__rb);
  and and_4 (ALU_1000, clock6, clk_en, adc_ra__rb);
  and and_5 (load_ACC, clock7, clk_en, adc_ra__rb);
  and and_6 (enable_TMP, clock5, clk_set, adc_ra__rb);
  and and_7 (enable_TMP1, clock5, clk_set, adc_ra__rb);
  and and_8 (set_ACC, clock6, clk_set, adc_ra__rb);
  and and_9 (set_arith_FLAGS, clock6, clk_set, adc_ra__rb);
  and and_10 (store_ra, clock7, clk_set, adc_ra__rb);
endmodule

module neg_ra__rb (
);

  wire ALU_1011, clk_en, clk_set, clock6, clock7, lead_ra, load_ACC, neg_ra, set_ACC, set_arith_FLAGS,
       store_ra;

  and and_1 (lead_ra, clock6, clk_en, neg_ra);
  and and_2 (ALU_1011, clock6, clk_en, neg_ra);
  and and_3 (load_ACC, clock7, clk_en, neg_ra);
  and and_4 (set_ACC, clock6, clk_set, neg_ra);
  and and_5 (set_arith_FLAGS, clock6, clk_set, neg_ra);
  and and_6 (store_ra, clock7, clk_set, neg_ra);
endmodule

module sub_ra__rb (
);

  wire ALU_1100, clk_en, clk_set, clock5, clock6, clock7, enable_TMP, load_ACC, load_ra, load_rb, set_ACC,
       set_arith_FLAGS, store_ra, sub_ra__rb;

  and and_1 (load_rb, clock5, clk_en, sub_ra__rb);
  and and_2 (load_ra, clock6, clk_en, sub_ra__rb);
  and and_3 (ALU_1100, clock6, clk_en, sub_ra__rb);
  and and_4 (load_ACC, clock7, clk_en, sub_ra__rb);
  and and_5 (enable_TMP, clock5, clk_set, sub_ra__rb);
  and and_6 (set_ACC, clock6, clk_set, sub_ra__rb);
  and and_7 (set_arith_FLAGS, clock6, clk_set, sub_ra__rb);
  and and_8 (store_ra, clock7, clk_set, sub_ra__rb);
endmodule

module mul_ra__rb (
);

  wire ALU_1101, clk_en, clk_set, clock5, clock6, clock7, enable_TMP, load_ACC, load_ra, load_rb, mul_ra__rb,
       set_ACC, set_arith_FLAGS, store_ra;

  and and_1 (load_rb, clock5, clk_en, mul_ra__rb);
  and and_2 (load_ra, clock6, clk_en, mul_ra__rb);
  and and_3 (ALU_1101, clock6, clk_en, mul_ra__rb);
  and and_4 (load_ACC, clock7, clk_en, mul_ra__rb);
  and and_5 (enable_TMP, clock5, clk_set, mul_ra__rb);
  and and_6 (set_ACC, clock6, clk_set, mul_ra__rb);
  and and_7 (set_arith_FLAGS, clock6, clk_set, mul_ra__rb);
  and and_8 (store_ra, clock7, clk_set, mul_ra__rb);
endmodule

module div_ra__rb (
);

  wire ALU_1110, clk_en, clk_set, clock5, clock6, clock7, div_ra__rb, enable_TMP, load_ACC, load_ra, load_rb,
       set_ACC, set_arith_FLAGS, store_ra;

  and and_1 (load_rb, clock5, clk_en, div_ra__rb);
  and and_2 (load_ra, clock6, clk_en, div_ra__rb);
  and and_3 (ALU_1110, clock6, clk_en, div_ra__rb);
  and and_4 (load_ACC, clock7, clk_en, div_ra__rb);
  and and_5 (enable_TMP, clock5, clk_set, div_ra__rb);
  and and_6 (set_ACC, clock6, clk_set, div_ra__rb);
  and and_7 (set_arith_FLAGS, clock6, clk_set, div_ra__rb);
  and and_8 (store_ra, clock7, clk_set, div_ra__rb);
endmodule

module mod_ra__rb (
);

  wire ALU_1111, clk_en, clk_set, clock5, clock6, clock7, enable_TMP, load_ACC, load_ra, load_rb, mod_ra__rb,
       set_ACC, set_arith_FLAGS, store_ra;

  and and_1 (load_rb, clock5, clk_en, mod_ra__rb);
  and and_2 (load_ra, clock6, clk_en, mod_ra__rb);
  and and_3 (ALU_1111, clock6, clk_en, mod_ra__rb);
  and and_4 (load_ACC, clock7, clk_en, mod_ra__rb);
  and and_5 (enable_TMP, clock5, clk_set, mod_ra__rb);
  and and_6 (set_ACC, clock6, clk_set, mod_ra__rb);
  and and_7 (set_arith_FLAGS, clock6, clk_set, mod_ra__rb);
  and and_8 (store_ra, clock7, clk_set, mod_ra__rb);
endmodule

module mov_ra__rb (
);

  wire clk_en, clk_set, clock5, load_rb, mov_ra__rb, store_ra;

  and and_1 (load_rb, clock5, clk_en, mov_ra__rb);
  and and_2 (store_ra, clock5, clk_set, mov_ra__rb);
endmodule

module xchg_ra__rb (
);

  wire ALU_0000, clk_en, clk_set, clock5, clock6, clock7, enable_CLR, load_ACC, load_ra, load_rb, set_ACC,
       store_ra, store_rb, xchg_ra__rb;

  and and_1 (load_rb, clock5, clk_en, xchg_ra__rb);
  and and_2 (enable_CLR, clock5, clk_en, xchg_ra__rb);
  and and_3 (ALU_0000, clock5, clk_en, xchg_ra__rb);
  and and_4 (load_ra, clock6, clk_en, xchg_ra__rb);
  and and_5 (load_ACC, clock7, clk_en, xchg_ra__rb);
  and and_6 (set_ACC, clock5, clk_set, xchg_ra__rb);
  and and_7 (store_rb, clock6, clk_set, xchg_ra__rb);
  and and_8 (store_ra, clock7, clk_set, xchg_ra__rb);
endmodule

module mov_ra__imm16 (
);

  wire ALU_0000, ALU_1000, clk_en, clk_set, clock5, clock6, clock7, clock8, clock9, enable_BUS1,
       enable_carry, enable_CLR, enable_TMP1, load_ACC, load_CS, load_IAR, load_RAM, mov_ra__imm16, sel_CS,
       sel_MAR, set_ACC, set_carry, set_IAR, store_CS, store_ra;

  and and_1 (sel_CS, clock5, clk_en, mov_ra__imm16);
  and and_2 (load_IAR, clock5, clk_en, mov_ra__imm16);
  and and_3 (enable_BUS1, clock5, clk_en, mov_ra__imm16);
  and and_4 (ALU_0000, clock5, clk_en, mov_ra__imm16);
  and and_5 (set_carry, clock5, clk_en, mov_ra__imm16);
  and and_6 (load_ACC, clock6, clk_en, mov_ra__imm16);
  and and_7 (load_CS, clock7, clk_en, mov_ra__imm16);
  and and_8 (enable_CLR, clock7, clk_en, mov_ra__imm16);
  and and_9 (ALU_1000, clock7, clk_en, mov_ra__imm16);
  and and_10 (load_ACC, clock8, clk_en, mov_ra__imm16);
  and and_11 (load_RAM, clock9, clk_en, mov_ra__imm16);
  and and_12 (sel_MAR, clock5, clk_set, mov_ra__imm16);
  and and_13 (set_ACC, clock5, clk_set, mov_ra__imm16);
  and and_14 (enable_carry, clock5, clk_set, mov_ra__imm16);
  and and_15 (enable_TMP1, clock5, clk_set, mov_ra__imm16);
  and and_16 (set_IAR, clock6, clk_set, mov_ra__imm16);
  and and_17 (set_ACC, clock7, clk_set, mov_ra__imm16);
  and and_18 (store_CS, clock8, clk_set, mov_ra__imm16);
  and and_19 (store_ra, clock9, clk_set, mov_ra__imm16);
endmodule

module add_ra__imm16 (
);

  wire add_ra__imm16, ALU_0000, ALU_1000, clk_en, clk_set, clock5, clock6, clock7, clock8, clock9, clock10,
       clock11, enable_BUS1, enable_carry, enable_CLR, enable_TMP, enable_TMP1, load_ACC, load_CS, load_IAR,
       load_ra, load_RAM, sel_CS, sel_MAR, set_ACC, set_arith_flags, set_carry, set_IAR, store_CS, store_ra;

  and and_1 (sel_CS, clock5, clk_en, add_ra__imm16);
  and and_2 (load_IAR, clock5, clk_en, add_ra__imm16);
  and and_3 (enable_BUS1, clock5, clk_en, add_ra__imm16);
  and and_4 (ALU_0000, clock5, clk_en, add_ra__imm16);
  and and_5 (set_carry, clock5, clk_en, add_ra__imm16);
  and and_6 (load_ACC, clock6, clk_en, add_ra__imm16);
  and and_7 (load_CS, clock7, clk_en, add_ra__imm16);
  and and_8 (enable_CLR, clock7, clk_en, add_ra__imm16);
  and and_9 (ALU_1000, clock7, clk_en, add_ra__imm16);
  and and_10 (load_ACC, clock8, clk_en, add_ra__imm16);
  and and_11 (load_RAM, clock9, clk_en, add_ra__imm16);
  and and_12 (load_ra, clock10, clk_en, add_ra__imm16);
  and and_13 (ALU_0000, clock10, clk_en, add_ra__imm16);
  and and_14 (load_ACC, clock11, clk_en, add_ra__imm16);
  and and_15 (sel_MAR, clock5, clk_set, add_ra__imm16);
  and and_16 (set_ACC, clock5, clk_set, add_ra__imm16);
  and and_17 (enable_carry, clock5, clk_set, add_ra__imm16);
  and and_18 (enable_TMP1, clock5, clk_set, add_ra__imm16);
  and and_19 (set_IAR, clock6, clk_set, add_ra__imm16);
  and and_20 (set_ACC, clock7, clk_set, add_ra__imm16);
  and and_21 (store_CS, clock8, clk_set, add_ra__imm16);
  and and_22 (enable_TMP, clock9, clk_set, add_ra__imm16);
  and and_23 (set_ACC, clock10, clk_set, add_ra__imm16);
  and and_24 (set_arith_flags, clock10, clk_set, add_ra__imm16);
  and and_25 (store_ra, clock11, clk_set, add_ra__imm16);
endmodule

module and_ra__imm16 (
);

  wire ALU_0000, ALU_0100, ALU_1000, and_ra__imm16, clk_en, clk_set, clock5, clock6, clock7, clock8, clock9,
       clock10, clock11, enable_BUS1, enable_carry, enable_CLR, enable_TMP, enable_TMP1, load_ACC, load_CS,
       load_IAR, load_ra, load_RAM, sel_CS, sel_MAR, set_ACC, set_arith_flags, set_carry, set_IAR, store_CS,
       store_ra;

  and and_1 (sel_CS, clock5, clk_en, and_ra__imm16);
  and and_2 (load_IAR, clock5, clk_en, and_ra__imm16);
  and and_3 (enable_BUS1, clock5, clk_en, and_ra__imm16);
  and and_4 (ALU_0000, clock5, clk_en, and_ra__imm16);
  and and_5 (set_carry, clock5, clk_en, and_ra__imm16);
  and and_6 (load_ACC, clock6, clk_en, and_ra__imm16);
  and and_7 (load_CS, clock7, clk_en, and_ra__imm16);
  and and_8 (enable_CLR, clock7, clk_en, and_ra__imm16);
  and and_9 (ALU_1000, clock7, clk_en, and_ra__imm16);
  and and_10 (load_ACC, clock8, clk_en, and_ra__imm16);
  and and_11 (load_RAM, clock9, clk_en, and_ra__imm16);
  and and_12 (load_ra, clock10, clk_en, and_ra__imm16);
  and and_13 (ALU_0100, clock10, clk_en, and_ra__imm16);
  and and_14 (load_ACC, clock11, clk_en, and_ra__imm16);
  and and_15 (sel_MAR, clock5, clk_set, and_ra__imm16);
  and and_16 (set_ACC, clock5, clk_set, and_ra__imm16);
  and and_17 (enable_carry, clock5, clk_set, and_ra__imm16);
  and and_18 (enable_TMP1, clock5, clk_set, and_ra__imm16);
  and and_19 (set_IAR, clock6, clk_set, and_ra__imm16);
  and and_20 (set_ACC, clock7, clk_set, and_ra__imm16);
  and and_21 (store_CS, clock8, clk_set, and_ra__imm16);
  and and_22 (enable_TMP, clock9, clk_set, and_ra__imm16);
  and and_23 (set_ACC, clock10, clk_set, and_ra__imm16);
  and and_24 (set_arith_flags, clock10, clk_set, and_ra__imm16);
  and and_25 (store_ra, clock11, clk_set, and_ra__imm16);
endmodule

module or_ra__imm16 (
);

  wire ALU_0000, ALU_0101, ALU_1000, clk_en, clk_set, clock5, clock6, clock7, clock8, clock9, clock10,
       clock11, enable_BUS1, enable_carry, enable_CLR, enable_TMP, enable_TMP1, load_ACC, load_CS, load_IAR,
       load_ra, load_RAM, or_ra__imm16, sel_CS, sel_MAR, set_ACC, set_arith_flags, set_carry, set_IAR,
       store_CS, store_ra;

  and and_1 (sel_CS, clock5, clk_en, or_ra__imm16);
  and and_2 (load_IAR, clock5, clk_en, or_ra__imm16);
  and and_3 (enable_BUS1, clock5, clk_en, or_ra__imm16);
  and and_4 (ALU_0000, clock5, clk_en, or_ra__imm16);
  and and_5 (set_carry, clock5, clk_en, or_ra__imm16);
  and and_6 (load_ACC, clock6, clk_en, or_ra__imm16);
  and and_7 (load_CS, clock7, clk_en, or_ra__imm16);
  and and_8 (enable_CLR, clock7, clk_en, or_ra__imm16);
  and and_9 (ALU_1000, clock7, clk_en, or_ra__imm16);
  and and_10 (load_ACC, clock8, clk_en, or_ra__imm16);
  and and_11 (load_RAM, clock9, clk_en, or_ra__imm16);
  and and_12 (load_ra, clock10, clk_en, or_ra__imm16);
  and and_13 (ALU_0101, clock10, clk_en, or_ra__imm16);
  and and_14 (load_ACC, clock11, clk_en, or_ra__imm16);
  and and_15 (sel_MAR, clock5, clk_set, or_ra__imm16);
  and and_16 (set_ACC, clock5, clk_set, or_ra__imm16);
  and and_17 (enable_carry, clock5, clk_set, or_ra__imm16);
  and and_18 (enable_TMP1, clock5, clk_set, or_ra__imm16);
  and and_19 (set_IAR, clock6, clk_set, or_ra__imm16);
  and and_20 (set_ACC, clock7, clk_set, or_ra__imm16);
  and and_21 (store_CS, clock8, clk_set, or_ra__imm16);
  and and_22 (enable_TMP, clock9, clk_set, or_ra__imm16);
  and and_23 (set_ACC, clock10, clk_set, or_ra__imm16);
  and and_24 (set_arith_flags, clock10, clk_set, or_ra__imm16);
  and and_25 (store_ra, clock11, clk_set, or_ra__imm16);
endmodule

module xor_ra__imm16 (
);

  wire ALU_0000, ALU_0110, ALU_1000, clk_en, clk_set, clock5, clock6, clock7, clock8, clock9, clock10,
       clock11, enable_BUS1, enable_carry, enable_CLR, enable_TMP, enable_TMP1, load_ACC, load_CS, load_IAR,
       load_ra, load_RAM, sel_CS, sel_MAR, set_ACC, set_arith_flags, set_carry, set_IAR, store_CS, store_ra,
       xor_ra__imm16;

  and and_1 (sel_CS, clock5, clk_en, xor_ra__imm16);
  and and_2 (load_IAR, clock5, clk_en, xor_ra__imm16);
  and and_3 (enable_BUS1, clock5, clk_en, xor_ra__imm16);
  and and_4 (ALU_0000, clock5, clk_en, xor_ra__imm16);
  and and_5 (set_carry, clock5, clk_en, xor_ra__imm16);
  and and_6 (load_ACC, clock6, clk_en, xor_ra__imm16);
  and and_7 (load_CS, clock7, clk_en, xor_ra__imm16);
  and and_8 (enable_CLR, clock7, clk_en, xor_ra__imm16);
  and and_9 (ALU_1000, clock7, clk_en, xor_ra__imm16);
  and and_10 (load_ACC, clock8, clk_en, xor_ra__imm16);
  and and_11 (load_RAM, clock9, clk_en, xor_ra__imm16);
  and and_12 (load_ra, clock10, clk_en, xor_ra__imm16);
  and and_13 (ALU_0110, clock10, clk_en, xor_ra__imm16);
  and and_14 (load_ACC, clock11, clk_en, xor_ra__imm16);
  and and_15 (sel_MAR, clock5, clk_set, xor_ra__imm16);
  and and_16 (set_ACC, clock5, clk_set, xor_ra__imm16);
  and and_17 (enable_carry, clock5, clk_set, xor_ra__imm16);
  and and_18 (enable_TMP1, clock5, clk_set, xor_ra__imm16);
  and and_19 (set_IAR, clock6, clk_set, xor_ra__imm16);
  and and_20 (set_ACC, clock7, clk_set, xor_ra__imm16);
  and and_21 (store_CS, clock8, clk_set, xor_ra__imm16);
  and and_22 (enable_TMP, clock9, clk_set, xor_ra__imm16);
  and and_23 (set_ACC, clock10, clk_set, xor_ra__imm16);
  and and_24 (set_arith_flags, clock10, clk_set, xor_ra__imm16);
  and and_25 (store_ra, clock11, clk_set, xor_ra__imm16);
endmodule

module cmp_ra__imm16 (
);

  wire ALU_0000, ALU_0111, ALU_1000, clk_en, clk_set, clock5, clock6, clock7, clock8, clock9, clock10,
       cmp_ra__imm16, enable_BUS1, enable_carry, enable_CLR, enable_TMP, enable_TMP1, load_ACC, load_CS,
       load_IAR, load_ra, load_RAM, sel_CS, sel_MAR, set_ACC, set_arith_flags, set_carry, set_IAR, store_CS;

  and and_1 (sel_CS, clock5, clk_en, cmp_ra__imm16);
  and and_2 (load_IAR, clock5, clk_en, cmp_ra__imm16);
  and and_3 (enable_BUS1, clock5, clk_en, cmp_ra__imm16);
  and and_4 (ALU_0000, clock5, clk_en, cmp_ra__imm16);
  and and_5 (set_carry, clock5, clk_en, cmp_ra__imm16);
  and and_6 (load_ACC, clock6, clk_en, cmp_ra__imm16);
  and and_7 (load_CS, clock7, clk_en, cmp_ra__imm16);
  and and_8 (enable_CLR, clock7, clk_en, cmp_ra__imm16);
  and and_9 (ALU_1000, clock7, clk_en, cmp_ra__imm16);
  and and_10 (load_ACC, clock8, clk_en, cmp_ra__imm16);
  and and_11 (load_RAM, clock9, clk_en, cmp_ra__imm16);
  and and_12 (load_ra, clock10, clk_en, cmp_ra__imm16);
  and and_13 (ALU_0111, clock10, clk_en, cmp_ra__imm16);
  and and_14 (sel_MAR, clock5, clk_set, cmp_ra__imm16);
  and and_15 (set_ACC, clock5, clk_set, cmp_ra__imm16);
  and and_16 (enable_carry, clock5, clk_set, cmp_ra__imm16);
  and and_17 (enable_TMP1, clock5, clk_set, cmp_ra__imm16);
  and and_18 (set_IAR, clock6, clk_set, cmp_ra__imm16);
  and and_19 (set_ACC, clock7, clk_set, cmp_ra__imm16);
  and and_20 (store_CS, clock8, clk_set, cmp_ra__imm16);
  and and_21 (enable_TMP, clock9, clk_set, cmp_ra__imm16);
  and and_22 (set_ACC, clock10, clk_set, cmp_ra__imm16);
  and and_23 (set_arith_flags, clock10, clk_set, cmp_ra__imm16);
endmodule

module adc_ra__imm16 (
);

  wire adc_ra__imm16, add_ra__imm16, ALU_0000, ALU_1000, clk_en, clk_set, clock5, clock6, clock7, clock8,
       clock9, clock10, clock11, enable_arith_carry, enable_BUS1, enable_carry, enable_CLR, enable_TMP,
       enable_TMP1, load_ACC, load_CS, load_IAR, load_ra, load_RAM, sel_CS, sel_MAR, set_ACC,
       set_arith_flags, set_carry, set_IAR, store_CS, store_ra;

  and and_1 (sel_CS, clock5, clk_en, add_ra__imm16);
  and and_2 (load_IAR, clock5, clk_en, add_ra__imm16);
  and and_3 (enable_BUS1, clock5, clk_en, add_ra__imm16);
  and and_4 (ALU_0000, clock5, clk_en, add_ra__imm16);
  and and_5 (set_carry, clock5, clk_en, add_ra__imm16);
  and and_6 (load_ACC, clock6, clk_en, adc_ra__imm16);
  and and_7 (load_CS, clock7, clk_en, adc_ra__imm16);
  and and_8 (enable_CLR, clock7, clk_en, adc_ra__imm16);
  and and_9 (ALU_1000, clock7, clk_en, adc_ra__imm16);
  and and_10 (load_ACC, clock8, clk_en, adc_ra__imm16);
  and and_11 (load_RAM, clock9, clk_en, adc_ra__imm16);
  and and_12 (enable_arith_carry, clock9, clk_en, adc_ra__imm16);
  and and_13 (load_ra, clock10, clk_en, adc_ra__imm16);
  and and_14 (ALU_1000, clock10, clk_en, adc_ra__imm16);
  and and_15 (load_ACC, clock11, clk_en, adc_ra__imm16);
  and and_16 (sel_MAR, clock5, clk_set, add_ra__imm16);
  and and_17 (set_ACC, clock5, clk_set, add_ra__imm16);
  and and_18 (enable_carry, clock5, clk_set, add_ra__imm16);
  and and_19 (enable_TMP1, clock5, clk_set, add_ra__imm16);
  and and_20 (set_IAR, clock6, clk_set, adc_ra__imm16);
  and and_21 (set_ACC, clock7, clk_set, adc_ra__imm16);
  and and_22 (store_CS, clock8, clk_set, adc_ra__imm16);
  and and_23 (enable_TMP, clock9, clk_set, adc_ra__imm16);
  and and_24 (enable_TMP1, clock9, clk_set, adc_ra__imm16);
  and and_25 (set_ACC, clock10, clk_set, adc_ra__imm16);
  and and_26 (set_arith_flags, clock10, clk_set, adc_ra__imm16);
  and and_27 (store_ra, clock11, clk_set, adc_ra__imm16);
endmodule

module sub_ra__imm16 (
);

  wire ALU_0000, ALU_1000, ALU_1100, clk_en, clk_set, clock5, clock6, clock7, clock8, clock9, clock10,
       clock11, enable_BUS1, enable_carry, enable_CLR, enable_TMP, enable_TMP1, load_ACC, load_CS, load_IAR,
       load_ra, load_RAM, sel_CS, sel_MAR, set_ACC, set_arith_flags, set_carry, set_IAR, store_CS, store_ra,
       sub_ra__imm16;

  and and_1 (sel_CS, clock5, clk_en, sub_ra__imm16);
  and and_2 (load_IAR, clock5, clk_en, sub_ra__imm16);
  and and_3 (enable_BUS1, clock5, clk_en, sub_ra__imm16);
  and and_4 (ALU_0000, clock5, clk_en, sub_ra__imm16);
  and and_5 (set_carry, clock5, clk_en, sub_ra__imm16);
  and and_6 (load_ACC, clock6, clk_en, sub_ra__imm16);
  and and_7 (load_CS, clock7, clk_en, sub_ra__imm16);
  and and_8 (enable_CLR, clock7, clk_en, sub_ra__imm16);
  and and_9 (ALU_1000, clock7, clk_en, sub_ra__imm16);
  and and_10 (load_ACC, clock8, clk_en, sub_ra__imm16);
  and and_11 (load_RAM, clock9, clk_en, sub_ra__imm16);
  and and_12 (load_ra, clock10, clk_en, sub_ra__imm16);
  and and_13 (ALU_1100, clock10, clk_en, sub_ra__imm16);
  and and_14 (load_ACC, clock11, clk_en, sub_ra__imm16);
  and and_15 (sel_MAR, clock5, clk_set, sub_ra__imm16);
  and and_16 (set_ACC, clock5, clk_set, sub_ra__imm16);
  and and_17 (enable_carry, clock5, clk_set, sub_ra__imm16);
  and and_18 (enable_TMP1, clock5, clk_set, sub_ra__imm16);
  and and_19 (set_IAR, clock6, clk_set, sub_ra__imm16);
  and and_20 (set_ACC, clock7, clk_set, sub_ra__imm16);
  and and_21 (store_CS, clock8, clk_set, sub_ra__imm16);
  and and_22 (enable_TMP, clock9, clk_set, sub_ra__imm16);
  and and_23 (set_ACC, clock10, clk_set, sub_ra__imm16);
  and and_24 (set_arith_flags, clock10, clk_set, sub_ra__imm16);
  and and_25 (store_ra, clock11, clk_set, sub_ra__imm16);
endmodule

module mul_ra__imm16 (
);

  wire ALU_0000, ALU_1000, ALU_1101, clk_en, clk_set, clock5, clock6, clock7, clock8, clock9, clock10,
       clock11, enable_BUS1, enable_carry, enable_CLR, enable_TMP, enable_TMP1, load_ACC, load_CS, load_IAR,
       load_ra, load_RAM, mul_ra__imm16, sel_CS, sel_MAR, set_ACC, set_arith_flags, set_carry, set_IAR,
       store_CS, store_ra;

  and and_1 (sel_CS, clock5, clk_en, mul_ra__imm16);
  and and_2 (load_IAR, clock5, clk_en, mul_ra__imm16);
  and and_3 (enable_BUS1, clock5, clk_en, mul_ra__imm16);
  and and_4 (ALU_0000, clock5, clk_en, mul_ra__imm16);
  and and_5 (set_carry, clock5, clk_en, mul_ra__imm16);
  and and_6 (load_ACC, clock6, clk_en, mul_ra__imm16);
  and and_7 (load_CS, clock7, clk_en, mul_ra__imm16);
  and and_8 (enable_CLR, clock7, clk_en, mul_ra__imm16);
  and and_9 (ALU_1000, clock7, clk_en, mul_ra__imm16);
  and and_10 (load_ACC, clock8, clk_en, mul_ra__imm16);
  and and_11 (load_RAM, clock9, clk_en, mul_ra__imm16);
  and and_12 (load_ra, clock10, clk_en, mul_ra__imm16);
  and and_13 (ALU_1101, clock10, clk_en, mul_ra__imm16);
  and and_14 (load_ACC, clock11, clk_en, mul_ra__imm16);
  and and_15 (sel_MAR, clock5, clk_set, mul_ra__imm16);
  and and_16 (set_ACC, clock5, clk_set, mul_ra__imm16);
  and and_17 (enable_carry, clock5, clk_set, mul_ra__imm16);
  and and_18 (enable_TMP1, clock5, clk_set, mul_ra__imm16);
  and and_19 (set_IAR, clock6, clk_set, mul_ra__imm16);
  and and_20 (set_ACC, clock7, clk_set, mul_ra__imm16);
  and and_21 (store_CS, clock8, clk_set, mul_ra__imm16);
  and and_22 (enable_TMP, clock9, clk_set, mul_ra__imm16);
  and and_23 (set_ACC, clock10, clk_set, mul_ra__imm16);
  and and_24 (set_arith_flags, clock10, clk_set, mul_ra__imm16);
  and and_25 (store_ra, clock11, clk_set, mul_ra__imm16);
endmodule

module div_ra__imm16 (
);

  wire ALU_0000, ALU_1000, ALU_1110, clk_en, clk_set, clock5, clock6, clock7, clock8, clock9, clock10,
       clock11, div_ra__imm16, enable_BUS1, enable_carry, enable_CLR, enable_TMP, enable_TMP1, load_ACC,
       load_CS, load_IAR, load_ra, load_RAM, sel_CS, sel_MAR, set_ACC, set_arith_flags, set_carry, set_IAR,
       store_CS, store_ra;

  and and_1 (sel_CS, clock5, clk_en, div_ra__imm16);
  and and_2 (load_IAR, clock5, clk_en, div_ra__imm16);
  and and_3 (enable_BUS1, clock5, clk_en, div_ra__imm16);
  and and_4 (ALU_0000, clock5, clk_en, div_ra__imm16);
  and and_5 (set_carry, clock5, clk_en, div_ra__imm16);
  and and_6 (load_ACC, clock6, clk_en, div_ra__imm16);
  and and_7 (load_CS, clock7, clk_en, div_ra__imm16);
  and and_8 (enable_CLR, clock7, clk_en, div_ra__imm16);
  and and_9 (ALU_1000, clock7, clk_en, div_ra__imm16);
  and and_10 (load_ACC, clock8, clk_en, div_ra__imm16);
  and and_11 (load_RAM, clock9, clk_en, div_ra__imm16);
  and and_12 (load_ra, clock10, clk_en, div_ra__imm16);
  and and_13 (ALU_1110, clock10, clk_en, div_ra__imm16);
  and and_14 (load_ACC, clock11, clk_en, div_ra__imm16);
  and and_15 (sel_MAR, clock5, clk_set, div_ra__imm16);
  and and_16 (set_ACC, clock5, clk_set, div_ra__imm16);
  and and_17 (enable_carry, clock5, clk_set, div_ra__imm16);
  and and_18 (enable_TMP1, clock5, clk_set, div_ra__imm16);
  and and_19 (set_IAR, clock6, clk_set, div_ra__imm16);
  and and_20 (set_ACC, clock7, clk_set, div_ra__imm16);
  and and_21 (store_CS, clock8, clk_set, div_ra__imm16);
  and and_22 (enable_TMP, clock9, clk_set, div_ra__imm16);
  and and_23 (set_ACC, clock10, clk_set, div_ra__imm16);
  and and_24 (set_arith_flags, clock10, clk_set, div_ra__imm16);
  and and_25 (store_ra, clock11, clk_set, div_ra__imm16);
endmodule

module mod_ra__imm16 (
);

  wire ALU_0000, ALU_1000, ALU_1111, clk_en, clk_set, clock5, clock6, clock7, clock8, clock9, clock10,
       clock11, enable_BUS1, enable_carry, enable_CLR, enable_TMP, enable_TMP1, load_ACC, load_CS, load_IAR,
       load_ra, load_RAM, mod_ra__imm16, sel_CS, sel_MAR, set_ACC, set_arith_flags, set_carry, set_IAR,
       store_CS, store_ra;

  and and_1 (sel_CS, clock5, clk_en, mod_ra__imm16);
  and and_2 (load_IAR, clock5, clk_en, mod_ra__imm16);
  and and_3 (enable_BUS1, clock5, clk_en, mod_ra__imm16);
  and and_4 (ALU_0000, clock5, clk_en, mod_ra__imm16);
  and and_5 (set_carry, clock5, clk_en, mod_ra__imm16);
  and and_6 (load_ACC, clock6, clk_en, mod_ra__imm16);
  and and_7 (load_CS, clock7, clk_en, mod_ra__imm16);
  and and_8 (enable_CLR, clock7, clk_en, mod_ra__imm16);
  and and_9 (ALU_1000, clock7, clk_en, mod_ra__imm16);
  and and_10 (load_ACC, clock8, clk_en, mod_ra__imm16);
  and and_11 (load_RAM, clock9, clk_en, mod_ra__imm16);
  and and_12 (load_ra, clock10, clk_en, mod_ra__imm16);
  and and_13 (ALU_1111, clock10, clk_en, mod_ra__imm16);
  and and_14 (load_ACC, clock11, clk_en, mod_ra__imm16);
  and and_15 (sel_MAR, clock5, clk_set, mod_ra__imm16);
  and and_16 (set_ACC, clock5, clk_set, mod_ra__imm16);
  and and_17 (enable_carry, clock5, clk_set, mod_ra__imm16);
  and and_18 (enable_TMP1, clock5, clk_set, mod_ra__imm16);
  and and_19 (set_IAR, clock6, clk_set, mod_ra__imm16);
  and and_20 (set_ACC, clock7, clk_set, mod_ra__imm16);
  and and_21 (store_CS, clock8, clk_set, mod_ra__imm16);
  and and_22 (enable_TMP, clock9, clk_set, mod_ra__imm16);
  and and_23 (set_ACC, clock10, clk_set, mod_ra__imm16);
  and and_24 (set_arith_flags, clock10, clk_set, mod_ra__imm16);
  and and_25 (store_ra, clock11, clk_set, mod_ra__imm16);
endmodule

module mov_ra__byte__rb_imm16 (
);

  wire ALU_0000, ALU_0100, ALU_1000, clk_en, clk_set, clock5, clock6, clock7, clock8, clock9, clock10,
       clock11, clock12, enable_BUS1, enable_carry, enable_CLR, enable_lowmask, enable_TMP1, load_ACC,
       load_CS, load_IAR, load_ra, load_RAM, mov_ra__byte__rb_imm16, sel_CS, sel_MAR, sel_rb, set_ACC,
       set_carry, set_IAR, store_CS, store_ra;

  and and_1 (sel_CS, clock5, clk_en, mov_ra__byte__rb_imm16);
  and and_2 (load_IAR, clock5, clk_en, mov_ra__byte__rb_imm16);
  and and_3 (enable_BUS1, clock5, clk_en, mov_ra__byte__rb_imm16);
  and and_4 (ALU_0000, clock5, clk_en, mov_ra__byte__rb_imm16);
  and and_5 (set_carry, clock5, clk_en, mov_ra__byte__rb_imm16);
  and and_6 (load_ACC, clock6, clk_en, mov_ra__byte__rb_imm16);
  and and_7 (load_CS, clock7, clk_en, mov_ra__byte__rb_imm16);
  and and_8 (enable_CLR, clock7, clk_en, mov_ra__byte__rb_imm16);
  and and_9 (ALU_1000, clock7, clk_en, mov_ra__byte__rb_imm16);
  and and_10 (load_ACC, clock8, clk_en, mov_ra__byte__rb_imm16);
  and and_11 (sel_rb, clock9, clk_en, mov_ra__byte__rb_imm16);
  and and_12 (load_RAM, clock9, clk_en, mov_ra__byte__rb_imm16);
  and and_13 (load_RAM, clock10, clk_en, mov_ra__byte__rb_imm16);
  and and_14 (load_ra, clock11, clk_en, mov_ra__byte__rb_imm16);
  and and_15 (enable_lowmask, clock11, clk_en, mov_ra__byte__rb_imm16);
  and and_16 (ALU_0100, clock11, clk_en, mov_ra__byte__rb_imm16);
  and and_17 (load_ACC, clock12, clk_en, mov_ra__byte__rb_imm16);
  and and_18 (sel_MAR, clock5, clk_set, mov_ra__byte__rb_imm16);
  and and_19 (set_ACC, clock5, clk_set, mov_ra__byte__rb_imm16);
  and and_20 (enable_carry, clock5, clk_set, mov_ra__byte__rb_imm16);
  and and_21 (enable_TMP1, clock5, clk_set, mov_ra__byte__rb_imm16);
  and and_22 (set_IAR, clock6, clk_set, mov_ra__byte__rb_imm16);
  and and_23 (set_ACC, clock7, clk_set, mov_ra__byte__rb_imm16);
  and and_24 (store_CS, clock8, clk_set, mov_ra__byte__rb_imm16);
  and and_25 (sel_MAR, clock9, clk_set, mov_ra__byte__rb_imm16);
  and and_26 (store_ra, clock10, clk_set, mov_ra__byte__rb_imm16);
  and and_27 (set_ACC, clock11, clk_set, mov_ra__byte__rb_imm16);
  and and_28 (store_ra, clock12, clk_set, mov_ra__byte__rb_imm16);
endmodule

module mov_ra__word__rb_imm16 (
);

  wire ALU_0000, ALU_1000, clk_en, clk_set, clock5, clock6, clock7, clock8, clock9, clock10, enable_BUS1,
       enable_carry, enable_CLR, enable_TMP1, load_ACC, load_CS, load_IAR, load_RAM, mov_ra__word__rb_imm16,
       sel_CS, sel_MAR, sel_rb, set_ACC, set_carry, set_IAR, store_CS, store_ra;

  and and_1 (sel_CS, clock5, clk_en, mov_ra__word__rb_imm16);
  and and_2 (load_IAR, clock5, clk_en, mov_ra__word__rb_imm16);
  and and_3 (enable_BUS1, clock5, clk_en, mov_ra__word__rb_imm16);
  and and_4 (ALU_0000, clock5, clk_en, mov_ra__word__rb_imm16);
  and and_5 (set_carry, clock5, clk_en, mov_ra__word__rb_imm16);
  and and_6 (load_ACC, clock6, clk_en, mov_ra__word__rb_imm16);
  and and_7 (load_CS, clock7, clk_en, mov_ra__word__rb_imm16);
  and and_8 (enable_CLR, clock7, clk_en, mov_ra__word__rb_imm16);
  and and_9 (ALU_1000, clock7, clk_en, mov_ra__word__rb_imm16);
  and and_10 (load_ACC, clock8, clk_en, mov_ra__word__rb_imm16);
  and and_11 (sel_rb, clock9, clk_en, mov_ra__word__rb_imm16);
  and and_12 (load_RAM, clock9, clk_en, mov_ra__word__rb_imm16);
  and and_13 (load_RAM, clock10, clk_en, mov_ra__word__rb_imm16);
  and and_14 (sel_MAR, clock5, clk_set, mov_ra__word__rb_imm16);
  and and_15 (set_ACC, clock5, clk_set, mov_ra__word__rb_imm16);
  and and_16 (enable_carry, clock5, clk_set, mov_ra__word__rb_imm16);
  and and_17 (enable_TMP1, clock5, clk_set, mov_ra__word__rb_imm16);
  and and_18 (set_IAR, clock6, clk_set, mov_ra__word__rb_imm16);
  and and_19 (set_ACC, clock7, clk_set, mov_ra__word__rb_imm16);
  and and_20 (store_CS, clock8, clk_set, mov_ra__word__rb_imm16);
  and and_21 (sel_MAR, clock9, clk_set, mov_ra__word__rb_imm16);
  and and_22 (store_ra, clock10, clk_set, mov_ra__word__rb_imm16);
endmodule

module mov_word__ra___rb (
);

  wire clk_en, clk_set, clock5, clock6, load_ra, load_rb, mov_word__ra___rb, sel_DS, sel_MAR, store_RAM;

  and and_1 (sel_DS, clock5, clk_en, mov_word__ra___rb);
  and and_2 (load_ra, clock5, clk_en, mov_word__ra___rb);
  and and_3 (load_rb, clock6, clk_en, mov_word__ra___rb);
  and and_4 (sel_MAR, clock5, clk_set, mov_word__ra___rb);
  and and_5 (store_RAM, clock6, clk_set, mov_word__ra___rb);
endmodule

module shr_word__ra_rb___imm4 (
);

  wire ALU_0000, ALU_0001, ALU_1000, clk_en, clk_set, clock5, clock6, clock7, clock8, clock9, clock10,
       clock11, clock12, enable_BUS1, enable_carry, enable_CLR, enable_TMP, enable_TMP1, load_ACC, load_cs,
       load_IAR, load_ra, load_RAM, load_rb, sel_cs, sel_MAR, sel_ra, set_ACC, set_arith_flags, set_carry,
       set_IAR, shr_word__ra_rb___imm4, store_cs, store_RAM;

  and and_1 (sel_cs, clock5, clk_en, shr_word__ra_rb___imm4);
  and and_2 (load_IAR, clock5, clk_en, shr_word__ra_rb___imm4);
  and and_3 (enable_BUS1, clock5, clk_en, shr_word__ra_rb___imm4);
  and and_4 (ALU_0000, clock5, clk_en, shr_word__ra_rb___imm4);
  and and_5 (set_carry, clock5, clk_en, shr_word__ra_rb___imm4);
  and and_6 (load_ACC, clock6, clk_en, shr_word__ra_rb___imm4);
  and and_7 (load_cs, clock7, clk_en, shr_word__ra_rb___imm4);
  and and_8 (enable_CLR, clock7, clk_en, shr_word__ra_rb___imm4);
  and and_9 (ALU_1000, clock7, clk_en, shr_word__ra_rb___imm4);
  and and_10 (load_ACC, clock8, clk_en, shr_word__ra_rb___imm4);
  and and_11 (load_RAM, clock9, clk_en, shr_word__ra_rb___imm4);
  and and_12 (sel_ra, clock10, clk_en, shr_word__ra_rb___imm4);
  and and_13 (load_rb, clock10, clk_en, shr_word__ra_rb___imm4);
  and and_14 (load_ra, clock11, clk_en, shr_word__ra_rb___imm4);
  and and_15 (ALU_0001, clock11, clk_en, shr_word__ra_rb___imm4);
  and and_16 (load_ACC, clock12, clk_en, shr_word__ra_rb___imm4);
  and and_17 (sel_MAR, clock5, clk_set, shr_word__ra_rb___imm4);
  and and_18 (set_ACC, clock5, clk_set, shr_word__ra_rb___imm4);
  and and_19 (enable_carry, clock5, clk_set, shr_word__ra_rb___imm4);
  and and_20 (enable_TMP1, clock5, clk_set, shr_word__ra_rb___imm4);
  and and_21 (set_IAR, clock6, clk_set, shr_word__ra_rb___imm4);
  and and_22 (set_ACC, clock7, clk_set, shr_word__ra_rb___imm4);
  and and_23 (store_cs, clock8, clk_set, shr_word__ra_rb___imm4);
  and and_24 (enable_TMP, clock9, clk_set, shr_word__ra_rb___imm4);
  and and_25 (sel_MAR, clock10, clk_set, shr_word__ra_rb___imm4);
  and and_26 (set_ACC, clock11, clk_set, shr_word__ra_rb___imm4);
  and and_27 (set_arith_flags, clock11, clk_set, shr_word__ra_rb___imm4);
  and and_28 (store_RAM, clock12, clk_set, shr_word__ra_rb___imm4);
endmodule

module shl_word__ra_rb___imm4 (
);

  wire ALU_0000, ALU_0010, ALU_1000, clk_en, clk_set, clock5, clock6, clock7, clock8, clock9, clock10,
       clock11, clock12, enable_BUS1, enable_carry, enable_CLR, enable_TMP, enable_TMP1, load_ACC, load_cs,
       load_IAR, load_ra, load_RAM, load_rb, sel_cs, sel_MAR, sel_ra, set_ACC, set_arith_flags, set_carry,
       set_IAR, shl_word__ra_rb___imm4, store_cs, store_RAM;

  and and_1 (sel_cs, clock5, clk_en, shl_word__ra_rb___imm4);
  and and_2 (load_IAR, clock5, clk_en, shl_word__ra_rb___imm4);
  and and_3 (enable_BUS1, clock5, clk_en, shl_word__ra_rb___imm4);
  and and_4 (ALU_0000, clock5, clk_en, shl_word__ra_rb___imm4);
  and and_5 (set_carry, clock5, clk_en, shl_word__ra_rb___imm4);
  and and_6 (load_ACC, clock6, clk_en, shl_word__ra_rb___imm4);
  and and_7 (load_cs, clock7, clk_en, shl_word__ra_rb___imm4);
  and and_8 (enable_CLR, clock7, clk_en, shl_word__ra_rb___imm4);
  and and_9 (ALU_1000, clock7, clk_en, shl_word__ra_rb___imm4);
  and and_10 (load_ACC, clock8, clk_en, shl_word__ra_rb___imm4);
  and and_11 (load_RAM, clock9, clk_en, shl_word__ra_rb___imm4);
  and and_12 (sel_ra, clock10, clk_en, shl_word__ra_rb___imm4);
  and and_13 (load_rb, clock10, clk_en, shl_word__ra_rb___imm4);
  and and_14 (load_ra, clock11, clk_en, shl_word__ra_rb___imm4);
  and and_15 (ALU_0010, clock11, clk_en, shl_word__ra_rb___imm4);
  and and_16 (load_ACC, clock12, clk_en, shl_word__ra_rb___imm4);
  and and_17 (sel_MAR, clock5, clk_set, shl_word__ra_rb___imm4);
  and and_18 (set_ACC, clock5, clk_set, shl_word__ra_rb___imm4);
  and and_19 (enable_carry, clock5, clk_set, shl_word__ra_rb___imm4);
  and and_20 (enable_TMP1, clock5, clk_set, shl_word__ra_rb___imm4);
  and and_21 (set_IAR, clock6, clk_set, shl_word__ra_rb___imm4);
  and and_22 (set_ACC, clock7, clk_set, shl_word__ra_rb___imm4);
  and and_23 (store_cs, clock8, clk_set, shl_word__ra_rb___imm4);
  and and_24 (enable_TMP, clock9, clk_set, shl_word__ra_rb___imm4);
  and and_25 (sel_MAR, clock10, clk_set, shl_word__ra_rb___imm4);
  and and_26 (set_ACC, clock11, clk_set, shl_word__ra_rb___imm4);
  and and_27 (set_arith_flags, clock11, clk_set, shl_word__ra_rb___imm4);
  and and_28 (store_RAM, clock12, clk_set, shl_word__ra_rb___imm4);
endmodule

module sar_word__ra_rb___imm4 (
);

  wire ALU_0000, ALU_1000, ALU_1001, clk_en, clk_set, clock5, clock6, clock7, clock8, clock9, clock10,
       clock11, clock12, enable_BUS1, enable_carry, enable_CLR, enable_TMP, enable_TMP1, load_ACC, load_cs,
       load_IAR, load_ra, load_RAM, load_rb, sar_word__ra_rb___imm4, sel_cs, sel_MAR, sel_ra, set_ACC,
       set_arith_flags, set_carry, set_IAR, store_cs, store_RAM;

  and and_1 (sel_cs, clock5, clk_en, sar_word__ra_rb___imm4);
  and and_2 (load_IAR, clock5, clk_en, sar_word__ra_rb___imm4);
  and and_3 (enable_BUS1, clock5, clk_en, sar_word__ra_rb___imm4);
  and and_4 (ALU_0000, clock5, clk_en, sar_word__ra_rb___imm4);
  and and_5 (set_carry, clock5, clk_en, sar_word__ra_rb___imm4);
  and and_6 (load_ACC, clock6, clk_en, sar_word__ra_rb___imm4);
  and and_7 (load_cs, clock7, clk_en, sar_word__ra_rb___imm4);
  and and_8 (enable_CLR, clock7, clk_en, sar_word__ra_rb___imm4);
  and and_9 (ALU_1000, clock7, clk_en, sar_word__ra_rb___imm4);
  and and_10 (load_ACC, clock8, clk_en, sar_word__ra_rb___imm4);
  and and_11 (load_RAM, clock9, clk_en, sar_word__ra_rb___imm4);
  and and_12 (sel_ra, clock10, clk_en, sar_word__ra_rb___imm4);
  and and_13 (load_rb, clock10, clk_en, sar_word__ra_rb___imm4);
  and and_14 (load_ra, clock11, clk_en, sar_word__ra_rb___imm4);
  and and_15 (ALU_1001, clock11, clk_en, sar_word__ra_rb___imm4);
  and and_16 (load_ACC, clock12, clk_en, sar_word__ra_rb___imm4);
  and and_17 (sel_MAR, clock5, clk_set, sar_word__ra_rb___imm4);
  and and_18 (set_ACC, clock5, clk_set, sar_word__ra_rb___imm4);
  and and_19 (enable_carry, clock5, clk_set, sar_word__ra_rb___imm4);
  and and_20 (enable_TMP1, clock5, clk_set, sar_word__ra_rb___imm4);
  and and_21 (set_IAR, clock6, clk_set, sar_word__ra_rb___imm4);
  and and_22 (set_ACC, clock7, clk_set, sar_word__ra_rb___imm4);
  and and_23 (store_cs, clock8, clk_set, sar_word__ra_rb___imm4);
  and and_24 (enable_TMP, clock9, clk_set, sar_word__ra_rb___imm4);
  and and_25 (sel_MAR, clock10, clk_set, sar_word__ra_rb___imm4);
  and and_26 (set_ACC, clock11, clk_set, sar_word__ra_rb___imm4);
  and and_27 (set_arith_flags, clock11, clk_set, sar_word__ra_rb___imm4);
  and and_28 (store_RAM, clock12, clk_set, sar_word__ra_rb___imm4);
endmodule

module flip_word__ra_rb (
);

  wire ALU_0011, clk_en, clk_set, clock5, clock6, clock7, flip_word__ra_rb, load_ACC, load_RAM, load_rb,
       sel_MAR, sel_ra, set_ACC, set_arith_flags, store_RAM;

  and and_1 (sel_ra, clock5, clk_en, flip_word__ra_rb);
  and and_2 (load_rb, clock5, clk_en, flip_word__ra_rb);
  and and_3 (load_RAM, clock6, clk_en, flip_word__ra_rb);
  and and_4 (ALU_0011, clock6, clk_en, flip_word__ra_rb);
  and and_5 (load_ACC, clock7, clk_en, flip_word__ra_rb);
  and and_6 (sel_MAR, clock5, clk_set, flip_word__ra_rb);
  and and_7 (set_ACC, clock6, clk_set, flip_word__ra_rb);
  and and_8 (set_arith_flags, clock6, clk_set, flip_word__ra_rb);
  and and_9 (store_RAM, clock7, clk_set, flip_word__ra_rb);
endmodule

module neg_word__ra_rb (
);

  wire ALU_1011, clk_en, clk_set, clock5, clock6, clock7, load_ACC, load_RAM, load_rb, neg_word__ra_rb,
       sel_MAR, sel_ra, set_ACC, set_arith_flags, store_RAM;

  and and_1 (sel_ra, clock5, clk_en, neg_word__ra_rb);
  and and_2 (load_rb, clock5, clk_en, neg_word__ra_rb);
  and and_3 (load_RAM, clock6, clk_en, neg_word__ra_rb);
  and and_4 (ALU_1011, clock6, clk_en, neg_word__ra_rb);
  and and_5 (load_ACC, clock7, clk_en, neg_word__ra_rb);
  and and_6 (sel_MAR, clock5, clk_set, neg_word__ra_rb);
  and and_7 (set_ACC, clock6, clk_set, neg_word__ra_rb);
  and and_8 (set_arith_flags, clock6, clk_set, neg_word__ra_rb);
  and and_9 (store_RAM, clock7, clk_set, neg_word__ra_rb);
endmodule

module mov_ra__word__rb (
);

  wire clk_en, clk_set, clock5, clock6, load_RAM, load_rb, mov_ra__word__rb, sel_DS, sel_MAR, store_ra;

  and and_1 (sel_DS, clock5, clk_en, mov_ra__word__rb);
  and and_2 (load_rb, clock5, clk_en, mov_ra__word__rb);
  and and_3 (load_RAM, clock6, clk_en, mov_ra__word__rb);
  and and_4 (sel_MAR, clock5, clk_set, mov_ra__word__rb);
  and and_5 (store_ra, clock6, clk_set, mov_ra__word__rb);
endmodule

module add_ra__word__rb (
);

  wire add_ra__word__rb, ALU_0000, clk_en, clk_set, clock5, clock6, clock7, clock8, enable_arith_flags,
       enable_TMP, load_ACC, load_ra, load_RAM, load_rb, sel_ds, sel_MAR, set_ACC, store_ra;

  and and_1 (sel_ds, clock5, clk_en, add_ra__word__rb);
  and and_2 (load_rb, clock5, clk_en, add_ra__word__rb);
  and and_3 (load_RAM, clock6, clk_en, add_ra__word__rb);
  and and_4 (load_ra, clock7, clk_en, add_ra__word__rb);
  and and_5 (ALU_0000, clock7, clk_en, add_ra__word__rb);
  and and_6 (load_ACC, clock8, clk_en, add_ra__word__rb);
  and and_7 (sel_MAR, clock5, clk_set, add_ra__word__rb);
  and and_8 (enable_TMP, clock6, clk_set, add_ra__word__rb);
  and and_9 (set_ACC, clock7, clk_set, add_ra__word__rb);
  and and_10 (enable_arith_flags, clock7, clk_set, add_ra__word__rb);
  and and_11 (store_ra, clock8, clk_set, add_ra__word__rb);
endmodule

module and_ra__word__rb (
);

  wire ALU_0100, and_ra__word__rb, clk_en, clk_set, clock5, clock6, clock7, clock8, enable_arith_flags,
       enable_TMP, load_ACC, load_ra, load_RAM, load_rb, sel_ds, sel_MAR, set_ACC, store_ra;

  and and_1 (sel_ds, clock5, clk_en, and_ra__word__rb);
  and and_2 (load_rb, clock5, clk_en, and_ra__word__rb);
  and and_3 (load_RAM, clock6, clk_en, and_ra__word__rb);
  and and_4 (load_ra, clock7, clk_en, and_ra__word__rb);
  and and_5 (ALU_0100, clock7, clk_en, and_ra__word__rb);
  and and_6 (load_ACC, clock8, clk_en, and_ra__word__rb);
  and and_7 (sel_MAR, clock5, clk_set, and_ra__word__rb);
  and and_8 (enable_TMP, clock6, clk_set, and_ra__word__rb);
  and and_9 (set_ACC, clock7, clk_set, and_ra__word__rb);
  and and_10 (enable_arith_flags, clock7, clk_set, and_ra__word__rb);
  and and_11 (store_ra, clock8, clk_set, and_ra__word__rb);
endmodule

module or_ra__word__rb (
);

  wire ALU_0101, clk_en, clk_set, clock5, clock6, clock7, clock8, enable_arith_flags, enable_TMP, load_ACC,
       load_ra, load_RAM, load_rb, or_ra__word__rb, sel_ds, sel_MAR, set_ACC, store_ra;

  and and_1 (sel_ds, clock5, clk_en, or_ra__word__rb);
  and and_2 (load_rb, clock5, clk_en, or_ra__word__rb);
  and and_3 (load_RAM, clock6, clk_en, or_ra__word__rb);
  and and_4 (load_ra, clock7, clk_en, or_ra__word__rb);
  and and_5 (ALU_0101, clock7, clk_en, or_ra__word__rb);
  and and_6 (load_ACC, clock8, clk_en, or_ra__word__rb);
  and and_7 (sel_MAR, clock5, clk_set, or_ra__word__rb);
  and and_8 (enable_TMP, clock6, clk_set, or_ra__word__rb);
  and and_9 (set_ACC, clock7, clk_set, or_ra__word__rb);
  and and_10 (enable_arith_flags, clock7, clk_set, or_ra__word__rb);
  and and_11 (store_ra, clock8, clk_set, or_ra__word__rb);
endmodule

module xor_ra__word__rb (
);

  wire ALU_0110, clk_en, clk_set, clock5, clock6, clock7, clock8, enable_arith_flags, enable_TMP, load_ACC,
       load_ra, load_RAM, load_rb, sel_ds, sel_MAR, set_ACC, store_ra, xor_ra__word__rb;

  and and_1 (sel_ds, clock5, clk_en, xor_ra__word__rb);
  and and_2 (load_rb, clock5, clk_en, xor_ra__word__rb);
  and and_3 (load_RAM, clock6, clk_en, xor_ra__word__rb);
  and and_4 (load_ra, clock7, clk_en, xor_ra__word__rb);
  and and_5 (ALU_0110, clock7, clk_en, xor_ra__word__rb);
  and and_6 (load_ACC, clock8, clk_en, xor_ra__word__rb);
  and and_7 (sel_MAR, clock5, clk_set, xor_ra__word__rb);
  and and_8 (enable_TMP, clock6, clk_set, xor_ra__word__rb);
  and and_9 (set_ACC, clock7, clk_set, xor_ra__word__rb);
  and and_10 (enable_arith_flags, clock7, clk_set, xor_ra__word__rb);
  and and_11 (store_ra, clock8, clk_set, xor_ra__word__rb);
endmodule

module cmp_ra__word__rb (
);

  wire ALU_0111, clk_en, clk_set, clock5, clock6, clock7, cmp_ra__word__rb, enable_arith_flags, enable_TMP,
       load_ra, load_RAM, load_rb, sel_ds, sel_MAR, set_ACC;

  and and_1 (sel_ds, clock5, clk_en, cmp_ra__word__rb);
  and and_2 (load_rb, clock5, clk_en, cmp_ra__word__rb);
  and and_3 (load_RAM, clock6, clk_en, cmp_ra__word__rb);
  and and_4 (load_ra, clock7, clk_en, cmp_ra__word__rb);
  and and_5 (ALU_0111, clock7, clk_en, cmp_ra__word__rb);
  and and_6 (sel_MAR, clock5, clk_set, cmp_ra__word__rb);
  and and_7 (enable_TMP, clock6, clk_set, cmp_ra__word__rb);
  and and_8 (set_ACC, clock7, clk_set, cmp_ra__word__rb);
  and and_9 (enable_arith_flags, clock7, clk_set, cmp_ra__word__rb);
endmodule

module adc_ra__word__rb (
);

  wire adc_ra__word__rb, ALU_1000, clk_en, clk_set, clock5, clock6, clock7, clock8, enable_arith_carry,
       enable_arith_flags, enable_TMP, enable_TMP1, load_ACC, load_ra, load_RAM, load_rb, sel_ds, sel_MAR,
       set_ACC, store_ra;

  and and_1 (sel_ds, clock5, clk_en, adc_ra__word__rb);
  and and_2 (load_rb, clock5, clk_en, adc_ra__word__rb);
  and and_3 (load_RAM, clock6, clk_en, adc_ra__word__rb);
  and and_4 (enable_arith_carry, clock6, clk_en, adc_ra__word__rb);
  and and_5 (load_ra, clock7, clk_en, adc_ra__word__rb);
  and and_6 (ALU_1000, clock7, clk_en, adc_ra__word__rb);
  and and_7 (load_ACC, clock8, clk_en, adc_ra__word__rb);
  and and_8 (sel_MAR, clock5, clk_set, adc_ra__word__rb);
  and and_9 (enable_TMP, clock6, clk_set, adc_ra__word__rb);
  and and_10 (enable_TMP1, clock6, clk_set, adc_ra__word__rb);
  and and_11 (set_ACC, clock7, clk_set, adc_ra__word__rb);
  and and_12 (enable_arith_flags, clock7, clk_set, adc_ra__word__rb);
  and and_13 (store_ra, clock8, clk_set, adc_ra__word__rb);
endmodule

module mul_ra__word__rb (
);

  wire ALU_1101, clk_en, clk_set, clock5, clock6, clock7, clock8, enable_arith_flags, enable_TMP, load_ACC,
       load_ra, load_RAM, load_rb, mul_ra__word__rb, sel_ds, sel_MAR, set_ACC, store_ra;

  and and_1 (sel_ds, clock5, clk_en, mul_ra__word__rb);
  and and_2 (load_rb, clock5, clk_en, mul_ra__word__rb);
  and and_3 (load_RAM, clock6, clk_en, mul_ra__word__rb);
  and and_4 (load_ra, clock7, clk_en, mul_ra__word__rb);
  and and_5 (ALU_1101, clock7, clk_en, mul_ra__word__rb);
  and and_6 (load_ACC, clock8, clk_en, mul_ra__word__rb);
  and and_7 (sel_MAR, clock5, clk_set, mul_ra__word__rb);
  and and_8 (enable_TMP, clock6, clk_set, mul_ra__word__rb);
  and and_9 (set_ACC, clock7, clk_set, mul_ra__word__rb);
  and and_10 (enable_arith_flags, clock7, clk_set, mul_ra__word__rb);
  and and_11 (store_ra, clock8, clk_set, mul_ra__word__rb);
endmodule

module div_ra__word__rb (
);

  wire ALU_1110, clk_en, clk_set, clock5, clock6, clock7, clock8, div_ra__word__rb, enable_arith_flags,
       enable_TMP, load_ACC, load_ra, load_RAM, load_rb, sel_ds, sel_MAR, set_ACC, store_ra;

  and and_1 (sel_ds, clock5, clk_en, div_ra__word__rb);
  and and_2 (load_rb, clock5, clk_en, div_ra__word__rb);
  and and_3 (load_RAM, clock6, clk_en, div_ra__word__rb);
  and and_4 (load_ra, clock7, clk_en, div_ra__word__rb);
  and and_5 (ALU_1110, clock7, clk_en, div_ra__word__rb);
  and and_6 (load_ACC, clock8, clk_en, div_ra__word__rb);
  and and_7 (sel_MAR, clock5, clk_set, div_ra__word__rb);
  and and_8 (enable_TMP, clock6, clk_set, div_ra__word__rb);
  and and_9 (set_ACC, clock7, clk_set, div_ra__word__rb);
  and and_10 (enable_arith_flags, clock7, clk_set, div_ra__word__rb);
  and and_11 (store_ra, clock8, clk_set, div_ra__word__rb);
endmodule

module mod_ra__word__rb (
);

  wire ALU_1111, clk_en, clk_set, clock5, clock6, clock7, clock8, enable_arith_flags, enable_TMP, load_ACC,
       load_ra, load_RAM, load_rb, mod_ra__word__rb, sel_ds, sel_MAR, set_ACC, store_ra;

  and and_1 (sel_ds, clock5, clk_en, mod_ra__word__rb);
  and and_2 (load_rb, clock5, clk_en, mod_ra__word__rb);
  and and_3 (load_RAM, clock6, clk_en, mod_ra__word__rb);
  and and_4 (load_ra, clock7, clk_en, mod_ra__word__rb);
  and and_5 (ALU_1111, clock7, clk_en, mod_ra__word__rb);
  and and_6 (load_ACC, clock8, clk_en, mod_ra__word__rb);
  and and_7 (sel_MAR, clock5, clk_set, mod_ra__word__rb);
  and and_8 (enable_TMP, clock6, clk_set, mod_ra__word__rb);
  and and_9 (set_ACC, clock7, clk_set, mod_ra__word__rb);
  and and_10 (enable_arith_flags, clock7, clk_set, mod_ra__word__rb);
  and and_11 (store_ra, clock8, clk_set, mod_ra__word__rb);
endmodule

module mov_ra__byte__rb (
);

  wire ALU_0100, clk_en, clk_set, clock5, clock6, clock7, clock8, enable_lowmask, load_ACC, load_ra,
       load_RAM, load_rb, mov_ra__byte__rb, sel_DS, sel_MAR, set_ACC, store_ra;

  and and_1 (sel_DS, clock5, clk_en, mov_ra__byte__rb);
  and and_2 (load_rb, clock5, clk_en, mov_ra__byte__rb);
  and and_3 (load_RAM, clock6, clk_en, mov_ra__byte__rb);
  and and_4 (load_ra, clock7, clk_en, mov_ra__byte__rb);
  and and_5 (enable_lowmask, clock7, clk_en, mov_ra__byte__rb);
  and and_6 (ALU_0100, clock7, clk_en, mov_ra__byte__rb);
  and and_7 (load_ACC, clock8, clk_en, mov_ra__byte__rb);
  and and_8 (sel_MAR, clock5, clk_set, mov_ra__byte__rb);
  and and_9 (store_ra, clock6, clk_set, mov_ra__byte__rb);
  and and_10 (set_ACC, clock7, clk_set, mov_ra__byte__rb);
  and and_11 (store_ra, clock8, clk_set, mov_ra__byte__rb);
endmodule

module add_ra__byte__rb (
);

  wire add_ra__byte__rb, ALU_0000, ALU_0100, clk_en, clk_set, clock5, clock6, clock7, clock8, clock9,
       enable_lowmask, enable_TMP, load_ACC, load_ra, load_RAM, load_rb, sel_ds, sel_MAR, set_ACC,
       set_arith_flags, store_ra;

  and and_1 (sel_ds, clock5, clk_en, add_ra__byte__rb);
  and and_2 (load_rb, clock5, clk_en, add_ra__byte__rb);
  and and_3 (load_RAM, clock6, clk_en, add_ra__byte__rb);
  and and_4 (enable_lowmask, clock6, clk_en, add_ra__byte__rb);
  and and_5 (ALU_0100, clock6, clk_en, add_ra__byte__rb);
  and and_6 (load_ACC, clock7, clk_en, add_ra__byte__rb);
  and and_7 (load_ra, clock8, clk_en, add_ra__byte__rb);
  and and_8 (ALU_0000, clock8, clk_en, add_ra__byte__rb);
  and and_9 (load_ACC, clock9, clk_en, add_ra__byte__rb);
  and and_10 (sel_MAR, clock5, clk_set, add_ra__byte__rb);
  and and_11 (set_ACC, clock6, clk_set, add_ra__byte__rb);
  and and_12 (enable_TMP, clock7, clk_set, add_ra__byte__rb);
  and and_13 (set_ACC, clock8, clk_set, add_ra__byte__rb);
  and and_14 (set_arith_flags, clock8, clk_set, add_ra__byte__rb);
  and and_15 (store_ra, clock9, clk_set, add_ra__byte__rb);
endmodule

module add_word__ra___rb (
);

  wire add_word__ra___rb, ALU_0000, clk_en, clk_set, clock5, clock6, clock7, clock8, enable_TMP, load_ACC,
       load_ra, load_RAM, load_rb, sel_ds, sel_MAR, set_ACC, set_arith_flags, store_RAM;

  and and_1 (sel_ds, clock5, clk_en, add_word__ra___rb);
  and and_2 (load_ra, clock5, clk_en, add_word__ra___rb);
  and and_3 (load_rb, clock6, clk_en, add_word__ra___rb);
  and and_4 (load_RAM, clock7, clk_en, add_word__ra___rb);
  and and_5 (ALU_0000, clock7, clk_en, add_word__ra___rb);
  and and_6 (load_ACC, clock8, clk_en, add_word__ra___rb);
  and and_7 (sel_MAR, clock5, clk_set, add_word__ra___rb);
  and and_8 (enable_TMP, clock6, clk_set, add_word__ra___rb);
  and and_9 (set_ACC, clock7, clk_set, add_word__ra___rb);
  and and_10 (set_arith_flags, clock7, clk_set, add_word__ra___rb);
  and and_11 (store_RAM, clock8, clk_set, add_word__ra___rb);
endmodule

module mov_word__ra_rb___imm16 (
);

  wire ALU_0000, ALU_1000, clk_en, clk_set, clock5, clock6, clock7, clock8, clock9, clock10, clock11,
       enable_BUS1, enable_carry, enable_CLR, enable_TMP1, load_ACC, load_CS, load_IAR, load_RAM, load_rb,
       mov_word__ra_rb___imm16, sel_CS, sel_MAR, sel_ra, set_ACC, set_carry, set_IAR, store_CS, store_RAM;

  and and_1 (sel_CS, clock5, clk_en, mov_word__ra_rb___imm16);
  and and_2 (load_IAR, clock5, clk_en, mov_word__ra_rb___imm16);
  and and_3 (enable_BUS1, clock5, clk_en, mov_word__ra_rb___imm16);
  and and_4 (ALU_0000, clock5, clk_en, mov_word__ra_rb___imm16);
  and and_5 (set_carry, clock5, clk_en, mov_word__ra_rb___imm16);
  and and_6 (load_ACC, clock6, clk_en, mov_word__ra_rb___imm16);
  and and_7 (load_CS, clock7, clk_en, mov_word__ra_rb___imm16);
  and and_8 (enable_CLR, clock7, clk_en, mov_word__ra_rb___imm16);
  and and_9 (ALU_1000, clock7, clk_en, mov_word__ra_rb___imm16);
  and and_10 (load_ACC, clock8, clk_en, mov_word__ra_rb___imm16);
  and and_11 (load_RAM, clock9, clk_en, mov_word__ra_rb___imm16);
  and and_12 (enable_CLR, clock9, clk_en, mov_word__ra_rb___imm16);
  and and_13 (ALU_0000, clock9, clk_en, mov_word__ra_rb___imm16);
  and and_14 (sel_ra, clock10, clk_en, mov_word__ra_rb___imm16);
  and and_15 (load_rb, clock10, clk_en, mov_word__ra_rb___imm16);
  and and_16 (load_ACC, clock11, clk_en, mov_word__ra_rb___imm16);
  and and_17 (sel_MAR, clock5, clk_set, mov_word__ra_rb___imm16);
  and and_18 (set_ACC, clock5, clk_set, mov_word__ra_rb___imm16);
  and and_19 (enable_carry, clock5, clk_set, mov_word__ra_rb___imm16);
  and and_20 (enable_TMP1, clock5, clk_set, mov_word__ra_rb___imm16);
  and and_21 (set_IAR, clock6, clk_set, mov_word__ra_rb___imm16);
  and and_22 (set_ACC, clock7, clk_set, mov_word__ra_rb___imm16);
  and and_23 (store_CS, clock8, clk_set, mov_word__ra_rb___imm16);
  and and_24 (set_ACC, clock9, clk_set, mov_word__ra_rb___imm16);
  and and_25 (sel_MAR, clock10, clk_set, mov_word__ra_rb___imm16);
  and and_26 (store_RAM, clock11, clk_set, mov_word__ra_rb___imm16);
endmodule

module add_word__ra_rb___imm16 (
);

  wire add_word__ra_rb___imm16, ALU_0000, ALU_1000, clk_en, clk_set, clock5, clock6, clock7, clock8, clock9,
       clock10, clock11, clock12, enable_BUS1, enable_carry, enable_CLR, enable_TMP, enable_TMP1, load_ACC,
       load_CS, load_IAR, load_RAM, load_rb, sel_CS, sel_MAR, sel_ra, set_ACC, set_arith_flags, set_carry,
       set_IAR, store_CS, store_RAM;

  and and_1 (sel_CS, clock5, clk_en, add_word__ra_rb___imm16);
  and and_2 (load_IAR, clock5, clk_en, add_word__ra_rb___imm16);
  and and_3 (enable_BUS1, clock5, clk_en, add_word__ra_rb___imm16);
  and and_4 (ALU_0000, clock5, clk_en, add_word__ra_rb___imm16);
  and and_5 (set_carry, clock5, clk_en, add_word__ra_rb___imm16);
  and and_6 (load_ACC, clock6, clk_en, add_word__ra_rb___imm16);
  and and_7 (load_CS, clock7, clk_en, add_word__ra_rb___imm16);
  and and_8 (enable_CLR, clock7, clk_en, add_word__ra_rb___imm16);
  and and_9 (ALU_1000, clock7, clk_en, add_word__ra_rb___imm16);
  and and_10 (load_ACC, clock8, clk_en, add_word__ra_rb___imm16);
  and and_11 (load_RAM, clock9, clk_en, add_word__ra_rb___imm16);
  and and_12 (sel_ra, clock10, clk_en, add_word__ra_rb___imm16);
  and and_13 (load_rb, clock10, clk_en, add_word__ra_rb___imm16);
  and and_14 (load_RAM, clock11, clk_en, add_word__ra_rb___imm16);
  and and_15 (ALU_0000, clock11, clk_en, add_word__ra_rb___imm16);
  and and_16 (load_ACC, clock12, clk_en, add_word__ra_rb___imm16);
  and and_17 (sel_MAR, clock5, clk_set, add_word__ra_rb___imm16);
  and and_18 (set_ACC, clock5, clk_set, add_word__ra_rb___imm16);
  and and_19 (enable_carry, clock5, clk_set, add_word__ra_rb___imm16);
  and and_20 (enable_TMP1, clock5, clk_set, add_word__ra_rb___imm16);
  and and_21 (set_IAR, clock6, clk_set, add_word__ra_rb___imm16);
  and and_22 (set_ACC, clock7, clk_set, add_word__ra_rb___imm16);
  and and_23 (store_CS, clock8, clk_set, add_word__ra_rb___imm16);
  and and_24 (enable_TMP, clock9, clk_set, add_word__ra_rb___imm16);
  and and_25 (sel_MAR, clock10, clk_set, add_word__ra_rb___imm16);
  and and_26 (set_ACC, clock11, clk_set, add_word__ra_rb___imm16);
  and and_27 (set_arith_flags, clock11, clk_set, add_word__ra_rb___imm16);
  and and_28 (store_RAM, clock12, clk_set, add_word__ra_rb___imm16);
endmodule

module and_word__ra_rb___imm16 (
);

  wire ALU_0000, ALU_0100, ALU_1000, and_word__ra_rb___imm16, clk_en, clk_set, clock5, clock6, clock7,
       clock8, clock9, clock10, clock11, clock12, enable_BUS1, enable_carry, enable_CLR, enable_TMP,
       enable_TMP1, load_ACC, load_CS, load_IAR, load_RAM, load_rb, sel_CS, sel_MAR, sel_ra, set_ACC,
       set_arith_flags, set_carry, set_IAR, store_CS, store_RAM;

  and and_1 (sel_CS, clock5, clk_en, and_word__ra_rb___imm16);
  and and_2 (load_IAR, clock5, clk_en, and_word__ra_rb___imm16);
  and and_3 (enable_BUS1, clock5, clk_en, and_word__ra_rb___imm16);
  and and_4 (ALU_0000, clock5, clk_en, and_word__ra_rb___imm16);
  and and_5 (set_carry, clock5, clk_en, and_word__ra_rb___imm16);
  and and_6 (load_ACC, clock6, clk_en, and_word__ra_rb___imm16);
  and and_7 (load_CS, clock7, clk_en, and_word__ra_rb___imm16);
  and and_8 (enable_CLR, clock7, clk_en, and_word__ra_rb___imm16);
  and and_9 (ALU_1000, clock7, clk_en, and_word__ra_rb___imm16);
  and and_10 (load_ACC, clock8, clk_en, and_word__ra_rb___imm16);
  and and_11 (load_RAM, clock9, clk_en, and_word__ra_rb___imm16);
  and and_12 (sel_ra, clock10, clk_en, and_word__ra_rb___imm16);
  and and_13 (load_rb, clock10, clk_en, and_word__ra_rb___imm16);
  and and_14 (load_RAM, clock11, clk_en, and_word__ra_rb___imm16);
  and and_15 (ALU_0100, clock11, clk_en, and_word__ra_rb___imm16);
  and and_16 (load_ACC, clock12, clk_en, and_word__ra_rb___imm16);
  and and_17 (sel_MAR, clock5, clk_set, and_word__ra_rb___imm16);
  and and_18 (set_ACC, clock5, clk_set, and_word__ra_rb___imm16);
  and and_19 (enable_carry, clock5, clk_set, and_word__ra_rb___imm16);
  and and_20 (enable_TMP1, clock5, clk_set, and_word__ra_rb___imm16);
  and and_21 (set_IAR, clock6, clk_set, and_word__ra_rb___imm16);
  and and_22 (set_ACC, clock7, clk_set, and_word__ra_rb___imm16);
  and and_23 (store_CS, clock8, clk_set, and_word__ra_rb___imm16);
  and and_24 (enable_TMP, clock9, clk_set, and_word__ra_rb___imm16);
  and and_25 (sel_MAR, clock10, clk_set, and_word__ra_rb___imm16);
  and and_26 (set_ACC, clock11, clk_set, and_word__ra_rb___imm16);
  and and_27 (set_arith_flags, clock11, clk_set, and_word__ra_rb___imm16);
  and and_28 (store_RAM, clock12, clk_set, and_word__ra_rb___imm16);
endmodule

module or_word__ra_rb___imm16 (
);

  wire ALU_0000, ALU_0101, ALU_1000, clk_en, clk_set, clock5, clock6, clock7, clock8, clock9, clock10,
       clock11, clock12, enable_BUS1, enable_carry, enable_CLR, enable_TMP, enable_TMP1, load_ACC, load_CS,
       load_IAR, load_RAM, load_rb, or_word__ra_rb___imm16, sel_CS, sel_MAR, sel_ra, set_ACC,
       set_arith_flags, set_carry, set_IAR, store_CS, store_RAM;

  and and_1 (sel_CS, clock5, clk_en, or_word__ra_rb___imm16);
  and and_2 (load_IAR, clock5, clk_en, or_word__ra_rb___imm16);
  and and_3 (enable_BUS1, clock5, clk_en, or_word__ra_rb___imm16);
  and and_4 (ALU_0000, clock5, clk_en, or_word__ra_rb___imm16);
  and and_5 (set_carry, clock5, clk_en, or_word__ra_rb___imm16);
  and and_6 (load_ACC, clock6, clk_en, or_word__ra_rb___imm16);
  and and_7 (load_CS, clock7, clk_en, or_word__ra_rb___imm16);
  and and_8 (enable_CLR, clock7, clk_en, or_word__ra_rb___imm16);
  and and_9 (ALU_1000, clock7, clk_en, or_word__ra_rb___imm16);
  and and_10 (load_ACC, clock8, clk_en, or_word__ra_rb___imm16);
  and and_11 (load_RAM, clock9, clk_en, or_word__ra_rb___imm16);
  and and_12 (sel_ra, clock10, clk_en, or_word__ra_rb___imm16);
  and and_13 (load_rb, clock10, clk_en, or_word__ra_rb___imm16);
  and and_14 (load_RAM, clock11, clk_en, or_word__ra_rb___imm16);
  and and_15 (ALU_0101, clock11, clk_en, or_word__ra_rb___imm16);
  and and_16 (load_ACC, clock12, clk_en, or_word__ra_rb___imm16);
  and and_17 (sel_MAR, clock5, clk_set, or_word__ra_rb___imm16);
  and and_18 (set_ACC, clock5, clk_set, or_word__ra_rb___imm16);
  and and_19 (enable_carry, clock5, clk_set, or_word__ra_rb___imm16);
  and and_20 (enable_TMP1, clock5, clk_set, or_word__ra_rb___imm16);
  and and_21 (set_IAR, clock6, clk_set, or_word__ra_rb___imm16);
  and and_22 (set_ACC, clock7, clk_set, or_word__ra_rb___imm16);
  and and_23 (store_CS, clock8, clk_set, or_word__ra_rb___imm16);
  and and_24 (enable_TMP, clock9, clk_set, or_word__ra_rb___imm16);
  and and_25 (sel_MAR, clock10, clk_set, or_word__ra_rb___imm16);
  and and_26 (set_ACC, clock11, clk_set, or_word__ra_rb___imm16);
  and and_27 (set_arith_flags, clock11, clk_set, or_word__ra_rb___imm16);
  and and_28 (store_RAM, clock12, clk_set, or_word__ra_rb___imm16);
endmodule

module xor_word__ra_rb___imm16 (
);

  wire ALU_0000, ALU_0110, ALU_1000, clk_en, clk_set, clock5, clock6, clock7, clock8, clock9, clock10,
       clock11, clock12, enable_BUS1, enable_carry, enable_CLR, enable_TMP, enable_TMP1, load_ACC, load_CS,
       load_IAR, load_RAM, load_rb, sel_CS, sel_MAR, sel_ra, set_ACC, set_arith_flags, set_carry, set_IAR,
       store_CS, store_RAM, sub_ra__imm16, xor_word__ra_rb___imm16;

  and and_1 (sel_CS, clock5, clk_en, xor_word__ra_rb___imm16);
  and and_2 (load_IAR, clock5, clk_en, xor_word__ra_rb___imm16);
  and and_3 (enable_BUS1, clock5, clk_en, xor_word__ra_rb___imm16);
  and and_4 (ALU_0000, clock5, clk_en, xor_word__ra_rb___imm16);
  and and_5 (set_carry, clock5, clk_en, sub_ra__imm16);
  and and_6 (load_ACC, clock6, clk_en, xor_word__ra_rb___imm16);
  and and_7 (load_CS, clock7, clk_en, xor_word__ra_rb___imm16);
  and and_8 (enable_CLR, clock7, clk_en, xor_word__ra_rb___imm16);
  and and_9 (ALU_1000, clock7, clk_en, xor_word__ra_rb___imm16);
  and and_10 (load_ACC, clock8, clk_en, xor_word__ra_rb___imm16);
  and and_11 (load_RAM, clock9, clk_en, xor_word__ra_rb___imm16);
  and and_12 (sel_ra, clock10, clk_en, xor_word__ra_rb___imm16);
  and and_13 (load_rb, clock10, clk_en, xor_word__ra_rb___imm16);
  and and_14 (load_RAM, clock11, clk_en, xor_word__ra_rb___imm16);
  and and_15 (ALU_0110, clock11, clk_en, xor_word__ra_rb___imm16);
  and and_16 (load_ACC, clock12, clk_en, xor_word__ra_rb___imm16);
  and and_17 (sel_MAR, clock5, clk_set, xor_word__ra_rb___imm16);
  and and_18 (set_ACC, clock5, clk_set, xor_word__ra_rb___imm16);
  and and_19 (enable_carry, clock5, clk_set, xor_word__ra_rb___imm16);
  and and_20 (enable_TMP1, clock5, clk_set, xor_word__ra_rb___imm16);
  and and_21 (set_IAR, clock6, clk_set, xor_word__ra_rb___imm16);
  and and_22 (set_ACC, clock7, clk_set, xor_word__ra_rb___imm16);
  and and_23 (store_CS, clock8, clk_set, xor_word__ra_rb___imm16);
  and and_24 (enable_TMP, clock9, clk_set, xor_word__ra_rb___imm16);
  and and_25 (sel_MAR, clock10, clk_set, xor_word__ra_rb___imm16);
  and and_26 (set_ACC, clock11, clk_set, xor_word__ra_rb___imm16);
  and and_27 (set_arith_flags, clock11, clk_set, xor_word__ra_rb___imm16);
  and and_28 (store_RAM, clock12, clk_set, xor_word__ra_rb___imm16);
endmodule

module cmp_word__ra_rb___imm16 (
);

  wire ALU_0000, ALU_0111, ALU_1000, clk_en, clk_set, clock5, clock6, clock7, clock8, clock9, clock10,
       clock11, cmp_word__ra_rb___imm16, enable_BUS1, enable_carry, enable_CLR, enable_TMP, enable_TMP1,
       load_ACC, load_CS, load_IAR, load_RAM, load_rb, sel_CS, sel_MAR, sel_ra, set_ACC, set_arith_flags,
       set_carry, set_IAR, store_CS, sub_ra__imm16, xor_word__ra_rb___imm16;

  and and_1 (sel_CS, clock5, clk_en, xor_word__ra_rb___imm16);
  and and_2 (load_IAR, clock5, clk_en, xor_word__ra_rb___imm16);
  and and_3 (enable_BUS1, clock5, clk_en, xor_word__ra_rb___imm16);
  and and_4 (ALU_0000, clock5, clk_en, xor_word__ra_rb___imm16);
  and and_5 (set_carry, clock5, clk_en, sub_ra__imm16);
  and and_6 (load_ACC, clock6, clk_en, xor_word__ra_rb___imm16);
  and and_7 (load_CS, clock7, clk_en, cmp_word__ra_rb___imm16);
  and and_8 (enable_CLR, clock7, clk_en, cmp_word__ra_rb___imm16);
  and and_9 (ALU_1000, clock7, clk_en, cmp_word__ra_rb___imm16);
  and and_10 (load_ACC, clock8, clk_en, cmp_word__ra_rb___imm16);
  and and_11 (load_RAM, clock9, clk_en, cmp_word__ra_rb___imm16);
  and and_12 (sel_ra, clock10, clk_en, cmp_word__ra_rb___imm16);
  and and_13 (load_rb, clock10, clk_en, cmp_word__ra_rb___imm16);
  and and_14 (load_RAM, clock11, clk_en, cmp_word__ra_rb___imm16);
  and and_15 (ALU_0111, clock11, clk_en, cmp_word__ra_rb___imm16);
  and and_16 (sel_MAR, clock5, clk_set, xor_word__ra_rb___imm16);
  and and_17 (set_ACC, clock5, clk_set, xor_word__ra_rb___imm16);
  and and_18 (enable_carry, clock5, clk_set, xor_word__ra_rb___imm16);
  and and_19 (enable_TMP1, clock5, clk_set, xor_word__ra_rb___imm16);
  and and_20 (set_IAR, clock6, clk_set, xor_word__ra_rb___imm16);
  and and_21 (set_ACC, clock7, clk_set, cmp_word__ra_rb___imm16);
  and and_22 (store_CS, clock8, clk_set, cmp_word__ra_rb___imm16);
  and and_23 (enable_TMP, clock9, clk_set, cmp_word__ra_rb___imm16);
  and and_24 (sel_MAR, clock10, clk_set, cmp_word__ra_rb___imm16);
  and and_25 (set_ACC, clock11, clk_set, cmp_word__ra_rb___imm16);
  and and_26 (set_arith_flags, clock11, clk_set, cmp_word__ra_rb___imm16);
endmodule

module push_ra (
);

  wire ALU_0000, ALU_1000, clk_en, clk_set, clock5, clock6, clock7, clock8, clock9, clock10, enable_BUS1,
       enable_carry, enable_CLR, enable_TMP1, load_ACC, load_ra, load_sp, load_SS, push_ra, sel_MAR, sel_ss,
       set_ACC, set_carry, store_RAM, store_sp, store_ss;

  and and_1 (load_sp, clock5, clk_en, push_ra);
  and and_2 (enable_BUS1, clock5, clk_en, push_ra);
  and and_3 (ALU_0000, clock5, clk_en, push_ra);
  and and_4 (set_carry, clock5, clk_en, push_ra);
  and and_5 (load_ACC, clock6, clk_en, push_ra);
  and and_6 (load_SS, clock7, clk_en, push_ra);
  and and_7 (enable_CLR, clock7, clk_en, push_ra);
  and and_8 (ALU_1000, clock7, clk_en, push_ra);
  and and_9 (load_ACC, clock8, clk_en, push_ra);
  and and_10 (sel_ss, clock9, clk_en, push_ra);
  and and_11 (load_sp, clock9, clk_en, push_ra);
  and and_12 (load_ra, clock10, clk_en, push_ra);
  and and_13 (set_ACC, clock5, clk_set, push_ra);
  and and_14 (enable_carry, clock5, clk_set, push_ra);
  and and_15 (enable_TMP1, clock5, clk_set, push_ra);
  and and_16 (store_sp, clock6, clk_set, push_ra);
  and and_17 (set_ACC, clock7, clk_set, push_ra);
  and and_18 (store_ss, clock8, clk_set, push_ra);
  and and_19 (sel_MAR, clock9, clk_set, push_ra);
  and and_20 (store_RAM, clock10, clk_set, push_ra);
endmodule

module push_imm16 (
);

  wire ALU_0000, ALU_1000, clk_en, clk_set, clock5, clock6, clock7, clock8, clock9, clock10, clock11,
       clock12, clock13, clock14, clock15, enable_BUS1, enable_carry, enable_CLR, enable_TMP1, load_ACC,
       load_cs, load_IAR, load_RAM, load_sp, load_SS, push_imm16, sel_cs, sel_MAR, sel_ss, set_ACC,
       set_carry, store_cs, store_IAR, store_RAM, store_sp, store_ss;

  and and_1 (load_sp, clock5, clk_en, push_imm16);
  and and_2 (enable_BUS1, clock5, clk_en, push_imm16);
  and and_3 (ALU_0000, clock5, clk_en, push_imm16);
  and and_4 (set_carry, clock5, clk_en, push_imm16);
  and and_5 (load_ACC, clock6, clk_en, push_imm16);
  and and_6 (load_SS, clock7, clk_en, push_imm16);
  and and_7 (enable_CLR, clock7, clk_en, push_imm16);
  and and_8 (ALU_1000, clock7, clk_en, push_imm16);
  and and_9 (load_ACC, clock8, clk_en, push_imm16);
  and and_10 (sel_cs, clock9, clk_en, push_imm16);
  and and_11 (load_IAR, clock9, clk_en, push_imm16);
  and and_12 (enable_BUS1, clock9, clk_en, push_imm16);
  and and_13 (ALU_0000, clock9, clk_en, push_imm16);
  and and_14 (set_carry, clock9, clk_en, push_imm16);
  and and_15 (load_ACC, clock10, clk_en, push_imm16);
  and and_16 (load_cs, clock11, clk_en, push_imm16);
  and and_17 (enable_CLR, clock11, clk_en, push_imm16);
  and and_18 (ALU_1000, clock11, clk_en, push_imm16);
  and and_19 (load_ACC, clock12, clk_en, push_imm16);
  and and_20 (load_RAM, clock13, clk_en, push_imm16);
  and and_21 (enable_CLR, clock13, clk_en, push_imm16);
  and and_22 (ALU_0000, clock13, clk_en, push_imm16);
  and and_23 (sel_ss, clock14, clk_en, push_imm16);
  and and_24 (load_sp, clock14, clk_en, push_imm16);
  and and_25 (load_ACC, clock15, clk_en, push_imm16);
  and and_26 (set_ACC, clock5, clk_set, push_imm16);
  and and_27 (enable_carry, clock5, clk_set, push_imm16);
  and and_28 (enable_TMP1, clock5, clk_set, push_imm16);
  and and_29 (store_sp, clock6, clk_set, push_imm16);
  and and_30 (set_ACC, clock7, clk_set, push_imm16);
  and and_31 (store_ss, clock8, clk_set, push_imm16);
  and and_32 (sel_MAR, clock9, clk_set, push_imm16);
  and and_33 (set_ACC, clock9, clk_set, push_imm16);
  and and_34 (enable_carry, clock9, clk_set, push_imm16);
  and and_35 (enable_TMP1, clock9, clk_set, push_imm16);
  and and_36 (store_IAR, clock10, clk_set, push_imm16);
  and and_37 (set_ACC, clock11, clk_set, push_imm16);
  and and_38 (store_cs, clock12, clk_set, push_imm16);
  and and_39 (set_ACC, clock13, clk_set, push_imm16);
  and and_40 (sel_MAR, clock14, clk_set, push_imm16);
  and and_41 (store_RAM, clock15, clk_set, push_imm16);
endmodule

module push_byte__ra_rb (
);

  wire ALU_0000, ALU_0100, ALU_1000, clk_en, clk_set, clock5, clock6, clock7, clock8, clock9, clock10,
       clock11, clock12, enable_BUS1, enable_carry, enable_CLR, enable_lowmask, enable_TMP1, load_ACC,
       load_RAM, load_rb, load_sp, load_SS, push_byte__ra_rb, sel_MAR, sel_ra, sel_ss, set_ACC, set_carry,
       store_RAM, store_sp, store_ss;

  and and_1 (load_sp, clock5, clk_en, push_byte__ra_rb);
  and and_2 (enable_BUS1, clock5, clk_en, push_byte__ra_rb);
  and and_3 (ALU_0000, clock5, clk_en, push_byte__ra_rb);
  and and_4 (set_carry, clock5, clk_en, push_byte__ra_rb);
  and and_5 (load_ACC, clock6, clk_en, push_byte__ra_rb);
  and and_6 (load_SS, clock7, clk_en, push_byte__ra_rb);
  and and_7 (enable_CLR, clock7, clk_en, push_byte__ra_rb);
  and and_8 (ALU_1000, clock7, clk_en, push_byte__ra_rb);
  and and_9 (load_ACC, clock8, clk_en, push_byte__ra_rb);
  and and_10 (sel_ra, clock9, clk_en, push_byte__ra_rb);
  and and_11 (load_rb, clock9, clk_en, push_byte__ra_rb);
  and and_12 (load_RAM, clock10, clk_en, push_byte__ra_rb);
  and and_13 (enable_lowmask, clock10, clk_en, push_byte__ra_rb);
  and and_14 (ALU_0100, clock10, clk_en, push_byte__ra_rb);
  and and_15 (sel_ss, clock11, clk_en, push_byte__ra_rb);
  and and_16 (load_sp, clock11, clk_en, push_byte__ra_rb);
  and and_17 (load_ACC, clock12, clk_en, push_byte__ra_rb);
  and and_18 (set_ACC, clock5, clk_set, push_byte__ra_rb);
  and and_19 (enable_carry, clock5, clk_set, push_byte__ra_rb);
  and and_20 (enable_TMP1, clock5, clk_set, push_byte__ra_rb);
  and and_21 (store_sp, clock6, clk_set, push_byte__ra_rb);
  and and_22 (set_ACC, clock7, clk_set, push_byte__ra_rb);
  and and_23 (store_ss, clock8, clk_set, push_byte__ra_rb);
  and and_24 (sel_MAR, clock9, clk_set, push_byte__ra_rb);
  and and_25 (set_ACC, clock10, clk_set, push_byte__ra_rb);
  and and_26 (sel_MAR, clock11, clk_set, push_byte__ra_rb);
  and and_27 (store_RAM, clock12, clk_set, push_byte__ra_rb);
endmodule

module push_word__ra_rb (
);

  wire ALU_0000, ALU_1000, clk_en, clk_set, clock5, clock6, clock7, clock8, clock9, clock10, clock11,
       clock12, enable_BUS1, enable_carry, enable_CLR, enable_TMP1, load_ACC, load_RAM, load_rb, load_sp,
       load_SS, push_word__ra_rb, sel_MAR, sel_ra, sel_ss, set_ACC, set_carry, store_RAM, store_sp, store_ss;

  and and_1 (load_sp, clock5, clk_en, push_word__ra_rb);
  and and_2 (enable_BUS1, clock5, clk_en, push_word__ra_rb);
  and and_3 (ALU_0000, clock5, clk_en, push_word__ra_rb);
  and and_4 (set_carry, clock5, clk_en, push_word__ra_rb);
  and and_5 (load_ACC, clock6, clk_en, push_word__ra_rb);
  and and_6 (load_SS, clock7, clk_en, push_word__ra_rb);
  and and_7 (enable_CLR, clock7, clk_en, push_word__ra_rb);
  and and_8 (ALU_1000, clock7, clk_en, push_word__ra_rb);
  and and_9 (load_ACC, clock8, clk_en, push_word__ra_rb);
  and and_10 (sel_ra, clock9, clk_en, push_word__ra_rb);
  and and_11 (load_rb, clock9, clk_en, push_word__ra_rb);
  and and_12 (load_RAM, clock10, clk_en, push_word__ra_rb);
  and and_13 (enable_CLR, clock10, clk_en, push_word__ra_rb);
  and and_14 (ALU_0000, clock10, clk_en, push_word__ra_rb);
  and and_15 (sel_ss, clock11, clk_en, push_word__ra_rb);
  and and_16 (load_sp, clock11, clk_en, push_word__ra_rb);
  and and_17 (load_ACC, clock12, clk_en, push_word__ra_rb);
  and and_18 (set_ACC, clock5, clk_set, push_word__ra_rb);
  and and_19 (enable_carry, clock5, clk_set, push_word__ra_rb);
  and and_20 (enable_TMP1, clock5, clk_set, push_word__ra_rb);
  and and_21 (store_sp, clock6, clk_set, push_word__ra_rb);
  and and_22 (set_ACC, clock7, clk_set, push_word__ra_rb);
  and and_23 (store_ss, clock8, clk_set, push_word__ra_rb);
  and and_24 (sel_MAR, clock9, clk_set, push_word__ra_rb);
  and and_25 (set_ACC, clock10, clk_set, push_word__ra_rb);
  and and_26 (sel_MAR, clock11, clk_set, push_word__ra_rb);
  and and_27 (store_RAM, clock12, clk_set, push_word__ra_rb);
endmodule

module pop_ra (
);

  wire ALU_1010, ALU_1100, clk_en, clk_set, clock5, clock6, clock7, clock8, clock9, enable_BUS1,
       enable_carry, enable_CLR, enable_TMP1, load_ACC, load_RAM, load_sp, load_ss, pop_ra, sel_MAR, sel_ss,
       set_ACC, set_carry, store_ra, store_sp, store_ss;

  and and_1 (sel_ss, clock5, clk_en, pop_ra);
  and and_2 (load_sp, clock5, clk_en, pop_ra);
  and and_3 (enable_BUS1, clock5, clk_en, pop_ra);
  and and_4 (ALU_1100, clock5, clk_en, pop_ra);
  and and_5 (set_carry, clock5, clk_en, pop_ra);
  and and_6 (load_ACC, clock6, clk_en, pop_ra);
  and and_7 (load_ss, clock7, clk_en, pop_ra);
  and and_8 (enable_CLR, clock7, clk_en, pop_ra);
  and and_9 (ALU_1010, clock7, clk_en, pop_ra);
  and and_10 (load_ACC, clock8, clk_en, pop_ra);
  and and_11 (load_RAM, clock9, clk_en, pop_ra);
  and and_12 (sel_MAR, clock5, clk_set, pop_ra);
  and and_13 (set_ACC, clock5, clk_set, pop_ra);
  and and_14 (enable_carry, clock5, clk_set, pop_ra);
  and and_15 (enable_TMP1, clock5, clk_set, pop_ra);
  and and_16 (store_sp, clock6, clk_set, pop_ra);
  and and_17 (set_ACC, clock7, clk_set, pop_ra);
  and and_18 (store_ss, clock8, clk_set, pop_ra);
  and and_19 (store_ra, clock9, clk_set, pop_ra);
endmodule

module pop_byte__ra_rb (
);

  wire ALU_0100, ALU_1010, ALU_1100, clk_en, clk_set, clock5, clock6, clock7, clock8, clock9, clock10,
       clock11, enable_BUS1, enable_carry, enable_CLR, enable_lowmask, enable_TMP1, load_ACC, load_RAM,
       load_rb, load_sp, load_ss, pop_byte__ra_rb, sel_MAR, sel_ra, sel_ss, set_ACC, set_carry, store_RAM,
       store_sp, store_ss;

  and and_1 (sel_ss, clock5, clk_en, pop_byte__ra_rb);
  and and_2 (load_sp, clock5, clk_en, pop_byte__ra_rb);
  and and_3 (enable_BUS1, clock5, clk_en, pop_byte__ra_rb);
  and and_4 (ALU_1100, clock5, clk_en, pop_byte__ra_rb);
  and and_5 (set_carry, clock5, clk_en, pop_byte__ra_rb);
  and and_6 (load_ACC, clock6, clk_en, pop_byte__ra_rb);
  and and_7 (load_ss, clock7, clk_en, pop_byte__ra_rb);
  and and_8 (enable_CLR, clock7, clk_en, pop_byte__ra_rb);
  and and_9 (ALU_1010, clock7, clk_en, pop_byte__ra_rb);
  and and_10 (load_ACC, clock8, clk_en, pop_byte__ra_rb);
  and and_11 (load_RAM, clock9, clk_en, pop_byte__ra_rb);
  and and_12 (enable_lowmask, clock9, clk_en, pop_byte__ra_rb);
  and and_13 (ALU_0100, clock9, clk_en, pop_byte__ra_rb);
  and and_14 (sel_ra, clock10, clk_en, pop_byte__ra_rb);
  and and_15 (load_rb, clock10, clk_en, pop_byte__ra_rb);
  and and_16 (load_ACC, clock11, clk_en, pop_byte__ra_rb);
  and and_17 (sel_MAR, clock5, clk_set, pop_byte__ra_rb);
  and and_18 (set_ACC, clock5, clk_set, pop_byte__ra_rb);
  and and_19 (enable_carry, clock5, clk_set, pop_byte__ra_rb);
  and and_20 (enable_TMP1, clock5, clk_set, pop_byte__ra_rb);
  and and_21 (store_sp, clock6, clk_set, pop_byte__ra_rb);
  and and_22 (set_ACC, clock7, clk_set, pop_byte__ra_rb);
  and and_23 (store_ss, clock8, clk_set, pop_byte__ra_rb);
  and and_24 (set_ACC, clock9, clk_set, pop_byte__ra_rb);
  and and_25 (sel_MAR, clock10, clk_set, pop_byte__ra_rb);
  and and_26 (store_RAM, clock11, clk_set, pop_byte__ra_rb);
endmodule

module pop_word__ra_rb (
);

  wire ALU_0000, ALU_1010, ALU_1100, clk_en, clk_set, clock5, clock6, clock7, clock8, clock9, clock10,
       clock11, enable_BUS1, enable_carry, enable_CLR, enable_TMP1, load_ACC, load_RAM, load_rb, load_sp,
       load_ss, pop_word__ra_rb, sel_MAR, sel_ra, sel_ss, set_ACC, set_carry, store_RAM, store_sp, store_ss;

  and and_1 (sel_ss, clock5, clk_en, pop_word__ra_rb);
  and and_2 (load_sp, clock5, clk_en, pop_word__ra_rb);
  and and_3 (enable_BUS1, clock5, clk_en, pop_word__ra_rb);
  and and_4 (ALU_1100, clock5, clk_en, pop_word__ra_rb);
  and and_5 (set_carry, clock5, clk_en, pop_word__ra_rb);
  and and_6 (load_ACC, clock6, clk_en, pop_word__ra_rb);
  and and_7 (load_ss, clock7, clk_en, pop_word__ra_rb);
  and and_8 (enable_CLR, clock7, clk_en, pop_word__ra_rb);
  and and_9 (ALU_1010, clock7, clk_en, pop_word__ra_rb);
  and and_10 (load_ACC, clock8, clk_en, pop_word__ra_rb);
  and and_11 (load_RAM, clock9, clk_en, pop_word__ra_rb);
  and and_12 (enable_CLR, clock9, clk_en, pop_word__ra_rb);
  and and_13 (ALU_0000, clock9, clk_en, pop_word__ra_rb);
  and and_14 (sel_ra, clock10, clk_en, pop_word__ra_rb);
  and and_15 (load_rb, clock10, clk_en, pop_word__ra_rb);
  and and_16 (load_ACC, clock11, clk_en, pop_word__ra_rb);
  and and_17 (sel_MAR, clock5, clk_set, pop_word__ra_rb);
  and and_18 (set_ACC, clock5, clk_set, pop_word__ra_rb);
  and and_19 (enable_carry, clock5, clk_set, pop_word__ra_rb);
  and and_20 (enable_TMP1, clock5, clk_set, pop_word__ra_rb);
  and and_21 (store_sp, clock6, clk_set, pop_word__ra_rb);
  and and_22 (set_ACC, clock7, clk_set, pop_word__ra_rb);
  and and_23 (store_ss, clock8, clk_set, pop_word__ra_rb);
  and and_24 (set_ACC, clock9, clk_set, pop_word__ra_rb);
  and and_25 (sel_MAR, clock10, clk_set, pop_word__ra_rb);
  and and_26 (store_RAM, clock11, clk_set, pop_word__ra_rb);
endmodule

module pop0 (
);

  wire ALU_1010, ALU_1100, clk_en, clk_set, clock5, clock6, clock7, clock8, enable_BUS1, enable_carry,
       enable_CLR, enable_TMP1, load_ACC, load_sp, load_ss, pop0, set_ACC, set_carry, store_sp, store_ss;

  and and_1 (load_sp, clock5, clk_en, pop0);
  and and_2 (enable_BUS1, clock5, clk_en, pop0);
  and and_3 (ALU_1100, clock5, clk_en, pop0);
  and and_4 (set_carry, clock5, clk_en, pop0);
  and and_5 (load_ACC, clock6, clk_en, pop0);
  and and_6 (load_ss, clock7, clk_en, pop0);
  and and_7 (enable_CLR, clock7, clk_en, pop0);
  and and_8 (ALU_1010, clock7, clk_en, pop0);
  and and_9 (load_ACC, clock8, clk_en, pop0);
  and and_10 (set_ACC, clock5, clk_set, pop0);
  and and_11 (enable_carry, clock5, clk_set, pop0);
  and and_12 (enable_TMP1, clock5, clk_set, pop0);
  and and_13 (store_sp, clock6, clk_set, pop0);
  and and_14 (set_ACC, clock7, clk_set, pop0);
  and and_15 (store_ss, clock8, clk_set, pop0);
endmodule

module jmp_ra_imm16 (
);

  wire clk_en, clk_set, clock5, clock6, clock7, jmp_ra_imm16, load_IAR, load_ra, load_RAM, sel_CS, sel_MAR,
       set_IAR, store_CS;

  and and_1 (sel_CS, clock5, clk_en, jmp_ra_imm16);
  and and_2 (load_IAR, clock5, clk_en, jmp_ra_imm16);
  and and_3 (load_RAM, clock6, clk_en, jmp_ra_imm16);
  and and_4 (load_ra, clock7, clk_en, jmp_ra_imm16);
  and and_5 (sel_MAR, clock5, clk_set, jmp_ra_imm16);
  and and_6 (set_IAR, clock6, clk_set, jmp_ra_imm16);
  and and_7 (store_CS, clock7, clk_set, jmp_ra_imm16);
endmodule

module jmp_ra_rb (
);

  wire clk_en, clk_set, clock5, clock6, jmp_ra_rb, load_ra, load_rb, store_CS, store_IAR;

  and and_1 (load_ra, clock5, clk_en, jmp_ra_rb);
  and and_2 (load_rb, clock6, clk_en, jmp_ra_rb);
  and and_3 (store_CS, clock5, clk_set, jmp_ra_rb);
  and and_4 (store_IAR, clock6, clk_set, jmp_ra_rb);
endmodule

module ja_ra_imm16 (
);

  wire clk_en, clock5, clock6, clock7, ja_ra_imm16, load_IAR, load_ra, load_RAM, sel_CS, sel_MAR, set_IAR,
       store_CS, tunnel;

  and and_1 (sel_CS, clock5, clk_en, ja_ra_imm16, tunnel);
  and and_2 (load_IAR, clock5, clk_en, ja_ra_imm16, tunnel);
  and and_3 (load_RAM, clock6, clk_en, ja_ra_imm16, tunnel);
  and and_4 (load_ra, clock7, clk_en, ja_ra_imm16, tunnel);
  and and_5 (sel_MAR, clock5, clk_en, ja_ra_imm16, tunnel);
  and and_6 (set_IAR, clock6, clk_en, ja_ra_imm16, tunnel);
  and and_7 (store_CS, clock7, clk_en, ja_ra_imm16, tunnel);
endmodule

module ja_ra_rb (
);

  wire clk_en, clock5, clock6, ja_ra_rb, load_ra, load_rb, store_CS, store_IAR, tunnel;

  and and_1 (load_ra, clock5, clk_en, ja_ra_rb, tunnel);
  and and_2 (load_rb, clock6, clk_en, ja_ra_rb, tunnel);
  and and_3 (store_CS, clock5, clk_en, ja_ra_rb, tunnel);
  and and_4 (store_IAR, clock6, clk_en, ja_ra_rb, tunnel);
endmodule

module jna_ra_imm16 (
);

  wire clk_en, clock5, clock6, clock7, jna_ra_imm16, load_IAR, load_ra, load_RAM, not_above, sel_CS, sel_MAR,
       set_IAR, store_CS, tunnel;

  not not_1 (not_above, tunnel);
  and and_1 (sel_CS, clock5, clk_en, jna_ra_imm16, not_above);
  and and_2 (load_IAR, clock5, clk_en, jna_ra_imm16, not_above);
  and and_3 (load_RAM, clock6, clk_en, jna_ra_imm16, not_above);
  and and_4 (load_ra, clock7, clk_en, jna_ra_imm16, not_above);
  and and_5 (sel_MAR, clock5, clk_en, jna_ra_imm16, not_above);
  and and_6 (set_IAR, clock6, clk_en, jna_ra_imm16, not_above);
  and and_7 (store_CS, clock7, clk_en, jna_ra_imm16, not_above);
endmodule
module jna_ra_rb (
);

  wire clk_en, clock5, clock6, jna_ra_rb, load_ra, load_rb, not_above, store_CS, store_IAR, tunnel;

  not not_1 (not_above, tunnel);
  and and_1 (load_ra, clock5, clk_en, jna_ra_rb, not_above);
  and and_2 (load_rb, clock6, clk_en, jna_ra_rb, not_above);
  and and_3 (store_CS, clock5, clk_en, jna_ra_rb, not_above);
  and and_4 (store_IAR, clock6, clk_en, jna_ra_rb, not_above);
endmodule

module jb_ra_imm16 (
);

  wire clk_en, clock5, clock6, clock7, jb_ra_imm16, load_IAR, load_ra, load_RAM, sel_CS, sel_MAR, set_IAR,
       store_CS, tunnel;

  and and_1 (sel_CS, clock5, clk_en, jb_ra_imm16, tunnel);
  and and_2 (load_IAR, clock5, clk_en, jb_ra_imm16, tunnel);
  and and_3 (load_RAM, clock6, clk_en, jb_ra_imm16, tunnel);
  and and_4 (load_ra, clock7, clk_en, jb_ra_imm16, tunnel);
  and and_5 (sel_MAR, clock5, clk_en, jb_ra_imm16, tunnel);
  and and_6 (set_IAR, clock6, clk_en, jb_ra_imm16, tunnel);
  and and_7 (store_CS, clock7, clk_en, jb_ra_imm16, tunnel);
endmodule

module jb_ra_rb (
);

  wire clk_en, clock5, clock6, jb_ra_rb, load_ra, load_rb, store_CS, store_IAR, tunnel;

  and and_1 (load_ra, clock5, clk_en, jb_ra_rb, tunnel);
  and and_2 (load_rb, clock6, clk_en, jb_ra_rb, tunnel);
  and and_3 (store_CS, clock5, clk_en, jb_ra_rb, tunnel);
  and and_4 (store_IAR, clock6, clk_en, jb_ra_rb, tunnel);
endmodule

module jnb_ra_imm16 (
);

  wire clk_en, clock5, clock6, clock7, jnb_ra_imm16, load_IAR, load_ra, load_RAM, not_below, sel_CS, sel_MAR,
       set_IAR, store_CS, tunnel;

  not not_1 (not_below, tunnel);
  and and_1 (sel_CS, clock5, clk_en, jnb_ra_imm16, not_below);
  and and_2 (load_IAR, clock5, clk_en, jnb_ra_imm16, not_below);
  and and_3 (load_RAM, clock6, clk_en, jnb_ra_imm16, not_below);
  and and_4 (load_ra, clock7, clk_en, jnb_ra_imm16, not_below);
  and and_5 (sel_MAR, clock5, clk_en, jnb_ra_imm16, not_below);
  and and_6 (set_IAR, clock6, clk_en, jnb_ra_imm16, not_below);
  and and_7 (store_CS, clock7, clk_en, jnb_ra_imm16, not_below);
endmodule

module jnb_ra_rb (
);

  wire clk_en, clock5, clock6, jnb_ra_rb, load_ra, load_rb, not_below, store_CS, store_IAR, tunnel;

  not not_1 (not_below, tunnel);
  and and_1 (load_ra, clock5, clk_en, jnb_ra_rb, not_below);
  and and_2 (load_rb, clock6, clk_en, jnb_ra_rb, not_below);
  and and_3 (store_CS, clock5, clk_en, jnb_ra_rb, not_below);
  and and_4 (store_IAR, clock6, clk_en, jnb_ra_rb, not_below);
endmodule

module jeq_ra_imm16 (
);

  wire clk_en, clock5, clock6, clock7, jeq_ra_imm16, load_IAR, load_ra, load_RAM, sel_CS, sel_MAR, set_IAR,
       store_CS, tunnel;

  and and_1 (sel_CS, clock5, clk_en, jeq_ra_imm16, tunnel);
  and and_2 (load_IAR, clock5, clk_en, jeq_ra_imm16, tunnel);
  and and_3 (load_RAM, clock6, clk_en, jeq_ra_imm16, tunnel);
  and and_4 (load_ra, clock7, clk_en, jeq_ra_imm16, tunnel);
  and and_5 (sel_MAR, clock5, clk_en, jeq_ra_imm16, tunnel);
  and and_6 (set_IAR, clock6, clk_en, jeq_ra_imm16, tunnel);
  and and_7 (store_CS, clock7, clk_en, jeq_ra_imm16, tunnel);
endmodule

module jeq_ra_rb (
);

  wire clk_en, clock5, clock6, jeq_ra_rb, load_ra, load_rb, store_CS, store_IAR, tunnel;

  and and_1 (load_ra, clock5, clk_en, jeq_ra_rb, tunnel);
  and and_2 (load_rb, clock6, clk_en, jeq_ra_rb, tunnel);
  and and_3 (store_CS, clock5, clk_en, jeq_ra_rb, tunnel);
  and and_4 (store_IAR, clock6, clk_en, jeq_ra_rb, tunnel);
endmodule

module jneq_ra_imm16 (
);

  wire clk_en, clock5, clock6, clock7, jneq_ra_imm16, load_IAR, load_ra, load_RAM, not_equal, sel_CS,
       sel_MAR, set_IAR, store_CS, tunnel;

  not not_1 (not_equal, tunnel);
  and and_1 (sel_CS, clock5, clk_en, jneq_ra_imm16, not_equal);
  and and_2 (load_IAR, clock5, clk_en, jneq_ra_imm16, not_equal);
  and and_3 (load_RAM, clock6, clk_en, jneq_ra_imm16, not_equal);
  and and_4 (load_ra, clock7, clk_en, jneq_ra_imm16, not_equal);
  and and_5 (sel_MAR, clock5, clk_en, jneq_ra_imm16, not_equal);
  and and_6 (set_IAR, clock6, clk_en, jneq_ra_imm16, not_equal);
  and and_7 (store_CS, clock7, clk_en, jneq_ra_imm16, not_equal);
endmodule

module jneq_ra_rb (
);

  wire clk_en, clock5, clock6, jneq_ra_rb, load_ra, load_rb, not_equal, store_CS, store_IAR, tunnel;

  not not_1 (not_equal, tunnel);
  and and_1 (load_ra, clock5, clk_en, jneq_ra_rb, not_equal);
  and and_2 (load_rb, clock6, clk_en, jneq_ra_rb, not_equal);
  and and_3 (store_CS, clock5, clk_en, jneq_ra_rb, not_equal);
  and and_4 (store_IAR, clock6, clk_en, jneq_ra_rb, not_equal);
endmodule

module jc_ra_imm16 (
);

  wire c, clk_en, clock5, clock6, clock7, jc_ra_imm16, load_IAR, load_ra, load_RAM, sel_CS, sel_MAR, set_IAR,
       store_CS;

  and and_1 (sel_CS, clock5, clk_en, jc_ra_imm16, c);
  and and_2 (load_IAR, clock5, clk_en, jc_ra_imm16, c);
  and and_3 (load_RAM, clock6, clk_en, jc_ra_imm16, c);
  and and_4 (load_ra, clock7, clk_en, jc_ra_imm16, c);
  and and_5 (sel_MAR, clock5, clk_en, jc_ra_imm16, c);
  and and_6 (set_IAR, clock6, clk_en, jc_ra_imm16, c);
  and and_7 (store_CS, clock7, clk_en, jc_ra_imm16, c);
endmodule

module jc_ra_rb (
);

  wire c, clk_en, clock5, clock6, jc_ra_rb, load_ra, load_rb, store_CS, store_IAR;

  and and_1 (load_ra, clock5, clk_en, jc_ra_rb, c);
  and and_2 (load_rb, clock6, clk_en, jc_ra_rb, c);
  and and_3 (store_CS, clock5, clk_en, jc_ra_rb, c);
  and and_4 (store_IAR, clock6, clk_en, jc_ra_rb, c);
endmodule

module jnc_ra_imm16 (
);

  wire c, clk_en, clock5, clock6, clock7, jnc_ra_imm16, load_IAR, load_ra, load_RAM, not_carry, sel_CS,
       sel_MAR, set_IAR, store_CS;

  not not_1 (not_carry, c);
  and and_1 (sel_CS, clock5, clk_en, jnc_ra_imm16, not_carry);
  and and_2 (load_IAR, clock5, clk_en, jnc_ra_imm16, not_carry);
  and and_3 (load_RAM, clock6, clk_en, jnc_ra_imm16, not_carry);
  and and_4 (load_ra, clock7, clk_en, jnc_ra_imm16, not_carry);
  and and_5 (sel_MAR, clock5, clk_en, jnc_ra_imm16, not_carry);
  and and_6 (set_IAR, clock6, clk_en, jnc_ra_imm16, not_carry);
  and and_7 (store_CS, clock7, clk_en, jnc_ra_imm16, not_carry);
endmodule

module jnc_ra_rb (
);

  wire c, clk_en, clock5, clock6, jnc_ra_rb, load_ra, load_rb, not_carry, store_CS, store_IAR;

  not not_1 (not_carry, c);
  and and_1 (load_ra, clock5, clk_en, jnc_ra_rb, not_carry);
  and and_2 (load_rb, clock6, clk_en, jnc_ra_rb, not_carry);
  and and_3 (store_CS, clock5, clk_en, jnc_ra_rb, not_carry);
  and and_4 (store_IAR, clock6, clk_en, jnc_ra_rb, not_carry);
endmodule

module jev_ra_imm16 (
);

  wire clk_en, clock5, clock6, clock7, e, jev_ra_imm16, load_IAR, load_ra, load_RAM, sel_CS, sel_MAR,
       set_IAR, store_CS;

  and and_1 (sel_CS, clock5, clk_en, jev_ra_imm16, e);
  and and_2 (load_IAR, clock5, clk_en, jev_ra_imm16, e);
  and and_3 (load_RAM, clock6, clk_en, jev_ra_imm16, e);
  and and_4 (load_ra, clock7, clk_en, jev_ra_imm16, e);
  and and_5 (sel_MAR, clock5, clk_en, jev_ra_imm16, e);
  and and_6 (set_IAR, clock6, clk_en, jev_ra_imm16, e);
  and and_7 (store_CS, clock7, clk_en, jev_ra_imm16, e);
endmodule

module jev_ra_rb (
);

  wire clk_en, clock5, clock6, e, jev_ra_rb, load_ra, load_rb, store_CS, store_IAR;

  and and_1 (load_ra, clock5, clk_en, jev_ra_rb, e);
  and and_2 (load_rb, clock6, clk_en, jev_ra_rb, e);
  and and_3 (store_CS, clock5, clk_en, jev_ra_rb, e);
  and and_4 (store_IAR, clock6, clk_en, jev_ra_rb, e);
endmodule

module jnev_ra_imm16 (
);

  wire clk_en, clock5, clock6, clock7, e, jnev_ra_imm16, load_IAR, load_ra, load_RAM, not_even, sel_CS,
       sel_MAR, set_IAR, store_CS;

  not not_1 (not_even, e);
  and and_1 (sel_CS, clock5, clk_en, jnev_ra_imm16, not_even);
  and and_2 (load_IAR, clock5, clk_en, jnev_ra_imm16, not_even);
  and and_3 (load_RAM, clock6, clk_en, jnev_ra_imm16, not_even);
  and and_4 (load_ra, clock7, clk_en, jnev_ra_imm16, not_even);
  and and_5 (sel_MAR, clock5, clk_en, jnev_ra_imm16, not_even);
  and and_6 (set_IAR, clock6, clk_en, jnev_ra_imm16, not_even);
  and and_7 (store_CS, clock7, clk_en, jnev_ra_imm16, not_even);
endmodule

module jnev_ra_rb (
);

  wire clk_en, clock5, clock6, e, jnev_ra_rb, load_ra, load_rb, not_even, store_CS, store_IAR;

  not not_1 (not_even, e);
  and and_1 (load_ra, clock5, clk_en, jnev_ra_rb, not_even);
  and and_2 (load_rb, clock6, clk_en, jnev_ra_rb, not_even);
  and and_3 (store_CS, clock5, clk_en, jnev_ra_rb, not_even);
  and and_4 (store_IAR, clock6, clk_en, jnev_ra_rb, not_even);
endmodule

module jp_ra_imm16 (
);

  wire clk_en, clock5, clock6, clock7, jp_ra_imm16, load_IAR, load_ra, load_RAM, p, sel_CS, sel_MAR, set_IAR,
       store_CS;

  and and_1 (sel_CS, clock5, clk_en, jp_ra_imm16, p);
  and and_2 (load_IAR, clock5, clk_en, jp_ra_imm16, p);
  and and_3 (load_RAM, clock6, clk_en, jp_ra_imm16, p);
  and and_4 (load_ra, clock7, clk_en, jp_ra_imm16, p);
  and and_5 (sel_MAR, clock5, clk_en, jp_ra_imm16, p);
  and and_6 (set_IAR, clock6, clk_en, jp_ra_imm16, p);
  and and_7 (store_CS, clock7, clk_en, jp_ra_imm16, p);
endmodule

module jp_ra_rb (
);

  wire clk_en, clock5, clock6, jp_ra_rb, load_ra, load_rb, p, store_CS, store_IAR;

  and and_1 (load_ra, clock5, clk_en, jp_ra_rb, p);
  and and_2 (load_rb, clock6, clk_en, jp_ra_rb, p);
  and and_3 (store_CS, clock5, clk_en, jp_ra_rb, p);
  and and_4 (store_IAR, clock6, clk_en, jp_ra_rb, p);
endmodule

module jnp_ra_imm16 (
);

  wire clk_en, clock5, clock6, clock7, jnp_ra_imm16, load_IAR, load_ra, load_RAM, not_positive, p, sel_CS,
       sel_MAR, set_IAR, store_CS;

  not not_1 (not_positive, p);
  and and_1 (sel_CS, clock5, clk_en, jnp_ra_imm16, not_positive);
  and and_2 (load_IAR, clock5, clk_en, jnp_ra_imm16, not_positive);
  and and_3 (load_RAM, clock6, clk_en, jnp_ra_imm16, not_positive);
  and and_4 (load_ra, clock7, clk_en, jnp_ra_imm16, not_positive);
  and and_5 (sel_MAR, clock5, clk_en, jnp_ra_imm16, not_positive);
  and and_6 (set_IAR, clock6, clk_en, jnp_ra_imm16, not_positive);
  and and_7 (store_CS, clock7, clk_en, jnp_ra_imm16, not_positive);
endmodule

module jnp_ra_rb (
);

  wire clk_en, clock5, clock6, jnp_ra_rb, load_ra, load_rb, not_positive, p, store_CS, store_IAR;

  not not_1 (not_positive, p);
  and and_1 (load_ra, clock5, clk_en, jnp_ra_rb, not_positive);
  and and_2 (load_rb, clock6, clk_en, jnp_ra_rb, not_positive);
  and and_3 (store_CS, clock5, clk_en, jnp_ra_rb, not_positive);
  and and_4 (store_IAR, clock6, clk_en, jnp_ra_rb, not_positive);
endmodule

module jz_ra_imm16 (
);

  wire clk_en, clock5, clock6, clock7, jz_ra_imm16, load_IAR, load_ra, load_RAM, sel_CS, sel_MAR, set_IAR,
       store_CS, z;

  and and_1 (sel_CS, clock5, clk_en, jz_ra_imm16, z);
  and and_2 (load_IAR, clock5, clk_en, jz_ra_imm16, z);
  and and_3 (load_RAM, clock6, clk_en, jz_ra_imm16, z);
  and and_4 (load_ra, clock7, clk_en, jz_ra_imm16, z);
  and and_5 (sel_MAR, clock5, clk_en, jz_ra_imm16, z);
  and and_6 (set_IAR, clock6, clk_en, jz_ra_imm16, z);
  and and_7 (store_CS, clock7, clk_en, jz_ra_imm16, z);
endmodule

module jz_ra_rb (
);

  wire clk_en, clock5, clock6, jz_ra_rb, load_ra, load_rb, store_CS, store_IAR, z;

  and and_1 (load_ra, clock5, clk_en, jz_ra_rb, z);
  and and_2 (load_rb, clock6, clk_en, jz_ra_rb, z);
  and and_3 (store_CS, clock5, clk_en, jz_ra_rb, z);
  and and_4 (store_IAR, clock6, clk_en, jz_ra_rb, z);
endmodule

module jnz_ra_imm16 (
);

  wire clk_en, clock5, clock6, clock7, jnz_ra_imm16, load_IAR, load_ra, load_RAM, not_zero, sel_CS, sel_MAR,
       set_IAR, store_CS, z;

  not not_1 (not_zero, z);
  and and_1 (sel_CS, clock5, clk_en, jnz_ra_imm16, not_zero);
  and and_2 (load_IAR, clock5, clk_en, jnz_ra_imm16, not_zero);
  and and_3 (load_RAM, clock6, clk_en, jnz_ra_imm16, not_zero);
  and and_4 (load_ra, clock7, clk_en, jnz_ra_imm16, not_zero);
  and and_5 (sel_MAR, clock5, clk_en, jnz_ra_imm16, not_zero);
  and and_6 (set_IAR, clock6, clk_en, jnz_ra_imm16, not_zero);
  and and_7 (store_CS, clock7, clk_en, jnz_ra_imm16, not_zero);
endmodule

module jnz_ra_rb (
);

  wire clk_en, clock5, clock6, jnz_ra_rb, load_ra, load_rb, not_zero, store_CS, store_IAR, z;

  not not_1 (not_zero, z);
  and and_1 (load_ra, clock5, clk_en, jnz_ra_rb, not_zero);
  and and_2 (load_rb, clock6, clk_en, jnz_ra_rb, not_zero);
  and and_3 (store_CS, clock5, clk_en, jnz_ra_rb, not_zero);
  and and_4 (store_IAR, clock6, clk_en, jnz_ra_rb, not_zero);
endmodule

module jr_ra_imm16 (
);

  wire clk_en, clock5, clock6, clock7, jr_ra_imm16, load_IAR, load_ra, load_RAM, r, sel_CS, sel_MAR, set_IAR,
       store_CS;

  and and_1 (sel_CS, clock5, clk_en, jr_ra_imm16, r);
  and and_2 (load_IAR, clock5, clk_en, jr_ra_imm16, r);
  and and_3 (load_RAM, clock6, clk_en, jr_ra_imm16, r);
  and and_4 (load_ra, clock7, clk_en, jr_ra_imm16, r);
  and and_5 (sel_MAR, clock5, clk_en, jr_ra_imm16, r);
  and and_6 (set_IAR, clock6, clk_en, jr_ra_imm16, r);
  and and_7 (store_CS, clock7, clk_en, jr_ra_imm16, r);
endmodule

module jr_ra_rb (
);

  wire clk_en, clock5, clock6, jr_ra_rb, load_ra, load_rb, r, store_CS, store_IAR;

  and and_1 (load_ra, clock5, clk_en, jr_ra_rb, r);
  and and_2 (load_rb, clock6, clk_en, jr_ra_rb, r);
  and and_3 (store_CS, clock5, clk_en, jr_ra_rb, r);
  and and_4 (store_IAR, clock6, clk_en, jr_ra_rb, r);
endmodule

module jnr_ra_imm16 (
);

  wire clk_en, clock5, clock6, clock7, jnr_ra_imm16, load_IAR, load_ra, load_RAM, not_reserved, r, sel_CS,
       sel_MAR, set_IAR, store_CS;

  not not_1 (not_reserved, r);
  and and_1 (sel_CS, clock5, clk_en, jnr_ra_imm16, not_reserved);
  and and_2 (load_IAR, clock5, clk_en, jnr_ra_imm16, not_reserved);
  and and_3 (load_RAM, clock6, clk_en, jnr_ra_imm16, not_reserved);
  and and_4 (load_ra, clock7, clk_en, jnr_ra_imm16, not_reserved);
  and and_5 (sel_MAR, clock5, clk_en, jnr_ra_imm16, not_reserved);
  and and_6 (set_IAR, clock6, clk_en, jnr_ra_imm16, not_reserved);
  and and_7 (store_CS, clock7, clk_en, jnr_ra_imm16, not_reserved);
endmodule

module jnr_ra_rb (
);

  wire clk_en, clock5, clock6, jnr_ra_rb, load_ra, load_rb, not_reserved, r, store_CS, store_IAR;

  not not_1 (not_reserved, r);
  and and_1 (load_ra, clock5, clk_en, jnr_ra_rb, not_reserved);
  and and_2 (load_rb, clock6, clk_en, jnr_ra_rb, not_reserved);
  and and_3 (store_CS, clock5, clk_en, jnr_ra_rb, not_reserved);
  and and_4 (store_IAR, clock6, clk_en, jnr_ra_rb, not_reserved);
endmodule

module instructions (
);

  wire adc_ra__imm16, adc_ra__rb, adc_ra__word__rb, add_ra__byte__rb, add_ra__imm16, add_ra__rb,
       add_ra__word__rb, add_word__ra___rb, add_word__ra_rb___imm16, ALU_0000, ALU_0001, ALU_0010, ALU_0011,
       ALU_0100, ALU_0101, ALU_0110, ALU_0111, ALU_1000, ALU_1001, ALU_1010, ALU_1011, ALU_1100, ALU_1101,
       ALU_1110, ALU_1111, and_1_out, and_2_out, and_3_out, and_4_out, and_5_out, and_6_out, and_7_out,
       and_8_out, and_9_out, and_10_out, and_11_out, and_12_out, and_13_out, and_14_out, and_15_out,
       and_16_out, and_17_out, and_18_out, and_19_out, and_20_out, and_21_out, and_22_out, and_23_out,
       and_24_out, and_25_out, and_26_out, and_27_out, and_29_out, and_30_out, and_31_out, and_32_out,
       and_33_out, and_34_out, and_35_out, and_36_out, and_37_out, and_38_out, and_39_out, and_40_out,
       and_41_out, and_42_out, and_43_out, and_44_out, and_45_out, and_46_out, and_47_out, and_48_out,
       and_49_out, and_50_out, and_51_out, and_52_out, and_53_out, and_54_out, and_55_out, and_56_out,
       and_58_out, and_64_out, and_65_out, and_69_out, and_78_out, and_79_out, and_80_out, and_81_out,
       and_82_out, and_83_out, and_84_out, and_85_out, and_86_out, and_87_out, and_88_out, and_89_out,
       and_90_out, and_91_out, and_92_out, and_93_out, and_94_out, and_95_out, and_96_out, and_97_out,
       and_99_out, and_100_out, and_101_out, and_103_out, and_104_out, and_105_out, and_106_out, and_107_out,
       and_108_out, and_109_out, and_110_out, and_111_out, and_112_out, and_113_out, and_114_out,
       and_116_out, and_117_out, and_119_out, and_121_out, and_123_out, and_124_out, and_125_out,
       and_126_out, and_127_out, and_128_out, and_130_out, and_132_out, and_133_out, and_134_out,
       and_135_out, and_136_out, and_137_out, and_138_out, and_139_out, and_140_out, and_141_out,
       and_142_out, and_143_out, and_145_out, and_146_out, and_147_out, and_149_out, and_150_out,
       and_151_out, and_152_out, and_153_out, and_154_out, and_155_out, and_158_out, and_159_out,
       and_160_out, and_161_out, and_162_out, and_163_out, and_165_out, and_166_out, and_167_out,
       and_168_out, and_169_out, and_171_out, and_172_out, and_173_out, and_174_out, and_175_out,
       and_176_out, and_177_out, and_179_out, and_180_out, and_181_out, and_183_out, and_184_out,
       and_185_out, and_186_out, and_189_out, and_191_out, and_192_out, and_193_out, and_194_out,
       and_196_out, and_197_out, and_205_out, and_206_out, and_207_out, and_208_out, and_209_out,
       and_210_out, and_211_out, and_212_out, and_213_out, and_214_out, and_215_out, and_216_out,
       and_217_out, and_218_out, and_219_out, and_220_out, and_221_out, and_222_out, and_223_out,
       and_224_out, and_225_out, and_226_out, and_227_out, and_228_out, and_229_out, and_230_out,
       and_231_out, and_232_out, and_233_out, and_234_out, and_235_out, and_236_out, and_ra__imm16,
       and_ra__rb, and_ra__word__rb, and_word__ra_rb___imm16, arith_ra, arith_ra__imm16, arith_ra__rb,
       arith_ra__word__rb, arith_word__ra_rb, arith_word__ra_rb___imm16, c, clk_en, clk_set, clock0, clock1,
       clock2, clock3, clock4, clock5, clock6, clock7, clock8, clock9, clock10, clock11, clock12, clock13,
       clock14, clock15, cmp_ra__imm16, cmp_ra__rb, cmp_ra__word__rb, cmp_word__ra_rb___imm16, div_ra__imm16,
       div_ra__rb, div_ra__word__rb, e, enable_arith_carry, enable_BUS1, enable_carry, enable_CLR,
       enable_lowmask, enable_TMP, enable_TMP1, END, flip_ra, flip_word__ra_rb, IR0, IR1, IR2, IR3, IR4, IR5,
       IR6, IR7, IR8, IR9, IR10, IR11, IR12, IR13, IR14, IR15, ja_ra_imm16, ja_ra_rb, jb_ra_imm16, jb_ra_rb,
       jc_ra_imm16, jc_ra_rb, jeq_ra_imm16, jeq_ra_rb, jev_ra_imm16, jev_ra_rb, jmp_ra_imm16, jmp_ra_rb,
       jna_ra_imm16, jna_ra_rb, jnb_ra_imm16, jnb_ra_rb, jnc_ra_imm16, jnc_ra_rb, jneq_ra_imm16, jneq_ra_rb,
       jnev_ra_imm16, jnev_ra_rb, jnp_ra_imm16, jnp_ra_rb, jnr_ra_imm16, jnr_ra_rb, jnz_ra_imm16, jnz_ra_rb,
       jp_ra_imm16, jp_ra_rb, jr_ra_imm16, jr_ra_rb, jump, jump_ra_imm16, jump_ra_rb, jz_ra_imm16, jz_ra_rb,
       load_ACC, load_cs, load_IAR, load_ra, load_RAM, load_rb, load_sp, load_ss, mod_ra__imm16, mod_ra__rb,
       mod_ra__word__rb, mov_ra__byte__rb, mov_ra__byte__rb_imm16, mov_ra__imm16, mov_ra__rb,
       mov_ra__word__rb, mov_ra__word__rb_imm16, mov_word__ra___rb, mov_word__ra_rb___imm16, mul_ra__imm16,
       mul_ra__rb, mul_ra__word__rb, neg_ra, neg_word__ra_rb, not_above, not_below, not_carry, not_equal,
       not_even, not_positive, not_reserved, not_zero, or_1_out, or_2_out, or_3_out, or_4_out, or_5_out,
       or_6_out, or_7_out, or_8_out, or_9_out, or_10_out, or_11_out, or_12_out, or_13_out, or_14_out,
       or_15_out, or_16_out, or_17_out, or_18_out, or_19_out, or_20_out, or_21_out, or_22_out, or_23_out,
       or_24_out, or_25_out, or_26_out, or_27_out, or_28_out, or_29_out, or_30_out, or_31_out, or_32_out,
       or_33_out, or_34_out, or_35_out, or_36_out, or_37_out, or_38_out, or_39_out, or_40_out, or_41_out,
       or_42_out, or_43_out, or_44_out, or_45_out, or_46_out, or_47_out, or_48_out, or_49_out, or_50_out,
       or_51_out, or_52_out, or_53_out, or_54_out, or_55_out, or_56_out, or_57_out, or_58_out, or_59_out,
       or_60_out, or_61_out, or_62_out, or_63_out, or_64_out, or_65_out, or_66_out, or_67_out, or_68_out,
       or_69_out, or_70_out, or_72_out, or_73_out, or_74_out, or_75_out, or_76_out, or_77_out, or_78_out,
       or_79_out, or_80_out, or_81_out, or_82_out, or_83_out, or_84_out, or_85_out, or_86_out, or_87_out,
       or_88_out, or_89_out, or_90_out, or_91_out, or_92_out, or_93_out, or_94_out, or_95_out, or_96_out,
       or_97_out, or_98_out, or_99_out, or_100_out, or_101_out, or_102_out, or_103_out, or_104_out,
       or_105_out, or_106_out, or_107_out, or_108_out, or_109_out, or_110_out, or_111_out, or_112_out,
       or_113_out, or_114_out, or_115_out, or_116_out, or_117_out, or_118_out, or_119_out, or_120_out,
       or_121_out, or_122_out, or_123_out, or_124_out, or_125_out, or_126_out, or_127_out, or_128_out,
       or_129_out, or_130_out, or_131_out, or_132_out, or_133_out, or_134_out, or_135_out, or_136_out,
       or_137_out, or_138_out, or_140_out, or_141_out, or_142_out, or_143_out, or_144_out, or_145_out,
       or_146_out, or_147_out, or_148_out, or_149_out, or_150_out, or_151_out, or_152_out, or_153_out,
       or_154_out, or_155_out, or_156_out, or_157_out, or_158_out, or_159_out, or_160_out, or_161_out,
       or_162_out, or_163_out, or_164_out, or_165_out, or_166_out, or_167_out, or_168_out, or_169_out,
       or_170_out, or_171_out, or_172_out, or_173_out, or_174_out, or_178_out, or_179_out, or_180_out,
       or_181_out, or_182_out, or_183_out, or_184_out, or_185_out, or_186_out, or_187_out, or_188_out,
       or_189_out, or_190_out, or_191_out, or_192_out, or_193_out, or_194_out, or_195_out, or_196_out,
       or_197_out, or_198_out, or_199_out, or_200_out, or_201_out, or_202_out, or_203_out, or_204_out,
       or_205_out, or_206_out, or_207_out, or_208_out, or_209_out, or_210_out, or_211_out, or_212_out,
       or_213_out, or_214_out, or_215_out, or_216_out, or_217_out, or_218_out, or_219_out, or_220_out,
       or_221_out, or_222_out, or_223_out, or_224_out, or_225_out, or_226_out, or_227_out, or_228_out,
       or_229_out, or_230_out, or_231_out, or_232_out, or_233_out, or_234_out, or_235_out, or_236_out,
       or_237_out, or_238_out, or_239_out, or_240_out, or_241_out, or_242_out, or_243_out, or_244_out,
       or_245_out, or_246_out, or_247_out, or_248_out, or_249_out, or_250_out, or_251_out, or_ra__imm16,
       or_ra__rb, or_ra__word__rb, or_word__ra_rb___imm16, p, pop, pop0, pop_byte__ra_rb, pop_ra,
       pop_word__ra_rb, push, push_byte__ra_rb, push_imm16, push_ra, push_word__ra_rb, r, sar_ra__imm4,
       sar_word__ra_rb___imm4, sel_cs, sel_ds, sel_MAR, sel_ra, sel_rb, sel_ss, set_ACC, set_arith_flags,
       set_carry, set_IAR, shift_ra__imm4, shift_word__ra_rb___imm4, shl_ra__imm4, shl_word__ra_rb___imm4,
       shr_ra__imm4, shr_word__ra_rb___imm4, store_cs, store_IR, store_ra, store_RAM, store_rb, store_sp,
       store_ss, sub_ra__imm16, sub_ra__rb, tunnel, tunnel_t, tunnel_t_t, undriven, undriven_2, xchg_ra__rb,
       xor_ra__imm16, xor_ra__rb, xor_ra__word__rb, xor_word__ra_rb___imm16, z;

  and and_1 (and_1_out, clock9, push_imm16);
  or or_1 (or_1_out, shift_ra__imm4, shift_word__ra_rb___imm4);
  or or_2 (or_2_out, arith_ra__imm16, cmp_ra__imm16);
  or or_3 (or_3_out, arith_word__ra_rb___imm16, cmp_word__ra_rb___imm16);
  or or_4 (or_4_out, mov_ra__imm16, mov_word__ra_rb___imm16);
  or or_5 (or_5_out, mov_ra__byte__rb_imm16, mov_ra__word__rb_imm16);
  or or_6 (or_6_out, jump_ra_rb, jump_ra_imm16);
  or or_7 (or_7_out, shift_ra__imm4, shift_word__ra_rb___imm4);
  or or_8 (or_8_out, arith_ra__imm16, cmp_ra__imm16);
  or or_9 (or_9_out, arith_word__ra_rb___imm16, cmp_word__ra_rb___imm16);
  or or_10 (or_10_out, mov_ra__byte__rb_imm16, mov_ra__word__rb_imm16, mov_word__ra_rb___imm16);
  and and_2 (and_2_out, clock10, push_imm16);
  or or_11 (or_11_out, mov_ra__byte__rb, mov_ra__word__rb);
  or or_12 (or_12_out, add_ra__byte__rb, arith_word__ra_rb, arith_ra__word__rb, cmp_ra__word__rb);
  and and_3 (and_3_out, clock7, add_word__ra___rb);
  or or_13 (or_13_out, shift_ra__imm4, shift_word__ra_rb___imm4);
  or or_14 (or_14_out, mov_ra__imm16, mov_word__ra_rb___imm16);
  or or_15 (or_15_out, mov_ra__byte__rb_imm16, mov_ra__word__rb_imm16);
  or or_16 (or_16_out, arith_word__ra_rb___imm16, cmp_word__ra_rb___imm16);
  or or_17 (or_17_out, arith_ra__imm16, cmp_ra__imm16);
  or or_18 (or_18_out, pop_ra, pop_byte__ra_rb, pop_word__ra_rb);
  or or_19 (or_19_out, push_byte__ra_rb, push_word__ra_rb);
  or or_20 (or_20_out, or_19_out, or_21_out);
  or or_21 (or_21_out, mov_ra__byte__rb_imm16, mov_ra__word__rb_imm16);
  and and_4 (and_4_out, clock11, or_22_out);
  or or_22 (or_22_out, arith_word__ra_rb___imm16, cmp_word__ra_rb___imm16);
  and and_5 (and_5_out, clock13, push_imm16);
  and and_6 (and_6_out, clock6, mov_word__ra___rb);
  and and_7 (and_7_out, clock7, arith_word__ra_rb);
  and and_8 (and_8_out, clock8, add_word__ra___rb);
  and and_9 (and_9_out, clock11, or_23_out);
  or or_23 (or_23_out, pop_byte__ra_rb, pop_word__ra_rb, mov_word__ra_rb___imm16);
  and and_10 (and_10_out, clock12, or_24_out);
  or or_24 (or_24_out, push_byte__ra_rb, push_word__ra_rb, shift_word__ra_rb___imm4, arith_word__ra_rb___imm16);
  and and_11 (and_11_out, clock15, push_imm16);
  or or_25 (or_25_out, shift_ra__imm4, shift_word__ra_rb___imm4);
  or or_26 (or_26_out, arith_word__ra_rb___imm16, cmp_word__ra_rb___imm16);
  or or_27 (or_27_out, mov_ra__imm16, arith_ra__imm16, cmp_ra__imm16);
  or or_28 (or_28_out, mov_word__ra_rb___imm16, mov_ra__byte__rb_imm16, mov_ra__word__rb_imm16);
  and and_12 (and_12_out, clock6, add_ra__rb);
  and and_13 (and_13_out, clock7, or_29_out);
  or or_29 (or_29_out, add_word__ra___rb, add_ra__word__rb);
  and and_14 (and_14_out, clock8, add_ra__byte__rb);
  or or_30 (or_30_out, push_imm16, pop_word__ra_rb, mov_word__ra_rb___imm16);
  and and_15 (and_15_out, clock10, or_31_out);
  or or_31 (or_31_out, add_ra__imm16, push_word__ra_rb);
  and and_16 (and_16_out, clock11, add_word__ra_rb___imm16);
  and and_17 (and_17_out, clock13, push_imm16);
  or or_32 (or_32_out, pop, pop0);
  or or_33 (or_33_out, pop, pop0);
  and and_18 (and_18_out, clock6, sub_ra__rb);
  and and_19 (and_19_out, clock10, sub_ra__imm16);
  and and_20 (and_20_out, clock5, mov_ra__rb);
  and and_21 (and_21_out, clock6, or_34_out);
  or or_34 (or_34_out, mov_ra__byte__rb, mov_ra__word__rb);
  and and_22 (and_22_out, clock7, or_35_out);
  or or_35 (or_35_out, arith_ra, arith_ra__rb, xchg_ra__rb);
  and and_23 (and_23_out, clock8, or_36_out);
  or or_36 (or_36_out, mov_ra__byte__rb, arith_ra__word__rb);
  and and_24 (and_24_out, clock9, or_37_out);
  or or_37 (or_37_out, pop_ra, mov_ra__imm16, add_ra__byte__rb);
  and and_25 (and_25_out, clock10, or_38_out);
  or or_38 (or_38_out, mov_ra__byte__rb_imm16, mov_ra__word__rb_imm16);
  and and_26 (and_26_out, clock11, or_39_out);
  or or_39 (or_39_out, shift_ra__imm4, arith_ra__imm16);
  and and_27 (and_27_out, clock12, mov_ra__byte__rb_imm16);
  and and_28 (store_IR, clock1, clk_set);
  and and_29 (and_29_out, clock9, push_imm16);
  or or_40 (or_40_out, shift_ra__imm4, shift_word__ra_rb___imm4);
  or or_41 (or_41_out, arith_ra__imm16, cmp_ra__imm16);
  or or_42 (or_42_out, mov_ra__imm16, mov_word__ra_rb___imm16);
  or or_43 (or_43_out, mov_ra__byte__rb_imm16, mov_ra__word__rb_imm16);
  or or_44 (or_44_out, arith_word__ra_rb___imm16, cmp_word__ra_rb___imm16);
  or or_45 (or_45_out, pop0, pop);
  or or_46 (or_46_out, pop, pop0);
  or or_47 (or_47_out, arith_ra__imm16, cmp_ra__imm16);
  or or_48 (or_48_out, shift_ra__imm4, shift_word__ra_rb___imm4);
  and and_30 (and_30_out, clock6, or_49_out);
  or or_49 (or_49_out, arith_ra, arith_ra__rb, cmp_ra__rb, arith_word__ra_rb, adc_ra__word__rb);
  and and_31 (and_31_out, clock7, or_50_out);
  or or_50 (or_50_out, add_word__ra___rb, arith_ra__word__rb, cmp_ra__word__rb);
  and and_32 (and_32_out, clock8, add_ra__byte__rb);
  and and_33 (and_33_out, clock10, or_51_out);
  or or_51 (or_51_out, shift_ra__imm4, arith_ra__imm16, cmp_ra__imm16);
  and and_34 (and_34_out, clock11, or_52_out);
  or or_52 (or_52_out, shift_word__ra_rb___imm4, arith_word__ra_rb___imm16, cmp_word__ra_rb___imm16);
  and and_35 (and_35_out, clock6, or_53_out);
  or or_53 (or_53_out, or_11_out, or_12_out, jump_ra_imm16);
  and and_36 (and_36_out, clock9, or_54_out);
  or or_54 (or_54_out, or_13_out, or_14_out, or_15_out, or_16_out, or_17_out, or_18_out);
  and and_37 (and_37_out, clock10, or_20_out);
  and and_38 (and_38_out, clock10, push_ra);
  and and_39 (and_39_out, clock5, or_55_out);
  or or_55 (or_55_out, jump_ra_imm16, or_1_out, or_2_out, or_3_out, or_4_out, or_5_out);
  or or_56 (or_56_out, mov_ra__imm16, or_6_out, or_7_out, or_8_out, or_9_out, or_10_out);
  or or_57 (or_57_out, push, xchg_ra__rb, or_25_out, or_26_out, or_27_out, or_28_out);
  and and_40 (and_40_out, clock9, or_30_out);
  or or_58 (or_58_out, neg_ra, neg_word__ra_rb);
  and and_41 (and_41_out, clock5, or_33_out);
  or or_59 (or_59_out, and_41_out, and_18_out, and_19_out);
  and and_42 (and_42_out, clock6, mul_ra__rb);
  and and_43 (and_43_out, clock7, mul_ra__word__rb);
  and and_44 (and_44_out, clock10, mul_ra__imm16);
  and and_45 (and_45_out, clock6, div_ra__rb);
  or or_60 (or_60_out, and_45_out, and_46_out, and_47_out);
  and and_46 (and_46_out, clock7, div_ra__word__rb);
  and and_47 (and_47_out, clock10, div_ra__imm16);
  and and_48 (and_48_out, clock6, mod_ra__rb);
  and and_49 (and_49_out, clock7, mod_ra__word__rb);
  or or_61 (or_61_out, and_48_out, and_49_out, and_50_out);
  and and_50 (and_50_out, clock10, mod_ra__imm16);
  or or_62 (or_62_out, arith_word__ra_rb___imm16, cmp_word__ra_rb___imm16);
  or or_63 (or_63_out, mov_ra__imm16, mov_ra__byte__rb_imm16, mov_ra__word__rb_imm16, mov_word__ra_rb___imm16);
  or or_64 (or_64_out, clock0, and_1_out, and_39_out);
  or or_65 (or_65_out, clock2, and_51_out, and_2_out);
  and and_51 (and_51_out, clock6, or_56_out);
  and and_52 (and_52_out, clock5, or_57_out);
  and and_53 (and_53_out, clock6, clk_en, cmp_ra__rb);
  and and_54 (and_54_out, clock7, clk_en, cmp_ra__word__rb);
  and and_55 (and_55_out, clock10, clk_en, cmp_ra__imm16);
  and and_56 (and_56_out, clock11, clk_en, cmp_word__ra_rb___imm16);
  and and_57 (ALU_1010, clock7, clk_en, or_32_out);
  and and_58 (and_58_out, clock6, or_58_out);
  and and_59 (ALU_1100, clk_en, or_59_out);
  and and_60 (ALU_1101, clk_en, or_66_out);
  or or_66 (or_66_out, and_42_out, and_43_out, and_44_out);
  and and_61 (ALU_1110, clk_en, or_60_out);
  and and_62 (ALU_1111, clk_en, or_61_out);
  or or_67 (or_67_out, or_40_out, or_41_out, or_42_out, or_43_out, or_44_out, or_45_out, push);
  or or_68 (or_68_out, push, or_46_out, or_47_out, or_48_out, or_62_out, or_63_out);
  or or_69 (or_69_out, and_30_out, and_31_out, and_32_out, and_33_out, and_34_out);
  or or_70 (or_70_out, and_6_out, and_7_out, and_8_out, and_38_out, and_9_out, and_10_out, and_11_out);
  or or_71 (ALU_0111, and_53_out, and_54_out, and_55_out, and_56_out);
  and and_63 (ALU_1011, clk_en, and_58_out);
  or or_72 (or_72_out, and_20_out, and_21_out, and_22_out, and_23_out, and_24_out, and_25_out, and_26_out, and_27_out);
  and and_64 (and_64_out, clock9, push_imm16);
  and and_65 (and_65_out, clock5, or_68_out);
  and and_66 (store_RAM, clk_set, or_70_out);
  and and_67 (load_IAR, clk_en, or_64_out);
  and and_68 (set_IAR, clk_set, or_65_out);
  or or_73 (or_73_out, clock0, and_52_out, and_12_out, and_13_out, and_14_out, and_40_out, and_15_out, and_16_out, and_17_out);
  and and_69 (and_69_out, clock5, or_67_out);
  and and_70 (set_arith_flags, clk_set, or_69_out);
  or or_74 (or_74_out, clock1, and_35_out, and_3_out, and_36_out, and_37_out, and_4_out, and_5_out);
  and and_71 (store_ra, clk_set, or_72_out);
  or or_75 (or_75_out, clock0, and_29_out, and_69_out);
  or or_76 (or_76_out, clock0, and_64_out, and_65_out);
  and and_72 (load_RAM, clk_en, or_74_out);
  and and_73 (ALU_0000, clk_en, or_73_out);
  and and_74 (enable_carry, clk_set, or_75_out);
  and and_75 (set_carry, clk_en, or_76_out);
  or or_77 (or_77_out, mov_ra__byte__rb_imm16, mov_ra__word__rb_imm16);
  or or_78 (or_78_out, flip_ra, flip_word__ra_rb);
  or or_79 (or_79_out, and_ra__rb, add_ra__byte__rb);
  or or_80 (or_80_out, mov_ra__byte__rb, and_ra__word__rb);
  or or_81 (or_81_out, and_ra__imm16, push_byte__ra_rb);
  or or_82 (or_82_out, mov_ra__byte__rb_imm16, and_word__ra_rb___imm16);
  and and_76 (sel_rb, clock9, clk_en, or_77_out);
  and and_77 (store_rb, clock6, clk_set, xchg_ra__rb);
  or or_83 (or_83_out, shift_ra__imm4, shift_word__ra_rb___imm4);
  or or_84 (or_84_out, arith_ra__imm16, cmp_ra__imm16);
  or or_85 (or_85_out, mov_ra__byte__rb_imm16, mov_ra__word__rb_imm16);
  or or_86 (or_86_out, arith_word__ra_rb___imm16, cmp_word__ra_rb___imm16);
  or or_87 (or_87_out, pop0, pop, push);
  or or_88 (or_88_out, xchg_ra__rb, mov_ra__imm16, mov_word__ra_rb___imm16);
  or or_89 (or_89_out, shift_ra__imm4, shift_word__ra_rb___imm4);
  or or_90 (or_90_out, arith_word__ra_rb___imm16, cmp_word__ra_rb___imm16);
  or or_91 (or_91_out, arith_ra__word__rb, cmp_ra__word__rb);
  or or_92 (or_92_out, arith_ra__imm16, cmp_ra__imm16);
  or or_93 (or_93_out, mov_ra__byte__rb, mov_ra__byte__rb_imm16, mov_ra__word__rb_imm16);
  or or_94 (or_94_out, add_word__ra___rb, mov_ra__imm16, mov_word__ra_rb___imm16);
  or or_95 (or_95_out, pop, pop0, push);
  or or_96 (or_96_out, push_imm16, pop_byte__ra_rb, pop_word__ra_rb);
  and and_78 (and_78_out, clock6, or_79_out);
  and and_79 (and_79_out, clock7, or_80_out);
  and and_80 (and_80_out, clock9, pop_byte__ra_rb);
  and and_81 (and_81_out, clock10, or_81_out);
  and and_82 (and_82_out, clock11, or_82_out);
  and and_83 (and_83_out, clock6, adc_ra__rb);
  or or_97 (or_97_out, arith_ra__imm16, cmp_ra__imm16);
  or or_98 (or_98_out, mov_ra__byte__rb_imm16, mov_ra__word__rb_imm16);
  or or_99 (or_99_out, shift_ra__imm4, shift_word__ra_rb___imm4);
  or or_100 (or_100_out, arith_word__ra_rb___imm16, cmp_word__ra_rb___imm16);
  or or_101 (or_101_out, mov_ra__imm16, mov_word__ra_rb___imm16, adc_ra__word__rb);
  and and_84 (and_84_out, clock10, adc_ra__imm16);
  and and_85 (and_85_out, clock11, push_imm16);
  and and_86 (and_86_out, clock5, jump_ra_rb);
  and and_87 (and_87_out, clock7, jump_ra_imm16);
  or or_102 (or_102_out, arith_ra__imm16, cmp_ra__imm16);
  or or_103 (or_103_out, arith_word__ra_rb___imm16, cmp_word__ra_rb___imm16);
  or or_104 (or_104_out, shift_ra__imm4, shift_word__ra_rb___imm4);
  and and_88 (and_88_out, clock12, push_imm16);
  and and_89 (and_89_out, clock6, or_105_out);
  or or_105 (or_105_out, arith_ra, arith_ra__rb, cmp_ra__rb, add_ra__byte__rb, arith_word__ra_rb);
  and and_90 (and_90_out, clock8, add_ra__byte__rb);
  and and_91 (and_91_out, clock10, or_106_out);
  or or_106 (or_106_out, shift_ra__imm4, arith_ra__imm16, cmp_ra__imm16, push_byte__ra_rb, push_word__ra_rb);
  and and_92 (and_92_out, clock11, or_107_out);
  or or_107 (or_107_out, push_imm16, shift_word__ra_rb___imm4, mov_ra__byte__rb_imm16, arith_word__ra_rb___imm16, cmp_word__ra_rb___imm16);
  and and_93 (and_93_out, clock13, push_imm16);
  and and_94 (and_94_out, clock6, or_78_out);
  or or_108 (or_108_out, and_78_out, and_79_out, and_80_out, and_81_out, and_82_out);
  and and_95 (and_95_out, clock9, push_imm16);
  or or_109 (or_109_out, shift_ra__imm4, shift_word__ra_rb___imm4);
  or or_110 (or_110_out, mov_ra__byte__rb_imm16, mov_ra__word__rb_imm16);
  or or_111 (or_111_out, arith_ra__imm16, cmp_ra__imm16, mov_ra__imm16);
  or or_112 (or_112_out, mov_word__ra_rb___imm16, cmp_word__ra_rb___imm16, arith_word__ra_rb___imm16);
  or or_113 (or_113_out, shift_ra__imm4, shift_word__ra_rb___imm4);
  or or_114 (or_114_out, arith_ra__imm16, cmp_ra__imm16);
  or or_115 (or_115_out, arith_word__ra_rb___imm16, cmp_word__ra_rb___imm16);
  or or_116 (or_116_out, mov_ra__byte__rb_imm16, mov_ra__word__rb_imm16);
  or or_117 (or_117_out, mov_ra__imm16, mov_word__ra_rb___imm16);
  and and_96 (and_96_out, clock11, push_imm16);
  or or_118 (or_118_out, mov_ra__imm16, mov_ra__byte__rb_imm16, mov_ra__word__rb_imm16, mov_word__ra_rb___imm16);
  and and_97 (and_97_out, clock9, or_119_out);
  or or_119 (or_119_out, mov_word__ra_rb___imm16, or_96_out);
  and and_98 (ALU_0011, clk_en, and_94_out);
  or or_120 (or_120_out, or_113_out, or_114_out, or_115_out, or_116_out, or_117_out);
  and and_99 (and_99_out, clock8, or_121_out);
  or or_121 (or_121_out, or_102_out, or_103_out, or_104_out, or_118_out);
  or or_122 (or_122_out, or_83_out, or_84_out, or_85_out, or_86_out, or_87_out, or_88_out);
  or or_123 (or_123_out, or_89_out, or_90_out, or_91_out, or_92_out, or_93_out, or_94_out, or_95_out);
  and and_100 (and_100_out, clock10, clk_en, shr_ra__imm4);
  and and_101 (and_101_out, clock11, clk_en, shr_word__ra_rb___imm4);
  and and_102 (ALU_0100, clk_en, or_108_out);
  and and_103 (and_103_out, clock7, or_124_out);
  or or_124 (or_124_out, push, or_97_out, or_98_out, or_99_out, or_100_out, or_101_out);
  and and_104 (and_104_out, clock5, or_125_out);
  or or_125 (or_125_out, or_109_out, or_110_out, or_111_out, or_112_out, jump_ra_imm16);
  and and_105 (and_105_out, clock7, or_120_out);
  or or_126 (or_126_out, mov_ra__imm16, mov_ra__word__rb);
  or or_127 (or_127_out, mov_word__ra___rb, mov_word__ra_rb___imm16);
  or or_128 (or_128_out, shift_ra__imm4, shift_word__ra_rb___imm4);
  or or_129 (or_129_out, arith_ra__imm16, cmp_ra__imm16);
  or or_130 (or_130_out, arith_ra__word__rb, cmp_ra__word__rb);
  or or_131 (or_131_out, arith_word__ra_rb, add_word__ra___rb);
  or or_132 (or_132_out, mov_ra__byte__rb_imm16, mov_ra__word__rb_imm16);
  or or_133 (or_133_out, push_ra, push_imm16);
  or or_134 (or_134_out, push_byte__ra_rb, push_word__ra_rb);
  or or_135 (or_135_out, pop_byte__ra_rb, pop_word__ra_rb);
  or or_136 (or_136_out, mov_word__ra_rb___imm16, shift_word__ra_rb___imm4);
  or or_137 (or_137_out, arith_word__ra_rb___imm16, cmp_word__ra_rb___imm16);
  and and_106 (and_106_out, clock11, or_138_out);
  or or_138 (or_138_out, push_byte__ra_rb, push_word__ra_rb);
  and and_107 (and_107_out, clock14, push_imm16);
  and and_108 (and_108_out, clock5, or_122_out);
  and and_109 (and_109_out, clock7, or_123_out);
  or or_139 (ALU_0001, and_100_out, and_101_out);
  or or_140 (or_140_out, clock0, and_95_out, and_104_out);
  or or_141 (or_141_out, clock3, and_105_out, and_96_out);
  and and_110 (and_110_out, sub_ra__rb, c);
  and and_111 (and_111_out, clock13, sub_ra__imm16, c);
  or or_142 (or_142_out, mov_ra__imm16, mov_ra__byte__rb_imm16, mov_ra__word__rb_imm16, mov_word__ra_rb___imm16);
  or or_143 (or_143_out, undriven, undriven_2);
  or or_144 (or_144_out, shift_ra__imm4, shift_word__ra_rb___imm4);
  or or_145 (or_145_out, arith_ra__imm16, cmp_ra__imm16);
  or or_146 (or_146_out, pop, pop0);
  or or_147 (or_147_out, mov_ra__imm16, mov_ra__byte__rb_imm16, mov_ra__word__rb_imm16, mov_word__ra_rb___imm16);
  or or_148 (or_148_out, shift_ra__imm4, shift_word__ra_rb___imm4);
  or or_149 (or_149_out, arith_word__ra_rb___imm16, cmp_word__ra_rb___imm16);
  and and_112 (and_112_out, clock6, adc_ra__word__rb);
  and and_113 (and_113_out, clock9, or_150_out);
  or or_150 (or_150_out, push_imm16, adc_ra__imm16);
  or or_151 (or_151_out, mov_ra__imm16, arith_ra__imm16, arith_word__ra_rb___imm16, cmp_word__ra_rb___imm16);
  or or_152 (or_152_out, pop, pop0, push);
  or or_153 (or_153_out, arith_word__ra_rb___imm16, cmp_word__ra_rb___imm16);
  or or_154 (or_154_out, mov_ra__byte__rb_imm16, mov_ra__word__rb_imm16);
  or or_155 (or_155_out, mov_ra__byte__rb, add_ra__byte__rb);
  or or_156 (or_156_out, or_132_out, or_133_out, or_134_out);
  and and_114 (and_114_out, clock10, or_157_out);
  or or_157 (or_157_out, or_135_out, or_136_out, or_137_out);
  and and_115 (sel_cs, clk_en, or_140_out);
  or or_158 (or_158_out, clock4, and_86_out, and_87_out, and_99_out, and_88_out);
  and and_116 (and_116_out, clock9, or_159_out);
  or or_159 (or_159_out, and_110_out, push_imm16);
  or or_160 (or_160_out, arith_ra__imm16, cmp_ra__imm16);
  or or_161 (or_161_out, pop, pop0);
  or or_162 (or_162_out, shift_ra__imm4, shift_word__ra_rb___imm4);
  or or_163 (or_163_out, adc_ra__rb, cmp_ra__imm16);
  or or_164 (or_164_out, mov_ra__byte__rb_imm16, mov_ra__word__rb_imm16, mov_word__ra_rb___imm16);
  and and_117 (and_117_out, clock9, or_156_out);
  and and_118 (load_cs, clk_en, or_141_out);
  or or_165 (or_165_out, or_162_out, or_163_out, or_164_out, or_151_out, or_152_out);
  and and_119 (and_119_out, clock5, or_166_out);
  or or_166 (or_166_out, or_126_out, or_127_out, or_128_out, or_129_out, or_130_out, or_131_out, or_153_out, or_154_out, or_155_out, jump_ra_imm16, pop);
  or or_167 (or_167_out, clock3, and_83_out, and_103_out, and_84_out, and_85_out);
  and and_120 (store_cs, clk_set, or_158_out);
  or or_168 (or_168_out, or_142_out, or_143_out, or_144_out, or_145_out, or_146_out, push);
  or or_169 (or_169_out, or_147_out, or_148_out, or_149_out, or_160_out, or_161_out, push);
  and and_121 (and_121_out, clock5, or_165_out);
  and and_122 (END, ~IR0, ~IR1, ~IR2, ~IR3, ~IR4, ~IR5, ~IR6, ~IR7, IR8, IR9, IR10, IR11, IR12, IR13, IR14, IR15);  // AND_Gate
  and and_123 (and_123_out, clock5, xchg_ra__rb);
  and and_124 (and_124_out, clock9, or_170_out);
  or or_170 (or_170_out, pop_word__ra_rb, mov_word__ra_rb___imm16);
  and and_125 (and_125_out, clock10, push_word__ra_rb);
  and and_126 (and_126_out, clock11, push_imm16);
  and and_127 (and_127_out, clock13, push_imm16);
  and and_128 (and_128_out, clock7, or_169_out);
  or or_171 (or_171_out, clock0, clock3, and_108_out, and_89_out, and_109_out, and_90_out, and_97_out, and_91_out, and_92_out, and_93_out);
  and and_129 (ALU_1000, clk_en, or_167_out);
  and and_130 (and_130_out, clock5, or_168_out);
  and and_131 (sel_MAR, clk_set, or_172_out);
  or or_172 (or_172_out, clock0, and_119_out, and_117_out, and_114_out, and_106_out, and_107_out);
  and and_132 (and_132_out, clock10, clk_en, shl_ra__imm4);
  and and_133 (and_133_out, clock11, clk_en, shl_word__ra_rb___imm4);
  and and_134 (and_134_out, clock6, clk_en, or_ra__rb);
  and and_135 (and_135_out, clock7, clk_en, or_ra__word__rb);
  and and_136 (and_136_out, clock10, clk_en, or_ra__imm16);
  and and_137 (and_137_out, clock11, clk_en, or_word__ra_rb___imm16);
  and and_138 (and_138_out, clock6, clk_en, xor_ra__rb);
  and and_139 (and_139_out, clock7, clk_en, xor_ra__word__rb);
  and and_140 (and_140_out, clock10, clk_en, xor_ra__imm16);
  and and_141 (and_141_out, clock11, clk_en, xor_word__ra_rb___imm16);
  and and_142 (and_142_out, clock10, sar_ra__imm4);
  and and_143 (and_143_out, clock11, sar_word__ra_rb___imm4);
  or or_173 (or_173_out, clock0, and_116_out, and_111_out, and_130_out);
  or or_174 (or_174_out, clock0, and_112_out, and_113_out, and_121_out);
  and and_144 (set_ACC, clk_set, or_171_out);
  or or_175 (ALU_0010, and_132_out, and_133_out);
  or or_176 (ALU_0101, and_134_out, and_135_out, and_136_out, and_137_out);
  or or_177 (ALU_0110, and_138_out, and_139_out, and_140_out, and_141_out);
  or or_178 (or_178_out, and_142_out, and_143_out);
  and and_145 (and_145_out, clock5, arith_word__ra_rb);
  and and_146 (and_146_out, clock9, or_179_out);
  or or_179 (or_179_out, push_byte__ra_rb, push_word__ra_rb);
  or or_180 (or_180_out, mov_word__ra_rb___imm16, shift_word__ra_rb___imm4);
  or or_181 (or_181_out, arith_word__ra_rb___imm16, cmp_word__ra_rb___imm16);
  or or_182 (or_182_out, or_180_out, or_181_out, or_183_out);
  or or_183 (or_183_out, pop_byte__ra_rb, pop_word__ra_rb);
  or or_184 (or_184_out, add_word__ra___rb, mov_word__ra___rb, jump_ra_rb);
  or or_185 (or_185_out, arith_ra, arith_ra__rb, cmp_ra__rb, xchg_ra__rb);
  or or_186 (or_186_out, mov_ra__byte__rb, arith_ra__word__rb, cmp_ra__word__rb, jump_ra_imm16);
  or or_187 (or_187_out, shift_ra__imm4, arith_ra__imm16, cmp_ra__imm16, push_ra);
  or or_188 (or_188_out, shift_word__ra_rb___imm4, mov_ra__byte__rb_imm16);
  and and_147 (and_147_out, clock12, sub_ra__imm16, c);
  and and_148 (ALU_1001, clk_en, or_178_out);
  or or_189 (or_189_out, and_145_out, and_146_out, and_149_out);
  and and_149 (and_149_out, clock10, or_182_out);
  and and_150 (and_150_out, clock5, or_184_out);
  and and_151 (and_151_out, clock6, or_185_out);
  and and_152 (and_152_out, clock7, or_186_out);
  and and_153 (and_153_out, clock8, add_ra__byte__rb);
  and and_154 (and_154_out, clock10, or_187_out);
  and and_155 (and_155_out, clock11, or_188_out);
  and and_156 (enable_BUS1, clk_en, or_173_out);
  and and_157 (enable_TMP1, clk_set, or_174_out);
  or or_190 (or_190_out, clock3, and_123_out, and_124_out, and_125_out, and_126_out, and_127_out, and_128_out);
  or or_191 (or_191_out, mov_ra__byte__rb, mov_ra__word__rb);
  or or_192 (or_192_out, arith_ra__rb, xchg_ra__rb, cmp_ra__rb, mov_ra__rb);
  or or_193 (or_193_out, add_ra__byte__rb, arith_word__ra_rb, arith_ra__word__rb, cmp_ra__word__rb);
  and and_158 (and_158_out, clock6, or_194_out);
  or or_194 (or_194_out, jump_ra_rb, mov_word__ra___rb, add_word__ra___rb);
  and and_159 (and_159_out, clock9, or_195_out);
  or or_195 (or_195_out, push_byte__ra_rb, push_word__ra_rb);
  or or_196 (or_196_out, pop_byte__ra_rb, pop_word__ra_rb);
  or or_197 (or_197_out, or_196_out, or_198_out);
  or or_198 (or_198_out, shift_word__ra_rb___imm4, mov_word__ra_rb___imm16, arith_word__ra_rb___imm16, cmp_word__ra_rb___imm16);
  and and_160 (and_160_out, clock5, pop);
  and and_161 (and_161_out, clock9, push_ra);
  and and_162 (and_162_out, clock11, or_199_out);
  or or_199 (or_199_out, push_byte__ra_rb, push_word__ra_rb);
  and and_163 (and_163_out, clock14, push_imm16);
  or or_200 (or_200_out, push, pop, pop0);
  or or_201 (or_201_out, push, pop, pop0);
  and and_164 (sel_ra, clk_en, or_189_out);
  and and_165 (and_165_out, clock6, add_ra__byte__rb);
  and and_166 (and_166_out, clock7, mov_ra__byte__rb);
  and and_167 (and_167_out, clock9, pop_byte__ra_rb);
  and and_168 (and_168_out, clock10, push_byte__ra_rb);
  and and_169 (and_169_out, clock11, mov_ra__byte__rb_imm16);
  and and_170 (enable_CLR, clk_en, or_190_out);
  or or_202 (or_202_out, shift_ra__imm4, shift_word__ra_rb___imm4);
  or or_203 (or_203_out, arith_word__ra_rb___imm16, cmp_word__ra_rb___imm16);
  or or_204 (or_204_out, xchg_ra__rb, add_ra__byte__rb);
  or or_205 (or_205_out, mov_ra__imm16, mov_ra__byte__rb);
  or or_206 (or_206_out, mov_ra__byte__rb_imm16, mov_ra__word__rb_imm16);
  or or_207 (or_207_out, arith_ra__word__rb, add_word__ra___rb);
  or or_208 (or_208_out, arith_ra__imm16, cmp_ra__imm16);
  or or_209 (or_209_out, shift_ra__imm4, shift_word__ra_rb___imm4);
  and and_171 (and_171_out, clock10, push_imm16);
  and and_172 (and_172_out, clock5, or_210_out);
  or or_210 (or_210_out, or_191_out, or_192_out, or_193_out);
  and and_173 (and_173_out, clock10, or_197_out);
  or or_211 (or_211_out, mov_ra__byte__rb, mov_ra__word__rb, mov_word__ra___rb);
  or or_212 (or_212_out, or_211_out, or_213_out);
  or or_213 (or_213_out, arith_ra__word__rb, cmp_ra__word__rb, add_ra__byte__rb, add_word__ra___rb);
  or or_214 (or_214_out, and_150_out, and_151_out, and_152_out, and_153_out, and_154_out, and_155_out, and_147_out);
  or or_215 (or_215_out, and_165_out, and_166_out, and_167_out, and_168_out, and_169_out);
  or or_216 (or_216_out, arith_ra__imm16, cmp_ra__imm16);
  or or_217 (or_217_out, arith_word__ra_rb___imm16, cmp_word__ra_rb___imm16);
  or or_218 (or_218_out, shift_ra__imm4, shift_word__ra_rb___imm4);
  or or_219 (or_219_out, arith_ra__imm16, cmp_ra__imm16, mov_ra__imm16);
  or or_220 (or_220_out, mov_word__ra_rb___imm16, mov_ra__byte__rb_imm16, mov_ra__word__rb_imm16);
  or or_221 (or_221_out, pop, pop0, push);
  and and_174 (and_174_out, clock7, or_222_out);
  or or_222 (or_222_out, or_204_out, or_223_out);
  or or_223 (or_223_out, arith_ra, arith_ra__rb, arith_word__ra_rb);
  or or_224 (or_224_out, mov_word__ra_rb___imm16, arith_word__ra_rb___imm16, cmp_word__ra_rb___imm16);
  or or_225 (or_225_out, push, pop, pop0);
  and and_175 (and_175_out, clock11, or_226_out);
  or or_226 (or_226_out, shift_ra__imm4, pop_byte__ra_rb, pop_word__ra_rb, arith_ra__imm16, mov_word__ra_rb___imm16);
  or or_227 (or_227_out, push_imm16, push_byte__ra_rb, push_word__ra_rb);
  or or_228 (or_228_out, or_227_out, or_229_out);
  or or_229 (or_229_out, mov_ra__byte__rb_imm16, arith_word__ra_rb___imm16, shift_word__ra_rb___imm4);
  and and_176 (and_176_out, clock15, push_imm16);
  and and_177 (and_177_out, clock5, or_212_out);
  or or_230 (or_230_out, and_160_out, and_161_out, and_162_out, and_163_out);
  and and_178 (load_ss, clock7, clk_en, or_200_out);
  or or_231 (or_231_out, pop, pop0, push);
  and and_179 (and_179_out, clock9, push_ra);
  and and_180 (and_180_out, clock11, or_232_out);
  or or_232 (or_232_out, push_byte__ra_rb, push_word__ra_rb);
  and and_181 (and_181_out, clock14, push_imm16);
  and and_182 (load_ra, clk_en, or_214_out);
  or or_233 (or_233_out, add_word__ra___rb, arith_ra__word__rb, cmp_ra__word__rb);
  or or_234 (or_234_out, arith_ra__rb, cmp_ra__rb);
  or or_235 (or_235_out, or_216_out, or_217_out, or_218_out);
  and and_183 (and_183_out, clock5, adc_ra__rb);
  or or_236 (or_236_out, and_183_out, and_184_out);
  and and_184 (and_184_out, clock9, adc_ra__imm16);
  and and_185 (and_185_out, clock9, add_ra__byte__rb);
  and and_186 (and_186_out, clock12, or_228_out);
  or or_237 (or_237_out, and_172_out, and_158_out, and_159_out, and_173_out);
  and and_187 (sel_ss, clk_en, or_230_out);
  and and_188 (store_ss, clock8, clk_set, or_201_out);
  and and_189 (and_189_out, clock5, or_231_out);
  or or_238 (or_238_out, push, pop, pop0);
  and and_190 (enable_lowmask, clk_en, or_215_out);
  and and_191 (and_191_out, clock6, or_233_out);
  and and_192 (and_192_out, clock5, or_234_out);
  and and_193 (and_193_out, clock7, add_ra__byte__rb);
  and and_194 (and_194_out, clock9, or_235_out);
  and and_195 (enable_arith_carry, clk_en, or_236_out);
  and and_196 (and_196_out, clock6, or_239_out);
  or or_239 (or_239_out, or_202_out, or_203_out, or_219_out, or_220_out, or_221_out);
  and and_197 (and_197_out, clock8, or_240_out);
  or or_240 (or_240_out, or_205_out, or_206_out, or_207_out, or_208_out, or_209_out, or_224_out, or_225_out);
  and and_198 (sel_ds, clk_en, and_177_out);
  or or_241 (or_241_out, and_189_out, and_179_out, and_180_out, and_181_out);
  or or_242 (or_242_out, and_191_out, and_192_out, and_193_out, and_194_out);
  and and_199 (load_rb, clk_en, or_237_out);
  and and_200 (store_rb, clock6, clk_set, xchg_ra__rb);
  and and_201 (store_sp, clock6, clk_set, or_238_out);
  and and_202 (load_sp, clk_en, or_241_out);
  or or_243 (or_243_out, clock2, clock4, and_196_out, and_174_out, and_197_out, and_185_out, and_171_out, and_175_out, and_186_out, and_176_out);
  and and_203 (enable_TMP, clk_set, or_242_out);
  and and_204 (load_ACC, clk_en, or_243_out);
  and and_205 (and_205_out, ja_ra_imm16, tunnel_t_t);
  and and_206 (and_206_out, jna_ra_imm16, not_above);
  and and_207 (and_207_out, jb_ra_imm16, tunnel);
  and and_208 (and_208_out, jnb_ra_imm16, not_below);
  and and_209 (and_209_out, jeq_ra_imm16, tunnel_t);
  and and_210 (and_210_out, jneq_ra_imm16, not_equal);
  and and_211 (and_211_out, jc_ra_imm16, c);
  and and_212 (and_212_out, jnc_ra_imm16, not_carry);
  and and_213 (and_213_out, jev_ra_imm16, e);
  and and_214 (and_214_out, jnev_ra_imm16, not_even);
  and and_215 (and_215_out, jp_ra_imm16, p);
  and and_216 (and_216_out, jnp_ra_imm16, not_positive);
  and and_217 (and_217_out, jz_ra_imm16, z);
  and and_218 (and_218_out, jnz_ra_imm16, not_zero);
  and and_219 (and_219_out, jr_ra_imm16, r);
  and and_220 (and_220_out, jnr_ra_imm16, not_reserved);
  and and_221 (and_221_out, ja_ra_rb, tunnel_t_t);
  and and_222 (and_222_out, jna_ra_rb, not_above);
  and and_223 (and_223_out, jb_ra_rb, tunnel);
  and and_224 (and_224_out, jnb_ra_rb, not_below);
  and and_225 (and_225_out, jeq_ra_rb, tunnel_t);
  and and_226 (and_226_out, jneq_ra_rb, not_equal);
  and and_227 (and_227_out, jc_ra_rb, c);
  and and_228 (and_228_out, jnc_ra_rb, not_carry);
  and and_229 (and_229_out, jev_ra_rb, e);
  and and_230 (and_230_out, jnev_ra_rb, not_even);
  and and_231 (and_231_out, jp_ra_rb, p);
  and and_232 (and_232_out, jnp_ra_rb, not_positive);
  and and_233 (and_233_out, jz_ra_rb, z);
  and and_234 (and_234_out, jnz_ra_rb, not_zero);
  and and_235 (and_235_out, jr_ra_rb, r);
  and and_236 (and_236_out, jnr_ra_rb, not_reserved);
  and and_237 (jump, jump_ra_rb, jump_ra_imm16);
  or or_244 (or_244_out, and_205_out, and_206_out, and_207_out, and_208_out);
  or or_245 (or_245_out, and_209_out, and_210_out, and_211_out, and_212_out);
  or or_246 (or_246_out, and_213_out, and_214_out, and_215_out, and_216_out);
  or or_247 (or_247_out, and_217_out, and_218_out, and_219_out, and_220_out);
  or or_248 (or_248_out, and_221_out, and_222_out, and_223_out, and_224_out);
  or or_249 (or_249_out, and_225_out, and_226_out, and_227_out, and_228_out);
  or or_250 (or_250_out, and_229_out, and_230_out, and_231_out, and_232_out);
  or or_251 (or_251_out, and_233_out, and_234_out, and_235_out, and_236_out);
  or or_252 (pop, pop_ra, pop_byte__ra_rb, pop_word__ra_rb);
  or or_253 (push, push_ra, push_imm16, push_byte__ra_rb, push_word__ra_rb);
  or or_254 (jump_ra_imm16, jmp_ra_imm16, or_244_out, or_245_out, or_246_out, or_247_out);
  or or_255 (jump_ra_rb, jmp_ra_rb, or_248_out, or_249_out, or_250_out, or_251_out);
  or or_256 (shift_word__ra_rb___imm4, shr_word__ra_rb___imm4, shl_word__ra_rb___imm4, sar_word__ra_rb___imm4);
  or or_257 (shift_ra__imm4, shr_ra__imm4, shl_ra__imm4, sar_ra__imm4);
  or or_258 (arith_word__ra_rb___imm16, add_word__ra_rb___imm16, and_word__ra_rb___imm16, or_word__ra_rb___imm16, xor_word__ra_rb___imm16);
  or or_259 (arith_ra__imm16, add_ra__imm16, and_ra__imm16, or_ra__imm16, xor_ra__imm16, mul_ra__imm16, div_ra__imm16, mod_ra__imm16, adc_ra__imm16, sub_ra__imm16);
  or or_260 (arith_ra__word__rb, add_ra__word__rb, and_ra__word__rb, or_ra__word__rb, xor_ra__word__rb, adc_ra__word__rb, mul_ra__word__rb, div_ra__word__rb, mod_ra__word__rb);
  or or_261 (arith_ra__rb, add_ra__rb, and_ra__rb, or_ra__rb, xor_ra__rb, mul_ra__rb, div_ra__rb, mod_ra__rb, adc_ra__rb, sub_ra__rb);
  or or_262 (arith_ra, flip_ra, neg_ra);
  or or_263 (arith_word__ra_rb, flip_word__ra_rb, neg_word__ra_rb);
endmodule
