// Logisim project instructions.circ as structural Verilog
module shr_ra__imm4 (
);

  wire ALU_0000, ALU_0001, ALU_1000, clk_en, clk_set, clock5, clock6, clock7, clock8, clock9, clock10,
       clock11, enable_BUS1, enable_carry, enable_CLR, enable_TMP1, load_ACC, load_CS, load_IAR, load_ra,
       load_RAM, sel_CS, sel_MAR, set_ACC, set_arith_FLAGS, set_carry, shr_ra__imm4, store_CS, store_IAR,
       store_ra, store_TMP;

  and and_1 (sel_CS, clock5, clk_en, shr_ra__imm4);
  and and_2 (load_IAR, clock5, clk_en, shr_ra__imm4);
  and and_3 (enable_BUS1, clock5, clk_en, shr_ra__imm4);
  and and_4 (ALU_0000, clock5, clk_en, shr_ra__imm4);
  and and_5 (set_carry, clock5, clk_en, shr_ra__imm4);
  and and_6 (load_ACC, clock6, clk_en, shr_ra__imm4);
  and and_7 (enable_CLR, clock7, clk_en, shr_ra__imm4);
  and and_8 (load_CS, clock7, clk_en, shr_ra__imm4);
  and and_9 (ALU_1000, clock7, clk_en, shr_ra__imm4);
  and and_10 (load_ACC, clock8, clk_en, shr_ra__imm4);
  and and_11 (load_RAM, clock9, clk_en, shr_ra__imm4);
  and and_12 (load_ra, clock10, clk_en, shr_ra__imm4);
  and and_13 (ALU_0001, clock10, clk_en, shr_ra__imm4);
  and and_14 (load_ACC, clock11, clk_en, shr_ra__imm4);
  and and_15 (sel_MAR, clock5, clk_set, shr_ra__imm4);
  and and_16 (set_ACC, clock5, clk_set, shr_ra__imm4);
  and and_17 (enable_carry, clock5, clk_set, shr_ra__imm4);
  and and_18 (enable_TMP1, clock5, clk_set, shr_ra__imm4);
  and and_19 (store_IAR, clock6, clk_set, shr_ra__imm4);
  and and_20 (set_ACC, clock7, clk_set, shr_ra__imm4);
  and and_21 (store_CS, clock8, clk_set, shr_ra__imm4);
  and and_22 (store_TMP, clock9, clk_set, shr_ra__imm4);
  and and_23 (set_ACC, clock10, clk_set, shr_ra__imm4);
  and and_24 (set_arith_FLAGS, clock10, clk_set, shr_ra__imm4);
  and and_25 (store_ra, clock11, clk_set, shr_ra__imm4);
endmodule

module shl_ra__imm4 (
);

  wire ALU_0000, ALU_0010, ALU_1000, clk_en, clk_set, clock5, clock6, clock7, clock8, clock9, clock10,
       clock11, enable_BUS1, enable_carry, enable_CLR, enable_TMP1, load_ACC, load_CS, load_IAR, load_ra,
       load_RAM, sel_CS, sel_MAR, set_ACC, set_arith_FLAGS, set_carry, shl_ra__imm4, store_CS, store_IAR,
       store_ra, store_TMP;

  and and_1 (sel_CS, clock5, clk_en, shl_ra__imm4);
  and and_2 (load_IAR, clock5, clk_en, shl_ra__imm4);
  and and_3 (enable_BUS1, clock5, clk_en, shl_ra__imm4);
  and and_4 (ALU_0000, clock5, clk_en, shl_ra__imm4);
  and and_5 (set_carry, clock5, clk_en, shl_ra__imm4);
  and and_6 (load_ACC, clock6, clk_en, shl_ra__imm4);
  and and_7 (enable_CLR, clock7, clk_en, shl_ra__imm4);
  and and_8 (load_CS, clock7, clk_en, shl_ra__imm4);
  and and_9 (ALU_1000, clock7, clk_en, shl_ra__imm4);
  and and_10 (load_ACC, clock8, clk_en, shl_ra__imm4);
  and and_11 (load_RAM, clock9, clk_en, shl_ra__imm4);
  and and_12 (load_ra, clock10, clk_en, shl_ra__imm4);
  and and_13 (ALU_0010, clock10, clk_en, shl_ra__imm4);
  and and_14 (load_ACC, clock11, clk_en, shl_ra__imm4);
  and and_15 (sel_MAR, clock5, clk_set, shl_ra__imm4);
  and and_16 (set_ACC, clock5, clk_set, shl_ra__imm4);
  and and_17 (enable_carry, clock5, clk_set, shl_ra__imm4);
  and and_18 (enable_TMP1, clock5, clk_set, shl_ra__imm4);
  and and_19 (store_IAR, clock6, clk_set, shl_ra__imm4);
  and and_20 (set_ACC, clock7, clk_set, shl_ra__imm4);
  and and_21 (store_CS, clock8, clk_set, shl_ra__imm4);
  and and_22 (store_TMP, clock9, clk_set, shl_ra__imm4);
  and and_23 (set_ACC, clock10, clk_set, shl_ra__imm4);
  and and_24 (set_arith_FLAGS, clock10, clk_set, shl_ra__imm4);
  and and_25 (store_ra, clock11, clk_set, shl_ra__imm4);
endmodule

module sar_ra__imm4 (
);

  wire ALU_0000, ALU_1000, ALU_1001, clk_en, clk_set, clock5, clock6, clock7, clock8, clock9, clock10,
       clock11, enable_BUS1, enable_carry, enable_CLR, enable_TMP1, load_ACC, load_CS, load_IAR, load_ra,
       load_RAM, sar_ra__imm4, sel_CS, sel_MAR, set_ACC, set_arith_FLAGS, set_carry, store_CS, store_IAR,
       store_ra, store_TMP;

  and and_1 (sel_CS, clock5, clk_en, sar_ra__imm4);
  and and_2 (load_IAR, clock5, clk_en, sar_ra__imm4);
  and and_3 (enable_BUS1, clock5, clk_en, sar_ra__imm4);
  and and_4 (ALU_0000, clock5, clk_en, sar_ra__imm4);
  and and_5 (set_carry, clock5, clk_en, sar_ra__imm4);
  and and_6 (load_ACC, clock6, clk_en, sar_ra__imm4);
  and and_7 (enable_CLR, clock7, clk_en, sar_ra__imm4);
  and and_8 (load_CS, clock7, clk_en, sar_ra__imm4);
  and and_9 (ALU_1000, clock7, clk_en, sar_ra__imm4);
  and and_10 (load_ACC, clock8, clk_en, sar_ra__imm4);
  and and_11 (load_RAM, clock9, clk_en, sar_ra__imm4);
  and and_12 (load_ra, clock10, clk_en, sar_ra__imm4);
  and and_13 (ALU_1001, clock10, clk_en, sar_ra__imm4);
  and and_14 (load_ACC, clock11, clk_en, sar_ra__imm4);
  and and_15 (sel_MAR, clock5, clk_set, sar_ra__imm4);
  and and_16 (set_ACC, clock5, clk_set, sar_ra__imm4);
  and and_17 (enable_carry, clock5, clk_set, sar_ra__imm4);
  and and_18 (enable_TMP1, clock5, clk_set, sar_ra__imm4);
  and and_19 (store_IAR, clock6, clk_set, sar_ra__imm4);
  and and_20 (set_ACC, clock7, clk_set, sar_ra__imm4);
  and and_21 (store_CS, clock8, clk_set, sar_ra__imm4);
  and and_22 (store_TMP, clock9, clk_set, sar_ra__imm4);
  and and_23 (set_ACC, clock10, clk_set, sar_ra__imm4);
  and and_24 (set_arith_FLAGS, clock10, clk_set, sar_ra__imm4);
  and and_25 (store_ra, clock11, clk_set, sar_ra__imm4);
endmodule

module shr_word__ra_rb___imm4 (
);

  wire ALU_0000, ALU_0001, ALU_1000, clk_en, clk_set, clock5, clock6, clock7, clock8, clock9, clock10,
       clock11, clock12, enable_BUS1, enable_carry, enable_CLR, enable_TMP, enable_TMP1, load_ACC, load_cs,
       load_IAR, load_ra, load_RAM, load_rb, sel_cs, sel_MAR, sel_ra, set_ACC, set_arith_flags, set_carry,
       set_IAR, shr_word__ra_rb___imm4, store_cs, store_RAM;

  and and_1 (sel_cs, clock5, clk_en, shr_word__ra_rb___imm4);
  and and_2 (load_IAR, clock5, clk_en, shr_word__ra_rb___imm4);
  and and_3 (enable_BUS1, clock5, clk_en, shr_word__ra_rb___imm4);
  and and_4 (ALU_0000, clock5, clk_en, shr_word__ra_rb___imm4);
  and and_5 (set_carry, clock5, clk_en, shr_word__ra_rb___imm4);
  and and_6 (load_ACC, clock6, clk_en, shr_word__ra_rb___imm4);
  and and_7 (load_cs, clock7, clk_en, shr_word__ra_rb___imm4);
  and and_8 (enable_CLR, clock7, clk_en, shr_word__ra_rb___imm4);
  and and_9 (ALU_1000, clock7, clk_en, shr_word__ra_rb___imm4);
  and and_10 (load_ACC, clock8, clk_en, shr_word__ra_rb___imm4);
  and and_11 (load_RAM, clock9, clk_en, shr_word__ra_rb___imm4);
  and and_12 (sel_ra, clock10, clk_en, shr_word__ra_rb___imm4);
  and and_13 (load_rb, clock10, clk_en, shr_word__ra_rb___imm4);
  and and_14 (load_ra, clock11, clk_en, shr_word__ra_rb___imm4);
  and and_15 (ALU_0001, clock11, clk_en, shr_word__ra_rb___imm4);
  and and_16 (load_ACC, clock12, clk_en, shr_word__ra_rb___imm4);
  and and_17 (sel_MAR, clock5, clk_set, shr_word__ra_rb___imm4);
  and and_18 (set_ACC, clock5, clk_set, shr_word__ra_rb___imm4);
  and and_19 (enable_carry, clock5, clk_set, shr_word__ra_rb___imm4);
  and and_20 (enable_TMP1, clock5, clk_set, shr_word__ra_rb___imm4);
  and and_21 (set_IAR, clock6, clk_set, shr_word__ra_rb___imm4);
  and and_22 (set_ACC, clock7, clk_set, shr_word__ra_rb___imm4);
  and and_23 (store_cs, clock8, clk_set, shr_word__ra_rb___imm4);
  and and_24 (enable_TMP, clock9, clk_set, shr_word__ra_rb___imm4);
  and and_25 (sel_MAR, clock10, clk_set, shr_word__ra_rb___imm4);
  and and_26 (set_ACC, clock11, clk_set, shr_word__ra_rb___imm4);
  and and_27 (set_arith_flags, clock11, clk_set, shr_word__ra_rb___imm4);
  and and_28 (store_RAM, clock12, clk_set, shr_word__ra_rb___imm4);
endmodule

module shl_word__ra_rb___imm4 (
);

  wire ALU_0000, ALU_0010, ALU_1000, clk_en, clk_set, clock5, clock6, clock7, clock8, clock9, clock10,
       clock11, clock12, enable_BUS1, enable_carry, enable_CLR, enable_TMP, enable_TMP1, load_ACC, load_cs,
       load_IAR, load_ra, load_RAM, load_rb, sel_cs, sel_MAR, sel_ra, set_ACC, set_arith_flags, set_carry,
       set_IAR, shl_word__ra_rb___imm4, store_cs, store_RAM;

  and and_1 (sel_cs, clock5, clk_en, shl_word__ra_rb___imm4);
  and and_2 (load_IAR, clock5, clk_en, shl_word__ra_rb___imm4);
  and and_3 (enable_BUS1, clock5, clk_en, shl_word__ra_rb___imm4);
  and and_4 (ALU_0000, clock5, clk_en, shl_word__ra_rb___imm4);
  and and_5 (set_carry, clock5, clk_en, shl_word__ra_rb___imm4);
  and and_6 (load_ACC, clock6, clk_en, shl_word__ra_rb___imm4);
  and and_7 (load_cs, clock7, clk_en, shl_word__ra_rb___imm4);
  and and_8 (enable_CLR, clock7, clk_en, shl_word__ra_rb___imm4);
  and and_9 (ALU_1000, clock7, clk_en, shl_word__ra_rb___imm4);
  and and_10 (load_ACC, clock8, clk_en, shl_word__ra_rb___imm4);
  and and_11 (load_RAM, clock9, clk_en, shl_word__ra_rb___imm4);
  and and_12 (sel_ra, clock10, clk_en, shl_word__ra_rb___imm4);
  and and_13 (load_rb, clock10, clk_en, shl_word__ra_rb___imm4);
  and and_14 (load_ra, clock11, clk_en, shl_word__ra_rb___imm4);
  and and_15 (ALU_0010, clock11, clk_en, shl_word__ra_rb___imm4);
  and and_16 (load_ACC, clock12, clk_en, shl_word__ra_rb___imm4);
  and and_17 (sel_MAR, clock5, clk_set, shl_word__ra_rb___imm4);
  and and_18 (set_ACC, clock5, clk_set, shl_word__ra_rb___imm4);
  and and_19 (enable_carry, clock5, clk_set, shl_word__ra_rb___imm4);
  and and_20 (enable_TMP1, clock5, clk_set, shl_word__ra_rb___imm4);
  and and_21 (set_IAR, clock6, clk_set, shl_word__ra_rb___imm4);
  and and_22 (set_ACC, clock7, clk_set, shl_word__ra_rb___imm4);
  and and_23 (store_cs, clock8, clk_set, shl_word__ra_rb___imm4);
  and and_24 (enable_TMP, clock9, clk_set, shl_word__ra_rb___imm4);
  and and_25 (sel_MAR, clock10, clk_set, shl_word__ra_rb___imm4);
  and and_26 (set_ACC, clock11, clk_set, shl_word__ra_rb___imm4);
  and and_27 (set_arith_flags, clock11, clk_set, shl_word__ra_rb___imm4);
  and and_28 (store_RAM, clock12, clk_set, shl_word__ra_rb___imm4);
endmodule

module sar_word__ra_rb___imm4 (
);

  wire ALU_0000, ALU_1000, ALU_1001, clk_en, clk_set, clock5, clock6, clock7, clock8, clock9, clock10,
       clock11, clock12, enable_BUS1, enable_carry, enable_CLR, enable_TMP, enable_TMP1, load_ACC, load_cs,
       load_IAR, load_ra, load_RAM, load_rb, sar_word__ra_rb___imm4, sel_cs, sel_MAR, sel_ra, set_ACC,
       set_arith_flags, set_carry, set_IAR, store_cs, store_RAM;

  and and_1 (sel_cs, clock5, clk_en, sar_word__ra_rb___imm4);
  and and_2 (load_IAR, clock5, clk_en, sar_word__ra_rb___imm4);
  and and_3 (enable_BUS1, clock5, clk_en, sar_word__ra_rb___imm4);
  and and_4 (ALU_0000, clock5, clk_en, sar_word__ra_rb___imm4);
  and and_5 (set_carry, clock5, clk_en, sar_word__ra_rb___imm4);
  and and_6 (load_ACC, clock6, clk_en, sar_word__ra_rb___imm4);
  and and_7 (load_cs, clock7, clk_en, sar_word__ra_rb___imm4);
  and and_8 (enable_CLR, clock7, clk_en, sar_word__ra_rb___imm4);
  and and_9 (ALU_1000, clock7, clk_en, sar_word__ra_rb___imm4);
  and and_10 (load_ACC, clock8, clk_en, sar_word__ra_rb___imm4);
  and and_11 (load_RAM, clock9, clk_en, sar_word__ra_rb___imm4);
  and and_12 (sel_ra, clock10, clk_en, sar_word__ra_rb___imm4);
  and and_13 (load_rb, clock10, clk_en, sar_word__ra_rb___imm4);
  and and_14 (load_ra, clock11, clk_en, sar_word__ra_rb___imm4);
  and and_15 (ALU_1001, clock11, clk_en, sar_word__ra_rb___imm4);
  and and_16 (load_ACC, clock12, clk_en, sar_word__ra_rb___imm4);
  and and_17 (sel_MAR, clock5, clk_set, sar_word__ra_rb___imm4);
  and and_18 (set_ACC, clock5, clk_set, sar_word__ra_rb___imm4);
  and and_19 (enable_carry, clock5, clk_set, sar_word__ra_rb___imm4);
  and and_20 (enable_TMP1, clock5, clk_set, sar_word__ra_rb___imm4);
  and and_21 (set_IAR, clock6, clk_set, sar_word__ra_rb___imm4);
  and and_22 (set_ACC, clock7, clk_set, sar_word__ra_rb___imm4);
  and and_23 (store_cs, clock8, clk_set, sar_word__ra_rb___imm4);
  and and_24 (enable_TMP, clock9, clk_set, sar_word__ra_rb___imm4);
  and and_25 (sel_MAR, clock10, clk_set, sar_word__ra_rb___imm4);
  and and_26 (set_ACC, clock11, clk_set, sar_word__ra_rb___imm4);
  and and_27 (set_arith_flags, clock11, clk_set, sar_word__ra_rb___imm4);
  and and_28 (store_RAM, clock12, clk_set, sar_word__ra_rb___imm4);
endmodule

module flip_ra (
);

  wire ALU_0011, clk_en, clk_set, clock6, clock7, flip_ra, lead_ra, load_ACC, set_ACC, set_arith_FLAGS,
       store_ra;

  and and_1 (lead_ra, clock6, clk_en, flip_ra);
  and and_2 (ALU_0011, clock6, clk_en, flip_ra);
  and and_3 (load_ACC, clock7, clk_en, flip_ra);
  and and_4 (set_ACC, clock6, clk_set, flip_ra);
  and and_5 (set_arith_FLAGS, clock6, clk_set, flip_ra);
  and and_6 (store_ra, clock7, clk_set, flip_ra);
endmodule

module neg_ra (
);

  wire ALU_1011, clk_en, clk_set, clock6, clock7, lead_ra, load_ACC, neg_ra, set_ACC, set_arith_FLAGS,
       store_ra;

  and and_1 (lead_ra, clock6, clk_en, neg_ra);
  and and_2 (ALU_1011, clock6, clk_en, neg_ra);
  and and_3 (load_ACC, clock7, clk_en, neg_ra);
  and and_4 (set_ACC, clock6, clk_set, neg_ra);
  and and_5 (set_arith_FLAGS, clock6, clk_set, neg_ra);
  and and_6 (store_ra, clock7, clk_set, neg_ra);
endmodule

module flip_word__ra_rb (
);

  wire ALU_0011, clk_en, clk_set, clock5, clock6, clock7, flip_word__ra_rb, load_ACC, load_RAM, load_rb,
       sel_MAR, sel_ra, set_ACC, set_arith_flags, store_RAM;

  and and_1 (sel_ra, clock5, clk_en, flip_word__ra_rb);
  and and_2 (load_rb, clock5, clk_en, flip_word__ra_rb);
  and and_3 (load_RAM, clock6, clk_en, flip_word__ra_rb);
  and and_4 (ALU_0011, clock6, clk_en, flip_word__ra_rb);
  and and_5 (load_ACC, clock7, clk_en, flip_word__ra_rb);
  and and_6 (sel_MAR, clock5, clk_set, flip_word__ra_rb);
  and and_7 (set_ACC, clock6, clk_set, flip_word__ra_rb);
  and and_8 (set_arith_flags, clock6, clk_set, flip_word__ra_rb);
  and and_9 (store_RAM, clock7, clk_set, flip_word__ra_rb);
endmodule

module neg_word__ra_rb (
);

  wire ALU_1011, clk_en, clk_set, clock5, clock6, clock7, load_ACC, load_RAM, load_rb, neg_word__ra_rb,
       sel_MAR, sel_ra, set_ACC, set_arith_flags, store_RAM;

  and and_1 (sel_ra, clock5, clk_en, neg_word__ra_rb);
  and and_2 (load_rb, clock5, clk_en, neg_word__ra_rb);
  and and_3 (load_RAM, clock6, clk_en, neg_word__ra_rb);
  and and_4 (ALU_1011, clock6, clk_en, neg_word__ra_rb);
  and and_5 (load_ACC, clock7, clk_en, neg_word__ra_rb);
  and and_6 (sel_MAR, clock5, clk_set, neg_word__ra_rb);
  and and_7 (set_ACC, clock6, clk_set, neg_word__ra_rb);
  and and_8 (set_arith_flags, clock6, clk_set, neg_word__ra_rb);
  and and_9 (store_RAM, clock7, clk_set, neg_word__ra_rb);
endmodule

module add_ra__rb (
);

  wire add_ra__rb, ALU_0000, clk_en, clk_set, clock5, clock6, clock7, enable_TMP, load_ACC, load_ra, load_rb,
       set_ACC, set_arith_FLAGS, store_ra;

  and and_1 (load_rb, clock5, clk_en, add_ra__rb);
  and and_2 (load_ra, clock6, clk_en, add_ra__rb);
  and and_3 (ALU_0000, clock6, clk_en, add_ra__rb);
  and and_4 (load_ACC, clock7, clk_en, add_ra__rb);
  and and_5 (enable_TMP, clock5, clk_set, add_ra__rb);
  and and_6 (set_ACC, clock6, clk_set, add_ra__rb);
  and and_7 (set_arith_FLAGS, clock6, clk_set, add_ra__rb);
  and and_8 (store_ra, clock7, clk_set, add_ra__rb);
endmodule

module and_ra__rb (
);

  wire ALU_0100, and_ra__rb, clk_en, clk_set, clock5, clock6, clock7, enable_TMP, load_ACC, load_ra, load_rb,
       set_ACC, set_arith_FLAGS, store_ra;

  and and_1 (load_rb, clock5, clk_en, and_ra__rb);
  and and_2 (load_ra, clock6, clk_en, and_ra__rb);
  and and_3 (ALU_0100, clock6, clk_en, and_ra__rb);
  and and_4 (load_ACC, clock7, clk_en, and_ra__rb);
  and and_5 (enable_TMP, clock5, clk_set, and_ra__rb);
  and and_6 (set_ACC, clock6, clk_set, and_ra__rb);
  and and_7 (set_arith_FLAGS, clock6, clk_set, and_ra__rb);
  and and_8 (store_ra, clock7, clk_set, and_ra__rb);
endmodule

module or_ra__rb (
);

  wire ALU_0101, clk_en, clk_set, clock5, clock6, clock7, enable_TMP, load_ACC, load_ra, load_rb, or_ra__rb,
       set_ACC, set_arith_FLAGS, store_ra;

  and and_1 (load_rb, clock5, clk_en, or_ra__rb);
  and and_2 (load_ra, clock6, clk_en, or_ra__rb);
  and and_3 (ALU_0101, clock6, clk_en, or_ra__rb);
  and and_4 (load_ACC, clock7, clk_en, or_ra__rb);
  and and_5 (enable_TMP, clock5, clk_set, or_ra__rb);
  and and_6 (set_ACC, clock6, clk_set, or_ra__rb);
  and and_7 (set_arith_FLAGS, clock6, clk_set, or_ra__rb);
  and and_8 (store_ra, clock7, clk_set, or_ra__rb);
endmodule

module xor_ra__rb (
);

  wire ALU_0110, clk_en, clk_set, clock5, clock6, clock7, enable_TMP, load_ACC, load_ra, load_rb, set_ACC,
       set_arith_FLAGS, store_ra, xor_ra__rb;

  and and_1 (load_rb, clock5, clk_en, xor_ra__rb);
  and and_2 (load_ra, clock6, clk_en, xor_ra__rb);
  and and_3 (ALU_0110, clock6, clk_en, xor_ra__rb);
  and and_4 (load_ACC, clock7, clk_en, xor_ra__rb);
  and and_5 (enable_TMP, clock5, clk_set, xor_ra__rb);
  and and_6 (set_ACC, clock6, clk_set, xor_ra__rb);
  and and_7 (set_arith_FLAGS, clock6, clk_set, xor_ra__rb);
  and and_8 (store_ra, clock7, clk_set, xor_ra__rb);
endmodule

module cmp_ra__rb (
);

  wire ALU_0111, clk_en, clk_set, clock5, clock6, cmp_ra__rb, enable_TMP, load_ra, load_rb, set_ACC,
       set_arith_FLAGS;

  and and_1 (load_rb, clock5, clk_en, cmp_ra__rb);
  and and_2 (load_ra, clock6, clk_en, cmp_ra__rb);
  and and_3 (ALU_0111, clock6, clk_en, cmp_ra__rb);
  and and_4 (enable_TMP, clock5, clk_set, cmp_ra__rb);
  and and_5 (set_ACC, clock6, clk_set, cmp_ra__rb);
  and and_6 (set_arith_FLAGS, clock6, clk_set, cmp_ra__rb);
endmodule

module adc_ra__rb (
);

  wire adc_ra__rb, ALU_1000, clk_en, clk_set, clock5, clock6, clock7, enable_arith_carry, enable_TMP,
       enable_TMP1, load_ACC, load_ra, load_rb, set_ACC, set_arith_FLAGS, store_ra;

  and and_1 (load_rb, clock5, clk_en, adc_ra__rb);
  and and_2 (enable_arith_carry, clock5, clk_en, adc_ra__rb);
  and and_3 (load_ra, clock6, clk_en, adc_ra__rb);
  and and_4 (ALU_1000, clock6, clk_en, adc_ra__rb);
  and and_5 (load_ACC, clock7, clk_en, adc_ra__rb);
  and and_6 (enable_TMP, clock5, clk_set, adc_ra__rb);
  and and_7 (enable_TMP1, clock5, clk_set, adc_ra__rb);
  and and_8 (set_ACC, clock6, clk_set, adc_ra__rb);
  and and_9 (set_arith_FLAGS, clock6, clk_set, adc_ra__rb);
  and and_10 (store_ra, clock7, clk_set, adc_ra__rb);
endmodule

module sub_ra__rb (
);

  wire ALU_1100, clk_en, clk_set, clock5, clock6, clock7, enable_TMP, load_ACC, load_ra, load_rb, set_ACC,
       set_arith_FLAGS, store_ra, sub_ra__rb;

  and and_1 (load_rb, clock5, clk_en, sub_ra__rb);
  and and_2 (load_ra, clock6, clk_en, sub_ra__rb);
  and and_3 (ALU_1100, clock6, clk_en, sub_ra__rb);
  and and_4 (load_ACC, clock7, clk_en, sub_ra__rb);
  and and_5 (enable_TMP, clock5, clk_set, sub_ra__rb);
  and and_6 (set_ACC, clock6, clk_set, sub_ra__rb);
  and and_7 (set_arith_FLAGS, clock6, clk_set, sub_ra__rb);
  and and_8 (store_ra, clock7, clk_set, sub_ra__rb);
endmodule

module mul_ra__rb (
);

  wire ALU_1101, clk_en, clk_set, clock5, clock6, clock7, enable_TMP, load_ACC, load_ra, load_rb, mul_ra__rb,
       set_ACC, set_arith_FLAGS, store_ra;

  and and_1 (load_rb, clock5, clk_en, mul_ra__rb);
  and and_2 (load_ra, clock6, clk_en, mul_ra__rb);
  and and_3 (ALU_1101, clock6, clk_en, mul_ra__rb);
  and and_4 (load_ACC, clock7, clk_en, mul_ra__rb);
  and and_5 (enable_TMP, clock5, clk_set, mul_ra__rb);
  and and_6 (set_ACC, clock6, clk_set, mul_ra__rb);
  and and_7 (set_arith_FLAGS, clock6, clk_set, mul_ra__rb);
  and and_8 (store_ra, clock7, clk_set, mul_ra__rb);
endmodule

module div_ra__rb (
);

  wire ALU_1110, clk_en, clk_set, clock5, clock6, clock7, div_ra__rb, enable_TMP, load_ACC, load_ra, load_rb,
       set_ACC, set_arith_FLAGS, store_ra;

  and and_1 (load_rb, clock5, clk_en, div_ra__rb);
  and and_2 (load_ra, clock6, clk_en, div_ra__rb);
  and and_3 (ALU_1110, clock6, clk_en, div_ra__rb);
  and and_4 (load_ACC, clock7, clk_en, div_ra__rb);
  and and_5 (enable_TMP, clock5, clk_set, div_ra__rb);
  and and_6 (set_ACC, clock6, clk_set, div_ra__rb);
  and and_7 (set_arith_FLAGS, clock6, clk_set, div_ra__rb);
  and and_8 (store_ra, clock7, clk_set, div_ra__rb);
endmodule

module mod_ra__rb (
);

  wire ALU_1111, clk_en, clk_set, clock5, clock6, clock7, enable_TMP, load_ACC, load_ra, load_rb, mod_ra__rb,
       set_ACC, set_arith_FLAGS, store_ra;

  and and_1 (load_rb, clock5, clk_en, mod_ra__rb);
  and and_2 (load_ra, clock6, clk_en, mod_ra__rb);
  and and_3 (ALU_1111, clock6, clk_en, mod_ra__rb);
  and and_4 (load_ACC, clock7, clk_en, mod_ra__rb);
  and and_5 (enable_TMP, clock5, clk_set, mod_ra__rb);
  and and_6 (set_ACC, clock6, clk_set, mod_ra__rb);
  and and_7 (set_arith_FLAGS, clock6, clk_set, mod_ra__rb);
  and and_8 (store_ra, clock7, clk_set, mod_ra__rb);
endmodule

module xchg_ra__rb (
);

  wire ALU_0000, clk_en, clk_set, clock5, clock6, clock7, enable_CLR, load_ACC, load_ra, load_rb, set_ACC,
       store_ra, store_rb, xchg_ra__rb;

  and and_1 (load_rb, clock5, clk_en, xchg_ra__rb);
  and and_2 (enable_CLR, clock5, clk_en, xchg_ra__rb);
  and and_3 (ALU_0000, clock5, clk_en, xchg_ra__rb);
  and and_4 (load_ra, clock6, clk_en, xchg_ra__rb);
  and and_5 (load_ACC, clock7, clk_en, xchg_ra__rb);
  and and_6 (set_ACC, clock5, clk_set, xchg_ra__rb);
  and and_7 (store_rb, clock6, clk_set, xchg_ra__rb);
  and and_8 (store_ra, clock7, clk_set, xchg_ra__rb);
endmodule

module mov_ra__rb (
);

  wire clk_en, clk_set, clock5, load_rb, mov_ra__rb, store_ra;

  and and_1 (load_rb, clock5, clk_en, mov_ra__rb);
  and and_2 (store_ra, clock5, clk_set, mov_ra__rb);
endmodule

module mov_ra__imm16 (
);

  wire ALU_0000, ALU_1000, clk_en, clk_set, clock5, clock6, clock7, clock8, clock9, enable_BUS1,
       enable_carry, enable_CLR, enable_TMP1, load_ACC, load_CS, load_IAR, load_RAM, mov_ra__imm16, sel_CS,
       sel_MAR, set_ACC, set_carry, set_IAR, store_CS, store_ra;

  and and_1 (sel_CS, clock5, clk_en, mov_ra__imm16);
  and and_2 (load_IAR, clock5, clk_en, mov_ra__imm16);
  and and_3 (enable_BUS1, clock5, clk_en, mov_ra__imm16);
  and and_4 (ALU_0000, clock5, clk_en, mov_ra__imm16);
  and and_5 (set_carry, clock5, clk_en, mov_ra__imm16);
  and and_6 (load_ACC, clock6, clk_en, mov_ra__imm16);
  and and_7 (load_CS, clock7, clk_en, mov_ra__imm16);
  and and_8 (enable_CLR, clock7, clk_en, mov_ra__imm16);
  and and_9 (ALU_1000, clock7, clk_en, mov_ra__imm16);
  and and_10 (load_ACC, clock8, clk_en, mov_ra__imm16);
  and and_11 (load_RAM, clock9, clk_en, mov_ra__imm16);
  and and_12 (sel_MAR, clock5, clk_set, mov_ra__imm16);
  and and_13 (set_ACC, clock5, clk_set, mov_ra__imm16);
  and and_14 (enable_carry, clock5, clk_set, mov_ra__imm16);
  and and_15 (enable_TMP1, clock5, clk_set, mov_ra__imm16);
  and and_16 (set_IAR, clock6, clk_set, mov_ra__imm16);
  and and_17 (set_ACC, clock7, clk_set, mov_ra__imm16);
  and and_18 (store_CS, clock8, clk_set, mov_ra__imm16);
  and and_19 (store_ra, clock9, clk_set, mov_ra__imm16);
endmodule

module add_ra__imm16 (
);

  wire add_ra__imm16, ALU_0000, ALU_1000, clk_en, clk_set, clock5, clock6, clock7, clock8, clock9, clock10,
       clock11, enable_BUS1, enable_carry, enable_CLR, enable_TMP, enable_TMP1, load_ACC, load_CS, load_IAR,
       load_ra, load_RAM, sel_CS, sel_MAR, set_ACC, set_arith_flags, set_carry, set_IAR, store_CS, store_ra;

  and and_1 (sel_CS, clock5, clk_en, add_ra__imm16);
  and and_2 (load_IAR, clock5, clk_en, add_ra__imm16);
  and and_3 (enable_BUS1, clock5, clk_en, add_ra__imm16);
  and and_4 (ALU_0000, clock5, clk_en, add_ra__imm16);
  and and_5 (set_carry, clock5, clk_en, add_ra__imm16);
  and and_6 (load_ACC, clock6, clk_en, add_ra__imm16);
  and and_7 (load_CS, clock7, clk_en, add_ra__imm16);
  and and_8 (enable_CLR, clock7, clk_en, add_ra__imm16);
  and and_9 (ALU_1000, clock7, clk_en, add_ra__imm16);
  and and_10 (load_ACC, clock8, clk_en, add_ra__imm16);
  and and_11 (load_RAM, clock9, clk_en, add_ra__imm16);
  and and_12 (load_ra, clock10, clk_en, add_ra__imm16);
  and and_13 (ALU_0000, clock10, clk_en, add_ra__imm16);
  and and_14 (load_ACC, clock11, clk_en, add_ra__imm16);
  and and_15 (sel_MAR, clock5, clk_set, add_ra__imm16);
  and and_16 (set_ACC, clock5, clk_set, add_ra__imm16);
  and and_17 (enable_carry, clock5, clk_set, add_ra__imm16);
  and and_18 (enable_TMP1, clock5, clk_set, add_ra__imm16);
  and and_19 (set_IAR, clock6, clk_set, add_ra__imm16);
  and and_20 (set_ACC, clock7, clk_set, add_ra__imm16);
  and and_21 (store_CS, clock8, clk_set, add_ra__imm16);
  and and_22 (enable_TMP, clock9, clk_set, add_ra__imm16);
  and and_23 (set_ACC, clock10, clk_set, add_ra__imm16);
  and and_24 (set_arith_flags, clock10, clk_set, add_ra__imm16);
  and and_25 (store_ra, clock11, clk_set, add_ra__imm16);
endmodule

module and_ra__imm16 (
);

  wire ALU_0000, ALU_0100, ALU_1000, and_ra__imm16, clk_en, clk_set, clock5, clock6, clock7, clock8, clock9,
       clock10, clock11, enable_BUS1, enable_carry, enable_CLR, enable_TMP, enable_TMP1, load_ACC, load_CS,
       load_IAR, load_ra, load_RAM, sel_CS, sel_MAR, set_ACC, set_arith_flags, set_carry, set_IAR, store_CS,
       store_ra;

  and and_1 (sel_CS, clock5, clk_en, and_ra__imm16);
  and and_2 (load_IAR, clock5, clk_en, and_ra__imm16);
  and and_3 (enable_BUS1, clock5, clk_en, and_ra__imm16);
  and and_4 (ALU_0000, clock5, clk_en, and_ra__imm16);
  and and_5 (set_carry, clock5, clk_en, and_ra__imm16);
  and and_6 (load_ACC, clock6, clk_en, and_ra__imm16);
  and and_7 (load_CS, clock7, clk_en, and_ra__imm16);
  and and_8 (enable_CLR, clock7, clk_en, and_ra__imm16);
  and and_9 (ALU_1000, clock7, clk_en, and_ra__imm16);
  and and_10 (load_ACC, clock8, clk_en, and_ra__imm16);
  and and_11 (load_RAM, clock9, clk_en, and_ra__imm16);
  and and_12 (load_ra, clock10, clk_en, and_ra__imm16);
  and and_13 (ALU_0100, clock10, clk_en, and_ra__imm16);
  and and_14 (load_ACC, clock11, clk_en, and_ra__imm16);
  and and_15 (sel_MAR, clock5, clk_set, and_ra__imm16);
  and and_16 (set_ACC, clock5, clk_set, and_ra__imm16);
  and and_17 (enable_carry, clock5, clk_set, and_ra__imm16);
  and and_18 (enable_TMP1, clock5, clk_set, and_ra__imm16);
  and and_19 (set_IAR, clock6, clk_set, and_ra__imm16);
  and and_20 (set_ACC, clock7, clk_set, and_ra__imm16);
  and and_21 (store_CS, clock8, clk_set, and_ra__imm16);
  and and_22 (enable_TMP, clock9, clk_set, and_ra__imm16);
  and and_23 (set_ACC, clock10, clk_set, and_ra__imm16);
  and and_24 (set_arith_flags, clock10, clk_set, and_ra__imm16);
  and and_25 (store_ra, clock11, clk_set, and_ra__imm16);
endmodule

module or_ra__imm16 (
);

  wire ALU_0000, ALU_0101, ALU_1000, clk_en, clk_set, clock5, clock6, clock7, clock8, clock9, clock10,
       clock11, enable_BUS1, enable_carry, enable_CLR, enable_TMP, enable_TMP1, load_ACC, load_CS, load_IAR,
       load_ra, load_RAM, or_ra__imm16, sel_CS, sel_MAR, set_ACC, set_arith_flags, set_carry, set_IAR,
       store_CS, store_ra;

  and and_1 (sel_CS, clock5, clk_en, or_ra__imm16);
  and and_2 (load_IAR, clock5, clk_en, or_ra__imm16);
  and and_3 (enable_BUS1, clock5, clk_en, or_ra__imm16);
  and and_4 (ALU_0000, clock5, clk_en, or_ra__imm16);
  and and_5 (set_carry, clock5, clk_en, or_ra__imm16);
  and and_6 (load_ACC, clock6, clk_en, or_ra__imm16);
  and and_7 (load_CS, clock7, clk_en, or_ra__imm16);
  and and_8 (enable_CLR, clock7, clk_en, or_ra__imm16);
  and and_9 (ALU_1000, clock7, clk_en, or_ra__imm16);
  and and_10 (load_ACC, clock8, clk_en, or_ra__imm16);
  and and_11 (load_RAM, clock9, clk_en, or_ra__imm16);
  and and_12 (load_ra, clock10, clk_en, or_ra__imm16);
  and and_13 (ALU_0101, clock10, clk_en, or_ra__imm16);
  and and_14 (load_ACC, clock11, clk_en, or_ra__imm16);
  and and_15 (sel_MAR, clock5, clk_set, or_ra__imm16);
  and and_16 (set_ACC, clock5, clk_set, or_ra__imm16);
  and and_17 (enable_carry, clock5, clk_set, or_ra__imm16);
  and and_18 (enable_TMP1, clock5, clk_set, or_ra__imm16);
  and and_19 (set_IAR, clock6, clk_set, or_ra__imm16);
  and and_20 (set_ACC, clock7, clk_set, or_ra__imm16);
  and and_21 (store_CS, clock8, clk_set, or_ra__imm16);
  and and_22 (enable_TMP, clock9, clk_set, or_ra__imm16);
  and and_23 (set_ACC, clock10, clk_set, or_ra__imm16);
  and and_24 (set_arith_flags, clock10, clk_set, or_ra__imm16);
  and and_25 (store_ra, clock11, clk_set, or_ra__imm16);
endmodule

module xor_ra__imm16 (
);

  wire ALU_0000, ALU_0110, ALU_1000, clk_en, clk_set, clock5, clock6, clock7, clock8, clock9, clock10,
       clock11, enable_BUS1, enable_carry, enable_CLR, enable_TMP, enable_TMP1, load_ACC, load_CS, load_IAR,
       load_ra, load_RAM, sel_CS, sel_MAR, set_ACC, set_arith_flags, set_carry, set_IAR, store_CS, store_ra,
       xor_ra__imm16;

  and and_1 (sel_CS, clock5, clk_en, xor_ra__imm16);
  and and_2 (load_IAR, clock5, clk_en, xor_ra__imm16);
  and and_3 (enable_BUS1, clock5, clk_en, xor_ra__imm16);
  and and_4 (ALU_0000, clock5, clk_en, xor_ra__imm16);
  and and_5 (set_carry, clock5, clk_en, xor_ra__imm16);
  and and_6 (load_ACC, clock6, clk_en, xor_ra__imm16);
  and and_7 (load_CS, clock7, clk_en, xor_ra__imm16);
  and and_8 (enable_CLR, clock7, clk_en, xor_ra__imm16);
  and and_9 (ALU_1000, clock7, clk_en, xor_ra__imm16);
  and and_10 (load_ACC, clock8, clk_en, xor_ra__imm16);
  and and_11 (load_RAM, clock9, clk_en, xor_ra__imm16);
  and and_12 (load_ra, clock10, clk_en, xor_ra__imm16);
  and and_13 (ALU_0110, clock10, clk_en, xor_ra__imm16);
  and and_14 (load_ACC, clock11, clk_en, xor_ra__imm16);
  and and_15 (sel_MAR, clock5, clk_set, xor_ra__imm16);
  and and_16 (set_ACC, clock5, clk_set, xor_ra__imm16);
  and and_17 (enable_carry, clock5, clk_set, xor_ra__imm16);
  and and_18 (enable_TMP1, clock5, clk_set, xor_ra__imm16);
  and and_19 (set_IAR, clock6, clk_set, xor_ra__imm16);
  and and_20 (set_ACC, clock7, clk_set, xor_ra__imm16);
  and and_21 (store_CS, clock8, clk_set, xor_ra__imm16);
  and and_22 (enable_TMP, clock9, clk_set, xor_ra__imm16);
  and and_23 (set_ACC, clock10, clk_set, xor_ra__imm16);
  and and_24 (set_arith_flags, clock10, clk_set, xor_ra__imm16);
  and and_25 (store_ra, clock11, clk_set, xor_ra__imm16);
endmodule

module cmp_ra__imm16 (
);

  wire ALU_0000, ALU_0111, ALU_1000, clk_en, clk_set, clock5, clock6, clock7, clock8, clock9, clock10,
       cmp_ra__imm16, enable_BUS1, enable_carry, enable_CLR, enable_TMP, enable_TMP1, load_ACC, load_CS,
       load_IAR, load_ra, load_RAM, sel_CS, sel_MAR, set_ACC, set_arith_flags, set_carry, set_IAR, store_CS;

  and and_1 (sel_CS, clock5, clk_en, cmp_ra__imm16);
  and and_2 (load_IAR, clock5, clk_en, cmp_ra__imm16);
  and and_3 (enable_BUS1, clock5, clk_en, cmp_ra__imm16);
  and and_4 (ALU_0000, clock5, clk_en, cmp_ra__imm16);
  and and_5 (set_carry, clock5, clk_en, cmp_ra__imm16);
  and and_6 (load_ACC, clock6, clk_en, cmp_ra__imm16);
  and and_7 (load_CS, clock7, clk_en, cmp_ra__imm16);
  and and_8 (enable_CLR, clock7, clk_en, cmp_ra__imm16);
  and and_9 (ALU_1000, clock7, clk_en, cmp_ra__imm16);
  and and_10 (load_ACC, clock8, clk_en, cmp_ra__imm16);
  and and_11 (load_RAM, clock9, clk_en, cmp_ra__imm16);
  and and_12 (load_ra, clock10, clk_en, cmp_ra__imm16);
  and and_13 (ALU_0111, clock10, clk_en, cmp_ra__imm16);
  and and_14 (sel_MAR, clock5, clk_set, cmp_ra__imm16);
  and and_15 (set_ACC, clock5, clk_set, cmp_ra__imm16);
  and and_16 (enable_carry, clock5, clk_set, cmp_ra__imm16);
  and and_17 (enable_TMP1, clock5, clk_set, cmp_ra__imm16);
  and and_18 (set_IAR, clock6, clk_set, cmp_ra__imm16);
  and and_19 (set_ACC, clock7, clk_set, cmp_ra__imm16);
  and and_20 (store_CS, clock8, clk_set, cmp_ra__imm16);
  and and_21 (enable_TMP, clock9, clk_set, cmp_ra__imm16);
  and and_22 (set_ACC, clock10, clk_set, cmp_ra__imm16);
  and and_23 (set_arith_flags, clock10, clk_set, cmp_ra__imm16);
endmodule

module adc_ra__imm16 (
);

  wire adc_ra__imm16, add_ra__imm16, ALU_0000, ALU_1000, clk_en, clk_set, clock5, clock6, clock7, clock8,
       clock9, clock10, clock11, enable_arith_carry, enable_BUS1, enable_carry, enable_CLR, enable_TMP,
       enable_TMP1, load_ACC, load_CS, load_IAR, load_ra, load_RAM, sel_CS, sel_MAR, set_ACC,
       set_arith_flags, set_carry, set_IAR, store_CS, store_ra;

  and and_1 (sel_CS, clock5, clk_en, add_ra__imm16);
  and and_2 (load_IAR, clock5, clk_en, add_ra__imm16);
  and and_3 (enable_BUS1, clock5, clk_en, add_ra__imm16);
  and and_4 (ALU_0000, clock5, clk_en, add_ra__imm16);
  and and_5 (set_carry, clock5, clk_en, add_ra__imm16);
  and and_6 (load_ACC, clock6, clk_en, adc_ra__imm16);
  and and_7 (load_CS, clock7, clk_en, adc_ra__imm16);
  and and_8 (enable_CLR, clock7, clk_en, adc_ra__imm16);
  and and_9 (ALU_1000, clock7, clk_en, adc_ra__imm16);
  and and_10 (load_ACC, clock8, clk_en, adc_ra__imm16);
  and and_11 (load_RAM, clock9, clk_en, adc_ra__imm16);
  and and_12 (enable_arith_carry, clock9, clk_en, adc_ra__imm16);
  and and_13 (load_ra, clock10, clk_en, adc_ra__imm16);
  and and_14 (ALU_1000, clock10, clk_en, adc_ra__imm16);
  and and_15 (load_ACC, clock11, clk_en, adc_ra__imm16);
  and and_16 (sel_MAR, clock5, clk_set, add_ra__imm16);
  and and_17 (set_ACC, clock5, clk_set, add_ra__imm16);
  and and_18 (enable_carry, clock5, clk_set, add_ra__imm16);
  and and_19 (enable_TMP1, clock5, clk_set, add_ra__imm16);
  and and_20 (set_IAR, clock6, clk_set, adc_ra__imm16);
  and and_21 (set_ACC, clock7, clk_set, adc_ra__imm16);
  and and_22 (store_CS, clock8, clk_set, adc_ra__imm16);
  and and_23 (enable_TMP, clock9, clk_set, adc_ra__imm16);
  and and_24 (enable_TMP1, clock9, clk_set, adc_ra__imm16);
  and and_25 (set_ACC, clock10, clk_set, adc_ra__imm16);
  and and_26 (set_arith_flags, clock10, clk_set, adc_ra__imm16);
  and and_27 (store_ra, clock11, clk_set, adc_ra__imm16);
endmodule

module sub_ra__imm16 (
);

  wire ALU_0000, ALU_1000, ALU_1100, clk_en, clk_set, clock5, clock6, clock7, clock8, clock9, clock10,
       clock11, enable_BUS1, enable_carry, enable_CLR, enable_TMP, enable_TMP1, load_ACC, load_CS, load_IAR,
       load_ra, load_RAM, sel_CS, sel_MAR, set_ACC, set_arith_flags, set_carry, set_IAR, store_CS, store_ra,
       sub_ra__imm16;

  and and_1 (sel_CS, clock5, clk_en, sub_ra__imm16);
  and and_2 (load_IAR, clock5, clk_en, sub_ra__imm16);
  and and_3 (enable_BUS1, clock5, clk_en, sub_ra__imm16);
  and and_4 (ALU_0000, clock5, clk_en, sub_ra__imm16);
  and and_5 (set_carry, clock5, clk_en, sub_ra__imm16);
  and and_6 (load_ACC, clock6, clk_en, sub_ra__imm16);
  and and_7 (load_CS, clock7, clk_en, sub_ra__imm16);
  and and_8 (enable_CLR, clock7, clk_en, sub_ra__imm16);
  and and_9 (ALU_1000, clock7, clk_en, sub_ra__imm16);
  and and_10 (load_ACC, clock8, clk_en, sub_ra__imm16);
  and and_11 (load_RAM, clock9, clk_en, sub_ra__imm16);
  and and_12 (load_ra, clock10, clk_en, sub_ra__imm16);
  and and_13 (ALU_1100, clock10, clk_en, sub_ra__imm16);
  and and_14 (load_ACC, clock11, clk_en, sub_ra__imm16);
  and and_15 (sel_MAR, clock5, clk_set, sub_ra__imm16);
  and and_16 (set_ACC, clock5, clk_set, sub_ra__imm16);
  and and_17 (enable_carry, clock5, clk_set, sub_ra__imm16);
  and and_18 (enable_TMP1, clock5, clk_set, sub_ra__imm16);
  and and_19 (set_IAR, clock6, clk_set, sub_ra__imm16);
  and and_20 (set_ACC, clock7, clk_set, sub_ra__imm16);
  and and_21 (store_CS, clock8, clk_set, sub_ra__imm16);
  and and_22 (enable_TMP, clock9, clk_set, sub_ra__imm16);
  and and_23 (set_ACC, clock10, clk_set, sub_ra__imm16);
  and and_24 (set_arith_flags, clock10, clk_set, sub_ra__imm16);
  and and_25 (store_ra, clock11, clk_set, sub_ra__imm16);
endmodule

module mul_ra__imm16 (
);

  wire ALU_0000, ALU_1000, ALU_1101, clk_en, clk_set, clock5, clock6, clock7, clock8, clock9, clock10,
       clock11, enable_BUS1, enable_carry, enable_CLR, enable_TMP, enable_TMP1, load_ACC, load_CS, load_IAR,
       load_ra, load_RAM, mul_ra__imm16, sel_CS, sel_MAR, set_ACC, set_arith_flags, set_carry, set_IAR,
       store_CS, store_ra;

  and and_1 (sel_CS, clock5, clk_en, mul_ra__imm16);
  and and_2 (load_IAR, clock5, clk_en, mul_ra__imm16);
  and and_3 (enable_BUS1, clock5, clk_en, mul_ra__imm16);
  and and_4 (ALU_0000, clock5, clk_en, mul_ra__imm16);
  and and_5 (set_carry, clock5, clk_en, mul_ra__imm16);
  and and_6 (load_ACC, clock6, clk_en, mul_ra__imm16);
  and and_7 (load_CS, clock7, clk_en, mul_ra__imm16);
  and and_8 (enable_CLR, clock7, clk_en, mul_ra__imm16);
  and and_9 (ALU_1000, clock7, clk_en, mul_ra__imm16);
  and and_10 (load_ACC, clock8, clk_en, mul_ra__imm16);
  and and_11 (load_RAM, clock9, clk_en, mul_ra__imm16);
  and and_12 (load_ra, clock10, clk_en, mul_ra__imm16);
  and and_13 (ALU_1101, clock10, clk_en, mul_ra__imm16);
  and and_14 (load_ACC, clock11, clk_en, mul_ra__imm16);
  and and_15 (sel_MAR, clock5, clk_set, mul_ra__imm16);
  and and_16 (set_ACC, clock5, clk_set, mul_ra__imm16);
  and and_17 (enable_carry, clock5, clk_set, mul_ra__imm16);
  and and_18 (enable_TMP1, clock5, clk_set, mul_ra__imm16);
  and and_19 (set_IAR, clock6, clk_set, mul_ra__imm16);
  and and_20 (set_ACC, clock7, clk_set, mul_ra__imm16);
  and and_21 (store_CS, clock8, clk_set, mul_ra__imm16);
  and and_22 (enable_TMP, clock9, clk_set, mul_ra__imm16);
  and and_23 (set_ACC, clock10, clk_set, mul_ra__imm16);
  and and_24 (set_arith_flags, clock10, clk_set, mul_ra__imm16);
  and and_25 (store_ra, clock11, clk_set, mul_ra__imm16);
endmodule

module div_ra__imm16 (
);

  wire ALU_0000, ALU_1000, ALU_1110, clk_en, clk_set, clock5, clock6, clock7, clock8, clock9, clock10,
       clock11, div_ra__imm16, enable_BUS1, enable_carry, enable_CLR, enable_TMP, enable_TMP1, load_ACC,
       load_CS, load_IAR, load_ra, load_RAM, sel_CS, sel_MAR, set_ACC, set_arith_flags, set_carry, set_IAR,
       store_CS, store_ra;

  and and_1 (sel_CS, clock5, clk_en, div_ra__imm16);
  and and_2 (load_IAR, clock5, clk_en, div_ra__imm16);
  and and_3 (enable_BUS1, clock5, clk_en, div_ra__imm16);
  and and_4 (ALU_0000, clock5, clk_en, div_ra__imm16);
  and and_5 (set_carry, clock5, clk_en, div_ra__imm16);
  and and_6 (load_ACC, clock6, clk_en, div_ra__imm16);
  and and_7 (load_CS, clock7, clk_en, div_ra__imm16);
  and and_8 (enable_CLR, clock7, clk_en, div_ra__imm16);
  and and_9 (ALU_1000, clock7, clk_en, div_ra__imm16);
  and and_10 (load_ACC, clock8, clk_en, div_ra__imm16);
  and and_11 (load_RAM, clock9, clk_en, div_ra__imm16);
  and and_12 (load_ra, clock10, clk_en, div_ra__imm16);
  and and_13 (ALU_1110, clock10, clk_en, div_ra__imm16);
  and and_14 (load_ACC, clock11, clk_en, div_ra__imm16);
  and and_15 (sel_MAR, clock5, clk_set, div_ra__imm16);
  and and_16 (set_ACC, clock5, clk_set, div_ra__imm16);
  and and_17 (enable_carry, clock5, clk_set, div_ra__imm16);
  and and_18 (enable_TMP1, clock5, clk_set, div_ra__imm16);
  and and_19 (set_IAR, clock6, clk_set, div_ra__imm16);
  and and_20 (set_ACC, clock7, clk_set, div_ra__imm16);
  and and_21 (store_CS, clock8, clk_set, div_ra__imm16);
  and and_22 (enable_TMP, clock9, clk_set, div_ra__imm16);
  and and_23 (set_ACC, clock10, clk_set, div_ra__imm16);
  and and_24 (set_arith_flags, clock10, clk_set, div_ra__imm16);
  and and_25 (store_ra, clock11, clk_set, div_ra__imm16);
endmodule

module mod_ra__imm16 (
);

  wire ALU_0000, ALU_1000, ALU_1111, clk_en, clk_set, clock5, clock6, clock7, clock8, clock9, clock10,
       clock11, enable_BUS1, enable_carry, enable_CLR, enable_TMP, enable_TMP1, load_ACC, load_CS, load_IAR,
       load_ra, load_RAM, mod_ra__imm16, sel_CS, sel_MAR, set_ACC, set_arith_flags, set_carry, set_IAR,
       store_CS, store_ra;

  and and_1 (sel_CS, clock5, clk_en, mod_ra__imm16);
  and and_2 (load_IAR, clock5, clk_en, mod_ra__imm16);
  and and_3 (enable_BUS1, clock5, clk_en, mod_ra__imm16);
  and and_4 (ALU_0000, clock5, clk_en, mod_ra__imm16);
  and and_5 (set_carry, clock5, clk_en, mod_ra__imm16);
  and and_6 (load_ACC, clock6, clk_en, mod_ra__imm16);
  and and_7 (load_CS, clock7, clk_en, mod_ra__imm16);
  and and_8 (enable_CLR, clock7, clk_en, mod_ra__imm16);
  and and_9 (ALU_1000, clock7, clk_en, mod_ra__imm16);
  and and_10 (load_ACC, clock8, clk_en, mod_ra__imm16);
  and and_11 (load_RAM, clock9, clk_en, mod_ra__imm16);
  and and_12 (load_ra, clock10, clk_en, mod_ra__imm16);
  and and_13 (ALU_1111, clock10, clk_en, mod_ra__imm16);
  and and_14 (load_ACC, clock11, clk_en, mod_ra__imm16);
  and and_15 (sel_MAR, clock5, clk_set, mod_ra__imm16);
  and and_16 (set_ACC, clock5, clk_set, mod_ra__imm16);
  and and_17 (enable_carry, clock5, clk_set, mod_ra__imm16);
  and and_18 (enable_TMP1, clock5, clk_set, mod_ra__imm16);
  and and_19 (set_IAR, clock6, clk_set, mod_ra__imm16);
  and and_20 (set_ACC, clock7, clk_set, mod_ra__imm16);
  and and_21 (store_CS, clock8, clk_set, mod_ra__imm16);
  and and_22 (enable_TMP, clock9, clk_set, mod_ra__imm16);
  and and_23 (set_ACC, clock10, clk_set, mod_ra__imm16);
  and and_24 (set_arith_flags, clock10, clk_set, mod_ra__imm16);
  and and_25 (store_ra, clock11, clk_set, mod_ra__imm16);
endmodule

module mov_ra__byte__rb_imm16 (
);

  wire ALU_0000, ALU_0100, ALU_1000, clk_en, clk_set, clock5, clock6, clock7, clock8, clock9, clock10,
       clock11, clock12, enable_BUS1, enable_carry, enable_CLR, enable_lowmask, enable_TMP1, load_ACC,
       load_CS, load_IAR, load_ra, load_RAM, mov_ra__byte__rb_imm16, sel_CS, sel_MAR, sel_rb, set_ACC,
       set_carry, set_IAR, store_CS, store_ra;

  and and_1 (sel_CS, clock5, clk_en, mov_ra__byte__rb_imm16);
  and and_2 (load_IAR, clock5, clk_en, mov_ra__byte__rb_imm16);
  and and_3 (enable_BUS1, clock5, clk_en, mov_ra__byte__rb_imm16);
  and and_4 (ALU_0000, clock5, clk_en, mov_ra__byte__rb_imm16);
  and and_5 (set_carry, clock5, clk_en, mov_ra__byte__rb_imm16);
  and and_6 (load_ACC, clock6, clk_en, mov_ra__byte__rb_imm16);
  and and_7 (load_CS, clock7, clk_en, mov_ra__byte__rb_imm16);
  and and_8 (enable_CLR, clock7, clk_en, mov_ra__byte__rb_imm16);
  and and_9 (ALU_1000, clock7, clk_en, mov_ra__byte__rb_imm16);
  and and_10 (load_ACC, clock8, clk_en, mov_ra__byte__rb_imm16);
  and and_11 (sel_rb, clock9, clk_en, mov_ra__byte__rb_imm16);
  and and_12 (load_RAM, clock9, clk_en, mov_ra__byte__rb_imm16);
  and and_13 (load_RAM, clock10, clk_en, mov_ra__byte__rb_imm16);
  and and_14 (load_ra, clock11, clk_en, mov_ra__byte__rb_imm16);
  and and_15 (enable_lowmask, clock11, clk_en, mov_ra__byte__rb_imm16);
  and and_16 (ALU_0100, clock11, clk_en, mov_ra__byte__rb_imm16);
  and and_17 (load_ACC, clock12, clk_en, mov_ra__byte__rb_imm16);
  and and_18 (sel_MAR, clock5, clk_set, mov_ra__byte__rb_imm16);
  and and_19 (set_ACC, clock5, clk_set, mov_ra__byte__rb_imm16);
  and and_20 (enable_carry, clock5, clk_set, mov_ra__byte__rb_imm16);
  and and_21 (enable_TMP1, clock5, clk_set, mov_ra__byte__rb_imm16);
  and and_22 (set_IAR, clock6, clk_set, mov_ra__byte__rb_imm16);
  and and_23 (set_ACC, clock7, clk_set, mov_ra__byte__rb_imm16);
  and and_24 (store_CS, clock8, clk_set, mov_ra__byte__rb_imm16);
  and and_25 (sel_MAR, clock9, clk_set, mov_ra__byte__rb_imm16);
  and and_26 (store_ra, clock10, clk_set, mov_ra__byte__rb_imm16);
  and and_27 (set_ACC, clock11, clk_set, mov_ra__byte__rb_imm16);
  and and_28 (store_ra, clock12, clk_set, mov_ra__byte__rb_imm16);
endmodule

module mov_ra__word__rb_imm16 (
);

  wire ALU_0000, ALU_1000, clk_en, clk_set, clock5, clock6, clock7, clock8, clock9, clock10, enable_BUS1,
       enable_carry, enable_CLR, enable_TMP1, load_ACC, load_CS, load_IAR, load_RAM, mov_ra__word__rb_imm16,
       sel_CS, sel_MAR, sel_rb, set_ACC, set_carry, set_IAR, store_CS, store_ra;

  and and_1 (sel_CS, clock5, clk_en, mov_ra__word__rb_imm16);
  and and_2 (load_IAR, clock5, clk_en, mov_ra__word__rb_imm16);
  and and_3 (enable_BUS1, clock5, clk_en, mov_ra__word__rb_imm16);
  and and_4 (ALU_0000, clock5, clk_en, mov_ra__word__rb_imm16);
  and and_5 (set_carry, clock5, clk_en, mov_ra__word__rb_imm16);
  and and_6 (load_ACC, clock6, clk_en, mov_ra__word__rb_imm16);
  and and_7 (load_CS, clock7, clk_en, mov_ra__word__rb_imm16);
  and and_8 (enable_CLR, clock7, clk_en, mov_ra__word__rb_imm16);
  and and_9 (ALU_1000, clock7, clk_en, mov_ra__word__rb_imm16);
  and and_10 (load_ACC, clock8, clk_en, mov_ra__word__rb_imm16);
  and and_11 (sel_rb, clock9, clk_en, mov_ra__word__rb_imm16);
  and and_12 (load_RAM, clock9, clk_en, mov_ra__word__rb_imm16);
  and and_13 (load_RAM, clock10, clk_en, mov_ra__word__rb_imm16);
  and and_14 (sel_MAR, clock5, clk_set, mov_ra__word__rb_imm16);
  and and_15 (set_ACC, clock5, clk_set, mov_ra__word__rb_imm16);
  and and_16 (enable_carry, clock5, clk_set, mov_ra__word__rb_imm16);
  and and_17 (enable_TMP1, clock5, clk_set, mov_ra__word__rb_imm16);
  and and_18 (set_IAR, clock6, clk_set, mov_ra__word__rb_imm16);
  and and_19 (set_ACC, clock7, clk_set, mov_ra__word__rb_imm16);
  and and_20 (store_CS, clock8, clk_set, mov_ra__word__rb_imm16);
  and and_21 (sel_MAR, clock9, clk_set, mov_ra__word__rb_imm16);
  and and_22 (store_ra, clock10, clk_set, mov_ra__word__rb_imm16);
endmodule

module mov_word__ra___rb (
);

  wire clk_en, clk_set, clock5, clock6, load_ra, load_rb, mov_word__ra___rb, sel_DS, sel_MAR, store_RAM;

  and and_1 (sel_DS, clock5, clk_en, mov_word__ra___rb);
  and and_2 (load_ra, clock5, clk_en, mov_word__ra___rb);
  and and_3 (load_rb, clock6, clk_en, mov_word__ra___rb);
  and and_4 (sel_MAR, clock5, clk_set, mov_word__ra___rb);
  and and_5 (store_RAM, clock6, clk_set, mov_word__ra___rb);
endmodule

module mov_ra__word__rb (
);

  wire clk_en, clk_set, clock5, clock6, load_RAM, load_rb, mov_ra__word__rb, sel_DS, sel_MAR, store_ra;

  and and_1 (sel_DS, clock5, clk_en, mov_ra__word__rb);
  and and_2 (load_rb, clock5, clk_en, mov_ra__word__rb);
  and and_3 (load_RAM, clock6, clk_en, mov_ra__word__rb);
  and and_4 (sel_MAR, clock5, clk_set, mov_ra__word__rb);
  and and_5 (store_ra, clock6, clk_set, mov_ra__word__rb);
endmodule

module add_ra__word__rb (
);

  wire add_ra__word__rb, ALU_0000, clk_en, clk_set, clock5, clock6, clock7, clock8, enable_arith_flags,
       enable_TMP, load_ACC, load_ra, load_RAM, load_rb, sel_ds, sel_MAR, set_ACC, store_ra;

  and and_1 (sel_ds, clock5, clk_en, add_ra__word__rb);
  and and_2 (load_rb, clock5, clk_en, add_ra__word__rb);
  and and_3 (load_RAM, clock6, clk_en, add_ra__word__rb);
  and and_4 (load_ra, clock7, clk_en, add_ra__word__rb);
  and and_5 (ALU_0000, clock7, clk_en, add_ra__word__rb);
  and and_6 (load_ACC, clock8, clk_en, add_ra__word__rb);
  and and_7 (sel_MAR, clock5, clk_set, add_ra__word__rb);
  and and_8 (enable_TMP, clock6, clk_set, add_ra__word__rb);
  and and_9 (set_ACC, clock7, clk_set, add_ra__word__rb);
  and and_10 (enable_arith_flags, clock7, clk_set, add_ra__word__rb);
  and and_11 (store_ra, clock8, clk_set, add_ra__word__rb);
endmodule

module and_ra__word__rb (
);

  wire ALU_0100, and_ra__word__rb, clk_en, clk_set, clock5, clock6, clock7, clock8, enable_arith_flags,
       enable_TMP, load_ACC, load_ra, load_RAM, load_rb, sel_ds, sel_MAR, set_ACC, store_ra;

  and and_1 (sel_ds, clock5, clk_en, and_ra__word__rb);
  and and_2 (load_rb, clock5, clk_en, and_ra__word__rb);
  and and_3 (load_RAM, clock6, clk_en, and_ra__word__rb);
  and and_4 (load_ra, clock7, clk_en, and_ra__word__rb);
  and and_5 (ALU_0100, clock7, clk_en, and_ra__word__rb);
  and and_6 (load_ACC, clock8, clk_en, and_ra__word__rb);
  and and_7 (sel_MAR, clock5, clk_set, and_ra__word__rb);
  and and_8 (enable_TMP, clock6, clk_set, and_ra__word__rb);
  and and_9 (set_ACC, clock7, clk_set, and_ra__word__rb);
  and and_10 (enable_arith_flags, clock7, clk_set, and_ra__word__rb);
  and and_11 (store_ra, clock8, clk_set, and_ra__word__rb);
endmodule

module or_ra__word__rb (
);

  wire ALU_0101, clk_en, clk_set, clock5, clock6, clock7, clock8, enable_arith_flags, enable_TMP, load_ACC,
       load_ra, load_RAM, load_rb, or_ra__word__rb, sel_ds, sel_MAR, set_ACC, store_ra;

  and and_1 (sel_ds, clock5, clk_en, or_ra__word__rb);
  and and_2 (load_rb, clock5, clk_en, or_ra__word__rb);
  and and_3 (load_RAM, clock6, clk_en, or_ra__word__rb);
  and and_4 (load_ra, clock7, clk_en, or_ra__word__rb);
  and and_5 (ALU_0101, clock7, clk_en, or_ra__word__rb);
  and and_6 (load_ACC, clock8, clk_en, or_ra__word__rb);
  and and_7 (sel_MAR, clock5, clk_set, or_ra__word__rb);
  and and_8 (enable_TMP, clock6, clk_set, or_ra__word__rb);
  and and_9 (set_ACC, clock7, clk_set, or_ra__word__rb);
  and and_10 (enable_arith_flags, clock7, clk_set, or_ra__word__rb);
  and and_11 (store_ra, clock8, clk_set, or_ra__word__rb);
endmodule

module xor_ra__word__rb (
);

  wire ALU_0110, clk_en, clk_set, clock5, clock6, clock7, clock8, enable_arith_flags, enable_TMP, load_ACC,
       load_ra, load_RAM, load_rb, sel_ds, sel_MAR, set_ACC, store_ra, xor_ra__word__rb;

  and and_1 (sel_ds, clock5, clk_en, xor_ra__word__rb);
  and and_2 (load_rb, clock5, clk_en, xor_ra__word__rb);
  and and_3 (load_RAM, clock6, clk_en, xor_ra__word__rb);
  and and_4 (load_ra, clock7, clk_en, xor_ra__word__rb);
  and and_5 (ALU_0110, clock7, clk_en, xor_ra__word__rb);
  and and_6 (load_ACC, clock8, clk_en, xor_ra__word__rb);
  and and_7 (sel_MAR, clock5, clk_set, xor_ra__word__rb);
  and and_8 (enable_TMP, clock6, clk_set, xor_ra__word__rb);
  and and_9 (set_ACC, clock7, clk_set, xor_ra__word__rb);
  and and_10 (enable_arith_flags, clock7, clk_set, xor_ra__word__rb);
  and and_11 (store_ra, clock8, clk_set, xor_ra__word__rb);
endmodule

module cmp_ra__word__rb (
);

  wire ALU_0111, clk_en, clk_set, clock5, clock6, clock7, cmp_ra__word__rb, enable_arith_flags, enable_TMP,
       load_ra, load_RAM, load_rb, sel_ds, sel_MAR, set_ACC;

  and and_1 (sel_ds, clock5, clk_en, cmp_ra__word__rb);
  and and_2 (load_rb, clock5, clk_en, cmp_ra__word__rb);
  and and_3 (load_RAM, clock6, clk_en, cmp_ra__word__rb);
  and and_4 (load_ra, clock7, clk_en, cmp_ra__word__rb);
  and and_5 (ALU_0111, clock7, clk_en, cmp_ra__word__rb);
  and and_6 (sel_MAR, clock5, clk_set, cmp_ra__word__rb);
  and and_7 (enable_TMP, clock6, clk_set, cmp_ra__word__rb);
  and and_8 (set_ACC, clock7, clk_set, cmp_ra__word__rb);
  and and_9 (enable_arith_flags, clock7, clk_set, cmp_ra__word__rb);
endmodule

module adc_ra__word__rb (
);

  wire adc_ra__word__rb, ALU_1000, clk_en, clk_set, clock5, clock6, clock7, clock8, enable_arith_carry,
       enable_arith_flags, enable_TMP, enable_TMP1, load_ACC, load_ra, load_RAM, load_rb, sel_ds, sel_MAR,
       set_ACC, store_ra;

  and and_1 (sel_ds, clock5, clk_en, adc_ra__word__rb);
  and and_2 (load_rb, clock5, clk_en, adc_ra__word__rb);
  and and_3 (load_RAM, clock6, clk_en, adc_ra__word__rb);
  and and_4 (enable_arith_carry, clock6, clk_en, adc_ra__word__rb);
  and and_5 (load_ra, clock7, clk_en, adc_ra__word__rb);
  and and_6 (ALU_1000, clock7, clk_en, adc_ra__word__rb);
  and and_7 (load_ACC, clock8, clk_en, adc_ra__word__rb);
  and and_8 (sel_MAR, clock5, clk_set, adc_ra__word__rb);
  and and_9 (enable_TMP, clock6, clk_set, adc_ra__word__rb);
  and and_10 (enable_TMP1, clock6, clk_set, adc_ra__word__rb);
  and and_11 (set_ACC, clock7, clk_set, adc_ra__word__rb);
  and and_12 (enable_arith_flags, clock7, clk_set, adc_ra__word__rb);
  and and_13 (store_ra, clock8, clk_set, adc_ra__word__rb);
endmodule

module mul_ra__word__rb (
);

  wire ALU_1101, clk_en, clk_set, clock5, clock6, clock7, clock8, enable_arith_flags, enable_TMP, load_ACC,
       load_ra, load_RAM, load_rb, mul_ra__word__rb, sel_ds, sel_MAR, set_ACC, store_ra;

  and and_1 (sel_ds, clock5, clk_en, mul_ra__word__rb);
  and and_2 (load_rb, clock5, clk_en, mul_ra__word__rb);
  and and_3 (load_RAM, clock6, clk_en, mul_ra__word__rb);
  and and_4 (load_ra, clock7, clk_en, mul_ra__word__rb);
  and and_5 (ALU_1101, clock7, clk_en, mul_ra__word__rb);
  and and_6 (load_ACC, clock8, clk_en, mul_ra__word__rb);
  and and_7 (sel_MAR, clock5, clk_set, mul_ra__word__rb);
  and and_8 (enable_TMP, clock6, clk_set, mul_ra__word__rb);
  and and_9 (set_ACC, clock7, clk_set, mul_ra__word__rb);
  and and_10 (enable_arith_flags, clock7, clk_set, mul_ra__word__rb);
  and and_11 (store_ra, clock8, clk_set, mul_ra__word__rb);
endmodule

module div_ra__word__rb (
);

  wire ALU_1110, clk_en, clk_set, clock5, clock6, clock7, clock8, div_ra__word__rb, enable_arith_flags,
       enable_TMP, load_ACC, load_ra, load_RAM, load_rb, sel_ds, sel_MAR, set_ACC, store_ra;

  and and_1 (sel_ds, clock5, clk_en, div_ra__word__rb);
  and and_2 (load_rb, clock5, clk_en, div_ra__word__rb);
  and and_3 (load_RAM, clock6, clk_en, div_ra__word__rb);
  and and_4 (load_ra, clock7, clk_en, div_ra__word__rb);
  and and_5 (ALU_1110, clock7, clk_en, div_ra__word__rb);
  and and_6 (load_ACC, clock8, clk_en, div_ra__word__rb);
  and and_7 (sel_MAR, clock5, clk_set, div_ra__word__rb);
  and and_8 (enable_TMP, clock6, clk_set, div_ra__word__rb);
  and and_9 (set_ACC, clock7, clk_set, div_ra__word__rb);
  and and_10 (enable_arith_flags, clock7, clk_set, div_ra__word__rb);
  and and_11 (store_ra, clock8, clk_set, div_ra__word__rb);
endmodule

module mod_ra__word__rb (
);

  wire ALU_1111, clk_en, clk_set, clock5, clock6, clock7, clock8, enable_arith_flags, enable_TMP, load_ACC,
       load_ra, load_RAM, load_rb, mod_ra__word__rb, sel_ds, sel_MAR, set_ACC, store_ra;

  and and_1 (sel_ds, clock5, clk_en, mod_ra__word__rb);
  and and_2 (load_rb, clock5, clk_en, mod_ra__word__rb);
  and and_3 (load_RAM, clock6, clk_en, mod_ra__word__rb);
  and and_4 (load_ra, clock7, clk_en, mod_ra__word__rb);
  and and_5 (ALU_1111, clock7, clk_en, mod_ra__word__rb);
  and and_6 (load_ACC, clock8, clk_en, mod_ra__word__rb);
  and and_7 (sel_MAR, clock5, clk_set, mod_ra__word__rb);
  and and_8 (enable_TMP, clock6, clk_set, mod_ra__word__rb);
  and and_9 (set_ACC, clock7, clk_set, mod_ra__word__rb);
  and and_10 (enable_arith_flags, clock7, clk_set, mod_ra__word__rb);
  and and_11 (store_ra, clock8, clk_set, mod_ra__word__rb);
endmodule

module mov_ra__byte__rb (
);

  wire ALU_0100, clk_en, clk_set, clock5, clock6, clock7, clock8, enable_lowmask, load_ACC, load_ra,
       load_RAM, load_rb, mov_ra__byte__rb, sel_DS, sel_MAR, set_ACC, store_ra;

  and and_1 (sel_DS, clock5, clk_en, mov_ra__byte__rb);
  and and_2 (load_rb, clock5, clk_en, mov_ra__byte__rb);
  and and_3 (load_RAM, clock6, clk_en, mov_ra__byte__rb);
  and and_4 (load_ra, clock7, clk_en, mov_ra__byte__rb);
  and and_5 (enable_lowmask, clock7, clk_en, mov_ra__byte__rb);
  and and_6 (ALU_0100, clock7, clk_en, mov_ra__byte__rb);
  and and_7 (load_ACC, clock8, clk_en, mov_ra__byte__rb);
  and and_8 (sel_MAR, clock5, clk_set, mov_ra__byte__rb);
  and and_9 (store_ra, clock6, clk_set, mov_ra__byte__rb);
  and and_10 (set_ACC, clock7, clk_set, mov_ra__byte__rb);
  and and_11 (store_ra, clock8, clk_set, mov_ra__byte__rb);
endmodule

module add_ra__byte__rb (
);

  wire add_ra__byte__rb, ALU_0000, ALU_0100, clk_en, clk_set, clock5, clock6, clock7, clock8, clock9,
       enable_lowmask, enable_TMP, load_ACC, load_ra, load_RAM, load_rb, sel_ds, sel_MAR, set_ACC,
       set_arith_flags, store_ra;

  and and_1 (sel_ds, clock5, clk_en, add_ra__byte__rb);
  and and_2 (load_rb, clock5, clk_en, add_ra__byte__rb);
  and and_3 (load_RAM, clock6, clk_en, add_ra__byte__rb);
  and and_4 (enable_lowmask, clock6, clk_en, add_ra__byte__rb);
  and and_5 (ALU_0100, clock6, clk_en, add_ra__byte__rb);
  and and_6 (load_ACC, clock7, clk_en, add_ra__byte__rb);
  and and_7 (load_ra, clock8, clk_en, add_ra__byte__rb);
  and and_8 (ALU_0000, clock8, clk_en, add_ra__byte__rb);
  and and_9 (load_ACC, clock9, clk_en, add_ra__byte__rb);
  and and_10 (sel_MAR, clock5, clk_set, add_ra__byte__rb);
  and and_11 (set_ACC, clock6, clk_set, add_ra__byte__rb);
  and and_12 (enable_TMP, clock7, clk_set, add_ra__byte__rb);
  and and_13 (set_ACC, clock8, clk_set, add_ra__byte__rb);
  and and_14 (set_arith_flags, clock8, clk_set, add_ra__byte__rb);
  and and_15 (store_ra, clock9, clk_set, add_ra__byte__rb);
endmodule

module add_word__ra___rb (
);

  wire add_word__ra___rb, ALU_0000, clk_en, clk_set, clock5, clock6, clock7, clock8, enable_TMP, load_ACC,
       load_ra, load_RAM, load_rb, sel_ds, sel_MAR, set_ACC, set_arith_flags, store_RAM;

  and and_1 (sel_ds, clock5, clk_en, add_word__ra___rb);
  and and_2 (load_ra, clock5, clk_en, add_word__ra___rb);
  and and_3 (load_rb, clock6, clk_en, add_word__ra___rb);
  and and_4 (load_RAM, clock7, clk_en, add_word__ra___rb);
  and and_5 (ALU_0000, clock7, clk_en, add_word__ra___rb);
  and and_6 (load_ACC, clock8, clk_en, add_word__ra___rb);
  and and_7 (sel_MAR, clock5, clk_set, add_word__ra___rb);
  and and_8 (enable_TMP, clock6, clk_set, add_word__ra___rb);
  and and_9 (set_ACC, clock7, clk_set, add_word__ra___rb);
  and and_10 (set_arith_flags, clock7, clk_set, add_word__ra___rb);
  and and_11 (store_RAM, clock8, clk_set, add_word__ra___rb);
endmodule

module mov_word__ra_rb___imm16 (
);

  wire ALU_0000, ALU_1000, clk_en, clk_set, clock5, clock6, clock7, clock8, clock9, clock10, clock11,
       enable_BUS1, enable_carry, enable_CLR, enable_TMP1, load_ACC, load_CS, load_IAR, load_RAM, load_rb,
       mov_word__ra_rb___imm16, sel_CS, sel_MAR, sel_ra, set_ACC, set_carry, set_IAR, store_CS, store_RAM;

  and and_1 (sel_CS, clock5, clk_en, mov_word__ra_rb___imm16);
  and and_2 (load_IAR, clock5, clk_en, mov_word__ra_rb___imm16);
  and and_3 (enable_BUS1, clock5, clk_en, mov_word__ra_rb___imm16);
  and and_4 (ALU_0000, clock5, clk_en, mov_word__ra_rb___imm16);
  and and_5 (set_carry, clock5, clk_en, mov_word__ra_rb___imm16);
  and and_6 (load_ACC, clock6, clk_en, mov_word__ra_rb___imm16);
  and and_7 (load_CS, clock7, clk_en, mov_word__ra_rb___imm16);
  and and_8 (enable_CLR, clock7, clk_en, mov_word__ra_rb___imm16);
  and and_9 (ALU_1000, clock7, clk_en, mov_word__ra_rb___imm16);
  and and_10 (load_ACC, clock8, clk_en, mov_word__ra_rb___imm16);
  and and_11 (load_RAM, clock9, clk_en, mov_word__ra_rb___imm16);
  and and_12 (enable_CLR, clock9, clk_en, mov_word__ra_rb___imm16);
  and and_13 (ALU_0000, clock9, clk_en, mov_word__ra_rb___imm16);
  and and_14 (sel_ra, clock10, clk_en, mov_word__ra_rb___imm16);
  and and_15 (load_rb, clock10, clk_en, mov_word__ra_rb___imm16);
  and and_16 (load_ACC, clock11, clk_en, mov_word__ra_rb___imm16);
  and and_17 (sel_MAR, clock5, clk_set, mov_word__ra_rb___imm16);
  and and_18 (set_ACC, clock5, clk_set, mov_word__ra_rb___imm16);
  and and_19 (enable_carry, clock5, clk_set, mov_word__ra_rb___imm16);
  and and_20 (enable_TMP1, clock5, clk_set, mov_word__ra_rb___imm16);
  and and_21 (set_IAR, clock6, clk_set, mov_word__ra_rb___imm16);
  and and_22 (set_ACC, clock7, clk_set, mov_word__ra_rb___imm16);
  and and_23 (store_CS, clock8, clk_set, mov_word__ra_rb___imm16);
  and and_24 (set_ACC, clock9, clk_set, mov_word__ra_rb___imm16);
  and and_25 (sel_MAR, clock10, clk_set, mov_word__ra_rb___imm16);
  and and_26 (store_RAM, clock11, clk_set, mov_word__ra_rb___imm16);
endmodule

module add_word__ra_rb___imm16 (
);

  wire add_word__ra_rb___imm16, ALU_0000, ALU_1000, clk_en, clk_set, clock5, clock6, clock7, clock8, clock9,
       clock10, clock11, clock12, enable_BUS1, enable_carry, enable_CLR, enable_TMP, enable_TMP1, load_ACC,
       load_CS, load_IAR, load_RAM, load_rb, sel_CS, sel_MAR, sel_ra, set_ACC, set_arith_flags, set_carry,
       set_IAR, store_CS, store_RAM;

  and and_1 (sel_CS, clock5, clk_en, add_word__ra_rb___imm16);
  and and_2 (load_IAR, clock5, clk_en, add_word__ra_rb___imm16);
  and and_3 (enable_BUS1, clock5, clk_en, add_word__ra_rb___imm16);
  and and_4 (ALU_0000, clock5, clk_en, add_word__ra_rb___imm16);
  and and_5 (set_carry, clock5, clk_en, add_word__ra_rb___imm16);
  and and_6 (load_ACC, clock6, clk_en, add_word__ra_rb___imm16);
  and and_7 (load_CS, clock7, clk_en, add_word__ra_rb___imm16);
  and and_8 (enable_CLR, clock7, clk_en, add_word__ra_rb___imm16);
  and and_9 (ALU_1000, clock7, clk_en, add_word__ra_rb___imm16);
  and and_10 (load_ACC, clock8, clk_en, add_word__ra_rb___imm16);
  and and_11 (load_RAM, clock9, clk_en, add_word__ra_rb___imm16);
  and and_12 (sel_ra, clock10, clk_en, add_word__ra_rb___imm16);
  and and_13 (load_rb, clock10, clk_en, add_word__ra_rb___imm16);
  and and_14 (load_RAM, clock11, clk_en, add_word__ra_rb___imm16);
  and and_15 (ALU_0000, clock11, clk_en, add_word__ra_rb___imm16);
  and and_16 (load_ACC, clock12, clk_en, add_word__ra_rb___imm16);
  and and_17 (sel_MAR, clock5, clk_set, add_word__ra_rb___imm16);
  and and_18 (set_ACC, clock5, clk_set, add_word__ra_rb___imm16);
  and and_19 (enable_carry, clock5, clk_set, add_word__ra_rb___imm16);
  and and_20 (enable_TMP1, clock5, clk_set, add_word__ra_rb___imm16);
  and and_21 (set_IAR, clock6, clk_set, add_word__ra_rb___imm16);
  and and_22 (set_ACC, clock7, clk_set, add_word__ra_rb___imm16);
  and and_23 (store_CS, clock8, clk_set, add_word__ra_rb___imm16);
  and and_24 (enable_TMP, clock9, clk_set, add_word__ra_rb___imm16);
  and and_25 (sel_MAR, clock10, clk_set, add_word__ra_rb___imm16);
  and and_26 (set_ACC, clock11, clk_set, add_word__ra_rb___imm16);
  and and_27 (set_arith_flags, clock11, clk_set, add_word__ra_rb___imm16);
  and and_28 (store_RAM, clock12, clk_set, add_word__ra_rb___imm16);
endmodule

module and_word__ra_rb___imm16 (
);

  wire ALU_0000, ALU_0100, ALU_1000, and_word__ra_rb___imm16, clk_en, clk_set, clock5, clock6, clock7,
       clock8, clock9, clock10, clock11, clock12, enable_BUS1, enable_carry, enable_CLR, enable_TMP,
       enable_TMP1, load_ACC, load_CS, load_IAR, load_RAM, load_rb, sel_CS, sel_MAR, sel_ra, set_ACC,
       set_arith_flags, set_carry, set_IAR, store_CS, store_RAM;

  and and_1 (sel_CS, clock5, clk_en, and_word__ra_rb___imm16);
  and and_2 (load_IAR, clock5, clk_en, and_word__ra_rb___imm16);
  and and_3 (enable_BUS1, clock5, clk_en, and_word__ra_rb___imm16);
  and and_4 (ALU_0000, clock5, clk_en, and_word__ra_rb___imm16);
  and and_5 (set_carry, clock5, clk_en, and_word__ra_rb___imm16);
  and and_6 (load_ACC, clock6, clk_en, and_word__ra_rb___imm16);
  and and_7 (load_CS, clock7, clk_en, and_word__ra_rb___imm16);
  and and_8 (enable_CLR, clock7, clk_en, and_word__ra_rb___imm16);
  and and_9 (ALU_1000, clock7, clk_en, and_word__ra_rb___imm16);
  and and_10 (load_ACC, clock8, clk_en, and_word__ra_rb___imm16);
  and and_11 (load_RAM, clock9, clk_en, and_word__ra_rb___imm16);
  and and_12 (sel_ra, clock10, clk_en, and_word__ra_rb___imm16);
  and and_13 (load_rb, clock10, clk_en, and_word__ra_rb___imm16);
  and and_14 (load_RAM, clock11, clk_en, and_word__ra_rb___imm16);
  and and_15 (ALU_0100, clock11, clk_en, and_word__ra_rb___imm16);
  and and_16 (load_ACC, clock12, clk_en, and_word__ra_rb___imm16);
  and and_17 (sel_MAR, clock5, clk_set, and_word__ra_rb___imm16);
  and and_18 (set_ACC, clock5, clk_set, and_word__ra_rb___imm16);
  and and_19 (enable_carry, clock5, clk_set, and_word__ra_rb___imm16);
  and and_20 (enable_TMP1, clock5, clk_set, and_word__ra_rb___imm16);
  and and_21 (set_IAR, clock6, clk_set, and_word__ra_rb___imm16);
  and and_22 (set_ACC, clock7, clk_set, and_word__ra_rb___imm16);
  and and_23 (store_CS, clock8, clk_set, and_word__ra_rb___imm16);
  and and_24 (enable_TMP, clock9, clk_set, and_word__ra_rb___imm16);
  and and_25 (sel_MAR, clock10, clk_set, and_word__ra_rb___imm16);
  and and_26 (set_ACC, clock11, clk_set, and_word__ra_rb___imm16);
  and and_27 (set_arith_flags, clock11, clk_set, and_word__ra_rb___imm16);
  and and_28 (store_RAM, clock12, clk_set, and_word__ra_rb___imm16);
endmodule

module or_word__ra_rb___imm16 (
);

  wire ALU_0000, ALU_0101, ALU_1000, clk_en, clk_set, clock5, clock6, clock7, clock8, clock9, clock10,
       clock11, clock12, enable_BUS1, enable_carry, enable_CLR, enable_TMP, enable_TMP1, load_ACC, load_CS,
       load_IAR, load_RAM, load_rb, or_word__ra_rb___imm16, sel_CS, sel_MAR, sel_ra, set_ACC,
       set_arith_flags, set_carry, set_IAR, store_CS, store_RAM;

  and and_1 (sel_CS, clock5, clk_en, or_word__ra_rb___imm16);
  and and_2 (load_IAR, clock5, clk_en, or_word__ra_rb___imm16);
  and and_3 (enable_BUS1, clock5, clk_en, or_word__ra_rb___imm16);
  and and_4 (ALU_0000, clock5, clk_en, or_word__ra_rb___imm16);
  and and_5 (set_carry, clock5, clk_en, or_word__ra_rb___imm16);
  and and_6 (load_ACC, clock6, clk_en, or_word__ra_rb___imm16);
  and and_7 (load_CS, clock7, clk_en, or_word__ra_rb___imm16);
  and and_8 (enable_CLR, clock7, clk_en, or_word__ra_rb___imm16);
  and and_9 (ALU_1000, clock7, clk_en, or_word__ra_rb___imm16);
  and and_10 (load_ACC, clock8, clk_en, or_word__ra_rb___imm16);
  and and_11 (load_RAM, clock9, clk_en, or_word__ra_rb___imm16);
  and and_12 (sel_ra, clock10, clk_en, or_word__ra_rb___imm16);
  and and_13 (load_rb, clock10, clk_en, or_word__ra_rb___imm16);
  and and_14 (load_RAM, clock11, clk_en, or_word__ra_rb___imm16);
  and and_15 (ALU_0101, clock11, clk_en, or_word__ra_rb___imm16);
  and and_16 (load_ACC, clock12, clk_en, or_word__ra_rb___imm16);
  and and_17 (sel_MAR, clock5, clk_set, or_word__ra_rb___imm16);
  and and_18 (set_ACC, clock5, clk_set, or_word__ra_rb___imm16);
  and and_19 (enable_carry, clock5, clk_set, or_word__ra_rb___imm16);
  and and_20 (enable_TMP1, clock5, clk_set, or_word__ra_rb___imm16);
  and and_21 (set_IAR, clock6, clk_set, or_word__ra_rb___imm16);
  and and_22 (set_ACC, clock7, clk_set, or_word__ra_rb___imm16);
  and and_23 (store_CS, clock8, clk_set, or_word__ra_rb___imm16);
  and and_24 (enable_TMP, clock9, clk_set, or_word__ra_rb___imm16);
  and and_25 (sel_MAR, clock10, clk_set, or_word__ra_rb___imm16);
  and and_26 (set_ACC, clock11, clk_set, or_word__ra_rb___imm16);
  and and_27 (set_arith_flags, clock11, clk_set, or_word__ra_rb___imm16);
  and and_28 (store_RAM, clock12, clk_set, or_word__ra_rb___imm16);
endmodule

module xor_word__ra_rb___imm16 (
);

  wire ALU_0000, ALU_0110, ALU_1000, clk_en, clk_set, clock5, clock6, clock7, clock8, clock9, clock10,
       clock11, clock12, enable_BUS1, enable_carry, enable_CLR, enable_TMP, enable_TMP1, load_ACC, load_CS,
       load_IAR, load_RAM, load_rb, sel_CS, sel_MAR, sel_ra, set_ACC, set_arith_flags, set_carry, set_IAR,
       store_CS, store_RAM, sub_ra__imm16, xor_word__ra_rb___imm16;

  and and_1 (sel_CS, clock5, clk_en, xor_word__ra_rb___imm16);
  and and_2 (load_IAR, clock5, clk_en, xor_word__ra_rb___imm16);
  and and_3 (enable_BUS1, clock5, clk_en, xor_word__ra_rb___imm16);
  and and_4 (ALU_0000, clock5, clk_en, xor_word__ra_rb___imm16);
  and and_5 (set_carry, clock5, clk_en, sub_ra__imm16);
  and and_6 (load_ACC, clock6, clk_en, xor_word__ra_rb___imm16);
  and and_7 (load_CS, clock7, clk_en, xor_word__ra_rb___imm16);
  and and_8 (enable_CLR, clock7, clk_en, xor_word__ra_rb___imm16);
  and and_9 (ALU_1000, clock7, clk_en, xor_word__ra_rb___imm16);
  and and_10 (load_ACC, clock8, clk_en, xor_word__ra_rb___imm16);
  and and_11 (load_RAM, clock9, clk_en, xor_word__ra_rb___imm16);
  and and_12 (sel_ra, clock10, clk_en, xor_word__ra_rb___imm16);
  and and_13 (load_rb, clock10, clk_en, xor_word__ra_rb___imm16);
  and and_14 (load_RAM, clock11, clk_en, xor_word__ra_rb___imm16);
  and and_15 (ALU_0110, clock11, clk_en, xor_word__ra_rb___imm16);
  and and_16 (load_ACC, clock12, clk_en, xor_word__ra_rb___imm16);
  and and_17 (sel_MAR, clock5, clk_set, xor_word__ra_rb___imm16);
  and and_18 (set_ACC, clock5, clk_set, xor_word__ra_rb___imm16);
  and and_19 (enable_carry, clock5, clk_set, xor_word__ra_rb___imm16);
  and and_20 (enable_TMP1, clock5, clk_set, xor_word__ra_rb___imm16);
  and and_21 (set_IAR, clock6, clk_set, xor_word__ra_rb___imm16);
  and and_22 (set_ACC, clock7, clk_set, xor_word__ra_rb___imm16);
  and and_23 (store_CS, clock8, clk_set, xor_word__ra_rb___imm16);
  and and_24 (enable_TMP, clock9, clk_set, xor_word__ra_rb___imm16);
  and and_25 (sel_MAR, clock10, clk_set, xor_word__ra_rb___imm16);
  and and_26 (set_ACC, clock11, clk_set, xor_word__ra_rb___imm16);
  and and_27 (set_arith_flags, clock11, clk_set, xor_word__ra_rb___imm16);
  and and_28 (store_RAM, clock12, clk_set, xor_word__ra_rb___imm16);
endmodule

module cmp_word__ra_rb___imm16 (
);

  wire ALU_0000, ALU_0111, ALU_1000, clk_en, clk_set, clock5, clock6, clock7, clock8, clock9, clock10,
       clock11, cmp_word__ra_rb___imm16, enable_BUS1, enable_carry, enable_CLR, enable_TMP, enable_TMP1,
       load_ACC, load_CS, load_IAR, load_RAM, load_rb, sel_CS, sel_MAR, sel_ra, set_ACC, set_arith_flags,
       set_carry, set_IAR, store_CS, sub_ra__imm16, xor_word__ra_rb___imm16;

  and and_1 (sel_CS, clock5, clk_en, xor_word__ra_rb___imm16);
  and and_2 (load_IAR, clock5, clk_en, xor_word__ra_rb___imm16);
  and and_3 (enable_BUS1, clock5, clk_en, xor_word__ra_rb___imm16);
  and and_4 (ALU_0000, clock5, clk_en, xor_word__ra_rb___imm16);
  and and_5 (set_carry, clock5, clk_en, sub_ra__imm16);
  and and_6 (load_ACC, clock6, clk_en, xor_word__ra_rb___imm16);
  and and_7 (load_CS, clock7, clk_en, cmp_word__ra_rb___imm16);
  and and_8 (enable_CLR, clock7, clk_en, cmp_word__ra_rb___imm16);
  and and_9 (ALU_1000, clock7, clk_en, cmp_word__ra_rb___imm16);
  and and_10 (load_ACC, clock8, clk_en, cmp_word__ra_rb___imm16);
  and and_11 (load_RAM, clock9, clk_en, cmp_word__ra_rb___imm16);
  and and_12 (sel_ra, clock10, clk_en, cmp_word__ra_rb___imm16);
  and and_13 (load_rb, clock10, clk_en, cmp_word__ra_rb___imm16);
  and and_14 (load_RAM, clock11, clk_en, cmp_word__ra_rb___imm16);
  and and_15 (ALU_0111, clock11, clk_en, cmp_word__ra_rb___imm16);
  and and_16 (sel_MAR, clock5, clk_set, xor_word__ra_rb___imm16);
  and and_17 (set_ACC, clock5, clk_set, xor_word__ra_rb___imm16);
  and and_18 (enable_carry, clock5, clk_set, xor_word__ra_rb___imm16);
  and and_19 (enable_TMP1, clock5, clk_set, xor_word__ra_rb___imm16);
  and and_20 (set_IAR, clock6, clk_set, xor_word__ra_rb___imm16);
  and and_21 (set_ACC, clock7, clk_set, cmp_word__ra_rb___imm16);
  and and_22 (store_CS, clock8, clk_set, cmp_word__ra_rb___imm16);
  and and_23 (enable_TMP, clock9, clk_set, cmp_word__ra_rb___imm16);
  and and_24 (sel_MAR, clock10, clk_set, cmp_word__ra_rb___imm16);
  and and_25 (set_ACC, clock11, clk_set, cmp_word__ra_rb___imm16);
  and and_26 (set_arith_flags, clock11, clk_set, cmp_word__ra_rb___imm16);
endmodule

module push_ra (
);

  wire ALU_0000, ALU_1000, clk_en, clk_set, clock5, clock6, clock7, clock8, clock9, clock10, enable_BUS1,
       enable_carry, enable_CLR, enable_TMP1, load_ACC, load_ra, load_sp, load_SS, push_ra, sel_MAR, sel_ss,
       set_ACC, set_carry, store_RAM, store_sp, store_ss;

  and and_1 (load_sp, clock5, clk_en, push_ra);
  and and_2 (enable_BUS1, clock5, clk_en, push_ra);
  and and_3 (ALU_0000, clock5, clk_en, push_ra);
  and and_4 (set_carry, clock5, clk_en, push_ra);
  and and_5 (load_ACC, clock6, clk_en, push_ra);
  and and_6 (load_SS, clock7, clk_en, push_ra);
  and and_7 (enable_CLR, clock7, clk_en, push_ra);
  and and_8 (ALU_1000, clock7, clk_en, push_ra);
  and and_9 (load_ACC, clock8, clk_en, push_ra);
  and and_10 (sel_ss, clock9, clk_en, push_ra);
  and and_11 (load_sp, clock9, clk_en, push_ra);
  and and_12 (load_ra, clock10, clk_en, push_ra);
  and and_13 (set_ACC, clock5, clk_set, push_ra);
  and and_14 (enable_carry, clock5, clk_set, push_ra);
  and and_15 (enable_TMP1, clock5, clk_set, push_ra);
  and and_16 (store_sp, clock6, clk_set, push_ra);
  and and_17 (set_ACC, clock7, clk_set, push_ra);
  and and_18 (store_ss, clock8, clk_set, push_ra);
  and and_19 (sel_MAR, clock9, clk_set, push_ra);
  and and_20 (store_RAM, clock10, clk_set, push_ra);
endmodule

module push_imm16 (
);

  wire ALU_0000, ALU_1000, clk_en, clk_set, clock5, clock6, clock7, clock8, clock9, clock10, clock11,
       clock12, clock13, clock14, clock15, enable_BUS1, enable_carry, enable_CLR, enable_TMP1, load_ACC,
       load_cs, load_IAR, load_RAM, load_sp, load_SS, push_imm16, sel_cs, sel_MAR, sel_ss, set_ACC,
       set_carry, store_cs, store_IAR, store_RAM, store_sp, store_ss;

  and and_1 (load_sp, clock5, clk_en, push_imm16);
  and and_2 (enable_BUS1, clock5, clk_en, push_imm16);
  and and_3 (ALU_0000, clock5, clk_en, push_imm16);
  and and_4 (set_carry, clock5, clk_en, push_imm16);
  and and_5 (load_ACC, clock6, clk_en, push_imm16);
  and and_6 (load_SS, clock7, clk_en, push_imm16);
  and and_7 (enable_CLR, clock7, clk_en, push_imm16);
  and and_8 (ALU_1000, clock7, clk_en, push_imm16);
  and and_9 (load_ACC, clock8, clk_en, push_imm16);
  and and_10 (sel_cs, clock9, clk_en, push_imm16);
  and and_11 (load_IAR, clock9, clk_en, push_imm16);
  and and_12 (enable_BUS1, clock9, clk_en, push_imm16);
  and and_13 (ALU_0000, clock9, clk_en, push_imm16);
  and and_14 (set_carry, clock9, clk_en, push_imm16);
  and and_15 (load_ACC, clock10, clk_en, push_imm16);
  and and_16 (load_cs, clock11, clk_en, push_imm16);
  and and_17 (enable_CLR, clock11, clk_en, push_imm16);
  and and_18 (ALU_1000, clock11, clk_en, push_imm16);
  and and_19 (load_ACC, clock12, clk_en, push_imm16);
  and and_20 (load_RAM, clock13, clk_en, push_imm16);
  and and_21 (enable_CLR, clock13, clk_en, push_imm16);
  and and_22 (ALU_0000, clock13, clk_en, push_imm16);
  and and_23 (sel_ss, clock14, clk_en, push_imm16);
  and and_24 (load_sp, clock14, clk_en, push_imm16);
  and and_25 (load_ACC, clock15, clk_en, push_imm16);
  and and_26 (set_ACC, clock5, clk_set, push_imm16);
  and and_27 (enable_carry, clock5, clk_set, push_imm16);
  and and_28 (enable_TMP1, clock5, clk_set, push_imm16);
  and and_29 (store_sp, clock6, clk_set, push_imm16);
  and and_30 (set_ACC, clock7, clk_set, push_imm16);
  and and_31 (store_ss, clock8, clk_set, push_imm16);
  and and_32 (sel_MAR, clock9, clk_set, push_imm16);
  and and_33 (set_ACC, clock9, clk_set, push_imm16);
  and and_34 (enable_carry, clock9, clk_set, push_imm16);
  and and_35 (enable_TMP1, clock9, clk_set, push_imm16);
  and and_36 (store_IAR, clock10, clk_set, push_imm16);
  and and_37 (set_ACC, clock11, clk_set, push_imm16);
  and and_38 (store_cs, clock12, clk_set, push_imm16);
  and and_39 (set_ACC, clock13, clk_set, push_imm16);
  and and_40 (sel_MAR, clock14, clk_set, push_imm16);
  and and_41 (store_RAM, clock15, clk_set, push_imm16);
endmodule

module push_byte__ra_rb (
);

  wire ALU_0000, ALU_0100, ALU_1000, clk_en, clk_set, clock5, clock6, clock7, clock8, clock9, clock10,
       clock11, clock12, enable_BUS1, enable_carry, enable_CLR, enable_lowmask, enable_TMP1, load_ACC,
       load_RAM, load_rb, load_sp, load_SS, push_byte__ra_rb, sel_MAR, sel_ra, sel_ss, set_ACC, set_carry,
       store_RAM, store_sp, store_ss;

  and and_1 (load_sp, clock5, clk_en, push_byte__ra_rb);
  and and_2 (enable_BUS1, clock5, clk_en, push_byte__ra_rb);
  and and_3 (ALU_0000, clock5, clk_en, push_byte__ra_rb);
  and and_4 (set_carry, clock5, clk_en, push_byte__ra_rb);
  and and_5 (load_ACC, clock6, clk_en, push_byte__ra_rb);
  and and_6 (load_SS, clock7, clk_en, push_byte__ra_rb);
  and and_7 (enable_CLR, clock7, clk_en, push_byte__ra_rb);
  and and_8 (ALU_1000, clock7, clk_en, push_byte__ra_rb);
  and and_9 (load_ACC, clock8, clk_en, push_byte__ra_rb);
  and and_10 (sel_ra, clock9, clk_en, push_byte__ra_rb);
  and and_11 (load_rb, clock9, clk_en, push_byte__ra_rb);
  and and_12 (load_RAM, clock10, clk_en, push_byte__ra_rb);
  and and_13 (enable_lowmask, clock10, clk_en, push_byte__ra_rb);
  and and_14 (ALU_0100, clock10, clk_en, push_byte__ra_rb);
  and and_15 (sel_ss, clock11, clk_en, push_byte__ra_rb);
  and and_16 (load_sp, clock11, clk_en, push_byte__ra_rb);
  and and_17 (load_ACC, clock12, clk_en, push_byte__ra_rb);
  and and_18 (set_ACC, clock5, clk_set, push_byte__ra_rb);
  and and_19 (enable_carry, clock5, clk_set, push_byte__ra_rb);
  and and_20 (enable_TMP1, clock5, clk_set, push_byte__ra_rb);
  and and_21 (store_sp, clock6, clk_set, push_byte__ra_rb);
  and and_22 (set_ACC, clock7, clk_set, push_byte__ra_rb);
  and and_23 (store_ss, clock8, clk_set, push_byte__ra_rb);
  and and_24 (sel_MAR, clock9, clk_set, push_byte__ra_rb);
  and and_25 (set_ACC, clock10, clk_set, push_byte__ra_rb);
  and and_26 (sel_MAR, clock11, clk_set, push_byte__ra_rb);
  and and_27 (store_RAM, clock12, clk_set, push_byte__ra_rb);
endmodule

module push_word__ra_rb (
);

  wire ALU_0000, ALU_1000, clk_en, clk_set, clock5, clock6, clock7, clock8, clock9, clock10, clock11,
       clock12, enable_BUS1, enable_carry, enable_CLR, enable_TMP1, load_ACC, load_RAM, load_rb, load_sp,
       load_SS, push_word__ra_rb, sel_MAR, sel_ra, sel_ss, set_ACC, set_carry, store_RAM, store_sp, store_ss;

  and and_1 (load_sp, clock5, clk_en, push_word__ra_rb);
  and and_2 (enable_BUS1, clock5, clk_en, push_word__ra_rb);
  and and_3 (ALU_0000, clock5, clk_en, push_word__ra_rb);
  and and_4 (set_carry, clock5, clk_en, push_word__ra_rb);
  and and_5 (load_ACC, clock6, clk_en, push_word__ra_rb);
  and and_6 (load_SS, clock7, clk_en, push_word__ra_rb);
  and and_7 (enable_CLR, clock7, clk_en, push_word__ra_rb);
  and and_8 (ALU_1000, clock7, clk_en, push_word__ra_rb);
  and and_9 (load_ACC, clock8, clk_en, push_word__ra_rb);
  and and_10 (sel_ra, clock9, clk_en, push_word__ra_rb);
  and and_11 (load_rb, clock9, clk_en, push_word__ra_rb);
  and and_12 (load_RAM, clock10, clk_en, push_word__ra_rb);
  and and_13 (enable_CLR, clock10, clk_en, push_word__ra_rb);
  and and_14 (ALU_0000, clock10, clk_en, push_word__ra_rb);
  and and_15 (sel_ss, clock11, clk_en, push_word__ra_rb);
  and and_16 (load_sp, clock11, clk_en, push_word__ra_rb);
  and and_17 (load_ACC, clock12, clk_en, push_word__ra_rb);
  and and_18 (set_ACC, clock5, clk_set, push_word__ra_rb);
  and and_19 (enable_carry, clock5, clk_set, push_word__ra_rb);
  and and_20 (enable_TMP1, clock5, clk_set, push_word__ra_rb);
  and and_21 (store_sp, clock6, clk_set, push_word__ra_rb);
  and and_22 (set_ACC, clock7, clk_set, push_word__ra_rb);
  and and_23 (store_ss, clock8, clk_set, push_word__ra_rb);
  and and_24 (sel_MAR, clock9, clk_set, push_word__ra_rb);
  and and_25 (set_ACC, clock10, clk_set, push_word__ra_rb);
  and and_26 (sel_MAR, clock11, clk_set, push_word__ra_rb);
  and and_27 (store_RAM, clock12, clk_set, push_word__ra_rb);
endmodule

module pop_ra (
);

  wire ALU_1010, ALU_1100, clk_en, clk_set, clock5, clock6, clock7, clock8, clock9, enable_BUS1,
       enable_carry, enable_CLR, enable_TMP1, load_ACC, load_RAM, load_sp, load_ss, pop_ra, sel_MAR, sel_ss,
       set_ACC, set_carry, store_ra, store_sp, store_ss;

  and and_1 (sel_ss, clock5, clk_en, pop_ra);
  and and_2 (load_sp, clock5, clk_en, pop_ra);
  and and_3 (enable_BUS1, clock5, clk_en, pop_ra);
  and and_4 (ALU_1100, clock5, clk_en, pop_ra);
  and and_5 (set_carry, clock5, clk_en, pop_ra);
  and and_6 (load_ACC, clock6, clk_en, pop_ra);
  and and_7 (load_ss, clock7, clk_en, pop_ra);
  and and_8 (enable_CLR, clock7, clk_en, pop_ra);
  and and_9 (ALU_1010, clock7, clk_en, pop_ra);
  and and_10 (load_ACC, clock8, clk_en, pop_ra);
  and and_11 (load_RAM, clock9, clk_en, pop_ra);
  and and_12 (sel_MAR, clock5, clk_set, pop_ra);
  and and_13 (set_ACC, clock5, clk_set, pop_ra);
  and and_14 (enable_carry, clock5, clk_set, pop_ra);
  and and_15 (enable_TMP1, clock5, clk_set, pop_ra);
  and and_16 (store_sp, clock6, clk_set, pop_ra);
  and and_17 (set_ACC, clock7, clk_set, pop_ra);
  and and_18 (store_ss, clock8, clk_set, pop_ra);
  and and_19 (store_ra, clock9, clk_set, pop_ra);
endmodule

module pop_byte__ra_rb (
);

  wire ALU_0100, ALU_1010, ALU_1100, clk_en, clk_set, clock5, clock6, clock7, clock8, clock9, clock10,
       clock11, enable_BUS1, enable_carry, enable_CLR, enable_lowmask, enable_TMP1, load_ACC, load_RAM,
       load_rb, load_sp, load_ss, pop_byte__ra_rb, sel_MAR, sel_ra, sel_ss, set_ACC, set_carry, store_RAM,
       store_sp, store_ss;

  and and_1 (sel_ss, clock5, clk_en, pop_byte__ra_rb);
  and and_2 (load_sp, clock5, clk_en, pop_byte__ra_rb);
  and and_3 (enable_BUS1, clock5, clk_en, pop_byte__ra_rb);
  and and_4 (ALU_1100, clock5, clk_en, pop_byte__ra_rb);
  and and_5 (set_carry, clock5, clk_en, pop_byte__ra_rb);
  and and_6 (load_ACC, clock6, clk_en, pop_byte__ra_rb);
  and and_7 (load_ss, clock7, clk_en, pop_byte__ra_rb);
  and and_8 (enable_CLR, clock7, clk_en, pop_byte__ra_rb);
  and and_9 (ALU_1010, clock7, clk_en, pop_byte__ra_rb);
  and and_10 (load_ACC, clock8, clk_en, pop_byte__ra_rb);
  and and_11 (load_RAM, clock9, clk_en, pop_byte__ra_rb);
  and and_12 (enable_lowmask, clock9, clk_en, pop_byte__ra_rb);
  and and_13 (ALU_0100, clock9, clk_en, pop_byte__ra_rb);
  and and_14 (sel_ra, clock10, clk_en, pop_byte__ra_rb);
  and and_15 (load_rb, clock10, clk_en, pop_byte__ra_rb);
  and and_16 (load_ACC, clock11, clk_en, pop_byte__ra_rb);
  and and_17 (sel_MAR, clock5, clk_set, pop_byte__ra_rb);
  and and_18 (set_ACC, clock5, clk_set, pop_byte__ra_rb);
  and and_19 (enable_carry, clock5, clk_set, pop_byte__ra_rb);
  and and_20 (enable_TMP1, clock5, clk_set, pop_byte__ra_rb);
  and and_21 (store_sp, clock6, clk_set, pop_byte__ra_rb);
  and and_22 (set_ACC, clock7, clk_set, pop_byte__ra_rb);
  and and_23 (store_ss, clock8, clk_set, pop_byte__ra_rb);
  and and_24 (set_ACC, clock9, clk_set, pop_byte__ra_rb);
  and and_25 (sel_MAR, clock10, clk_set, pop_byte__ra_rb);
  and and_26 (store_RAM, clock11, clk_set, pop_byte__ra_rb);
endmodule

module pop_word__ra_rb (
);

  wire ALU_0000, ALU_1010, ALU_1100, clk_en, clk_set, clock5, clock6, clock7, clock8, clock9, clock10,
       clock11, enable_BUS1, enable_carry, enable_CLR, enable_TMP1, load_ACC, load_RAM, load_rb, load_sp,
       load_ss, pop_word__ra_rb, sel_MAR, sel_ra, sel_ss, set_ACC, set_carry, store_RAM, store_sp, store_ss;

  and and_1 (sel_ss, clock5, clk_en, pop_word__ra_rb);
  and and_2 (load_sp, clock5, clk_en, pop_word__ra_rb);
  and and_3 (enable_BUS1, clock5, clk_en, pop_word__ra_rb);
  and and_4 (ALU_1100, clock5, clk_en, pop_word__ra_rb);
  and and_5 (set_carry, clock5, clk_en, pop_word__ra_rb);
  and and_6 (load_ACC, clock6, clk_en, pop_word__ra_rb);
  and and_7 (load_ss, clock7, clk_en, pop_word__ra_rb);
  and and_8 (enable_CLR, clock7, clk_en, pop_word__ra_rb);
  and and_9 (ALU_1010, clock7, clk_en, pop_word__ra_rb);
  and and_10 (load_ACC, clock8, clk_en, pop_word__ra_rb);
  and and_11 (load_RAM, clock9, clk_en, pop_word__ra_rb);
  and and_12 (enable_CLR, clock9, clk_en, pop_word__ra_rb);
  and and_13 (ALU_0000, clock9, clk_en, pop_word__ra_rb);
  and and_14 (sel_ra, clock10, clk_en, pop_word__ra_rb);
  and and_15 (load_rb, clock10, clk_en, pop_word__ra_rb);
  and and_16 (load_ACC, clock11, clk_en, pop_word__ra_rb);
  and and_17 (sel_MAR, clock5, clk_set, pop_word__ra_rb);
  and and_18 (set_ACC, clock5, clk_set, pop_word__ra_rb);
  and and_19 (enable_carry, clock5, clk_set, pop_word__ra_rb);
  and and_20 (enable_TMP1, clock5, clk_set, pop_word__ra_rb);
  and and_21 (store_sp, clock6, clk_set, pop_word__ra_rb);
  and and_22 (set_ACC, clock7, clk_set, pop_word__ra_rb);
  and and_23 (store_ss, clock8, clk_set, pop_word__ra_rb);
  and and_24 (set_ACC, clock9, clk_set, pop_word__ra_rb);
  and and_25 (sel_MAR, clock10, clk_set, pop_word__ra_rb);
  and and_26 (store_RAM, clock11, clk_set, pop_word__ra_rb);
endmodule

module pop0 (
);

  wire ALU_1010, ALU_1100, clk_en, clk_set, clock5, clock6, clock7, clock8, enable_BUS1, enable_carry,
       enable_CLR, enable_TMP1, load_ACC, load_sp, load_ss, pop0, set_ACC, set_carry, store_sp, store_ss;

  and and_1 (load_sp, clock5, clk_en, pop0);
  and and_2 (enable_BUS1, clock5, clk_en, pop0);
  and and_3 (ALU_1100, clock5, clk_en, pop0);
  and and_4 (set_carry, clock5, clk_en, pop0);
  and and_5 (load_ACC, clock6, clk_en, pop0);
  and and_6 (load_ss, clock7, clk_en, pop0);
  and and_7 (enable_CLR, clock7, clk_en, pop0);
  and and_8 (ALU_1010, clock7, clk_en, pop0);
  and and_9 (load_ACC, clock8, clk_en, pop0);
  and and_10 (set_ACC, clock5, clk_set, pop0);
  and and_11 (enable_carry, clock5, clk_set, pop0);
  and and_12 (enable_TMP1, clock5, clk_set, pop0);
  and and_13 (store_sp, clock6, clk_set, pop0);
  and and_14 (set_ACC, clock7, clk_set, pop0);
  and and_15 (store_ss, clock8, clk_set, pop0);
endmodule

module jmp_ra_imm16 (
);

  wire clk_en, clk_set, clock5, clock6, clock7, jmp_ra_imm16, load_IAR, load_ra, load_RAM, sel_CS, sel_MAR,
       set_IAR, store_CS;

  and and_1 (sel_CS, clock5, clk_en, jmp_ra_imm16);
  and and_2 (load_IAR, clock5, clk_en, jmp_ra_imm16);
  and and_3 (load_RAM, clock6, clk_en, jmp_ra_imm16);
  and and_4 (load_ra, clock7, clk_en, jmp_ra_imm16);
  and and_5 (sel_MAR, clock5, clk_set, jmp_ra_imm16);
  and and_6 (set_IAR, clock6, clk_set, jmp_ra_imm16);
  and and_7 (store_CS, clock7, clk_set, jmp_ra_imm16);
endmodule

module jmp_ra_rb (
);

  wire clk_en, clk_set, clock5, clock6, jmp_ra_rb, load_ra, load_rb, store_CS, store_IAR;

  and and_1 (load_ra, clock5, clk_en, jmp_ra_rb);
  and and_2 (load_rb, clock6, clk_en, jmp_ra_rb);
  and and_3 (store_CS, clock5, clk_set, jmp_ra_rb);
  and and_4 (store_IAR, clock6, clk_set, jmp_ra_rb);
endmodule

module ja_ra_imm16 (
);

  wire clk_en, clock5, clock6, clock7, ja_ra_imm16, load_IAR, load_ra, load_RAM, sel_CS, sel_MAR, set_IAR,
       store_CS, tunnel;

  and and_1 (sel_CS, clock5, clk_en, ja_ra_imm16, tunnel);
  and and_2 (load_IAR, clock5, clk_en, ja_ra_imm16, tunnel);
  and and_3 (load_RAM, clock6, clk_en, ja_ra_imm16, tunnel);
  and and_4 (load_ra, clock7, clk_en, ja_ra_imm16, tunnel);
  and and_5 (sel_MAR, clock5, clk_en, ja_ra_imm16, tunnel);
  and and_6 (set_IAR, clock6, clk_en, ja_ra_imm16, tunnel);
  and and_7 (store_CS, clock7, clk_en, ja_ra_imm16, tunnel);
endmodule

module ja_ra_rb (
);

  wire clk_en, clock5, clock6, ja_ra_rb, load_ra, load_rb, store_CS, store_IAR, tunnel;

  and and_1 (load_ra, clock5, clk_en, ja_ra_rb, tunnel);
  and and_2 (load_rb, clock6, clk_en, ja_ra_rb, tunnel);
  and and_3 (store_CS, clock5, clk_en, ja_ra_rb, tunnel);
  and and_4 (store_IAR, clock6, clk_en, ja_ra_rb, tunnel);
endmodule

module jna_ra_imm16 (
);

  wire clk_en, clock5, clock6, clock7, jna_ra_imm16, load_IAR, load_ra, load_RAM, not_above, sel_CS, sel_MAR,
       set_IAR, store_CS, tunnel;

  not not_1 (not_above, tunnel);
  and and_1 (sel_CS, clock5, clk_en, jna_ra_imm16, not_above);
  and and_2 (load_IAR, clock5, clk_en, jna_ra_imm16, not_above);
  and and_3 (load_RAM, clock6, clk_en, jna_ra_imm16, not_above);
  and and_4 (load_ra, clock7, clk_en, jna_ra_imm16, not_above);
  and and_5 (sel_MAR, clock5, clk_en, jna_ra_imm16, not_above);
  and and_6 (set_IAR, clock6, clk_en, jna_ra_imm16, not_above);
  and and_7 (store_CS, clock7, clk_en, jna_ra_imm16, not_above);
endmodule

module jna_ra_rb (
);

  wire clk_en, clock5, clock6, jna_ra_rb, load_ra, load_rb, not_above, store_CS, store_IAR, tunnel;

  not not_1 (not_above, tunnel);
  and and_1 (load_ra, clock5, clk_en, jna_ra_rb, not_above);
  and and_2 (load_rb, clock6, clk_en, jna_ra_rb, not_above);
  and and_3 (store_CS, clock5, clk_en, jna_ra_rb, not_above);
  and and_4 (store_IAR, clock6, clk_en, jna_ra_rb, not_above);
endmodule

module jb_ra_imm16 (
);

  wire clk_en, clock5, clock6, clock7, jb_ra_imm16, load_IAR, load_ra, load_RAM, sel_CS, sel_MAR, set_IAR,
       store_CS, tunnel;

  and and_1 (sel_CS, clock5, clk_en, jb_ra_imm16, tunnel);
  and and_2 (load_IAR, clock5, clk_en, jb_ra_imm16, tunnel);
  and and_3 (load_RAM, clock6, clk_en, jb_ra_imm16, tunnel);
  and and_4 (load_ra, clock7, clk_en, jb_ra_imm16, tunnel);
  and and_5 (sel_MAR, clock5, clk_en, jb_ra_imm16, tunnel);
  and and_6 (set_IAR, clock6, clk_en, jb_ra_imm16, tunnel);
  and and_7 (store_CS, clock7, clk_en, jb_ra_imm16, tunnel);
endmodule

module jb_ra_rb (
);

  wire clk_en, clock5, clock6, jb_ra_rb, load_ra, load_rb, store_CS, store_IAR, tunnel;

  and and_1 (load_ra, clock5, clk_en, jb_ra_rb, tunnel);
  and and_2 (load_rb, clock6, clk_en, jb_ra_rb, tunnel);
  and and_3 (store_CS, clock5, clk_en, jb_ra_rb, tunnel);
  and and_4 (store_IAR, clock6, clk_en, jb_ra_rb, tunnel);
endmodule

module jnb_ra_imm16 (
);

  wire clk_en, clock5, clock6, clock7, jnb_ra_imm16, load_IAR, load_ra, load_RAM, not_below, sel_CS, sel_MAR,
       set_IAR, store_CS, tunnel;

  not not_1 (not_below, tunnel);
  and and_1 (sel_CS, clock5, clk_en, jnb_ra_imm16, not_below);
  and and_2 (load_IAR, clock5, clk_en, jnb_ra_imm16, not_below);
  and and_3 (load_RAM, clock6, clk_en, jnb_ra_imm16, not_below);
  and and_4 (load_ra, clock7, clk_en, jnb_ra_imm16, not_below);
  and and_5 (sel_MAR, clock5, clk_en, jnb_ra_imm16, not_below);
  and and_6 (set_IAR, clock6, clk_en, jnb_ra_imm16, not_below);
  and and_7 (store_CS, clock7, clk_en, jnb_ra_imm16, not_below);
endmodule

module jnb_ra_rb (
);

  wire clk_en, clock5, clock6, jnb_ra_rb, load_ra, load_rb, not_below, store_CS, store_IAR, tunnel;

  not not_1 (not_below, tunnel);
  and and_1 (load_ra, clock5, clk_en, jnb_ra_rb, not_below);
  and and_2 (load_rb, clock6, clk_en, jnb_ra_rb, not_below);
  and and_3 (store_CS, clock5, clk_en, jnb_ra_rb, not_below);
  and and_4 (store_IAR, clock6, clk_en, jnb_ra_rb, not_below);
endmodule

module jeq_ra_imm16 (
);

  wire clk_en, clock5, clock6, clock7, jeq_ra_imm16, load_IAR, load_ra, load_RAM, sel_CS, sel_MAR, set_IAR,
       store_CS, tunnel;

  and and_1 (sel_CS, clock5, clk_en, jeq_ra_imm16, tunnel);
  and and_2 (load_IAR, clock5, clk_en, jeq_ra_imm16, tunnel);
  and and_3 (load_RAM, clock6, clk_en, jeq_ra_imm16, tunnel);
  and and_4 (load_ra, clock7, clk_en, jeq_ra_imm16, tunnel);
  and and_5 (sel_MAR, clock5, clk_en, jeq_ra_imm16, tunnel);
  and and_6 (set_IAR, clock6, clk_en, jeq_ra_imm16, tunnel);
  and and_7 (store_CS, clock7, clk_en, jeq_ra_imm16, tunnel);
endmodule

module jeq_ra_rb (
);

  wire clk_en, clock5, clock6, jeq_ra_rb, load_ra, load_rb, store_CS, store_IAR, tunnel;

  and and_1 (load_ra, clock5, clk_en, jeq_ra_rb, tunnel);
  and and_2 (load_rb, clock6, clk_en, jeq_ra_rb, tunnel);
  and and_3 (store_CS, clock5, clk_en, jeq_ra_rb, tunnel);
  and and_4 (store_IAR, clock6, clk_en, jeq_ra_rb, tunnel);
endmodule

module jneq_ra_imm16 (
);

  wire clk_en, clock5, clock6, clock7, jneq_ra_imm16, load_IAR, load_ra, load_RAM, not_equal, sel_CS,
       sel_MAR, set_IAR, store_CS, tunnel;

  not not_1 (not_equal, tunnel);
  and and_1 (sel_CS, clock5, clk_en, jneq_ra_imm16, not_equal);
  and and_2 (load_IAR, clock5, clk_en, jneq_ra_imm16, not_equal);
  and and_3 (load_RAM, clock6, clk_en, jneq_ra_imm16, not_equal);
  and and_4 (load_ra, clock7, clk_en, jneq_ra_imm16, not_equal);
  and and_5 (sel_MAR, clock5, clk_en, jneq_ra_imm16, not_equal);
  and and_6 (set_IAR, clock6, clk_en, jneq_ra_imm16, not_equal);
  and and_7 (store_CS, clock7, clk_en, jneq_ra_imm16, not_equal);
endmodule

module jneq_ra_rb (
);

  wire clk_en, clock5, clock6, jneq_ra_rb, load_ra, load_rb, not_equal, store_CS, store_IAR, tunnel;

  not not_1 (not_equal, tunnel);
  and and_1 (load_ra, clock5, clk_en, jneq_ra_rb, not_equal);
  and and_2 (load_rb, clock6, clk_en, jneq_ra_rb, not_equal);
  and and_3 (store_CS, clock5, clk_en, jneq_ra_rb, not_equal);
  and and_4 (store_IAR, clock6, clk_en, jneq_ra_rb, not_equal);
endmodule

module jc_ra_imm16 (
);

  wire c, clk_en, clock5, clock6, clock7, jc_ra_imm16, load_IAR, load_ra, load_RAM, sel_CS, sel_MAR, set_IAR,
       store_CS;

  and and_1 (sel_CS, clock5, clk_en, jc_ra_imm16, c);
  and and_2 (load_IAR, clock5, clk_en, jc_ra_imm16, c);
  and and_3 (load_RAM, clock6, clk_en, jc_ra_imm16, c);
  and and_4 (load_ra, clock7, clk_en, jc_ra_imm16, c);
  and and_5 (sel_MAR, clock5, clk_en, jc_ra_imm16, c);
  and and_6 (set_IAR, clock6, clk_en, jc_ra_imm16, c);
  and and_7 (store_CS, clock7, clk_en, jc_ra_imm16, c);
endmodule

module jc_ra_rb (
);

  wire c, clk_en, clock5, clock6, jc_ra_rb, load_ra, load_rb, store_CS, store_IAR;

  and and_1 (load_ra, clock5, clk_en, jc_ra_rb, c);
  and and_2 (load_rb, clock6, clk_en, jc_ra_rb, c);
  and and_3 (store_CS, clock5, clk_en, jc_ra_rb, c);
  and and_4 (store_IAR, clock6, clk_en, jc_ra_rb, c);
endmodule

module jnc_ra_imm16 (
);

  wire c, clk_en, clock5, clock6, clock7, jnc_ra_imm16, load_IAR, load_ra, load_RAM, not_carry, sel_CS,
       sel_MAR, set_IAR, store_CS;

  not not_1 (not_carry, c);
  and and_1 (sel_CS, clock5, clk_en, jnc_ra_imm16, not_carry);
  and and_2 (load_IAR, clock5, clk_en, jnc_ra_imm16, not_carry);
  and and_3 (load_RAM, clock6, clk_en, jnc_ra_imm16, not_carry);
  and and_4 (load_ra, clock7, clk_en, jnc_ra_imm16, not_carry);
  and and_5 (sel_MAR, clock5, clk_en, jnc_ra_imm16, not_carry);
  and and_6 (set_IAR, clock6, clk_en, jnc_ra_imm16, not_carry);
  and and_7 (store_CS, clock7, clk_en, jnc_ra_imm16, not_carry);
endmodule

module jnc_ra_rb (
);

  wire c, clk_en, clock5, clock6, jnc_ra_rb, load_ra, load_rb, not_carry, store_CS, store_IAR;

  not not_1 (not_carry, c);
  and and_1 (load_ra, clock5, clk_en, jnc_ra_rb, not_carry);
  and and_2 (load_rb, clock6, clk_en, jnc_ra_rb, not_carry);
  and and_3 (store_CS, clock5, clk_en, jnc_ra_rb, not_carry);
  and and_4 (store_IAR, clock6, clk_en, jnc_ra_rb, not_carry);
endmodule

module jev_ra_imm16 (
);

  wire clk_en, clock5, clock6, clock7, e, jev_ra_imm16, load_IAR, load_ra, load_RAM, sel_CS, sel_MAR,
       set_IAR, store_CS;

  and and_1 (sel_CS, clock5, clk_en, jev_ra_imm16, e);
  and and_2 (load_IAR, clock5, clk_en, jev_ra_imm16, e);
  and and_3 (load_RAM, clock6, clk_en, jev_ra_imm16, e);
  and and_4 (load_ra, clock7, clk_en, jev_ra_imm16, e);
  and and_5 (sel_MAR, clock5, clk_en, jev_ra_imm16, e);
  and and_6 (set_IAR, clock6, clk_en, jev_ra_imm16, e);
  and and_7 (store_CS, clock7, clk_en, jev_ra_imm16, e);
endmodule

module jev_ra_rb (
);

  wire clk_en, clock5, clock6, e, jev_ra_rb, load_ra, load_rb, store_CS, store_IAR;

  and and_1 (load_ra, clock5, clk_en, jev_ra_rb, e);
  and and_2 (load_rb, clock6, clk_en, jev_ra_rb, e);
  and and_3 (store_CS, clock5, clk_en, jev_ra_rb, e);
  and and_4 (store_IAR, clock6, clk_en, jev_ra_rb, e);
endmodule

module jnev_ra_imm16 (
);

  wire clk_en, clock5, clock6, clock7, e, jnev_ra_imm16, load_IAR, load_ra, load_RAM, not_even, sel_CS,
       sel_MAR, set_IAR, store_CS;

  not not_1 (not_even, e);
  and and_1 (sel_CS, clock5, clk_en, jnev_ra_imm16, not_even);
  and and_2 (load_IAR, clock5, clk_en, jnev_ra_imm16, not_even);
  and and_3 (load_RAM, clock6, clk_en, jnev_ra_imm16, not_even);
  and and_4 (load_ra, clock7, clk_en, jnev_ra_imm16, not_even);
  and and_5 (sel_MAR, clock5, clk_en, jnev_ra_imm16, not_even);
  and and_6 (set_IAR, clock6, clk_en, jnev_ra_imm16, not_even);
  and and_7 (store_CS, clock7, clk_en, jnev_ra_imm16, not_even);
endmodule

module jnev_ra_rb (
);

  wire clk_en, clock5, clock6, e, jnev_ra_rb, load_ra, load_rb, not_even, store_CS, store_IAR;

  not not_1 (not_even, e);
  and and_1 (load_ra, clock5, clk_en, jnev_ra_rb, not_even);
  and and_2 (load_rb, clock6, clk_en, jnev_ra_rb, not_even);
  and and_3 (store_CS, clock5, clk_en, jnev_ra_rb, not_even);
  and and_4 (store_IAR, clock6, clk_en, jnev_ra_rb, not_even);
endmodule

module jp_ra_imm16 (
);

  wire clk_en, clock5, clock6, clock7, jp_ra_imm16, load_IAR, load_ra, load_RAM, p, sel_CS, sel_MAR, set_IAR,
       store_CS;

  and and_1 (sel_CS, clock5, clk_en, jp_ra_imm16, p);
  and and_2 (load_IAR, clock5, clk_en, jp_ra_imm16, p);
  and and_3 (load_RAM, clock6, clk_en, jp_ra_imm16, p);
  and and_4 (load_ra, clock7, clk_en, jp_ra_imm16, p);
  and and_5 (sel_MAR, clock5, clk_en, jp_ra_imm16, p);
  and and_6 (set_IAR, clock6, clk_en, jp_ra_imm16, p);
  and and_7 (store_CS, clock7, clk_en, jp_ra_imm16, p);
endmodule

module jp_ra_rb (
);

  wire clk_en, clock5, clock6, jp_ra_rb, load_ra, load_rb, p, store_CS, store_IAR;

  and and_1 (load_ra, clock5, clk_en, jp_ra_rb, p);
  and and_2 (load_rb, clock6, clk_en, jp_ra_rb, p);
  and and_3 (store_CS, clock5, clk_en, jp_ra_rb, p);
  and and_4 (store_IAR, clock6, clk_en, jp_ra_rb, p);
endmodule

module jnp_ra_imm16 (
);

  wire clk_en, clock5, clock6, clock7, jnp_ra_imm16, load_IAR, load_ra, load_RAM, not_positive, p, sel_CS,
       sel_MAR, set_IAR, store_CS;

  not not_1 (not_positive, p);
  and and_1 (sel_CS, clock5, clk_en, jnp_ra_imm16, not_positive);
  and and_2 (load_IAR, clock5, clk_en, jnp_ra_imm16, not_positive);
  and and_3 (load_RAM, clock6, clk_en, jnp_ra_imm16, not_positive);
  and and_4 (load_ra, clock7, clk_en, jnp_ra_imm16, not_positive);
  and and_5 (sel_MAR, clock5, clk_en, jnp_ra_imm16, not_positive);
  and and_6 (set_IAR, clock6, clk_en, jnp_ra_imm16, not_positive);
  and and_7 (store_CS, clock7, clk_en, jnp_ra_imm16, not_positive);
endmodule

module jnp_ra_rb (
);

  wire clk_en, clock5, clock6, jnp_ra_rb, load_ra, load_rb, not_positive, p, store_CS, store_IAR;

  not not_1 (not_positive, p);
  and and_1 (load_ra, clock5, clk_en, jnp_ra_rb, not_positive);
  and and_2 (load_rb, clock6, clk_en, jnp_ra_rb, not_positive);
  and and_3 (store_CS, clock5, clk_en, jnp_ra_rb, not_positive);
  and and_4 (store_IAR, clock6, clk_en, jnp_ra_rb, not_positive);
endmodule

module jz_ra_imm16 (
);

  wire clk_en, clock5, clock6, clock7, jz_ra_imm16, load_IAR, load_ra, load_RAM, sel_CS, sel_MAR, set_IAR,
       store_CS, z;

  and and_1 (sel_CS, clock5, clk_en, jz_ra_imm16, z);
  and and_2 (load_IAR, clock5, clk_en, jz_ra_imm16, z);
  and and_3 (load_RAM, clock6, clk_en, jz_ra_imm16, z);
  and and_4 (load_ra, clock7, clk_en, jz_ra_imm16, z);
  and and_5 (sel_MAR, clock5, clk_en, jz_ra_imm16, z);
  and and_6 (set_IAR, clock6, clk_en, jz_ra_imm16, z);
  and and_7 (store_CS, clock7, clk_en, jz_ra_imm16, z);
endmodule

module jz_ra_rb (
);

  wire clk_en, clock5, clock6, jz_ra_rb, load_ra, load_rb, store_CS, store_IAR, z;

  and and_1 (load_ra, clock5, clk_en, jz_ra_rb, z);
  and and_2 (load_rb, clock6, clk_en, jz_ra_rb, z);
  and and_3 (store_CS, clock5, clk_en, jz_ra_rb, z);
  and and_4 (store_IAR, clock6, clk_en, jz_ra_rb, z);
endmodule

module jnz_ra_imm16 (
);

  wire clk_en, clock5, clock6, clock7, jnz_ra_imm16, load_IAR, load_ra, load_RAM, not_zero, sel_CS, sel_MAR,
       set_IAR, store_CS, z;

  not not_1 (not_zero, z);
  and and_1 (sel_CS, clock5, clk_en, jnz_ra_imm16, not_zero);
  and and_2 (load_IAR, clock5, clk_en, jnz_ra_imm16, not_zero);
  and and_3 (load_RAM, clock6, clk_en, jnz_ra_imm16, not_zero);
  and and_4 (load_ra, clock7, clk_en, jnz_ra_imm16, not_zero);
  and and_5 (sel_MAR, clock5, clk_en, jnz_ra_imm16, not_zero);
  and and_6 (set_IAR, clock6, clk_en, jnz_ra_imm16, not_zero);
  and and_7 (store_CS, clock7, clk_en, jnz_ra_imm16, not_zero);
endmodule

module jnz_ra_rb (
);

  wire clk_en, clock5, clock6, jnz_ra_rb, load_ra, load_rb, not_zero, store_CS, store_IAR, z;

  not not_1 (not_zero, z);
  and and_1 (load_ra, clock5, clk_en, jnz_ra_rb, not_zero);
  and and_2 (load_rb, clock6, clk_en, jnz_ra_rb, not_zero);
  and and_3 (store_CS, clock5, clk_en, jnz_ra_rb, not_zero);
  and and_4 (store_IAR, clock6, clk_en, jnz_ra_rb, not_zero);
endmodule

module jr_ra_imm16 (
);

  wire clk_en, clock5, clock6, clock7, jr_ra_imm16, load_IAR, load_ra, load_RAM, r, sel_CS, sel_MAR, set_IAR,
       store_CS;

  and and_1 (sel_CS, clock5, clk_en, jr_ra_imm16, r);
  and and_2 (load_IAR, clock5, clk_en, jr_ra_imm16, r);
  and and_3 (load_RAM, clock6, clk_en, jr_ra_imm16, r);
  and and_4 (load_ra, clock7, clk_en, jr_ra_imm16, r);
  and and_5 (sel_MAR, clock5, clk_en, jr_ra_imm16, r);
  and and_6 (set_IAR, clock6, clk_en, jr_ra_imm16, r);
  and and_7 (store_CS, clock7, clk_en, jr_ra_imm16, r);
endmodule
module jr_ra_rb (
);

  wire clk_en, clock5, clock6, jr_ra_rb, load_ra, load_rb, r, store_CS, store_IAR;

  and and_1 (load_ra, clock5, clk_en, jr_ra_rb, r);
  and and_2 (load_rb, clock6, clk_en, jr_ra_rb, r);
  and and_3 (store_CS, clock5, clk_en, jr_ra_rb, r);
  and and_4 (store_IAR, clock6, clk_en, jr_ra_rb, r);
endmodule

module jnr_ra_imm16 (
);

  wire clk_en, clock5, clock6, clock7, jnr_ra_imm16, load_IAR, load_ra, load_RAM, not_reserved, r, sel_CS,
       sel_MAR, set_IAR, store_CS;

  not not_1 (not_reserved, r);
  and and_1 (sel_CS, clock5, clk_en, jnr_ra_imm16, not_reserved);
  and and_2 (load_IAR, clock5, clk_en, jnr_ra_imm16, not_reserved);
  and and_3 (load_RAM, clock6, clk_en, jnr_ra_imm16, not_reserved);
  and and_4 (load_ra, clock7, clk_en, jnr_ra_imm16, not_reserved);
  and and_5 (sel_MAR, clock5, clk_en, jnr_ra_imm16, not_reserved);
  and and_6 (set_IAR, clock6, clk_en, jnr_ra_imm16, not_reserved);
  and and_7 (store_CS, clock7, clk_en, jnr_ra_imm16, not_reserved);
endmodule

module jnr_ra_rb (
);

  wire clk_en, clock5, clock6, jnr_ra_rb, load_ra, load_rb, not_reserved, r, store_CS, store_IAR;

  not not_1 (not_reserved, r);
  and and_1 (load_ra, clock5, clk_en, jnr_ra_rb, not_reserved);
  and and_2 (load_rb, clock6, clk_en, jnr_ra_rb, not_reserved);
  and and_3 (store_CS, clock5, clk_en, jnr_ra_rb, not_reserved);
  and and_4 (store_IAR, clock6, clk_en, jnr_ra_rb, not_reserved);
endmodule
